// Logisim project cpu21-riscv各种流水线+分支预测.circ as structural Verilog: 24 circuits, main circuit ◆重定向流水线
module \单周期RISC_V  (
  input  IR1,
  input  IR2,
  input  IR3,
  output RegWrite,
  output MemWrite,
  output [31:0] PC,
  output [31:0] IR,
  output [31:0] RDin,
  output [31:0] MDin,
  output [31:0] LedData
);

  wire alu_2_equal, alu_2_out_6, and_1_out, and_2_out, and_3_out, and_4_out, and_5_out, CLK, clock_1_out,
       comparator_1_eq, comparator_1_lt, d_ff_1_q, ecall, Go, halt, IR1_t, IR2_t, IR3_t, IRA, IRB, IRC, JAL,
       JALR, LBU, nand_1_out, not_1_out, not_2_out, not_3_out, not_4_out, not_5_out, not_7_out, or_1_out,
       or_4_out, or_5_out, or_7_out, RST, uret, W1, W2, W3, \单周期硬布线控制器_1_alu_src , \单周期硬布线控制器_1_beq ,
       \单周期硬布线控制器_1_blt , \单周期硬布线控制器_1_bne , \单周期硬布线控制器_1_memtoreg , \单周期硬布线控制器_1_s_type ;
  wire [3:0] \单周期硬布线控制器_1_alu_op ;
  wire [4:0] multiplexer_2_out, multiplexer_3_out;
  wire [7:0] bitselector_1_out;
  wire [11:0] multiplexer_4_out, shifter_1_out;
  wire [12:0] CNT_num;
  wire [15:0] \总周期数 ;
  wire [19:0] shifter_2_out;
  wire [31:0] adder_1_out, alu_1_result, alu_2_result, bit_extender_1_out, bit_extender_2_out,
       bit_extender_3_out, bit_extender_4_out, multiplexer_1_out, multiplexer_6_out, multiplexer_7_out,
       multiplexer_8_out, multiplexer_9_out, multiplexer_10_out, multiplexer_11_out, multiplexer_12_out,
       ram_1_data, regifile_1_r1;

  Button \u_继续运行  (.out(Go));
  Button _1 (.out(IRA));
  Button _2 (.out(IRB));
  Button _3 (.out(IRC));
  LED #(.active("true")) led_1 (.in(W1));
  LED #(.active("true")) led_2 (.in(W2));
  LED #(.active("true")) led_3 (.in(W3));
  Counter #(.width(16), .max('hffff), .ongoal("wrap"), .trigger("rising"), .behavior("old")) counter_1 (
    .count(not_1_out), .Q(\总周期数 ), .clk(CLK));  // open: load, D, carry, clr, preset
  not not_1 (not_1_out, halt);
  Hex_Digit_Display hex_digit_display_1 (.value(LedData[31:28]));  // open: dp
  Multiplexer #(.select(1), .width(32), .disabled("Z"), .enable("false")) multiplexer_1 (
    .in0(adder_1_out), .in1(alu_1_result), .out(multiplexer_1_out), .sel(or_1_out));
  Hex_Digit_Display hex_digit_display_2 (.value(LedData[27:24]));  // open: dp
  Hex_Digit_Display hex_digit_display_3 (.value(LedData[23:20]));  // open: dp
  Register #(.width(32), .trigger("rising"), .Select("low")) u_PC (
    .D(multiplexer_1_out), .en(not_2_out), .Q(PC), .clk(CLK), .clr(RST));
  not not_2 (not_2_out, halt);
  Hex_Digit_Display hex_digit_display_4 (.value(LedData[15:12]));  // open: dp
  Hex_Digit_Display hex_digit_display_5 (.value(LedData[19:16]));  // open: dp
  Adder #(.width(32)) adder_1 (.a(PC), .b(32'h4), .out(adder_1_out));  // open: cin, cout
  Hex_Digit_Display hex_digit_display_6 (.value(LedData[11:8]));  // open: dp
  Hex_Digit_Display hex_digit_display_7 (.value(LedData[7:4]));  // open: dp
  // Probe on \总周期数 
  Hex_Digit_Display hex_digit_display_8 (.value(LedData[3:0]));  // open: dp
  or or_1 (or_1_out, or_4_out, JALR, JAL);
  // RiscV_Probe riscv_probe_1: pin names not known; wires that end beside it: IR
  ROM #(.addrWidth(10), .dataWidth(32), .Select("high")) rom_1 (.addr(PC[11:2]), .data(IR));
  or or_2 (IR1_t, IR1, IRA);
  \单周期硬布线控制器  \u_单周期硬布线控制器_1  (
    .Funct({IR[30], IR[25], IR[14:12]}), .OP(IR[6:2]), .ALU_OP(\单周期硬布线控制器_1_alu_op ),
    .MemToReg(\单周期硬布线控制器_1_memtoreg ), .MemWrite(MemWrite), .ALU_SRC(\单周期硬布线控制器_1_alu_src ),
    .RegWrite(RegWrite), .ecall(ecall), .S_type(\单周期硬布线控制器_1_s_type ), .Jalr(JALR), .Beq(\单周期硬布线控制器_1_beq ),
    .JAL(JAL), .Bne(\单周期硬布线控制器_1_bne ), .in_3(IR[21]), .uret(uret), .LBU(LBU), .BLT(\单周期硬布线控制器_1_blt ));  // open: Csrsi, Csrci
  Multiplexer #(.select(1), .width(5), .disabled("Z"), .enable("false")) multiplexer_2 (
    .in0(IR[19:15]), .in1(5'b10001), .out(multiplexer_2_out), .sel(ecall));
  Multiplexer #(.select(1), .width(5), .disabled("Z"), .enable("false")) multiplexer_3 (
    .in0(IR[24:20]), .in1(5'b01010), .out(multiplexer_3_out), .sel(ecall));
  or or_3 (IR2_t, IR2, IRB);
  and and_1 (and_1_out, \单周期硬布线控制器_1_beq , alu_2_equal);
  Multiplexer #(.select(1), .width(12), .disabled("Z"), .enable("false")) multiplexer_4 (
    .in0(IR[31:20]), .in1({IR[31:25], IR[11:7]}), .out(multiplexer_4_out), .sel(\单周期硬布线控制器_1_s_type ));
  Shifter #(.width(12), .shift("ll")) shifter_1 (
    .in({IR[31], IR[7], IR[30:25], IR[11:8]}), .\dist (4'b0001), .out(shifter_1_out));
  Shifter #(.width(20), .shift("ll")) shifter_2 (
    .in({IR[31], IR[19:12], IR[20], IR[30:21]}), .\dist (5'b00001), .out(shifter_2_out));
  Multiplexer #(.select(1), .width(32), .disabled("Z"), .enable("false")) multiplexer_5 (
    .in0(multiplexer_12_out), .in1(adder_1_out), .out(RDin), .sel(or_5_out));
  or or_4 (or_4_out, and_1_out, and_2_out, and_3_out);
  and and_2 (and_2_out, \单周期硬布线控制器_1_blt , alu_2_out_6);
  Regifile regifile_1 (
    .Din(RDin), .Clk(CLK), .R1(regifile_1_r1), .R2(MDin), .WE(RegWrite), .W_num(IR[11:7]),
    .R1_num(multiplexer_2_out), .R2_num(multiplexer_3_out));
  assign bit_extender_1_out = {{20{multiplexer_4_out[11]}}, multiplexer_4_out};  // Bit_Extender bit_extender_1
  assign bit_extender_2_out = {{20{shifter_1_out[11]}}, shifter_1_out};  // Bit_Extender bit_extender_2
  Multiplexer #(.select(1), .width(32), .disabled("Z"), .enable("false")) multiplexer_6 (
    .in0(bit_extender_2_out), .in1(bit_extender_3_out), .out(multiplexer_6_out), .sel(JAL));
  assign bit_extender_3_out = {{12{shifter_2_out[19]}}, shifter_2_out};  // Bit_Extender bit_extender_3
  or or_5 (or_5_out, JAL, JALR);
  or or_6 (IR3_t, IR3, IRC);
  and and_3 (and_3_out, \单周期硬布线控制器_1_bne , not_3_out);
  not not_3 (not_3_out, alu_2_equal);
  Multiplexer #(.select(1), .width(32), .disabled("Z"), .enable("false")) multiplexer_7 (
    .in0(multiplexer_6_out), .in1(bit_extender_1_out), .out(multiplexer_7_out), .sel(JALR));
  Multiplexer #(.select(1), .width(32), .disabled("Z"), .enable("false")) multiplexer_8 (
    .in0(MDin), .in1(bit_extender_1_out), .out(multiplexer_8_out), .sel(\单周期硬布线控制器_1_alu_src ));
  Multiplexer #(.select(1), .width(32), .disabled("Z"), .enable("false")) multiplexer_9 (
    .in0(PC), .in1(regifile_1_r1), .out(multiplexer_9_out), .sel(JALR));
  ALU alu_1 (
    .X(multiplexer_7_out), .Y(multiplexer_9_out), .AluOP(4'b0101), .Result(alu_1_result));  // open: Equal, Result_2, out_4, out_6
  Multiplexer #(.select(1), .width(32), .disabled("Z"), .enable("false")) multiplexer_10 (
    .in0(multiplexer_8_out), .in1(32'h22), .out(multiplexer_10_out), .sel(ecall));
  not not_4 (not_4_out, alu_2_equal);
  ALU alu_2 (
    .X(regifile_1_r1), .Y(multiplexer_10_out), .AluOP(\单周期硬布线控制器_1_alu_op ), .Equal(alu_2_equal),
    .Result(alu_2_result), .out_6(alu_2_out_6));  // open: Result_2, out_4
  not not_5 (not_5_out, and_4_out);
  and and_4 (and_4_out, ecall, not_4_out);
  and and_5 (and_5_out, ecall, alu_2_equal);
  not not_6 (halt, or_7_out);
  or or_7 (or_7_out, Go, not_5_out);
  Register #(.width(32), .trigger("rising"), .Select("low")) register_1 (
    .D(MDin), .en(and_5_out), .Q(LedData), .clk(CLK));  // open: clr
  not not_7 (not_7_out, halt);
  D_Flip_Flop #(.trigger("high"), .Pre_Clr_Positions("LEGACY"), .NegatePresetClear("false"), .enable("true"), .NewFFLayout("false")) d_ff_1 (.Q(d_ff_1_q));  // open: clk, D, Qn, preset, en, reset
  // Probe on 13'h176
  RAM #(.addrWidth(10), .dataWidth(32), .bus("separate"), .Select("high")) ram_1 (
    .addr(alu_2_result[11:2]), .din(MDin), .data(ram_1_data), .str(MemWrite), .sel(not_7_out), .clk(CLK));  // open: ld, clr
  Comparator #(.width(13), .mode("twosComplement")) comparator_1 (
    .a(CNT_num), .b(13'h176), .eq(comparator_1_eq), .lt(comparator_1_lt));  // open: gt
  Clock #(.highDuration(1), .lowDuration(1)) clock_1 (.out(clock_1_out));
  Multiplexer #(.select(1), .width(32), .disabled("Z"), .enable("false")) multiplexer_11 (
    .in0(alu_2_result), .in1(ram_1_data), .out(multiplexer_11_out), .sel(\单周期硬布线控制器_1_memtoreg ));
  assign bit_extender_4_out = {{24{1'b0}}, bitselector_1_out};  // Bit_Extender bit_extender_4
  BitSelector #(.width(32), .group(8)) bitselector_1 (
    .in(ram_1_data), .out(bitselector_1_out), .sel(alu_2_result[1:0]));
  Counter #(.width(13), .max('h1fff), .ongoal("stay"), .trigger("rising"), .behavior("old")) counter_2 (
    .count(comparator_1_lt), .Q(CNT_num), .clk(clock_1_out));  // open: load, D, carry, clr, preset
  Multiplexer #(.select(1), .width(32), .disabled("Z"), .enable("false")) multiplexer_12 (
    .in0(multiplexer_11_out), .in1(bit_extender_4_out), .out(multiplexer_12_out), .sel(LBU));
  nand nand_1 (nand_1_out, d_ff_1_q, comparator_1_eq);
  assign CLK = nand_1_out ? clock_1_out : 1'bz;  // Controlled_Buffer controlled_buffer_1
  Pull_Resistor #(.pull(1)) pull_resistor_1 (.node(CLK));

  // Notes on the sheet:
  //   中断源
  //   中断等待指示
  //   数码管输出应该用寄存器锁存，否则显示数据只能一闪而过
  //   数码管输出
  //   PC_branch
  //   指令探针
  //   指令存储器
  //   指令字
  //   contents of rom_1 (hex, n*v repeats v):
  //   100493 100006f 100493 200913 300993 100006f 100493 200913 300993 100006f 100493 200913 300993
  //   100006f 100493 200913 300993 3d0000ef 100413 100493 1f49493 900533 2200893 73 24d493 48463 fedff06f
  //   900533 2200893 73 100493 249493 900533 2200893 73 48463 fedff06f 100493 1f49493 900533 2200893 73
  //   4034d493 900533 2200893 73 4044d493 900533 2200893 73 4044d493 900533 2200893 73 4044d493 900533
  //   2200893 73 4044d493 900533 2200893 73 4044d493 900533 2200893 73 4044d493 900533 2200893 73 4044d493
  //   900533 2200893 73 100413 1f41993 41f9d993 433 c00913 300b13 140413 f47413 800293 100313 499993
  //   89e9b3 1300533 2200893 73 406282b3 fe0294e3 140413 f00f93 1f47433 1c41413 800293 100313 49d993
  //   89e9b3 1300533 2200893 73 406282b3 fe0294e3 1c45413 406b0b33 b0463 f95ff06f 2b3 fff2c293 829293
  //   ff2e293 500533 2200893 73 fff00413 493 84a023 140413 448493 84a023 140413 448493 84a023 140413
  //   448493 84a023 140413 448493 84a023 140413 448493 84a023 140413 448493 84a023 140413 448493 84a023
  //   140413 448493 84a023 140413 448493 84a023 140413 448493 84a023 140413 448493 84a023 140413 448493
  //   84a023 140413 448493 84a023 140413 448493 84a023 140413 448493 84a023 140413 448493 140413 433
  //   3c00493 42983 4aa03 149a2b3 28663 134a023 1442023 ffc48493 fe9412e3 800533 2200893 73 440413 3c00493
  //   fc9416e3 3200893 73 100293 300313 800493 849493 7648493 1449493 900533 2200893 73 800e13 54d4b3
  //   64d4b3 900533 2200893 73 fffe0e13 fe0e14e3 a00893 73 fff00293 7700493 849493 7748493 900533 2200893
  //   73 1000e13 54c4b3 900533 2200893 73 fffe0e13 fe0e16e3 a00893 73 313 1000e13 8400493 849493 8348493
  //   400913 891913 490913 849493 8248493 849493 8148493 891913 490913 891913 490913 932023 12484b3 430313
  //   fffe0e13 fe0e18e3 2000e13 313 34483 900533 2200893 73 130313 fffe0e13 fe0e14e3 a00893 73 ff100493
  //   900533 2200893 73 148493 fe04c8e3 a00893 73 a00893 73 413 140413 800533 2200893 73 240413 800533
  //   2200893 73 340413 800533 2200893 73 440413 800533 2200893 73 540413 800533 2200893 73 640413 800533
  //   2200893 73 740413 800533 2200893 73 840413 800533 2200893 2200893 73 8067
  //   J
  //   I
  //   S
  //   B
  //   Beq
  //   Bne
  //   AluOP
  //   AluSrcB
  //   RegWrite
  //   ecall时,判断a17==34?
  //   ALU1的imm默认为I型，置1为S型
  //   JAL,JALR需把PC+4存入寄存器
  //    PC+4
  //   B_type
  //   MemToReg
  //   MemWrite
  //   equal
  //   B=PC/寄存器
  //   为方便自动评测，需要输出PC，IR，寄存器堆写如数据RDin
  //   RAM写使能MemWrite、RAM写入数据MDin等信号
  //   数据存储器
  //   控制位
  //   暂停节拍，不能为0
  //   戳工具置1进入计数暂停模式，ctrl+k时钟自动运行到对应节拍暂停
  //   ctrl+k关闭时钟连续运行，将控制位置零，进入单步调试模式调试
  //   用这个时钟源需要去掉电路中的其他时钟源
  //   可计数暂停的时钟源
endmodule

// 单周期硬布线控制器
module \单周期硬布线控制器  (
  input  [4:0] OP,
  input  [4:0] Funct,
  input  in_3,
  output [3:0] ALU_OP,
  output uret,
  output MemToReg,
  output ecall,
  output MemWrite,
  output ALU_SRC,
  output RegWrite,
  output S_type,
  output Beq,
  output Bne,
  output Jalr,
  output JAL,
  output LBU,
  output BLT,
  output Csrsi,
  output Csrci
);

  wire \控制信号自动生成_1_ecall ;

  \运算控制器自动生成  \u_运算控制器自动生成_1  (
    .OP2(OP[0]), .OP3(OP[1]), .OP4(OP[2]), .OP5(OP[3]), .OP6(OP[4]), .F12(Funct[0]), .F13(Funct[1]),
    .F14(Funct[2]), .F25(Funct[3]), .F30(Funct[4]), .S0(ALU_OP[0]), .S1(ALU_OP[1]), .S2(ALU_OP[2]),
    .S3(ALU_OP[3]));
  \控制信号自动生成  \u_控制信号自动生成_1  (
    .OP2(OP[0]), .OP3(OP[1]), .OP4(OP[2]), .OP5(OP[3]), .OP6(OP[4]), .MemToReg(MemToReg), .F12(Funct[0]),
    .F13(Funct[1]), .F14(Funct[2]), .F25(Funct[3]), .F30(Funct[4]), .MemWrite(MemWrite), .ALU_SRC(ALU_SRC),
    .RegWrite(RegWrite), .ecall(\控制信号自动生成_1_ecall ), .S_Type(S_type), .BEQ(Beq), .BNE(Bne), .JALR(Jalr),
    .JAL(JAL), .LBU(LBU), .BLT(BLT), .CSRSI(Csrsi), .CSRCI(Csrci));
  and and_1 (uret, in_3, \控制信号自动生成_1_ecall );
  and and_2 (ecall, ~in_3, \控制信号自动生成_1_ecall );  // AND_Gate

  // Other names for the same wires on the sheet: IR21 = in_3; OP_CODE[4:0] = OP

  // Notes on the sheet:
  //   运算器控制器，根据指令生成运算器功能选择信号
  //   控制信号生成，产生数据通路需要的其他控制信号
endmodule

// 运算器控制器
module \运算控制器自动生成  (
  input  OP2,
  input  OP3,
  input  OP4,
  input  OP5,
  input  OP6,
  input  F12,
  input  F13,
  input  F14,
  input  F25,
  input  F30,
  output S0,
  output S1,
  output S2,
  output S3
);

  wire and_1_out, and_2_out, and_3_out, and_4_out, and_5_out, and_6_out, and_7_out, and_8_out, and_9_out,
       and_10_out, and_11_out, and_12_out, and_13_out, and_14_out, and_15_out, and_16_out, and_17_out,
       and_18_out, and_19_out, and_20_out, and_21_out, and_22_out, and_23_out, and_24_out, and_25_out,
       and_26_out, and_27_out, and_28_out, and_29_out, and_30_out, and_31_out, and_32_out, and_33_out,
       and_34_out, and_35_out, and_36_out, not_1_out, not_2_out, not_3_out, not_4_out, not_5_out, not_6_out,
       not_7_out, not_8_out, not_9_out, not_10_out, not_11_out, not_12_out, not_13_out, not_14_out,
       not_15_out, not_16_out, not_17_out, not_18_out, not_19_out, not_20_out, not_21_out, not_22_out,
       not_23_out, not_24_out, not_25_out, not_26_out, not_27_out, not_28_out, not_29_out, not_30_out,
       not_31_out, not_32_out, not_33_out, not_34_out, not_35_out, not_36_out, not_37_out, not_38_out,
       not_39_out, not_40_out, not_41_out, not_42_out, not_43_out, not_44_out, not_45_out, not_46_out,
       not_47_out, not_48_out, not_49_out, not_50_out, not_51_out, not_52_out, not_53_out, not_54_out,
       not_55_out, not_56_out, not_57_out, not_58_out, not_59_out, not_60_out, not_61_out, not_62_out,
       not_63_out, not_64_out, not_65_out, not_66_out, not_67_out, not_68_out, not_69_out, not_70_out,
       not_71_out, not_72_out, not_73_out, not_74_out, not_75_out, not_76_out, not_77_out, not_78_out,
       not_79_out, not_80_out, not_81_out, not_82_out, not_83_out, not_84_out, not_85_out, not_86_out,
       not_87_out, not_88_out, not_89_out, not_90_out, not_91_out, not_92_out, not_93_out, not_94_out,
       not_95_out, not_96_out, not_97_out, not_98_out, not_99_out, not_100_out, not_101_out, not_102_out,
       not_103_out, not_104_out, not_105_out, not_106_out, not_107_out, not_108_out, not_109_out,
       not_110_out, not_111_out, not_112_out, not_113_out, not_114_out, not_115_out, not_116_out,
       not_117_out, not_118_out, not_119_out, not_120_out, not_121_out, not_122_out, not_123_out,
       not_124_out, not_125_out, not_126_out, not_127_out, not_128_out, not_129_out, not_130_out,
       not_131_out, not_132_out, not_133_out, not_134_out, not_135_out, not_136_out, not_137_out,
       not_138_out, not_139_out, not_140_out, not_141_out, not_142_out, not_143_out, not_144_out,
       not_145_out, not_146_out, not_147_out, not_148_out, not_149_out, not_150_out, not_151_out,
       not_152_out, not_153_out, not_154_out, not_155_out, not_156_out, not_157_out, not_158_out,
       not_159_out, not_160_out, not_161_out, not_162_out, not_163_out, not_164_out, not_165_out,
       not_166_out, not_167_out, not_168_out, not_169_out, not_170_out, not_171_out, not_172_out,
       not_173_out, not_174_out, not_175_out, not_176_out, not_177_out, not_178_out, not_179_out,
       not_180_out, not_181_out, not_182_out, not_183_out, not_184_out, not_185_out, not_186_out,
       not_187_out, not_188_out, not_189_out, not_190_out, not_191_out, not_192_out, not_193_out,
       not_194_out, not_195_out, not_196_out, not_197_out, not_198_out, not_199_out, not_200_out,
       not_201_out, not_202_out, not_203_out, not_204_out, not_205_out, not_206_out, not_207_out,
       not_208_out, not_209_out, not_210_out, not_211_out, not_212_out, not_213_out, not_214_out,
       not_215_out, not_216_out, not_217_out, not_218_out, not_219_out, not_220_out, not_221_out;

  not not_1 (not_1_out, F30);
  not not_2 (not_2_out, F25);
  not not_3 (not_3_out, F14);
  not not_4 (not_4_out, F13);
  not not_5 (not_5_out, F12);
  not not_6 (not_6_out, OP6);
  not not_7 (not_7_out, OP3);
  not not_8 (not_8_out, OP2);
  not not_9 (not_9_out, F30);
  not not_10 (not_10_out, F25);
  not not_11 (not_11_out, OP6);
  not not_12 (not_12_out, OP3);
  not not_13 (not_13_out, OP2);
  not not_14 (not_14_out, F30);
  not not_15 (not_15_out, F25);
  not not_16 (not_16_out, F14);
  not not_17 (not_17_out, F12);
  not not_18 (not_18_out, OP6);
  not not_19 (not_19_out, OP3);
  not not_20 (not_20_out, OP2);
  not not_21 (not_21_out, F14);
  not not_22 (not_22_out, F13);
  not not_23 (not_23_out, F12);
  not not_24 (not_24_out, OP6);
  not not_25 (not_25_out, OP5);
  not not_26 (not_26_out, OP3);
  not not_27 (not_27_out, OP2);
  not not_28 (not_28_out, OP6);
  not not_29 (not_29_out, OP5);
  not not_30 (not_30_out, OP3);
  not not_31 (not_31_out, OP2);
  not not_32 (not_32_out, F13);
  not not_33 (not_33_out, F12);
  not not_34 (not_34_out, OP6);
  not not_35 (not_35_out, OP5);
  not not_36 (not_36_out, OP3);
  not not_37 (not_37_out, OP2);
  not not_38 (not_38_out, F14);
  not not_39 (not_39_out, F12);
  not not_40 (not_40_out, OP6);
  not not_41 (not_41_out, OP5);
  not not_42 (not_42_out, OP3);
  not not_43 (not_43_out, OP2);
  not not_44 (not_44_out, F25);
  not not_45 (not_45_out, F13);
  not not_46 (not_46_out, OP6);
  not not_47 (not_47_out, OP5);
  not not_48 (not_48_out, OP3);
  not not_49 (not_49_out, OP2);
  not not_50 (not_50_out, F14);
  not not_51 (not_51_out, F12);
  not not_52 (not_52_out, OP6);
  not not_53 (not_53_out, OP5);
  not not_54 (not_54_out, OP4);
  not not_55 (not_55_out, OP3);
  not not_56 (not_56_out, OP2);
  not not_57 (not_57_out, F30);
  not not_58 (not_58_out, F25);
  not not_59 (not_59_out, F13);
  not not_60 (not_60_out, F12);
  not not_61 (not_61_out, OP6);
  not not_62 (not_62_out, OP3);
  not not_63 (not_63_out, OP2);
  not not_64 (not_64_out, F13);
  not not_65 (not_65_out, F12);
  not not_66 (not_66_out, OP6);
  not not_67 (not_67_out, OP5);
  not not_68 (not_68_out, OP4);
  not not_69 (not_69_out, OP3);
  not not_70 (not_70_out, OP2);
  not not_71 (not_71_out, F13);
  not not_72 (not_72_out, F12);
  not not_73 (not_73_out, OP4);
  not not_74 (not_74_out, OP3);
  not not_75 (not_75_out, OP2);
  not not_76 (not_76_out, F25);
  not not_77 (not_77_out, F14);
  not not_78 (not_78_out, F13);
  not not_79 (not_79_out, F12);
  not not_80 (not_80_out, OP6);
  not not_81 (not_81_out, OP3);
  not not_82 (not_82_out, OP2);
  not not_83 (not_83_out, F30);
  not not_84 (not_84_out, F25);
  not not_85 (not_85_out, OP6);
  not not_86 (not_86_out, OP3);
  not not_87 (not_87_out, OP2);
  not not_88 (not_88_out, F30);
  not not_89 (not_89_out, F25);
  not not_90 (not_90_out, F14);
  not not_91 (not_91_out, F12);
  not not_92 (not_92_out, OP6);
  not not_93 (not_93_out, OP3);
  not not_94 (not_94_out, OP2);
  not not_95 (not_95_out, OP6);
  not not_96 (not_96_out, OP5);
  not not_97 (not_97_out, OP3);
  not not_98 (not_98_out, OP2);
  not not_99 (not_99_out, F14);
  not not_100 (not_100_out, F12);
  not not_101 (not_101_out, OP6);
  not not_102 (not_102_out, OP5);
  not not_103 (not_103_out, OP3);
  not not_104 (not_104_out, OP2);
  not not_105 (not_105_out, F30);
  not not_106 (not_106_out, F25);
  not not_107 (not_107_out, F13);
  not not_108 (not_108_out, OP6);
  not not_109 (not_109_out, OP5);
  not not_110 (not_110_out, OP3);
  not not_111 (not_111_out, OP2);
  not not_112 (not_112_out, F30);
  not not_113 (not_113_out, F25);
  not not_114 (not_114_out, F13);
  not not_115 (not_115_out, OP6);
  not not_116 (not_116_out, OP3);
  not not_117 (not_117_out, OP2);
  not not_118 (not_118_out, F13);
  not not_119 (not_119_out, F12);
  not not_120 (not_120_out, OP4);
  not not_121 (not_121_out, OP3);
  not not_122 (not_122_out, OP2);
  not not_123 (not_123_out, F30);
  not not_124 (not_124_out, F25);
  not not_125 (not_125_out, F14);
  not not_126 (not_126_out, F13);
  not not_127 (not_127_out, F12);
  not not_128 (not_128_out, OP6);
  not not_129 (not_129_out, OP3);
  not not_130 (not_130_out, OP2);
  not not_131 (not_131_out, F25);
  not not_132 (not_132_out, F14);
  not not_133 (not_133_out, F13);
  not not_134 (not_134_out, F12);
  not not_135 (not_135_out, OP6);
  not not_136 (not_136_out, OP3);
  not not_137 (not_137_out, OP2);
  not not_138 (not_138_out, F30);
  not not_139 (not_139_out, F25);
  not not_140 (not_140_out, OP6);
  not not_141 (not_141_out, OP3);
  not not_142 (not_142_out, OP2);
  not not_143 (not_143_out, F30);
  not not_144 (not_144_out, F25);
  not not_145 (not_145_out, F14);
  not not_146 (not_146_out, OP6);
  not not_147 (not_147_out, OP3);
  not not_148 (not_148_out, OP2);
  not not_149 (not_149_out, F14);
  not not_150 (not_150_out, F13);
  not not_151 (not_151_out, F12);
  not not_152 (not_152_out, OP6);
  not not_153 (not_153_out, OP5);
  not not_154 (not_154_out, OP3);
  not not_155 (not_155_out, OP2);
  not not_156 (not_156_out, OP6);
  not not_157 (not_157_out, OP5);
  not not_158 (not_158_out, OP3);
  not not_159 (not_159_out, OP2);
  not not_160 (not_160_out, F14);
  not not_161 (not_161_out, F12);
  not not_162 (not_162_out, OP6);
  not not_163 (not_163_out, OP5);
  not not_164 (not_164_out, OP4);
  not not_165 (not_165_out, OP3);
  not not_166 (not_166_out, OP2);
  not not_167 (not_167_out, F13);
  not not_168 (not_168_out, F12);
  not not_169 (not_169_out, OP6);
  not not_170 (not_170_out, OP5);
  not not_171 (not_171_out, OP4);
  not not_172 (not_172_out, OP3);
  not not_173 (not_173_out, OP2);
  not not_174 (not_174_out, F30);
  not not_175 (not_175_out, F25);
  not not_176 (not_176_out, F12);
  not not_177 (not_177_out, OP6);
  not not_178 (not_178_out, OP3);
  not not_179 (not_179_out, OP2);
  not not_180 (not_180_out, F30);
  not not_181 (not_181_out, F25);
  not not_182 (not_182_out, F14);
  not not_183 (not_183_out, F12);
  not not_184 (not_184_out, OP6);
  not not_185 (not_185_out, OP3);
  not not_186 (not_186_out, OP2);
  not not_187 (not_187_out, F30);
  not not_188 (not_188_out, F25);
  not not_189 (not_189_out, F14);
  not not_190 (not_190_out, OP6);
  not not_191 (not_191_out, OP3);
  not not_192 (not_192_out, OP2);
  not not_193 (not_193_out, F12);
  not not_194 (not_194_out, OP6);
  not not_195 (not_195_out, OP5);
  not not_196 (not_196_out, OP3);
  not not_197 (not_197_out, OP2);
  not not_198 (not_198_out, F13);
  not not_199 (not_199_out, F12);
  not not_200 (not_200_out, OP6);
  not not_201 (not_201_out, OP5);
  not not_202 (not_202_out, OP3);
  not not_203 (not_203_out, OP2);
  not not_204 (not_204_out, F14);
  not not_205 (not_205_out, F12);
  not not_206 (not_206_out, OP6);
  not not_207 (not_207_out, OP5);
  not not_208 (not_208_out, OP3);
  not not_209 (not_209_out, OP2);
  not not_210 (not_210_out, F30);
  not not_211 (not_211_out, F25);
  not not_212 (not_212_out, F13);
  not not_213 (not_213_out, F12);
  not not_214 (not_214_out, OP6);
  not not_215 (not_215_out, OP3);
  not not_216 (not_216_out, OP2);
  not not_217 (not_217_out, F13);
  not not_218 (not_218_out, F12);
  not not_219 (not_219_out, OP4);
  not not_220 (not_220_out, OP3);
  not not_221 (not_221_out, OP2);
  and and_1 (and_1_out, not_1_out, not_2_out, not_3_out, not_4_out, not_5_out, not_6_out, OP5, OP4, not_7_out, not_8_out);
  and and_2 (and_2_out, not_9_out, not_10_out, F14, F13, F12, not_11_out, OP5, OP4, not_12_out, not_13_out);
  and and_3 (and_3_out, not_14_out, not_15_out, not_16_out, F13, not_17_out, not_18_out, OP5, OP4, not_19_out, not_20_out);
  and and_4 (and_4_out, not_21_out, not_22_out, not_23_out, not_24_out, not_25_out, OP4, not_26_out, not_27_out);
  and and_5 (and_5_out, F14, F13, F12, not_28_out, not_29_out, OP4, not_30_out, not_31_out);
  and and_6 (and_6_out, F14, not_32_out, not_33_out, not_34_out, not_35_out, OP4, not_36_out, not_37_out);
  and and_7 (and_7_out, not_38_out, F13, not_39_out, not_40_out, not_41_out, OP4, not_42_out, not_43_out);
  and and_8 (and_8_out, F30, not_44_out, F14, not_45_out, F12, not_46_out, not_47_out, OP4, not_48_out, not_49_out);
  and and_9 (and_9_out, not_50_out, F13, not_51_out, not_52_out, not_53_out, not_54_out, not_55_out, not_56_out);
  and and_10 (and_10_out, not_57_out, not_58_out, F14, not_59_out, not_60_out, not_61_out, OP5, OP4, not_62_out, not_63_out);
  and and_11 (and_11_out, F14, not_64_out, not_65_out, not_66_out, not_67_out, not_68_out, not_69_out, not_70_out);
  and and_12 (and_12_out, F14, not_71_out, not_72_out, OP6, OP5, not_73_out, not_74_out, not_75_out);
  and and_13 (and_13_out, F30, not_76_out, not_77_out, not_78_out, not_79_out, not_80_out, OP5, OP4, not_81_out, not_82_out);
  and and_14 (and_14_out, not_83_out, not_84_out, F14, F13, F12, not_85_out, OP5, OP4, not_86_out, not_87_out);
  and and_15 (and_15_out, not_88_out, not_89_out, not_90_out, F13, not_91_out, not_92_out, OP5, OP4, not_93_out, not_94_out);
  and and_16 (and_16_out, F14, F13, F12, not_95_out, not_96_out, OP4, not_97_out, not_98_out);
  and and_17 (and_17_out, not_99_out, F13, not_100_out, not_101_out, not_102_out, OP4, not_103_out, not_104_out);
  and and_18 (and_18_out, not_105_out, not_106_out, F14, not_107_out, F12, not_108_out, not_109_out, OP4, not_110_out, not_111_out);
  and and_19 (and_19_out, not_112_out, not_113_out, F14, not_114_out, F12, not_115_out, OP5, OP4, not_116_out, not_117_out);
  and and_20 (and_20_out, F14, not_118_out, not_119_out, OP6, OP5, not_120_out, not_121_out, not_122_out);
  and and_21 (and_21_out, not_123_out, not_124_out, not_125_out, not_126_out, not_127_out, not_128_out, OP5, OP4, not_129_out, not_130_out);
  and and_22 (and_22_out, F30, not_131_out, not_132_out, not_133_out, not_134_out, not_135_out, OP5, OP4, not_136_out, not_137_out);
  and and_23 (and_23_out, not_138_out, not_139_out, F14, F13, F12, not_140_out, OP5, OP4, not_141_out, not_142_out);
  and and_24 (and_24_out, not_143_out, not_144_out, not_145_out, F13, F12, not_146_out, OP5, OP4, not_147_out, not_148_out);
  and and_25 (and_25_out, not_149_out, not_150_out, not_151_out, not_152_out, not_153_out, OP4, not_154_out, not_155_out);
  and and_26 (and_26_out, F14, F13, F12, not_156_out, not_157_out, OP4, not_158_out, not_159_out);
  and and_27 (and_27_out, not_160_out, F13, not_161_out, not_162_out, not_163_out, not_164_out, not_165_out, not_166_out);
  and and_28 (and_28_out, F14, not_167_out, not_168_out, not_169_out, not_170_out, not_171_out, not_172_out, not_173_out);
  and and_29 (and_29_out, not_174_out, not_175_out, F14, F13, not_176_out, not_177_out, OP5, OP4, not_178_out, not_179_out);
  and and_30 (and_30_out, not_180_out, not_181_out, not_182_out, F13, not_183_out, not_184_out, OP5, OP4, not_185_out, not_186_out);
  and and_31 (and_31_out, not_187_out, not_188_out, not_189_out, F13, F12, not_190_out, OP5, OP4, not_191_out, not_192_out);
  and and_32 (and_32_out, F14, F13, not_193_out, not_194_out, not_195_out, OP4, not_196_out, not_197_out);
  and and_33 (and_33_out, F14, not_198_out, not_199_out, not_200_out, not_201_out, OP4, not_202_out, not_203_out);
  and and_34 (and_34_out, not_204_out, F13, not_205_out, not_206_out, not_207_out, OP4, not_208_out, not_209_out);
  and and_35 (and_35_out, not_210_out, not_211_out, F14, not_212_out, not_213_out, not_214_out, OP5, OP4, not_215_out, not_216_out);
  and and_36 (and_36_out, F14, not_217_out, not_218_out, OP6, OP5, not_219_out, not_220_out, not_221_out);
  or or_1 (S0, and_1_out, and_2_out, and_3_out, and_4_out, and_5_out, and_6_out, and_7_out, and_8_out, and_9_out, and_10_out, and_11_out, and_12_out);
  or or_2 (S1, and_13_out, and_14_out, and_15_out, and_16_out, and_17_out, and_18_out, and_19_out, and_20_out);
  or or_3 (S2, and_21_out, and_22_out, and_23_out, and_24_out, and_25_out, and_26_out, and_27_out, and_28_out);
  or or_4 (S3, and_29_out, and_30_out, and_31_out, and_32_out, and_33_out, and_34_out, and_35_out, and_36_out);
endmodule

// 控制信号生成
module \控制信号自动生成  (
  input  OP2,
  input  OP3,
  input  OP4,
  input  OP5,
  input  OP6,
  input  F12,
  input  F13,
  input  F14,
  input  F25,
  input  F30,
  output MemToReg,
  output MemWrite,
  output ALU_SRC,
  output RegWrite,
  output ecall,
  output S_Type,
  output BEQ,
  output BNE,
  output JALR,
  output JAL,
  output LBU,
  output BLT,
  output CSRSI,
  output CSRCI
);

  wire and_1_out, and_2_out, and_4_out, and_5_out, and_6_out, and_7_out, and_8_out, and_9_out, and_10_out,
       and_11_out, and_12_out, and_13_out, and_14_out, and_15_out, and_16_out, and_17_out, and_18_out,
       and_19_out, and_20_out, and_21_out, and_22_out, and_23_out, and_24_out, and_25_out, and_26_out,
       and_27_out, and_28_out, and_29_out, not_1_out, not_2_out, not_3_out, not_4_out, not_5_out, not_6_out,
       not_7_out, not_8_out, not_9_out, not_10_out, not_11_out, not_12_out, not_13_out, not_14_out,
       not_15_out, not_16_out, not_17_out, not_18_out, not_19_out, not_20_out, not_21_out, not_22_out,
       not_23_out, not_24_out, not_25_out, not_26_out, not_27_out, not_28_out, not_29_out, not_30_out,
       not_31_out, not_32_out, not_33_out, not_34_out, not_35_out, not_36_out, not_37_out, not_38_out,
       not_39_out, not_40_out, not_41_out, not_42_out, not_43_out, not_44_out, not_45_out, not_46_out,
       not_47_out, not_48_out, not_49_out, not_50_out, not_51_out, not_52_out, not_53_out, not_54_out,
       not_55_out, not_56_out, not_57_out, not_58_out, not_59_out, not_60_out, not_61_out, not_62_out,
       not_63_out, not_64_out, not_65_out, not_66_out, not_67_out, not_68_out, not_69_out, not_70_out,
       not_71_out, not_72_out, not_73_out, not_74_out, not_75_out, not_76_out, not_77_out, not_78_out,
       not_79_out, not_80_out, not_81_out, not_82_out, not_83_out, not_84_out, not_85_out, not_86_out,
       not_87_out, not_88_out, not_89_out, not_90_out, not_91_out, not_92_out, not_93_out, not_94_out,
       not_95_out, not_96_out, not_97_out, not_98_out, not_99_out, not_100_out, not_101_out, not_102_out,
       not_103_out, not_104_out, not_105_out, not_106_out, not_107_out, not_108_out, not_109_out,
       not_110_out, not_111_out, not_112_out, not_113_out, not_114_out, not_115_out, not_116_out,
       not_117_out, not_118_out, not_119_out, not_120_out, not_121_out, not_122_out, not_123_out,
       not_124_out, not_125_out, not_126_out, not_127_out, not_128_out, not_129_out, not_130_out,
       not_131_out, not_132_out, not_133_out, not_134_out, not_135_out, not_136_out, not_137_out,
       not_138_out, not_139_out, not_140_out, not_141_out, not_142_out, not_143_out, not_144_out,
       not_145_out, not_146_out, not_147_out, not_148_out, not_149_out, not_150_out, not_151_out,
       not_152_out, not_153_out, not_154_out, not_155_out, not_156_out, not_157_out, not_158_out,
       not_159_out, not_160_out, not_161_out, not_162_out, not_163_out, not_164_out, not_165_out,
       not_166_out, not_167_out, not_168_out, not_169_out, not_170_out, not_171_out, not_172_out,
       not_173_out, not_174_out, not_175_out, not_176_out, not_177_out, not_178_out, not_179_out,
       not_180_out, not_181_out, not_182_out, not_183_out, not_184_out, not_185_out, not_186_out,
       not_187_out, not_188_out, not_189_out, not_190_out, not_191_out, not_192_out, not_193_out,
       not_194_out, not_195_out, not_196_out, not_197_out, not_198_out, not_199_out, not_200_out,
       not_201_out, not_202_out, not_203_out, not_204_out, not_205_out, not_206_out, not_207_out,
       not_208_out, not_209_out, not_210_out, not_211_out, not_212_out, not_213_out, not_214_out,
       not_215_out, not_216_out, not_217_out;

  not not_1 (not_1_out, OP2);
  not not_2 (not_2_out, OP3);
  not not_3 (not_3_out, OP4);
  not not_4 (not_4_out, OP5);
  not not_5 (not_5_out, OP6);
  not not_6 (not_6_out, F12);
  not not_7 (not_7_out, F13);
  not not_8 (not_8_out, OP2);
  not not_9 (not_9_out, OP3);
  not not_10 (not_10_out, OP4);
  not not_11 (not_11_out, OP5);
  not not_12 (not_12_out, OP6);
  not not_13 (not_13_out, F12);
  not not_14 (not_14_out, F14);
  not not_15 (not_15_out, OP2);
  not not_16 (not_16_out, OP3);
  not not_17 (not_17_out, OP4);
  not not_18 (not_18_out, OP6);
  not not_19 (not_19_out, F12);
  not not_20 (not_20_out, F14);
  not not_21 (not_21_out, OP2);
  not not_22 (not_22_out, OP3);
  not not_23 (not_23_out, OP5);
  not not_24 (not_24_out, OP6);
  not not_25 (not_25_out, F12);
  not not_26 (not_26_out, F13);
  not not_27 (not_27_out, OP2);
  not not_28 (not_28_out, OP3);
  not not_29 (not_29_out, OP4);
  not not_30 (not_30_out, OP6);
  not not_31 (not_31_out, F12);
  not not_32 (not_32_out, F14);
  not not_33 (not_33_out, OP2);
  not not_34 (not_34_out, OP3);
  not not_35 (not_35_out, OP5);
  not not_36 (not_36_out, OP6);
  not not_37 (not_37_out, F12);
  not not_38 (not_38_out, OP2);
  not not_39 (not_39_out, OP3);
  not not_40 (not_40_out, OP5);
  not not_41 (not_41_out, OP6);
  not not_42 (not_42_out, F13);
  not not_43 (not_43_out, F14);
  not not_44 (not_44_out, OP2);
  not not_45 (not_45_out, OP3);
  not not_46 (not_46_out, OP5);
  not not_47 (not_47_out, OP6);
  not not_48 (not_48_out, F13);
  not not_49 (not_49_out, F25);
  not not_50 (not_50_out, OP2);
  not not_51 (not_51_out, OP3);
  not not_52 (not_52_out, OP5);
  not not_53 (not_53_out, OP6);
  not not_54 (not_54_out, F30);
  not not_55 (not_55_out, F25);
  not not_56 (not_56_out, F14);
  not not_57 (not_57_out, F13);
  not not_58 (not_58_out, F12);
  not not_59 (not_59_out, OP6);
  not not_60 (not_60_out, OP3);
  not not_61 (not_61_out, OP2);
  not not_62 (not_62_out, F25);
  not not_63 (not_63_out, F14);
  not not_64 (not_64_out, F13);
  not not_65 (not_65_out, F12);
  not not_66 (not_66_out, OP6);
  not not_67 (not_67_out, OP3);
  not not_68 (not_68_out, OP2);
  not not_69 (not_69_out, F30);
  not not_70 (not_70_out, F25);
  not not_71 (not_71_out, OP6);
  not not_72 (not_72_out, OP3);
  not not_73 (not_73_out, OP2);
  not not_74 (not_74_out, F30);
  not not_75 (not_75_out, F25);
  not not_76 (not_76_out, F12);
  not not_77 (not_77_out, OP6);
  not not_78 (not_78_out, OP3);
  not not_79 (not_79_out, OP2);
  not not_80 (not_80_out, F30);
  not not_81 (not_81_out, F25);
  not not_82 (not_82_out, F14);
  not not_83 (not_83_out, F12);
  not not_84 (not_84_out, OP6);
  not not_85 (not_85_out, OP3);
  not not_86 (not_86_out, OP2);
  not not_87 (not_87_out, F30);
  not not_88 (not_88_out, F25);
  not not_89 (not_89_out, F14);
  not not_90 (not_90_out, OP6);
  not not_91 (not_91_out, OP3);
  not not_92 (not_92_out, OP2);
  not not_93 (not_93_out, F14);
  not not_94 (not_94_out, F13);
  not not_95 (not_95_out, F12);
  not not_96 (not_96_out, OP6);
  not not_97 (not_97_out, OP5);
  not not_98 (not_98_out, OP3);
  not not_99 (not_99_out, OP2);
  not not_100 (not_100_out, OP6);
  not not_101 (not_101_out, OP5);
  not not_102 (not_102_out, OP3);
  not not_103 (not_103_out, OP2);
  not not_104 (not_104_out, F12);
  not not_105 (not_105_out, OP6);
  not not_106 (not_106_out, OP5);
  not not_107 (not_107_out, OP3);
  not not_108 (not_108_out, OP2);
  not not_109 (not_109_out, F13);
  not not_110 (not_110_out, F12);
  not not_111 (not_111_out, OP6);
  not not_112 (not_112_out, OP5);
  not not_113 (not_113_out, OP3);
  not not_114 (not_114_out, OP2);
  not not_115 (not_115_out, F14);
  not not_116 (not_116_out, F12);
  not not_117 (not_117_out, OP6);
  not not_118 (not_118_out, OP5);
  not not_119 (not_119_out, OP3);
  not not_120 (not_120_out, OP2);
  not not_121 (not_121_out, F14);
  not not_122 (not_122_out, F13);
  not not_123 (not_123_out, OP6);
  not not_124 (not_124_out, OP5);
  not not_125 (not_125_out, OP3);
  not not_126 (not_126_out, OP2);
  not not_127 (not_127_out, F30);
  not not_128 (not_128_out, F25);
  not not_129 (not_129_out, F13);
  not not_130 (not_130_out, OP6);
  not not_131 (not_131_out, OP5);
  not not_132 (not_132_out, OP3);
  not not_133 (not_133_out, OP2);
  not not_134 (not_134_out, F25);
  not not_135 (not_135_out, F13);
  not not_136 (not_136_out, OP6);
  not not_137 (not_137_out, OP5);
  not not_138 (not_138_out, OP3);
  not not_139 (not_139_out, OP2);
  not not_140 (not_140_out, F14);
  not not_141 (not_141_out, F12);
  not not_142 (not_142_out, OP6);
  not not_143 (not_143_out, OP5);
  not not_144 (not_144_out, OP4);
  not not_145 (not_145_out, OP3);
  not not_146 (not_146_out, OP2);
  not not_147 (not_147_out, OP4);
  not not_148 (not_148_out, F14);
  not not_149 (not_149_out, F13);
  not not_150 (not_150_out, F12);
  not not_151 (not_151_out, OP4);
  not not_152 (not_152_out, OP3);
  not not_153 (not_153_out, F30);
  not not_154 (not_154_out, F25);
  not not_155 (not_155_out, F13);
  not not_156 (not_156_out, OP6);
  not not_157 (not_157_out, OP3);
  not not_158 (not_158_out, OP2);
  not not_159 (not_159_out, F30);
  not not_160 (not_160_out, F25);
  not not_161 (not_161_out, F13);
  not not_162 (not_162_out, F12);
  not not_163 (not_163_out, OP6);
  not not_164 (not_164_out, OP3);
  not not_165 (not_165_out, OP2);
  not not_166 (not_166_out, F13);
  not not_167 (not_167_out, F12);
  not not_168 (not_168_out, OP6);
  not not_169 (not_169_out, OP5);
  not not_170 (not_170_out, OP4);
  not not_171 (not_171_out, OP3);
  not not_172 (not_172_out, OP2);
  not not_173 (not_173_out, OP2);
  not not_174 (not_174_out, OP3);
  not not_175 (not_175_out, F12);
  not not_176 (not_176_out, F13);
  not not_177 (not_177_out, F14);
  not not_178 (not_178_out, OP2);
  not not_179 (not_179_out, OP3);
  not not_180 (not_180_out, OP4);
  not not_181 (not_181_out, OP6);
  not not_182 (not_182_out, F12);
  not not_183 (not_183_out, F14);
  not not_184 (not_184_out, OP2);
  not not_185 (not_185_out, OP3);
  not not_186 (not_186_out, OP4);
  not not_187 (not_187_out, F12);
  not not_188 (not_188_out, F13);
  not not_189 (not_189_out, F14);
  not not_190 (not_190_out, OP2);
  not not_191 (not_191_out, OP3);
  not not_192 (not_192_out, OP4);
  not not_193 (not_193_out, F13);
  not not_194 (not_194_out, F14);
  not not_195 (not_195_out, OP3);
  not not_196 (not_196_out, OP4);
  not not_197 (not_197_out, F12);
  not not_198 (not_198_out, F13);
  not not_199 (not_199_out, F14);
  not not_200 (not_200_out, OP4);
  not not_201 (not_201_out, OP2);
  not not_202 (not_202_out, OP3);
  not not_203 (not_203_out, OP4);
  not not_204 (not_204_out, OP5);
  not not_205 (not_205_out, OP6);
  not not_206 (not_206_out, F12);
  not not_207 (not_207_out, F13);
  not not_208 (not_208_out, OP2);
  not not_209 (not_209_out, OP3);
  not not_210 (not_210_out, OP4);
  not not_211 (not_211_out, F12);
  not not_212 (not_212_out, F13);
  not not_213 (not_213_out, OP2);
  not not_214 (not_214_out, OP3);
  not not_215 (not_215_out, F12);
  not not_216 (not_216_out, OP2);
  not not_217 (not_217_out, OP3);
  and and_1 (and_1_out, not_1_out, not_2_out, not_3_out, not_4_out, not_5_out, not_6_out, not_7_out, F14);
  and and_2 (and_2_out, not_8_out, not_9_out, not_10_out, not_11_out, not_12_out, not_13_out, F13, not_14_out);
  and and_3 (MemWrite, not_15_out, not_16_out, not_17_out, OP5, not_18_out, not_19_out, F13, not_20_out);
  and and_4 (and_4_out, not_21_out, not_22_out, not_23_out, not_24_out, not_25_out, not_26_out, F14);
  and and_5 (and_5_out, not_27_out, not_28_out, not_29_out, not_30_out, not_31_out, F13, not_32_out);
  and and_6 (and_6_out, not_33_out, not_34_out, OP4, not_35_out, not_36_out, not_37_out);
  and and_7 (and_7_out, not_38_out, not_39_out, OP4, not_40_out, not_41_out, not_42_out, not_43_out);
  and and_8 (and_8_out, not_44_out, not_45_out, OP4, not_46_out, not_47_out, not_48_out, not_49_out);
  and and_9 (and_9_out, not_50_out, not_51_out, OP4, not_52_out, not_53_out, F13, F14);
  and and_10 (and_10_out, not_54_out, not_55_out, not_56_out, not_57_out, not_58_out, not_59_out, OP5, OP4, not_60_out, not_61_out);
  and and_11 (and_11_out, F30, not_62_out, not_63_out, not_64_out, not_65_out, not_66_out, OP5, OP4, not_67_out, not_68_out);
  and and_12 (and_12_out, not_69_out, not_70_out, F14, F13, F12, not_71_out, OP5, OP4, not_72_out, not_73_out);
  and and_13 (and_13_out, not_74_out, not_75_out, F14, F13, not_76_out, not_77_out, OP5, OP4, not_78_out, not_79_out);
  and and_14 (and_14_out, not_80_out, not_81_out, not_82_out, F13, not_83_out, not_84_out, OP5, OP4, not_85_out, not_86_out);
  and and_15 (and_15_out, not_87_out, not_88_out, not_89_out, F13, F12, not_90_out, OP5, OP4, not_91_out, not_92_out);
  and and_16 (and_16_out, not_93_out, not_94_out, not_95_out, not_96_out, not_97_out, OP4, not_98_out, not_99_out);
  and and_17 (and_17_out, F14, F13, F12, not_100_out, not_101_out, OP4, not_102_out, not_103_out);
  and and_18 (and_18_out, F14, F13, not_104_out, not_105_out, not_106_out, OP4, not_107_out, not_108_out);
  and and_19 (and_19_out, F14, not_109_out, not_110_out, not_111_out, not_112_out, OP4, not_113_out, not_114_out);
  and and_20 (and_20_out, not_115_out, F13, not_116_out, not_117_out, not_118_out, OP4, not_119_out, not_120_out);
  and and_21 (and_21_out, not_121_out, not_122_out, F12, not_123_out, not_124_out, OP4, not_125_out, not_126_out);
  and and_22 (and_22_out, not_127_out, not_128_out, F14, not_129_out, F12, not_130_out, not_131_out, OP4, not_132_out, not_133_out);
  and and_23 (and_23_out, F30, not_134_out, F14, not_135_out, F12, not_136_out, not_137_out, OP4, not_138_out, not_139_out);
  and and_24 (and_24_out, not_140_out, F13, not_141_out, not_142_out, not_143_out, not_144_out, not_145_out, not_146_out);
  and and_25 (and_25_out, OP6, OP5, not_147_out, OP3, OP2);
  and and_26 (and_26_out, not_148_out, not_149_out, not_150_out, OP6, OP5, not_151_out, not_152_out, OP2);
  and and_27 (and_27_out, not_153_out, not_154_out, F14, not_155_out, F12, not_156_out, OP5, OP4, not_157_out, not_158_out);
  and and_28 (and_28_out, not_159_out, not_160_out, F14, not_161_out, not_162_out, not_163_out, OP5, OP4, not_164_out, not_165_out);
  and and_29 (and_29_out, F14, not_166_out, not_167_out, not_168_out, not_169_out, not_170_out, not_171_out, not_172_out);
  and and_30 (ecall, not_173_out, not_174_out, OP4, OP5, OP6, not_175_out, not_176_out, not_177_out);
  and and_31 (S_Type, not_178_out, not_179_out, not_180_out, OP5, not_181_out, not_182_out, F13, not_183_out);
  and and_32 (BEQ, not_184_out, not_185_out, not_186_out, OP5, OP6, not_187_out, not_188_out, not_189_out);
  and and_33 (BNE, not_190_out, not_191_out, not_192_out, OP5, OP6, F12, not_193_out, not_194_out);
  and and_34 (JALR, OP2, not_195_out, not_196_out, OP5, OP6, not_197_out, not_198_out, not_199_out);
  and and_35 (JAL, OP2, OP3, not_200_out, OP5, OP6);
  and and_36 (LBU, not_201_out, not_202_out, not_203_out, not_204_out, not_205_out, not_206_out, not_207_out, F14);
  and and_37 (BLT, not_208_out, not_209_out, not_210_out, OP5, OP6, not_211_out, not_212_out, F14);
  and and_38 (CSRSI, not_213_out, not_214_out, OP4, OP5, OP6, not_215_out, F13, F14);
  and and_39 (CSRCI, not_216_out, not_217_out, OP4, OP5, OP6, F12, F13, F14);
  or or_1 (MemToReg, and_1_out, and_2_out);
  or or_2 (ALU_SRC, and_4_out, and_5_out, and_6_out, and_7_out, and_8_out, and_9_out);
  or or_3 (RegWrite, and_10_out, and_11_out, and_12_out, and_13_out, and_14_out, and_15_out, and_16_out, and_17_out, and_18_out, and_19_out, and_20_out, and_21_out, and_22_out, and_23_out, and_24_out, and_25_out, and_26_out, and_27_out, and_28_out, and_29_out);
endmodule

// ALU
module ALU (
  input  [31:0] X,
  input  [31:0] Y,
  input  [3:0] AluOP,
  output out_4,
  output Equal,
  output out_6,
  output [31:0] Result,
  output [31:0] Result_2
);

  wire [0:0] comparator_1_lt, comparator_2_lt;
  wire [31:0] adder_1_out, AND_out, divider_1_out, divider_1_rem, multiplier_1_cout, multiplier_1_out,
       NOR_out, OR_out, shifter_1_out, shifter_2_out, shifter_3_out, subtractor_1_out, XOR_out;

  assign AND_out = X & Y;  // AND_Gate AND, 32 bits wide
  assign OR_out = X | Y;  // OR_Gate OR, 32 bits wide
  Shifter #(.width(32), .shift("ll")) shifter_1 (.in(X), .\dist (Y[4:0]), .out(shifter_1_out));
  Shifter #(.width(32), .shift("ar")) shifter_2 (.in(X), .\dist (Y[4:0]), .out(shifter_2_out));
  Shifter #(.width(32), .shift("lr")) shifter_3 (.in(X), .\dist (Y[4:0]), .out(shifter_3_out));
  Multiplier #(.width(32)) multiplier_1 (.a(X), .b(Y), .out(multiplier_1_out), .cout(multiplier_1_cout));  // open: cin
  Divider #(.width(32)) divider_1 (.a(X), .b(Y), .out(divider_1_out), .rem(divider_1_rem));  // open: upper
  Adder #(.width(32)) adder_1 (.a(X), .b(Y), .out(adder_1_out));  // open: cin, cout
  Subtractor #(.width(32)) subtractor_1 (.a(X), .b(Y), .out(subtractor_1_out));  // open: bin, bout
  assign XOR_out = X ^ Y;  // XOR_Gate XOR, 32 bits wide
  assign NOR_out = ~(X | Y);  // NOR_Gate NOR, 32 bits wide
  Comparator #(.width(32), .mode("twosComplement")) comparator_1 (
    .a(X), .b(Y), .eq(Equal), .lt(comparator_1_lt[0]));  // open: gt
  Comparator #(.width(32), .mode("unsigned")) comparator_2 (.a(X), .b(Y), .lt(comparator_2_lt[0]));  // open: gt, eq
  Multiplexer #(.select(4), .width(32), .disabled("Z"), .enable("false")) multiplexer_1 (
    .in0(shifter_1_out), .in1(shifter_2_out), .in2(shifter_3_out), .in3(multiplier_1_out),
    .in4(divider_1_out), .in5(adder_1_out), .in6(subtractor_1_out), .in7(AND_out), .in8(OR_out),
    .in9(XOR_out), .in10(NOR_out), .in11({{31{1'b0}}, comparator_1_lt[0]}),
    .in12({{31{1'b0}}, comparator_2_lt[0]}), .in13({32{1'b0}}), .in14({32{1'b0}}), .in15({32{1'b0}}),
    .out(Result), .sel(AluOP));
  Multiplexer #(.select(4), .width(32), .disabled("Z"), .enable("false")) multiplexer_2 (
    .in0({32{1'b0}}), .in1({32{1'b0}}), .in2({32{1'b0}}), .in3(multiplier_1_cout), .in4(divider_1_rem),
    .in5({32{1'b0}}), .in6({32{1'b0}}), .in7({32{1'b0}}), .in8({32{1'b0}}), .in9({32{1'b0}}),
    .in10({32{1'b0}}), .in11({32{1'b0}}), .in12({32{1'b0}}), .in13({32{1'b0}}), .in14({32{1'b0}}),
    .in15({32{1'b0}}), .out(Result_2), .sel(AluOP));
  Multiplexer #(.select(4), .width(1), .disabled("Z"), .enable("false")) multiplexer_3 (
    .in0(1'b0), .in1(1'b0), .in2(1'b0), .in3(1'b0), .in4(1'b0), .in5(1'b0), .in6(1'b0), .in7(1'b0),
    .in8(1'b0), .in9(1'b0), .in10(1'b0), .in11(comparator_1_lt[0]), .in12(comparator_2_lt[0]), .in13(1'b0),
    .in14(1'b0), .in15(1'b0), .out(out_6), .sel(AluOP));
  not not_1 (out_4, out_6);

  // Other names for the same wires on the sheet: Result2[31:0] = Result_2; S[3:0] = AluOP; tunnel = out_6;
  //   tunnel_t = out_4

  // Notes on the sheet:
  //   不要改变此引脚区域内容，也不要改变ALU封装形式
  //   输入引脚
  //   输出引脚
endmodule

module Regifile (
  input  [31:0] Din,
  input  Clk,
  input  WE,
  input  [4:0] R1_num,
  input  [4:0] W_num,
  input  [4:0] R2_num,
  output [31:0] R1,
  output [31:0] R2
);

  // RegisterFile registerfile_1: pin names not known; wires that end beside it: Din, Clk, WE, W_num, R1_num, R2_num, R1, R2
endmodule

module \理想流水线  (
  output RegWrite,
  output MemWrite,
  output [31:0] IF_PC,
  output [31:0] ID_PC,
  output [31:0] EX_PC,
  output [31:0] M_PC,
  output [31:0] WB_PC,
  output [31:0] RDin,
  output [31:0] MDin,
  output [31:0] LedData
);

  wire alu_2_equal, and_1_out, and_2_out, and_3_out, and_4_out, and_5_out, CLK, clock_1_out, comparator_1_eq,
       comparator_1_lt, comparator_2_eq, d_ff_1_q, ecall, ex_mem_1_halt_2, ex_mem_1_memtoreg_2,
       ex_mem_1_regwrite_2, Go, halt, id_ex_1_alusrcb_2, id_ex_1_beq_2, id_ex_1_bne_2, id_ex_1_ecall_2,
       id_ex_1_memtoreg_2, id_ex_1_memtoreg_3, id_ex_1_regwrite_2, IR1, IR2, IR3, JAL, JALR, mem_wb_1_halt_2,
       nand_1_out, not_1_out, not_2_out, not_3_out, not_4_out, not_5_out, not_6_out, not_7_out, or_1_out,
       or_2_out, or_3_out, or_4_out, RST, W1, W2, W3, \单周期硬布线控制器_1_alu_src , \单周期硬布线控制器_1_beq ,
       \单周期硬布线控制器_1_bne , \单周期硬布线控制器_1_memtoreg , \单周期硬布线控制器_1_memwrite , \单周期硬布线控制器_1_regwrite ,
       \单周期硬布线控制器_1_s_type , \单周期硬布线控制器_1_uret ;
  wire [3:0] id_ex_1_aluop_2, \单周期硬布线控制器_1_alu_op ;
  wire [4:0] multiplexer_2_out, multiplexer_3_out, W_num;
  wire [11:0] multiplexer_4_out, shifter_1_out;
  wire [12:0] CNT_num;
  wire [15:0] \LoadUse次数 , \总周期数 , \插入气泡数 , \无条件分支数 , \条件分支成功数 ;
  wire [19:0] shifter_2_out;
  wire [31:0] adder_1_out, alu_1_result, alu_2_result, bit_extender_1_out, bit_extender_2_out,
       bit_extender_3_out, EX_IR, ex_mem_1_adress, id_ex_1_b, id_ex_1_imm_bj_i_2, id_ex_1_imm_i_s_2,
       id_ex_1_r1_2, id_ex_1_r2_2, ID_IR, IF_IR, MEM_IR, mem_wb_1_md_2, multiplexer_1_out, multiplexer_6_out,
       multiplexer_7_out, multiplexer_8_out, multiplexer_9_out, multiplexer_10_out, PC, ram_1_data,
       regifile_1_r1, regifile_1_r2, WB_IR;

  Button \u_总复位  (.out(RST));
  Button _1 (.out(IR1));
  Button _2 (.out(IR2));
  Button _3 (.out(IR3));
  // Probe on \总周期数 
  // Probe on \总周期数 
  Button \u_继续运行  (.out(Go));
  LED #(.active("true")) led_1 (.in(W1));
  LED #(.active("true")) led_2 (.in(W2));
  LED #(.active("true")) led_3 (.in(W3));
  Counter #(.width(16), .max('hffff), .ongoal("wrap"), .trigger("rising"), .behavior("old")) counter_1 (
    .Q(\总周期数 ), .clk(and_1_out));  // open: load, D, count, carry, clr, preset
  and and_1 (and_1_out, CLK, not_1_out);
  not not_1 (not_1_out, halt);
  Hex_Digit_Display hex_digit_display_1 (.value(LedData[31:28]));  // open: dp
  // Probe on IF_PC[19:0]
  // RiscV_Probe riscv_probe_1: pin names not known; wires that end beside it: IF_IR
  Multiplexer #(.select(1), .width(32), .disabled("Z"), .enable("false")) multiplexer_1 (
    .in0(adder_1_out), .in1(alu_1_result), .out(multiplexer_1_out), .sel(or_1_out));
  not not_2 (not_2_out, halt);
  Hex_Digit_Display hex_digit_display_2 (.value(LedData[23:20]));  // open: dp
  Hex_Digit_Display hex_digit_display_3 (.value(LedData[27:24]));  // open: dp
  // Probe on ID_PC[19:0]
  // RiscV_Probe riscv_probe_2: pin names not known; wires that end beside it: ID_IR
  Register #(.width(32), .trigger("rising"), .Select("low")) u_PC (
    .D(multiplexer_1_out), .en(not_2_out), .Q(IF_PC), .clk(CLK), .clr(RST));
  Hex_Digit_Display hex_digit_display_4 (.value(LedData[15:12]));  // open: dp
  Hex_Digit_Display hex_digit_display_5 (.value(LedData[19:16]));  // open: dp
  Adder #(.width(32)) adder_1 (.a(IF_PC), .b(32'h4), .out(adder_1_out));  // open: cin, cout
  Hex_Digit_Display hex_digit_display_6 (.value(LedData[11:8]));  // open: dp
  Hex_Digit_Display hex_digit_display_7 (.value(LedData[7:4]));  // open: dp
  // Probe on EX_PC[19:0]
  // RiscV_Probe riscv_probe_3: pin names not known; wires that end beside it: EX_IR
  ROM #(.addrWidth(10), .dataWidth(32), .Select("high")) rom_1 (.addr(IF_PC[11:2]), .data(IF_IR));
  Hex_Digit_Display hex_digit_display_8 (.value(LedData[3:0]));  // open: dp
  // Probe on \总周期数 
  // Probe on M_PC[19:0]
  // RiscV_Probe riscv_probe_4: pin names not known; wires that end beside it: MEM_IR
  IF_ID if_id_1 (
    .\指令字 (IF_IR), .\指令字_2 (ID_IR), .PC_2(ID_PC), .CLK(CLK), .\保持 (halt), .\同步清零 (1'b0), .PC(IF_PC));  // open: Branch_Pre, Branch_PRe_2
  // Probe on \总周期数 
  // Probe on \无条件分支数 
  // Probe on \条件分支成功数 
  // Probe on \插入气泡数 
  // Probe on \LoadUse次数 
  // Probe on IF_PC[11:0]
  // Probe on WB_PC[19:0]
  // RiscV_Probe riscv_probe_5: pin names not known; wires that end beside it: {WB_IR[31:12], W_num, WB_IR[6:0]}
  or or_1 (or_1_out, or_3_out, JALR, JAL);
  // Probe on ID_PC[11:0]
  // Probe on EX_PC[11:0]
  // Probe on M_PC[11:0]
  D_Flip_Flop #(.trigger("high"), .Pre_Clr_Positions("LEGACY"), .NegatePresetClear("false"), .enable("true"), .NewFFLayout("false")) d_ff_1 (.Q(d_ff_1_q));  // open: clk, D, Qn, preset, en, reset
  // Probe on 13'hc
  \单周期硬布线控制器  \u_单周期硬布线控制器_1  (
    .Funct({ID_IR[30], ID_IR[25], ID_IR[14:12]}), .OP(ID_IR[6:2]), .ALU_OP(\单周期硬布线控制器_1_alu_op ),
    .MemToReg(\单周期硬布线控制器_1_memtoreg ), .MemWrite(\单周期硬布线控制器_1_memwrite ), .ALU_SRC(\单周期硬布线控制器_1_alu_src ),
    .RegWrite(\单周期硬布线控制器_1_regwrite ), .ecall(ecall), .S_type(\单周期硬布线控制器_1_s_type ), .Jalr(JALR),
    .Beq(\单周期硬布线控制器_1_beq ), .JAL(JAL), .Bne(\单周期硬布线控制器_1_bne ), .in_3(ID_IR[21]), .uret(\单周期硬布线控制器_1_uret ));  // open: LBU, BLT, Csrsi, Csrci
  Multiplexer #(.select(1), .width(5), .disabled("Z"), .enable("false")) multiplexer_2 (
    .in0(ID_IR[19:15]), .in1(5'b10001), .out(multiplexer_2_out), .sel(ecall));
  Multiplexer #(.select(1), .width(5), .disabled("Z"), .enable("false")) multiplexer_3 (
    .in0(ID_IR[24:20]), .in1(5'b01010), .out(multiplexer_3_out), .sel(ecall));
  \Conflict_气泡  \conflict_气泡_1  ();  // open: IR, W_num, R1, R2, Data_Conflict
  // Probe on WB_PC[11:0]
  Comparator #(.width(13), .mode("twosComplement")) comparator_1 (
    .a(CNT_num), .b(13'hc), .eq(comparator_1_eq), .lt(comparator_1_lt));  // open: gt
  Clock #(.highDuration(1), .lowDuration(1)) clock_1 (.out(clock_1_out));
  Multiplexer #(.select(1), .width(12), .disabled("Z"), .enable("false")) multiplexer_4 (
    .in0(ID_IR[31:20]), .in1({ID_IR[31:25], ID_IR[11:7]}), .out(multiplexer_4_out), .sel(\单周期硬布线控制器_1_s_type ));
  Shifter #(.width(12), .shift("ll")) shifter_1 (
    .in({ID_IR[31], ID_IR[7], ID_IR[30:25], ID_IR[11:8]}), .\dist (4'b0001), .out(shifter_1_out));
  Shifter #(.width(20), .shift("ll")) shifter_2 (
    .in({ID_IR[31], ID_IR[19:12], ID_IR[20], ID_IR[30:21]}), .\dist (5'b00001), .out(shifter_2_out));
  Multiplexer #(.select(1), .width(32), .disabled("Z"), .enable("false")) multiplexer_5 (
    .in0(mem_wb_1_md_2), .in1(adder_1_out), .out(RDin), .sel(or_2_out));
  nand nand_1 (nand_1_out, d_ff_1_q, comparator_1_eq);
  Counter #(.width(13), .max('h1fff), .ongoal("stay"), .trigger("rising"), .behavior("old")) counter_2 (
    .count(comparator_1_lt), .Q(CNT_num), .clk(clock_1_out));  // open: load, D, carry, clr, preset
  Regifile regifile_1 (
    .Din(RDin), .Clk(CLK), .R1(regifile_1_r1), .R2(regifile_1_r2), .WE(RegWrite), .W_num(W_num),
    .R1_num(multiplexer_2_out), .R2_num(multiplexer_3_out));
  assign bit_extender_1_out = {{20{multiplexer_4_out[11]}}, multiplexer_4_out};  // Bit_Extender bit_extender_1
  assign bit_extender_2_out = {{20{shifter_1_out[11]}}, shifter_1_out};  // Bit_Extender bit_extender_2
  Multiplexer #(.select(1), .width(32), .disabled("Z"), .enable("false")) multiplexer_6 (
    .in0(bit_extender_2_out), .in1(bit_extender_3_out), .out(multiplexer_6_out), .sel(JAL));
  assign bit_extender_3_out = {{12{shifter_2_out[19]}}, shifter_2_out};  // Bit_Extender bit_extender_3
  or or_2 (or_2_out, JAL, JALR);
  assign CLK = nand_1_out ? clock_1_out : 1'bz;  // Controlled_Buffer controlled_buffer_1
  Multiplexer #(.select(1), .width(32), .disabled("Z"), .enable("false")) multiplexer_7 (
    .in0(PC), .in1(regifile_1_r1), .out(multiplexer_7_out), .sel(JALR));
  Multiplexer #(.select(1), .width(32), .disabled("Z"), .enable("false")) multiplexer_8 (
    .in0(multiplexer_6_out), .out(multiplexer_8_out), .sel(JALR));  // open: in1
  Pull_Resistor #(.pull(1)) pull_resistor_1 (.node(CLK));
  ID_EX id_ex_1 (
    .\指令字 (ID_PC), .PC(ID_IR), .Aluop(\单周期硬布线控制器_1_alu_op ), .AlusrcB(\单周期硬布线控制器_1_alu_src ),
    .R1(regifile_1_r1), .R2(regifile_1_r2), .imm_I_S(bit_extender_1_out), .imm_BJ_I(multiplexer_8_out),
    .PC_2(EX_PC), .IR(EX_IR), .Aluop_2(id_ex_1_aluop_2), .AlusrcB_2(id_ex_1_alusrcb_2), .R1_2(id_ex_1_r1_2),
    .R2_2(id_ex_1_r2_2), .imm_I_S_2(id_ex_1_imm_i_s_2), .imm_BJ_I_2(id_ex_1_imm_bj_i_2), .CLK(CLK),
    .B(id_ex_1_b), .PC_R(multiplexer_7_out), .RegWrite(\单周期硬布线控制器_1_regwrite ),
    .RegWrite_2(id_ex_1_regwrite_2), .\保持 (halt), .ecall_2(id_ex_1_ecall_2), .ecall(ecall), .\同步清零 (1'b0),
    .Bne(\单周期硬布线控制器_1_bne ), .Bne_2(id_ex_1_bne_2), .MemToReg(\单周期硬布线控制器_1_memtoreg ),
    .MemToReg_2(id_ex_1_memtoreg_2), .MemWrite(\单周期硬布线控制器_1_memwrite ), .MemToReg_3(id_ex_1_memtoreg_3),
    .Beq(\单周期硬布线控制器_1_beq ), .Beq_2(id_ex_1_beq_2));  // open: Branch_Pre_2, Branch_Pre, JAL_JALR, JAL_JALR_2, Blt, Blt_2, Lbu, Lbu_2
  Multiplexer #(.select(1), .width(32), .disabled("Z"), .enable("false")) multiplexer_9 (
    .in0(id_ex_1_r2_2), .in1(id_ex_1_imm_i_s_2), .out(multiplexer_9_out), .sel(id_ex_1_alusrcb_2));
  ALU alu_1 (
    .X(id_ex_1_imm_bj_i_2), .Y(id_ex_1_b), .AluOP(4'b0101), .Result(alu_1_result));  // open: Equal, Result_2, out_4, out_6
  or or_3 (or_3_out, and_2_out, and_3_out);
  and and_2 (and_2_out, alu_2_equal, id_ex_1_beq_2);
  not not_3 (not_3_out, alu_2_equal);
  and and_3 (and_3_out, not_3_out, id_ex_1_bne_2);
  Comparator #(.width(32), .mode("twosComplement")) comparator_2 (
    .a(id_ex_1_r1_2), .b(32'h22), .eq(comparator_2_eq));  // open: gt, lt
  ALU alu_2 (
    .X(id_ex_1_r1_2), .Y(multiplexer_9_out), .AluOP(id_ex_1_aluop_2), .Equal(alu_2_equal),
    .Result(alu_2_result));  // open: Result_2, out_4, out_6
  not not_4 (not_4_out, comparator_2_eq);
  and and_4 (and_4_out, id_ex_1_ecall_2, comparator_2_eq);
  or or_4 (or_4_out, Go, not_5_out);
  not not_5 (not_5_out, and_5_out);
  and and_5 (and_5_out, id_ex_1_ecall_2, not_4_out);
  Register #(.width(32), .trigger("rising"), .Select("low")) register_1 (
    .D(MDin), .en(and_4_out), .Q(LedData), .clk(CLK));  // open: clr
  not not_6 (not_6_out, or_4_out);
  EX_MEM ex_mem_1 (
    .MemToReg(id_ex_1_memtoreg_2), .MemWrite(id_ex_1_memtoreg_3), .MemToReg_2(ex_mem_1_memtoreg_2),
    .MemWrite_2(MemWrite), .CLK(CLK), .\指令字 (EX_PC), .\指令字_2 (M_PC), .PC(EX_IR), .PC_2(MEM_IR),
    .Adress(ex_mem_1_adress), .ALU(alu_2_result), .MDin_2(MDin), .MDin(id_ex_1_r2_2),
    .RegWrite(id_ex_1_regwrite_2), .RegWrite_2(ex_mem_1_regwrite_2), .halt(not_6_out),
    .halt_2(ex_mem_1_halt_2), .\保持 (halt));  // open: JAL_JALR, JAL_JALR_2, Lbu, Lbu_2
  not not_7 (not_7_out, halt);
  RAM #(.addrWidth(10), .dataWidth(32), .bus("separate"), .Select("high")) ram_1 (
    .addr(ex_mem_1_adress[11:2]), .din(MDin), .data(ram_1_data), .str(MemWrite), .sel(not_7_out), .clk(CLK));  // open: ld, clr
  Multiplexer #(.select(1), .width(32), .disabled("Z"), .enable("false")) multiplexer_10 (
    .in0(ex_mem_1_adress), .in1(ram_1_data), .out(multiplexer_10_out), .sel(ex_mem_1_memtoreg_2));
  MEM_WB mem_wb_1 (
    .\指令字 (M_PC), .PC(MEM_IR), .\指令字_2 (WB_PC), .PC_2({WB_IR[31:12], W_num, WB_IR[6:0]}), .CLK(CLK),
    .RegWrite(ex_mem_1_regwrite_2), .RegWrite_2(RegWrite), .halt(ex_mem_1_halt_2), .halt_2(mem_wb_1_halt_2),
    .\保持 (halt), .MD(multiplexer_10_out), .MD_2(mem_wb_1_md_2));  // open: ALU, ALU_2, JAL_JALR, JAL_JALR_2, Lbu, Lbu_2
  Register #(.width(1), .trigger("rising"), .Select("low")) register_2 (
    .D(mem_wb_1_halt_2), .Q(halt), .clk(CLK));  // open: en, clr

  // Other names for the same wires on the sheet: MEM_PC[31:0] = M_PC; WB_IR[11:7] = W_num

  // Notes on the sheet:
  //   中断源
  //   时空图监测，可删除
  //   中断等待指示
  //   PC_branch
  //   数码管输出
  //   指令存储器
  //   contents of rom_1 (hex, n*v repeats v):
  //   413 493 913 993 46413 14e493 296913 39e993 842023 942223 1242423 1342623 a00893 493 913 993 73
  //   指令字
  //   I
  //   S
  //   控制位
  //   JAL
  //   JALR
  //   URET
  //   流水调试日志用
  //   暂停节拍，不能为0
  //   Beq
  //   Bne
  //   MemToReg
  //   MemWrite
  //   AluOP
  //   AluSrcB
  //   RegWrite
  //   ecall时,判断a17==34?
  //   ALU1的imm默认为I型，置1为S型
  //    PC+4
  //   戳工具置1进入计数暂停模式，ctrl+k时钟自动运行到对应节拍暂停
  //   ctrl+k关闭时钟连续运行，将控制位置零，进入单步调试模式调试
  //   JAL,JALR需把PC+4存入寄存器
  //   B/J
  //   可计数暂停的时钟源
  //   用这个时钟源需要去掉电路中的其他时钟源
  //   BJ/I
  //   B=PC/R
  //   imm I/S
  //   imm BJ/I
  //   为方便自动评测，需要输出流水线各段保存的PC值，注意是PC不是PC+4，另外ID段寄存器写入信息，Mem段内存写入信息也要输出
  //   equal
  //   B_type
  //   Branch模块
  //   ecall模块
  //   数据存储器
endmodule

module IF_ID (
  input  [31:0] \指令字 ,
  input  [31:0] PC,
  input  Branch_Pre,
  input  CLK,
  input  \同步清零 ,
  input  \保持 ,
  output [31:0] \指令字_2 ,
  output [31:0] PC_2,
  output Branch_PRe_2
);

  wire multiplexer_3_out, not_1_out;
  wire [31:0] multiplexer_1_out, multiplexer_2_out;

  Multiplexer #(.select(1), .width(32), .disabled("Z"), .enable("false")) multiplexer_1 (
    .in0(\指令字 ), .in1({32{1'b0}}), .out(multiplexer_1_out), .sel(\同步清零 ));
  Multiplexer #(.select(1), .width(32), .disabled("Z"), .enable("false")) multiplexer_2 (
    .in0(PC), .in1({32{1'b0}}), .out(multiplexer_2_out), .sel(\同步清零 ));
  Multiplexer #(.select(1), .width(1), .disabled("Z"), .enable("false")) multiplexer_3 (
    .in0(Branch_Pre), .in1(1'b0), .out(multiplexer_3_out), .sel(\同步清零 ));
  not not_1 (not_1_out, \保持 );
  Register #(.width(32), .trigger("rising"), .Select("low")) register_1 (
    .D(multiplexer_1_out), .en(not_1_out), .Q(\指令字_2 ), .clk(CLK));  // open: clr
  Register #(.width(32), .trigger("rising"), .Select("low")) register_2 (
    .D(multiplexer_2_out), .en(not_1_out), .Q(PC_2), .clk(CLK));  // open: clr
  Register #(.width(1), .trigger("rising"), .Select("low")) register_3 (
    .D(multiplexer_3_out), .en(not_1_out), .Q(Branch_PRe_2), .clk(CLK));  // open: clr
endmodule

module ID_EX (
  input  [31:0] \指令字 ,
  input  [31:0] PC,
  input  Branch_Pre,
  input  JAL_JALR,
  input  Lbu,
  input  Beq,
  input  Blt,
  input  Bne,
  input  MemToReg,
  input  MemWrite,
  input  [3:0] Aluop,
  input  AlusrcB,
  input  RegWrite,
  input  ecall,
  input  [31:0] R1,
  input  [31:0] R2,
  input  [31:0] imm_I_S,
  input  [31:0] imm_BJ_I,
  input  [31:0] PC_R,
  input  CLK,
  input  \保持 ,
  input  \同步清零 ,
  output [31:0] PC_2,
  output [31:0] IR,
  output Branch_Pre_2,
  output JAL_JALR_2,
  output Lbu_2,
  output Beq_2,
  output Blt_2,
  output Bne_2,
  output MemToReg_2,
  output MemToReg_3,
  output [3:0] Aluop_2,
  output AlusrcB_2,
  output RegWrite_2,
  output ecall_2,
  output [31:0] R1_2,
  output [31:0] R2_2,
  output [31:0] imm_I_S_2,
  output [31:0] imm_BJ_I_2,
  output [31:0] B
);

  wire multiplexer_3_out, multiplexer_4_out, multiplexer_5_out, multiplexer_6_out, multiplexer_7_out,
       multiplexer_8_out, multiplexer_9_out, multiplexer_10_out, multiplexer_12_out, multiplexer_13_out,
       multiplexer_14_out, not_1_out;
  wire [3:0] multiplexer_11_out;
  wire [31:0] multiplexer_1_out, multiplexer_2_out, multiplexer_15_out, multiplexer_16_out,
       multiplexer_17_out, multiplexer_18_out, multiplexer_19_out;

  Multiplexer #(.select(1), .width(32), .disabled("Z"), .enable("false")) multiplexer_1 (
    .in0(\指令字 ), .in1({32{1'b0}}), .out(multiplexer_1_out), .sel(\同步清零 ));
  Multiplexer #(.select(1), .width(32), .disabled("Z"), .enable("false")) multiplexer_2 (
    .in0(PC), .in1({32{1'b0}}), .out(multiplexer_2_out), .sel(\同步清零 ));
  Multiplexer #(.select(1), .width(1), .disabled("Z"), .enable("false")) multiplexer_3 (
    .in0(Branch_Pre), .in1(1'b0), .out(multiplexer_3_out), .sel(\同步清零 ));
  Multiplexer #(.select(1), .width(1), .disabled("Z"), .enable("false")) multiplexer_4 (
    .in0(JAL_JALR), .in1(1'b0), .out(multiplexer_4_out), .sel(\同步清零 ));
  Multiplexer #(.select(1), .width(1), .disabled("Z"), .enable("false")) multiplexer_5 (
    .in0(Lbu), .in1(1'b0), .out(multiplexer_5_out), .sel(\同步清零 ));
  Multiplexer #(.select(1), .width(1), .disabled("Z"), .enable("false")) multiplexer_6 (
    .in0(Beq), .in1(1'b0), .out(multiplexer_6_out), .sel(\同步清零 ));
  Multiplexer #(.select(1), .width(1), .disabled("Z"), .enable("false")) multiplexer_7 (
    .in0(Blt), .in1(1'b0), .out(multiplexer_7_out), .sel(\同步清零 ));
  Multiplexer #(.select(1), .width(1), .disabled("Z"), .enable("false")) multiplexer_8 (
    .in0(Bne), .in1(1'b0), .out(multiplexer_8_out), .sel(\同步清零 ));
  Multiplexer #(.select(1), .width(1), .disabled("Z"), .enable("false")) multiplexer_9 (
    .in0(MemToReg), .in1(1'b0), .out(multiplexer_9_out), .sel(\同步清零 ));
  Multiplexer #(.select(1), .width(1), .disabled("Z"), .enable("false")) multiplexer_10 (
    .in0(MemWrite), .in1(1'b0), .out(multiplexer_10_out), .sel(\同步清零 ));
  Multiplexer #(.select(1), .width(4), .disabled("Z"), .enable("false")) multiplexer_11 (
    .in0(Aluop), .in1(4'b0000), .out(multiplexer_11_out), .sel(1'b0));
  Multiplexer #(.select(1), .width(1), .disabled("Z"), .enable("false")) multiplexer_12 (
    .in0(AlusrcB), .in1(1'b0), .out(multiplexer_12_out), .sel(\同步清零 ));
  Multiplexer #(.select(1), .width(1), .disabled("Z"), .enable("false")) multiplexer_13 (
    .in0(RegWrite), .in1(1'b0), .out(multiplexer_13_out), .sel(\同步清零 ));
  Multiplexer #(.select(1), .width(1), .disabled("Z"), .enable("false")) multiplexer_14 (
    .in0(ecall), .in1(1'b0), .out(multiplexer_14_out), .sel(\同步清零 ));
  Multiplexer #(.select(1), .width(32), .disabled("Z"), .enable("false")) multiplexer_15 (
    .in0(R1), .in1({32{1'b0}}), .out(multiplexer_15_out), .sel(\同步清零 ));
  Multiplexer #(.select(1), .width(32), .disabled("Z"), .enable("false")) multiplexer_16 (
    .in0(R2), .in1({32{1'b0}}), .out(multiplexer_16_out), .sel(\同步清零 ));
  Multiplexer #(.select(1), .width(32), .disabled("Z"), .enable("false")) multiplexer_17 (
    .in0(imm_I_S), .in1({32{1'b0}}), .out(multiplexer_17_out), .sel(\同步清零 ));
  Multiplexer #(.select(1), .width(32), .disabled("Z"), .enable("false")) multiplexer_18 (
    .in0(imm_BJ_I), .in1({32{1'b0}}), .out(multiplexer_18_out), .sel(\同步清零 ));
  Multiplexer #(.select(1), .width(32), .disabled("Z"), .enable("false")) multiplexer_19 (
    .in0(PC_R), .in1({32{1'b0}}), .out(multiplexer_19_out), .sel(\同步清零 ));
  not not_1 (not_1_out, \保持 );
  Register #(.width(32), .trigger("rising"), .Select("low")) register_1 (
    .D(multiplexer_1_out), .en(not_1_out), .Q(PC_2), .clk(CLK));  // open: clr
  Register #(.width(32), .trigger("rising"), .Select("low")) register_2 (
    .D(multiplexer_2_out), .en(not_1_out), .Q(IR), .clk(CLK));  // open: clr
  Register #(.width(1), .trigger("rising"), .Select("low")) register_3 (
    .D(multiplexer_3_out), .en(not_1_out), .Q(Branch_Pre_2), .clk(CLK));  // open: clr
  Register #(.width(1), .trigger("rising"), .Select("low")) register_4 (
    .D(multiplexer_4_out), .en(not_1_out), .Q(JAL_JALR_2), .clk(CLK));  // open: clr
  Register #(.width(1), .trigger("rising"), .Select("low")) register_5 (
    .D(multiplexer_5_out), .en(not_1_out), .Q(Lbu_2), .clk(CLK));  // open: clr
  Register #(.width(1), .trigger("rising"), .Select("low")) register_6 (
    .D(multiplexer_6_out), .en(not_1_out), .Q(Beq_2), .clk(CLK));  // open: clr
  Register #(.width(1), .trigger("rising"), .Select("low")) register_7 (
    .D(multiplexer_7_out), .en(not_1_out), .Q(Blt_2), .clk(CLK));  // open: clr
  Register #(.width(1), .trigger("rising"), .Select("low")) register_8 (
    .D(multiplexer_8_out), .en(not_1_out), .Q(Bne_2), .clk(CLK));  // open: clr
  Register #(.width(1), .trigger("rising"), .Select("low")) register_9 (
    .D(multiplexer_9_out), .en(not_1_out), .Q(MemToReg_2), .clk(CLK));  // open: clr
  Register #(.width(1), .trigger("rising"), .Select("low")) register_10 (
    .D(multiplexer_10_out), .en(not_1_out), .Q(MemToReg_3), .clk(CLK));  // open: clr
  Register #(.width(4), .trigger("rising"), .Select("low")) register_11 (
    .D(multiplexer_11_out), .en(not_1_out), .Q(Aluop_2), .clk(CLK));  // open: clr
  Register #(.width(1), .trigger("rising"), .Select("low")) register_12 (
    .D(multiplexer_12_out), .en(not_1_out), .Q(AlusrcB_2), .clk(CLK));  // open: clr
  Register #(.width(1), .trigger("rising"), .Select("low")) register_13 (
    .D(multiplexer_13_out), .en(not_1_out), .Q(RegWrite_2), .clk(CLK));  // open: clr
  Register #(.width(1), .trigger("rising"), .Select("low")) register_14 (
    .D(multiplexer_14_out), .en(not_1_out), .Q(ecall_2), .clk(CLK));  // open: clr
  Register #(.width(32), .trigger("rising"), .Select("low")) register_15 (
    .D(multiplexer_15_out), .en(not_1_out), .Q(R1_2), .clk(CLK));  // open: clr
  Register #(.width(32), .trigger("rising"), .Select("low")) register_16 (
    .D(multiplexer_16_out), .en(not_1_out), .Q(R2_2), .clk(CLK));  // open: clr
  Register #(.width(32), .trigger("rising"), .Select("low")) register_17 (
    .D(multiplexer_17_out), .en(not_1_out), .Q(imm_I_S_2), .clk(CLK));  // open: clr
  Register #(.width(32), .trigger("rising"), .Select("low")) register_18 (
    .D(multiplexer_18_out), .en(not_1_out), .Q(imm_BJ_I_2), .clk(CLK));  // open: clr
  Register #(.width(32), .trigger("rising"), .Select("low")) register_19 (
    .D(multiplexer_19_out), .en(not_1_out), .Q(B), .clk(CLK));  // open: clr
endmodule

module EX_MEM (
  input  [31:0] \指令字 ,
  input  [31:0] PC,
  input  Lbu,
  input  JAL_JALR,
  input  MemToReg,
  input  MemWrite,
  input  RegWrite,
  input  halt,
  input  [31:0] ALU,
  input  [31:0] MDin,
  input  \保持 ,
  input  CLK,
  output [31:0] \指令字_2 ,
  output [31:0] PC_2,
  output Lbu_2,
  output JAL_JALR_2,
  output MemToReg_2,
  output MemWrite_2,
  output RegWrite_2,
  output halt_2,
  output [31:0] Adress,
  output [31:0] MDin_2
);

  wire not_1_out;

  not not_1 (not_1_out, \保持 );
  Register #(.width(32), .trigger("rising"), .Select("low")) register_1 (
    .D(\指令字 ), .en(not_1_out), .Q(\指令字_2 ), .clk(CLK));  // open: clr
  Register #(.width(32), .trigger("rising"), .Select("low")) register_2 (
    .D(PC), .en(not_1_out), .Q(PC_2), .clk(CLK));  // open: clr
  Register #(.width(1), .trigger("rising"), .Select("low")) register_3 (
    .D(Lbu), .en(not_1_out), .Q(Lbu_2), .clk(CLK));  // open: clr
  Register #(.width(1), .trigger("rising"), .Select("low")) register_4 (
    .D(JAL_JALR), .en(not_1_out), .Q(JAL_JALR_2), .clk(CLK));  // open: clr
  Register #(.width(1), .trigger("rising"), .Select("low")) register_5 (
    .D(MemToReg), .en(not_1_out), .Q(MemToReg_2), .clk(CLK));  // open: clr
  Register #(.width(1), .trigger("rising"), .Select("low")) register_6 (
    .D(MemWrite), .en(not_1_out), .Q(MemWrite_2), .clk(CLK));  // open: clr
  Register #(.width(1), .trigger("rising"), .Select("low")) register_7 (
    .D(RegWrite), .en(not_1_out), .Q(RegWrite_2), .clk(CLK));  // open: clr
  Register #(.width(1), .trigger("falling"), .Select("low")) register_8 (
    .D(halt), .en(not_1_out), .Q(halt_2), .clk(CLK));  // open: clr
  Register #(.width(32), .trigger("rising"), .Select("low")) register_9 (
    .D(ALU), .en(not_1_out), .Q(Adress), .clk(CLK));  // open: clr
  Register #(.width(32), .trigger("rising"), .Select("low")) register_10 (
    .D(MDin), .en(not_1_out), .Q(MDin_2), .clk(CLK));  // open: clr
endmodule

module MEM_WB (
  input  [31:0] \指令字 ,
  input  [31:0] PC,
  input  Lbu,
  input  JAL_JALR,
  input  RegWrite,
  input  halt,
  input  [31:0] ALU,
  input  [31:0] MD,
  input  \保持 ,
  input  CLK,
  output [31:0] \指令字_2 ,
  output [31:0] PC_2,
  output Lbu_2,
  output JAL_JALR_2,
  output RegWrite_2,
  output halt_2,
  output [31:0] ALU_2,
  output [31:0] MD_2
);

  wire not_1_out;

  not not_1 (not_1_out, \保持 );
  Register #(.width(32), .trigger("rising"), .Select("low")) register_1 (
    .D(\指令字 ), .en(not_1_out), .Q(\指令字_2 ), .clk(CLK));  // open: clr
  Register #(.width(32), .trigger("rising"), .Select("low")) register_2 (
    .D(PC), .en(not_1_out), .Q(PC_2), .clk(CLK));  // open: clr
  Register #(.width(1), .trigger("rising"), .Select("low")) register_3 (
    .D(Lbu), .en(CLK), .Q(Lbu_2), .clk(CLK));  // open: clr
  Register #(.width(1), .trigger("rising"), .Select("low")) register_4 (
    .D(JAL_JALR), .en(not_1_out), .Q(JAL_JALR_2), .clk(CLK));  // open: clr
  Register #(.width(1), .trigger("rising"), .Select("low")) register_5 (
    .D(RegWrite), .Q(RegWrite_2), .clk(CLK));  // open: en, clr
  Register #(.width(1), .trigger("falling"), .Select("low")) register_6 (
    .D(halt), .en(not_1_out), .Q(halt_2), .clk(CLK));  // open: clr
  Register #(.width(32), .trigger("rising"), .Select("low")) register_7 (
    .D(ALU), .en(not_1_out), .Q(ALU_2), .clk(CLK));  // open: clr
  Register #(.width(32), .trigger("rising"), .Select("low")) register_8 (
    .D(MD), .en(not_1_out), .Q(MD_2), .clk(CLK));  // open: clr
endmodule

module \气泡流水线  (
  output RegWrite,
  output MemWrite,
  output [31:0] IF_PC,
  output [31:0] ID_PC,
  output [31:0] EX_PC,
  output [31:0] M_PC,
  output [31:0] WB_PC,
  output [31:0] RDin,
  output [31:0] MDin,
  output [31:0] LedData
);

  wire alu_2_equal, alu_2_out_6, and_1_out, and_2_out, and_3_out, and_4_out, and_5_out, and_6_out, and_7_out,
       and_8_out, and_9_out, and_10_out, B_type, CLK, clock_1_out, comparator_1_eq, comparator_1_lt,
       comparator_2_eq, \conflict_气泡_1_data_conflict , \conflict_气泡_2_data_conflict , d_ff_1_q,
       Data_Conflict, EX_Branch, ex_mem_1_halt_2, ex_mem_1_jal_jalr_2, ex_mem_1_lbu_2, ex_mem_1_memtoreg_2,
       ex_mem_1_regwrite_2, Go, halt, id_ex_1_alusrcb_2, id_ex_1_beq_2, id_ex_1_blt_2, id_ex_1_bne_2,
       id_ex_1_ecall_2, id_ex_1_lbu_2, id_ex_1_memtoreg_2, id_ex_1_memtoreg_3, id_ex_1_regwrite_2,
       if_id_1_branch_pre_2, IR1, IR2, IR3, JAL, JAL_JALR, JALR, mem_wb_1_halt_2, mem_wb_1_jal_jalr_2,
       nand_1_out, not_1_out, not_2_out, not_3_out, not_4_out, not_5_out, not_6_out, not_7_out, not_8_out,
       not_9_out, not_10_out, not_11_out, or_1_out, or_2_out, or_3_out, or_5_out, or_8_out, RST, W1, W2, W3,
       \单周期硬布线控制器_1_alu_src , \单周期硬布线控制器_1_beq , \单周期硬布线控制器_1_blt , \单周期硬布线控制器_1_bne , \单周期硬布线控制器_1_ecall ,
       \单周期硬布线控制器_1_lbu , \单周期硬布线控制器_1_memtoreg , \单周期硬布线控制器_1_memwrite , \单周期硬布线控制器_1_regwrite ,
       \单周期硬布线控制器_1_s_type ;
  wire [3:0] id_ex_1_aluop_2, \单周期硬布线控制器_1_alu_op ;
  wire [4:0] multiplexer_2_out, multiplexer_3_out;
  wire [7:0] bitselector_1_out;
  wire [11:0] multiplexer_4_out, shifter_1_out;
  wire [12:0] CNT_num;
  wire [15:0] \LoadUse次数 , \总周期数 , \插入气泡数 , \无条件分支数 , \条件分支成功数 ;
  wire [19:0] shifter_2_out;
  wire [31:0] adder_1_out, adder_2_out, alu_1_result, alu_2_result, bit_extender_1_out, bit_extender_2_out,
       bit_extender_3_out, bit_extender_4_out, EX_IR, ex_mem_1_adress, id_ex_1_b, id_ex_1_imm_bj_i_2,
       id_ex_1_imm_i_s_2, id_ex_1_r1_2, id_ex_1_r2_2, ID_IR, IF_IR, MEM_IR, mem_wb_1_md_2, multiplexer_1_out,
       multiplexer_5_out, multiplexer_6_out, multiplexer_7_out, multiplexer_8_out, multiplexer_9_out,
       multiplexer_10_out, ram_1_data, regifile_1_r1, regifile_1_r2, WB_IR;

  Button \u_总复位  (.out(RST));
  Button _1 (.out(IR1));
  Button _2 (.out(IR2));
  Button _3 (.out(IR3));
  // Probe on \总周期数 
  // Probe on \总周期数 
  Button \u_继续运行  (.out(Go));
  LED #(.active("true")) led_1 (.in(W1));
  LED #(.active("true")) led_2 (.in(W2));
  LED #(.active("true")) led_3 (.in(W3));
  not not_1 (not_1_out, halt);
  Hex_Digit_Display hex_digit_display_1 (.value(LedData[31:28]));  // open: dp
  // Probe on IF_PC[19:0]
  // RiscV_Probe riscv_probe_1: pin names not known; wires that end beside it: IF_IR
  Multiplexer #(.select(1), .width(32), .disabled("Z"), .enable("false")) multiplexer_1 (
    .in0(adder_1_out), .in1(alu_1_result), .out(multiplexer_1_out), .sel(EX_Branch));
  not not_2 (not_2_out, or_1_out);
  or or_1 (or_1_out, and_1_out, halt);
  and and_1 (and_1_out, not_3_out, Data_Conflict);
  not not_3 (not_3_out, EX_Branch);
  Counter #(.width(16), .max('hffff), .ongoal("wrap"), .trigger("rising"), .behavior("old")) counter_1 (
    .count(not_1_out), .Q(\总周期数 ), .clk(CLK));  // open: load, D, carry, clr, preset
  Hex_Digit_Display hex_digit_display_2 (.value(LedData[27:24]));  // open: dp
  Hex_Digit_Display hex_digit_display_3 (.value(LedData[23:20]));  // open: dp
  // Probe on ID_PC[19:0]
  // RiscV_Probe riscv_probe_2: pin names not known; wires that end beside it: ID_IR
  Register #(.width(32), .trigger("rising"), .Select("low")) PC (
    .D(multiplexer_1_out), .en(not_2_out), .Q(IF_PC), .clk(CLK), .clr(RST));
  Hex_Digit_Display hex_digit_display_4 (.value(LedData[19:16]));  // open: dp
  Hex_Digit_Display hex_digit_display_5 (.value(LedData[15:12]));  // open: dp
  Adder #(.width(32)) adder_1 (.a(IF_PC), .b(32'h4), .out(adder_1_out));  // open: cin, cout
  Hex_Digit_Display hex_digit_display_6 (.value(LedData[7:4]));  // open: dp
  Hex_Digit_Display hex_digit_display_7 (.value(LedData[11:8]));  // open: dp
  // Probe on EX_PC[19:0]
  // RiscV_Probe riscv_probe_3: pin names not known; wires that end beside it: EX_IR
  ROM #(.addrWidth(10), .dataWidth(32), .Select("high")) rom_1 (.addr(IF_PC[11:2]), .data(IF_IR));
  Counter #(.width(16), .max('hffff), .ongoal("wrap"), .trigger("rising"), .behavior("old")) counter_2 (
    .count(JAL_JALR), .Q(\无条件分支数 ), .clk(and_2_out));  // open: load, D, carry, clr, preset
  and and_2 (and_2_out, CLK, not_4_out);
  not not_4 (not_4_out, halt);
  Counter #(.width(16), .max('hffff), .ongoal("wrap"), .trigger("rising"), .behavior("old")) counter_3 (
    .count(B_type), .Q(\条件分支成功数 ), .clk(and_3_out));  // open: load, D, carry, clr, preset
  and and_3 (and_3_out, CLK, not_5_out);
  not not_5 (not_5_out, halt);
  Hex_Digit_Display hex_digit_display_8 (.value(LedData[3:0]));  // open: dp
  // Probe on \总周期数 
  // Probe on M_PC[19:0]
  // RiscV_Probe riscv_probe_4: pin names not known; wires that end beside it: MEM_IR
  IF_ID if_id_1 (
    .\指令字 (IF_IR), .\指令字_2 (ID_IR), .PC_2(ID_PC), .CLK(CLK), .\保持 (or_2_out), .\同步清零 (EX_Branch),
    .Branch_PRe_2(if_id_1_branch_pre_2), .PC(IF_PC));  // open: Branch_Pre
  or or_2 (or_2_out, halt, Data_Conflict);
  // Probe on \总周期数 
  // Probe on \无条件分支数 
  // Probe on \条件分支成功数 
  // Probe on \插入气泡数 
  // Probe on \LoadUse次数 
  // Probe on IF_PC[11:0]
  // Probe on WB_PC[19:0]
  // RiscV_Probe riscv_probe_5: pin names not known; wires that end beside it: WB_IR
  Multiplexer #(.select(1), .width(5), .disabled("Z"), .enable("false")) multiplexer_2 (
    .in0(ID_IR[19:15]), .in1(5'b10001), .out(multiplexer_2_out), .sel(\单周期硬布线控制器_1_ecall ));
  Multiplexer #(.select(1), .width(5), .disabled("Z"), .enable("false")) multiplexer_3 (
    .in0(ID_IR[24:20]), .in1(5'b01010), .out(multiplexer_3_out), .sel(\单周期硬布线控制器_1_ecall ));
  Counter #(.width(16), .max('hffff), .ongoal("wrap"), .trigger("rising"), .behavior("old")) counter_4 (
    .count(Data_Conflict), .Q(\插入气泡数 ), .clk(and_4_out));  // open: load, D, carry, clr, preset
  and and_4 (and_4_out, CLK, not_6_out);
  not not_6 (not_6_out, halt);
  // Probe on EX_PC[11:0]
  // Probe on ID_PC[11:0]
  \Conflict_气泡  \conflict_气泡_1  (
    .IR(ID_IR), .W_num(EX_IR[11:7]), .R1(multiplexer_2_out), .R2(multiplexer_3_out),
    .Data_Conflict(\conflict_气泡_1_data_conflict ));
  \Conflict_气泡  \conflict_气泡_2  (
    .IR(ID_IR), .W_num(MEM_IR[11:7]), .R1(multiplexer_2_out), .R2(multiplexer_3_out),
    .Data_Conflict(\conflict_气泡_2_data_conflict ));
  // Probe on M_PC[11:0]
  D_Flip_Flop #(.trigger("high"), .Pre_Clr_Positions("LEGACY"), .NegatePresetClear("false"), .enable("true"), .NewFFLayout("false")) d_ff_1 (.Q(d_ff_1_q));  // open: clk, D, Qn, preset, en, reset
  // Probe on 13'h19
  or or_3 (or_3_out, JAL, JALR);
  \单周期硬布线控制器  \u_单周期硬布线控制器_1  (
    .Funct({ID_IR[30], ID_IR[25], ID_IR[14:12]}), .OP(ID_IR[6:2]), .ALU_OP(\单周期硬布线控制器_1_alu_op ),
    .MemToReg(\单周期硬布线控制器_1_memtoreg ), .MemWrite(\单周期硬布线控制器_1_memwrite ), .ALU_SRC(\单周期硬布线控制器_1_alu_src ),
    .RegWrite(\单周期硬布线控制器_1_regwrite ), .ecall(\单周期硬布线控制器_1_ecall ), .S_type(\单周期硬布线控制器_1_s_type ),
    .Jalr(JALR), .Beq(\单周期硬布线控制器_1_beq ), .JAL(JAL), .Bne(\单周期硬布线控制器_1_bne ), .in_3(ID_IR[21]),
    .LBU(\单周期硬布线控制器_1_lbu ), .BLT(\单周期硬布线控制器_1_blt ));  // open: uret, Csrsi, Csrci
  or or_4 (Data_Conflict, \conflict_气泡_1_data_conflict , \conflict_气泡_2_data_conflict );
  // Probe on WB_PC[11:0]
  Comparator #(.width(13), .mode("twosComplement")) comparator_1 (
    .a(CNT_num), .b(13'h19), .eq(comparator_1_eq), .lt(comparator_1_lt));  // open: gt
  Clock #(.highDuration(1), .lowDuration(1)) clock_1 (.out(clock_1_out));
  Multiplexer #(.select(1), .width(12), .disabled("Z"), .enable("false")) multiplexer_4 (
    .in0(ID_IR[31:20]), .in1({ID_IR[31:25], ID_IR[11:7]}), .out(multiplexer_4_out), .sel(\单周期硬布线控制器_1_s_type ));
  Shifter #(.width(12), .shift("ll")) shifter_1 (
    .in({ID_IR[31], ID_IR[7], ID_IR[30:25], ID_IR[11:8]}), .\dist (4'b0001), .out(shifter_1_out));
  Shifter #(.width(20), .shift("ll")) shifter_2 (
    .in({ID_IR[31], ID_IR[19:12], ID_IR[20], ID_IR[30:21]}), .\dist (5'b00001), .out(shifter_2_out));
  nand nand_1 (nand_1_out, d_ff_1_q, comparator_1_eq);
  Counter #(.width(13), .max('h1fff), .ongoal("stay"), .trigger("rising"), .behavior("old")) counter_5 (
    .count(comparator_1_lt), .Q(CNT_num), .clk(clock_1_out));  // open: load, D, carry, clr, preset
  Regifile regifile_1 (
    .Din(RDin), .Clk(CLK), .R1(regifile_1_r1), .R2(regifile_1_r2), .WE(RegWrite), .W_num(WB_IR[11:7]),
    .R1_num(multiplexer_2_out), .R2_num(multiplexer_3_out));
  assign bit_extender_1_out = {{20{multiplexer_4_out[11]}}, multiplexer_4_out};  // Bit_Extender bit_extender_1
  assign bit_extender_2_out = {{20{shifter_1_out[11]}}, shifter_1_out};  // Bit_Extender bit_extender_2
  Multiplexer #(.select(1), .width(32), .disabled("Z"), .enable("false")) multiplexer_5 (
    .in0(bit_extender_2_out), .in1(bit_extender_3_out), .out(multiplexer_5_out), .sel(JAL));
  assign bit_extender_3_out = {{12{shifter_2_out[19]}}, shifter_2_out};  // Bit_Extender bit_extender_3
  assign CLK = nand_1_out ? clock_1_out : 1'bz;  // Controlled_Buffer controlled_buffer_1
  Multiplexer #(.select(1), .width(32), .disabled("Z"), .enable("false")) multiplexer_6 (
    .in0(ID_PC), .in1(regifile_1_r1), .out(multiplexer_6_out), .sel(JALR));
  Multiplexer #(.select(1), .width(32), .disabled("Z"), .enable("false")) multiplexer_7 (
    .in0(multiplexer_5_out), .out(multiplexer_7_out), .sel(JALR));  // open: in1
  Pull_Resistor #(.pull(1)) pull_resistor_1 (.node(CLK));
  ID_EX id_ex_1 (
    .\指令字 (ID_PC), .PC(ID_IR), .Aluop(\单周期硬布线控制器_1_alu_op ), .AlusrcB(\单周期硬布线控制器_1_alu_src ),
    .R1(regifile_1_r1), .R2(regifile_1_r2), .imm_I_S(bit_extender_1_out), .imm_BJ_I(multiplexer_7_out),
    .PC_2(EX_PC), .IR(EX_IR), .Aluop_2(id_ex_1_aluop_2), .AlusrcB_2(id_ex_1_alusrcb_2), .R1_2(id_ex_1_r1_2),
    .R2_2(id_ex_1_r2_2), .imm_I_S_2(id_ex_1_imm_i_s_2), .imm_BJ_I_2(id_ex_1_imm_bj_i_2), .CLK(CLK),
    .B(id_ex_1_b), .PC_R(multiplexer_6_out), .RegWrite(\单周期硬布线控制器_1_regwrite ),
    .RegWrite_2(id_ex_1_regwrite_2), .\保持 (halt), .ecall_2(id_ex_1_ecall_2), .ecall(\单周期硬布线控制器_1_ecall ),
    .\同步清零 (or_5_out), .Branch_Pre(if_id_1_branch_pre_2), .Bne(\单周期硬布线控制器_1_bne ), .Bne_2(id_ex_1_bne_2),
    .MemToReg(\单周期硬布线控制器_1_memtoreg ), .MemToReg_2(id_ex_1_memtoreg_2), .MemWrite(\单周期硬布线控制器_1_memwrite ),
    .MemToReg_3(id_ex_1_memtoreg_3), .JAL_JALR(or_3_out), .JAL_JALR_2(JAL_JALR), .Beq(\单周期硬布线控制器_1_beq ),
    .Beq_2(id_ex_1_beq_2), .Blt(\单周期硬布线控制器_1_blt ), .Blt_2(id_ex_1_blt_2), .Lbu(\单周期硬布线控制器_1_lbu ),
    .Lbu_2(id_ex_1_lbu_2));  // open: Branch_Pre_2
  or or_5 (or_5_out, Data_Conflict, EX_Branch);
  Multiplexer #(.select(1), .width(32), .disabled("Z"), .enable("false")) multiplexer_8 (
    .in0(id_ex_1_r2_2), .in1(id_ex_1_imm_i_s_2), .out(multiplexer_8_out), .sel(id_ex_1_alusrcb_2));
  ALU alu_1 (
    .X(id_ex_1_imm_bj_i_2), .Y(id_ex_1_b), .AluOP(4'b0101), .Result(alu_1_result));  // open: Equal, Result_2, out_4, out_6
  and and_5 (and_5_out, alu_2_equal, id_ex_1_beq_2);
  not not_7 (not_7_out, alu_2_equal);
  and and_6 (and_6_out, not_7_out, id_ex_1_bne_2);
  Comparator #(.width(32), .mode("twosComplement")) comparator_2 (
    .a(id_ex_1_r1_2), .b(32'h22), .eq(comparator_2_eq));  // open: gt, lt
  ALU alu_2 (
    .X(id_ex_1_r1_2), .Y(multiplexer_8_out), .AluOP(id_ex_1_aluop_2), .Equal(alu_2_equal),
    .Result(alu_2_result), .out_6(alu_2_out_6));  // open: Result_2, out_4
  and and_7 (and_7_out, id_ex_1_blt_2, alu_2_out_6);
  or or_6 (EX_Branch, JAL_JALR, B_type);
  or or_7 (B_type, and_7_out, and_5_out, and_6_out);
  and and_8 (and_8_out, id_ex_1_ecall_2, not_8_out);
  not not_8 (not_8_out, comparator_2_eq);
  and and_9 (and_9_out, id_ex_1_ecall_2, comparator_2_eq);
  not not_9 (not_9_out, or_8_out);
  or or_8 (or_8_out, Go, not_10_out);
  not not_10 (not_10_out, and_8_out);
  Register #(.width(32), .trigger("rising"), .Select("low")) register_1 (
    .D(id_ex_1_r2_2), .en(and_9_out), .Q(LedData), .clk(CLK));  // open: clr
  EX_MEM ex_mem_1 (
    .MemToReg(id_ex_1_memtoreg_2), .MemWrite(id_ex_1_memtoreg_3), .MemToReg_2(ex_mem_1_memtoreg_2),
    .MemWrite_2(MemWrite), .CLK(CLK), .\指令字 (EX_PC), .\指令字_2 (M_PC), .PC(EX_IR), .PC_2(MEM_IR),
    .Adress(ex_mem_1_adress), .ALU(alu_2_result), .MDin_2(MDin), .MDin(id_ex_1_r2_2),
    .RegWrite(id_ex_1_regwrite_2), .RegWrite_2(ex_mem_1_regwrite_2), .halt(not_9_out),
    .halt_2(ex_mem_1_halt_2), .\保持 (halt), .JAL_JALR(JAL_JALR), .JAL_JALR_2(ex_mem_1_jal_jalr_2),
    .Lbu(id_ex_1_lbu_2), .Lbu_2(ex_mem_1_lbu_2));
  not not_11 (not_11_out, halt);
  RAM #(.addrWidth(10), .dataWidth(32), .bus("separate"), .Select("high")) ram_1 (
    .addr(ex_mem_1_adress[11:2]), .din(MDin), .data(ram_1_data), .str(MemWrite), .sel(not_11_out), .clk(CLK));  // open: ld, clr
  BitSelector #(.width(32), .group(8)) bitselector_1 (
    .in(ram_1_data), .out(bitselector_1_out), .sel(ex_mem_1_adress[1:0]));
  Multiplexer #(.select(1), .width(32), .disabled("Z"), .enable("false")) multiplexer_9 (
    .in0(ex_mem_1_adress), .in1(ram_1_data), .out(multiplexer_9_out), .sel(ex_mem_1_memtoreg_2));
  assign bit_extender_4_out = {{24{1'b0}}, bitselector_1_out};  // Bit_Extender bit_extender_4
  MEM_WB mem_wb_1 (
    .\指令字 (M_PC), .PC(MEM_IR), .\指令字_2 (WB_PC), .PC_2(WB_IR), .CLK(CLK), .RegWrite(ex_mem_1_regwrite_2),
    .RegWrite_2(RegWrite), .halt(ex_mem_1_halt_2), .halt_2(mem_wb_1_halt_2), .\保持 (and_10_out),
    .JAL_JALR(ex_mem_1_jal_jalr_2), .JAL_JALR_2(mem_wb_1_jal_jalr_2), .MD(multiplexer_10_out),
    .MD_2(mem_wb_1_md_2), .Lbu(ex_mem_1_lbu_2));  // open: ALU, ALU_2, Lbu_2
  Multiplexer #(.select(1), .width(32), .disabled("Z"), .enable("false")) multiplexer_10 (
    .in0(multiplexer_9_out), .in1(bit_extender_4_out), .out(multiplexer_10_out), .sel(ex_mem_1_lbu_2));
  and and_10 (and_10_out, halt, ~Go);  // AND_Gate
  Adder #(.width(32)) adder_2 (.a(WB_PC), .b(32'h4), .out(adder_2_out));  // open: cin, cout
  Register #(.width(1), .trigger("rising"), .Select("low")) register_2 (
    .D(mem_wb_1_halt_2), .Q(halt), .clk(CLK));  // open: en, clr
  Multiplexer #(.select(1), .width(32), .disabled("Z"), .enable("false")) multiplexer_11 (
    .in0(mem_wb_1_md_2), .in1(adder_2_out), .out(RDin), .sel(mem_wb_1_jal_jalr_2));

  // Other names for the same wires on the sheet: MEM_PC[31:0] = M_PC; WB_W_num[4:0] = WB_IR[11:7]

  // Notes on the sheet:
  //   中断源
  //   时空图监测，可删除
  //   中断等待指示
  //   数码管输出
  //   指令存储器
  //   contents of rom_1 (hex, n*v repeats v):
  //   100493 100006f 100493 200913 300993 100006f 100493 200913 300993 100006f 100493 200913 300993
  //   100006f 100493 200913 300993 3d0000ef 100413 100493 1f49493 900533 2200893 73 24d493 48463 fedff06f
  //   900533 2200893 73 100493 249493 900533 2200893 73 48463 fedff06f 100493 1f49493 900533 2200893 73
  //   4034d493 900533 2200893 73 4044d493 900533 2200893 73 4044d493 900533 2200893 73 4044d493 900533
  //   2200893 73 4044d493 900533 2200893 73 4044d493 900533 2200893 73 4044d493 900533 2200893 73 4044d493
  //   900533 2200893 73 100413 1f41993 41f9d993 433 c00913 300b13 140413 f47413 800293 100313 499993
  //   89e9b3 1300533 2200893 73 406282b3 fe0294e3 140413 f00f93 1f47433 1c41413 800293 100313 49d993
  //   89e9b3 1300533 2200893 73 406282b3 fe0294e3 1c45413 406b0b33 b0463 f95ff06f 2b3 fff2c293 829293
  //   ff2e293 500533 2200893 73 fff00413 493 84a023 140413 448493 84a023 140413 448493 84a023 140413
  //   448493 84a023 140413 448493 84a023 140413 448493 84a023 140413 448493 84a023 140413 448493 84a023
  //   140413 448493 84a023 140413 448493 84a023 140413 448493 84a023 140413 448493 84a023 140413 448493
  //   84a023 140413 448493 84a023 140413 448493 84a023 140413 448493 84a023 140413 448493 140413 433
  //   3c00493 42983 4aa03 149a2b3 28663 134a023 1442023 ffc48493 fe9412e3 800533 2200893 73 440413 3c00493
  //   fc9416e3 3200893 73 100293 300313 800493 849493 7648493 1449493 900533 2200893 73 800e13 54d4b3
  //   64d4b3 900533 2200893 73 fffe0e13 fe0e14e3 a00893 73 fff00293 7700493 849493 7748493 900533 2200893
  //   73 1000e13 54c4b3 900533 2200893 73 fffe0e13 fe0e16e3 a00893 73 313 1000e13 8400493 849493 8348493
  //   400913 891913 490913 849493 8248493 849493 8148493 891913 490913 891913 490913 932023 12484b3 430313
  //   fffe0e13 fe0e18e3 2000e13 313 34483 900533 2200893 73 130313 fffe0e13 fe0e14e3 a00893 73 ff100493
  //   900533 2200893 73 148493 fe04c8e3 a00893 73 a00893 73 413 140413 800533 2200893 73 240413 800533
  //   2200893 73 340413 800533 2200893 73 440413 800533 2200893 73 540413 800533 2200893 73 640413 800533
  //   2200893 73 740413 800533 2200893 73 840413 800533 2200893 2200893 73 8067
  //   指令字
  //   上一条指令的W#
  //   I
  //   S
  //   控制位
  //   流水调试日志用
  //   暂停节拍，不能为0
  //   Beq
  //   Bne
  //   MemToReg
  //   MemWrite
  //   AluOP
  //   AluSrcB
  //   RegWrite
  //   ecall时,判断a17==34?
  //   ALU1的imm默认为I型，置1为S型
  //   戳工具置1进入计数暂停模式，ctrl+k时钟自动运行到对应节拍暂停
  //   ctrl+k关闭时钟连续运行，将控制位置零，进入单步调试模式调试
  //   B/J
  //   可计数暂停的时钟源
  //   BJ/I
  //   B=PC/R
  //   imm I/S
  //   imm BJ/I
  //   为方便自动评测，需要输出流水线各段保存的PC值，注意是PC不是PC+4，另外ID段寄存器写入信息，Mem段内存写入信息也要输出
  //   equal
  //   B_type
  //   Branch模块
  //   ecall模块
  //   数据存储器
  //   JAL,JALR需把PC+4存入寄存器
  //   PC+4
endmodule
module \重定向流水线  (
  output RegWrite,
  output MemWrite,
  output [31:0] IF_PC,
  output [31:0] ID_PC,
  output [31:0] EX_PC,
  output [31:0] M_PC,
  output [31:0] WB_PC,
  output [31:0] RDin,
  output [31:0] MDin,
  output [31:0] LedData
);

  wire alu_2_equal, alu_2_out_6, and_1_out, and_2_out, and_3_out, and_4_out, and_5_out, and_6_out, and_7_out,
       and_8_out, and_13_out, and_14_out, and_18_out, and_19_out, and_20_out, and_21_out, and_22_out, B_type,
       CLK, clock_1_out, comparator_1_eq, comparator_1_lt, comparator_2_eq, comparator_3_eq, comparator_4_eq,
       comparator_5_eq, comparator_6_eq, \conflict_重定向_1_r1_error , \conflict_重定向_1_r2_error ,
       \conflict_重定向_2_r1_error , \conflict_重定向_2_r2_error , d_ff_1_q, DataIMM, EX_Branch,
       ex_mem_1_jal_jalr_2, ex_mem_1_lbu_2, ex_mem_1_memtoreg_2, EX_RegWrite, Go, halt, id_ex_1_alusrcb_2,
       id_ex_1_beq_2, id_ex_1_blt_2, id_ex_1_bne_2, id_ex_1_ecall_2, id_ex_1_jal_jalr_2, id_ex_1_lbu_2,
       id_ex_1_memtoreg_2, id_ex_1_memtoreg_3, if_id_1_branch_pre_2, IR1, IR2, IR3, JAL, JAL_JALR, JALR,
       loaduse, MEM_RegWrite, mem_wb_1_jal_jalr_2, nand_1_out, not_1_out, not_2_out, not_3_out, not_4_out,
       not_5_out, not_6_out, not_7_out, not_8_out, not_9_out, not_10_out, not_11_out, or_1_out, or_2_out,
       or_3_out, or_5_out, or_6_out, or_7_out, or_8_out, or_9_out, R1_Ex, R1_Mem, R2_Ex, R2_Mem, RST, W1, W2,
       W3, WB_R1, WB_R2, \单周期硬布线控制器_1_alu_src , \单周期硬布线控制器_1_beq , \单周期硬布线控制器_1_blt , \单周期硬布线控制器_1_bne ,
       \单周期硬布线控制器_1_ecall , \单周期硬布线控制器_1_lbu , \单周期硬布线控制器_1_memtoreg , \单周期硬布线控制器_1_memwrite ,
       \单周期硬布线控制器_1_regwrite , \单周期硬布线控制器_1_s_type ;
  wire [1:0] encoder_1_out, encoder_2_out, f1_q, f2_q;
  wire [3:0] id_ex_1_aluop_2, \单周期硬布线控制器_1_alu_op ;
  wire [4:0] R1_num, R2_num;
  wire [7:0] bitselector_1_out;
  wire [11:0] multiplexer_5_out, shifter_1_out;
  wire [12:0] CNT_num;
  wire [15:0] \LoadUse次数 , \总周期数 , \插入气泡数 , \无条件分支数 , \条件分支成功数 ;
  wire [19:0] shifter_2_out;
  wire [31:0] adder_1_out, adder_2_out, alu_1_result, alu_2_result, alu_2_result_2, ALU_Result1, ALU_Result2,
       bit_extender_1_out, bit_extender_2_out, bit_extender_3_out, bit_extender_4_out, EX_IR, id_ex_1_b,
       id_ex_1_imm_bj_i_2, id_ex_1_imm_i_s_2, ID_IR, IF_IR, MEM_IR, mem_wb_1_md_2, multiplexer_1_out,
       multiplexer_6_out, multiplexer_7_out, multiplexer_8_out, multiplexer_9_out, multiplexer_11_out,
       multiplexer_12_out, R1, R2, ram_1_data, rd2, regifile_1_r1, regifile_1_r2, rs, WB_IR;

  Button \u_总复位  (.out(RST));
  Button _1 (.out(IR1));
  Button _2 (.out(IR2));
  Button _3 (.out(IR3));
  // Probe on \总周期数 
  // Probe on \总周期数 
  Button \u_继续运行  (.out(Go));
  LED #(.active("true")) led_1 (.in(W1));
  LED #(.active("true")) led_2 (.in(W2));
  LED #(.active("true")) led_3 (.in(W3));
  Hex_Digit_Display hex_digit_display_1 (.value(LedData[31:28]));  // open: dp
  // Probe on IF_PC[19:0]
  // RiscV_Probe riscv_probe_1: pin names not known; wires that end beside it: IF_IR
  Multiplexer #(.select(1), .width(32), .disabled("Z"), .enable("false")) multiplexer_1 (
    .in0(adder_1_out), .in1(alu_1_result), .out(multiplexer_1_out), .sel(EX_Branch));
  not not_1 (not_1_out, or_1_out);
  or or_1 (or_1_out, and_1_out, halt);
  and and_1 (and_1_out, ~EX_Branch, loaduse);  // AND_Gate
  Counter #(.width(16), .max('hffff), .ongoal("wrap"), .trigger("rising"), .behavior("old")) counter_1 (
    .count(JAL_JALR), .Q(\无条件分支数 ), .clk(and_2_out));  // open: load, D, carry, clr, preset
  and and_2 (and_2_out, CLK, not_2_out);
  not not_2 (not_2_out, halt);
  Counter #(.width(16), .max('hffff), .ongoal("wrap"), .trigger("rising"), .behavior("old")) counter_2 (
    .count(B_type), .Q(\条件分支成功数 ), .clk(and_3_out));  // open: load, D, carry, clr, preset
  and and_3 (and_3_out, CLK, not_3_out);
  not not_3 (not_3_out, halt);
  Hex_Digit_Display hex_digit_display_2 (.value(LedData[23:20]));  // open: dp
  Hex_Digit_Display hex_digit_display_3 (.value(LedData[27:24]));  // open: dp
  // Probe on ID_PC[19:0]
  // RiscV_Probe riscv_probe_2: pin names not known; wires that end beside it: ID_IR
  Register #(.width(32), .trigger("rising"), .Select("low")) PC (
    .D(multiplexer_1_out), .en(not_1_out), .Q(IF_PC), .clk(CLK), .clr(RST));
  Counter #(.width(16), .max('hffff), .ongoal("wrap"), .trigger("rising"), .behavior("old")) counter_3 (
    .count(not_4_out), .Q(\总周期数 ), .clk(CLK));  // open: load, D, carry, clr, preset
  not not_4 (not_4_out, halt);
  Hex_Digit_Display hex_digit_display_4 (.value(LedData[19:16]));  // open: dp
  Hex_Digit_Display hex_digit_display_5 (.value(LedData[15:12]));  // open: dp
  Adder #(.width(32)) adder_1 (.a(IF_PC), .b(32'h4), .out(adder_1_out));  // open: cin, cout
  Hex_Digit_Display hex_digit_display_6 (.value(LedData[11:8]));  // open: dp
  Hex_Digit_Display hex_digit_display_7 (.value(LedData[7:4]));  // open: dp
  // Probe on EX_PC[19:0]
  // RiscV_Probe riscv_probe_3: pin names not known; wires that end beside it: EX_IR
  ROM #(.addrWidth(10), .dataWidth(32), .Select("high")) rom_1 (.addr(IF_PC[11:2]), .data(IF_IR));
  Hex_Digit_Display hex_digit_display_8 (.value(LedData[3:0]));  // open: dp
  and and_4 (and_4_out, loaduse, ~EX_Branch);  // AND_Gate
  Counter #(.width(16), .max('hffff), .ongoal("wrap"), .trigger("rising"), .behavior("old")) counter_4 (
    .count(EX_Branch), .Q(\插入气泡数 ), .clk(and_5_out));  // open: load, D, carry, clr, preset
  and and_5 (and_5_out, CLK, not_5_out);
  not not_5 (not_5_out, halt);
  // Probe on \总周期数 
  // Probe on M_PC[19:0]
  // RiscV_Probe riscv_probe_4: pin names not known; wires that end beside it: MEM_IR
  IF_ID if_id_1 (
    .\指令字 (IF_IR), .\指令字_2 (ID_IR), .PC_2(ID_PC), .CLK(CLK), .\保持 (or_2_out), .\同步清零 (EX_Branch),
    .Branch_PRe_2(if_id_1_branch_pre_2), .PC(IF_PC));  // open: Branch_Pre
  or or_2 (or_2_out, halt, and_4_out);
  or or_3 (or_3_out, R1_Ex, R1_Mem, WB_R1);
  and and_6 (and_6_out, R1_Ex, ~WB_R1);  // AND_Gate
  and and_7 (and_7_out, R1_Mem, ~WB_R1);  // AND_Gate
  // Probe on \总周期数 
  // Probe on \无条件分支数 
  // Probe on \条件分支成功数 
  // Probe on \插入气泡数 
  // Probe on \LoadUse次数 
  not not_6 (not_6_out, or_3_out);
  Encoder encoder_1 (.in1(not_6_out), .in2(and_6_out), .in3(and_7_out), .in4(WB_R1), .out(encoder_1_out));
  // Probe on IF_PC[11:0]
  // Probe on WB_PC[19:0]
  // RiscV_Probe riscv_probe_5: pin names not known; wires that end beside it: WB_IR
  Multiplexer #(.select(1), .width(5), .disabled("Z"), .enable("false")) multiplexer_2 (
    .in0(ID_IR[19:15]), .in1(5'b10001), .out(R1_num), .sel(\单周期硬布线控制器_1_ecall ));
  Multiplexer #(.select(1), .width(5), .disabled("Z"), .enable("false")) multiplexer_3 (
    .in0(ID_IR[24:20]), .in1(5'b01010), .out(R2_num), .sel(\单周期硬布线控制器_1_ecall ));
  \Conflict_重定向  \conflict_重定向_1  (
    .IR(ID_IR), .W_num(EX_IR[11:7]), .R1(R1_num), .R2(R2_num), .R1_error(\conflict_重定向_1_r1_error ),
    .R2_error(\conflict_重定向_1_r2_error ));
  \Conflict_重定向  \conflict_重定向_2  (
    .IR(ID_IR), .W_num(MEM_IR[11:7]), .R1(R1_num), .R2(R2_num), .R1_error(\conflict_重定向_2_r1_error ),
    .R2_error(\conflict_重定向_2_r2_error ));
  // Probe on encoder_1_out
  Counter #(.width(16), .max('hffff), .ongoal("wrap"), .trigger("rising"), .behavior("old")) counter_5 (
    .count(loaduse), .Q(\LoadUse次数 ), .clk(and_8_out));  // open: load, D, carry, clr, preset
  and and_8 (and_8_out, CLK, not_7_out);
  not not_7 (not_7_out, halt);
  // Probe on ID_PC[11:0]
  // Probe on EX_PC[11:0]
  Register #(.width(2), .trigger("rising"), .Select("low")) f1 (
    .D(encoder_1_out), .Q(f1_q), .clk(CLK), .clr(Go));  // open: en
  // Probe on M_PC[11:0]
  D_Flip_Flop #(.trigger("high"), .Pre_Clr_Positions("LEGACY"), .NegatePresetClear("false"), .enable("true"), .NewFFLayout("false")) d_ff_1 (.Q(d_ff_1_q));  // open: clk, D, Qn, preset, en, reset
  // Probe on 13'h8f6
  or or_4 (JAL_JALR, JAL, JALR);
  \单周期硬布线控制器  \u_单周期硬布线控制器_1  (
    .Funct({ID_IR[30], ID_IR[25], ID_IR[14:12]}), .OP(ID_IR[6:2]), .ALU_OP(\单周期硬布线控制器_1_alu_op ),
    .MemToReg(\单周期硬布线控制器_1_memtoreg ), .MemWrite(\单周期硬布线控制器_1_memwrite ), .ALU_SRC(\单周期硬布线控制器_1_alu_src ),
    .RegWrite(\单周期硬布线控制器_1_regwrite ), .ecall(\单周期硬布线控制器_1_ecall ), .S_type(\单周期硬布线控制器_1_s_type ),
    .Jalr(JALR), .Beq(\单周期硬布线控制器_1_beq ), .JAL(JAL), .Bne(\单周期硬布线控制器_1_bne ), .in_3(ID_IR[21]),
    .LBU(\单周期硬布线控制器_1_lbu ), .BLT(\单周期硬布线控制器_1_blt ));  // open: uret, Csrsi, Csrci
  and and_9 (R1_Ex, EX_RegWrite, \conflict_重定向_1_r1_error );
  and and_10 (R2_Ex, EX_RegWrite, \conflict_重定向_1_r2_error );
  // Probe on rs
  Multiplexer #(.select(2), .width(32), .disabled("Z"), .enable("false")) multiplexer_4 (
    .in0(R1), .in1(ALU_Result1), .in2(ALU_Result2), .in3(RDin), .out(rs), .sel(f1_q));
  // Probe on RDin
  // Probe on WB_PC[11:0]
  Comparator #(.width(13), .mode("twosComplement")) comparator_1 (
    .a(CNT_num), .b(13'h8f6), .eq(comparator_1_eq), .lt(comparator_1_lt));  // open: gt
  Clock #(.highDuration(1), .lowDuration(1)) clock_1 (.out(clock_1_out));
  Multiplexer #(.select(1), .width(12), .disabled("Z"), .enable("false")) multiplexer_5 (
    .in0(ID_IR[31:20]), .in1({ID_IR[31:25], ID_IR[11:7]}), .out(multiplexer_5_out), .sel(\单周期硬布线控制器_1_s_type ));
  Shifter #(.width(12), .shift("ll")) shifter_1 (
    .in({ID_IR[31], ID_IR[7], ID_IR[30:25], ID_IR[11:8]}), .\dist (4'b0001), .out(shifter_1_out));
  Shifter #(.width(20), .shift("ll")) shifter_2 (
    .in({ID_IR[31], ID_IR[19:12], ID_IR[20], ID_IR[30:21]}), .\dist (5'b00001), .out(shifter_2_out));
  and and_11 (R1_Mem, \conflict_重定向_2_r1_error , ~R1_Ex, MEM_RegWrite);  // AND_Gate
  and and_12 (R2_Mem, \conflict_重定向_2_r2_error , ~R2_Ex, MEM_RegWrite);  // AND_Gate
  nand nand_1 (nand_1_out, d_ff_1_q, comparator_1_eq);
  Counter #(.width(13), .max('h1fff), .ongoal("stay"), .trigger("rising"), .behavior("old")) counter_6 (
    .count(comparator_1_lt), .Q(CNT_num), .clk(clock_1_out));  // open: load, D, carry, clr, preset
  Regifile regifile_1 (
    .Din(RDin), .Clk(CLK), .R1(regifile_1_r1), .R2(regifile_1_r2), .WE(RegWrite), .W_num(WB_IR[11:7]),
    .R1_num(R1_num), .R2_num(R2_num));
  assign bit_extender_1_out = {{20{multiplexer_5_out[11]}}, multiplexer_5_out};  // Bit_Extender bit_extender_1
  assign bit_extender_2_out = {{20{shifter_1_out[11]}}, shifter_1_out};  // Bit_Extender bit_extender_2
  Multiplexer #(.select(1), .width(32), .disabled("Z"), .enable("false")) multiplexer_6 (
    .in0(bit_extender_2_out), .in1(bit_extender_3_out), .out(multiplexer_6_out), .sel(JAL));
  assign bit_extender_3_out = {{12{shifter_2_out[19]}}, shifter_2_out};  // Bit_Extender bit_extender_3
  assign CLK = nand_1_out ? clock_1_out : 1'bz;  // Controlled_Buffer controlled_buffer_1
  Multiplexer #(.select(1), .width(32), .disabled("Z"), .enable("false")) multiplexer_7 (
    .in0(ID_PC), .in1(regifile_1_r1), .out(multiplexer_7_out), .sel(JALR));
  Multiplexer #(.select(1), .width(32), .disabled("Z"), .enable("false")) multiplexer_8 (
    .in0(multiplexer_6_out), .out(multiplexer_8_out), .sel(JALR));  // open: in1
  or or_5 (or_5_out, R2_Ex, R2_Mem, WB_R2);
  and and_13 (and_13_out, R2_Ex, ~WB_R2);  // AND_Gate
  and and_14 (and_14_out, R2_Mem, ~WB_R2);  // AND_Gate
  Pull_Resistor #(.pull(1)) pull_resistor_1 (.node(CLK));
  ID_EX id_ex_1 (
    .\指令字 (ID_PC), .PC(ID_IR), .Aluop(\单周期硬布线控制器_1_alu_op ), .AlusrcB(\单周期硬布线控制器_1_alu_src ),
    .R1(regifile_1_r1), .R2(regifile_1_r2), .imm_I_S(bit_extender_1_out), .imm_BJ_I(multiplexer_8_out),
    .PC_2(EX_PC), .IR(EX_IR), .Aluop_2(id_ex_1_aluop_2), .AlusrcB_2(id_ex_1_alusrcb_2), .R1_2(R1), .R2_2(R2),
    .imm_I_S_2(id_ex_1_imm_i_s_2), .imm_BJ_I_2(id_ex_1_imm_bj_i_2), .CLK(CLK), .B(id_ex_1_b),
    .PC_R(multiplexer_7_out), .RegWrite(\单周期硬布线控制器_1_regwrite ), .RegWrite_2(EX_RegWrite), .\保持 (halt),
    .ecall_2(id_ex_1_ecall_2), .ecall(\单周期硬布线控制器_1_ecall ), .\同步清零 (or_6_out),
    .Branch_Pre(if_id_1_branch_pre_2), .Bne(\单周期硬布线控制器_1_bne ), .Bne_2(id_ex_1_bne_2),
    .MemToReg(\单周期硬布线控制器_1_memtoreg ), .MemToReg_2(id_ex_1_memtoreg_2), .MemWrite(\单周期硬布线控制器_1_memwrite ),
    .MemToReg_3(id_ex_1_memtoreg_3), .JAL_JALR(JAL_JALR), .JAL_JALR_2(id_ex_1_jal_jalr_2),
    .Beq(\单周期硬布线控制器_1_beq ), .Beq_2(id_ex_1_beq_2), .Blt(\单周期硬布线控制器_1_blt ), .Blt_2(id_ex_1_blt_2),
    .Lbu(\单周期硬布线控制器_1_lbu ), .Lbu_2(id_ex_1_lbu_2));  // open: Branch_Pre_2
  or or_6 (or_6_out, and_4_out, EX_Branch);
  Comparator #(.width(5), .mode("twosComplement")) comparator_2 (
    .a(5'b00011), .b(MEM_IR[6:2]), .eq(comparator_2_eq));  // open: gt, lt
  Comparator #(.width(5), .mode("twosComplement")) comparator_3 (
    .a({5{1'b0}}), .b(MEM_IR[6:2]), .eq(comparator_3_eq));  // open: gt, lt
  Comparator #(.width(5), .mode("twosComplement")) comparator_4 (
    .a(EX_IR[6:2]), .b(5'b00011), .eq(comparator_4_eq));  // open: gt, lt
  Comparator #(.width(5), .mode("twosComplement")) comparator_5 (
    .a(EX_IR[6:2]), .b({5{1'b0}}), .eq(comparator_5_eq));  // open: gt, lt
  not not_8 (not_8_out, or_5_out);
  Encoder encoder_2 (.in1(not_8_out), .in2(and_13_out), .in3(and_14_out), .in4(WB_R2), .out(encoder_2_out));
  or or_7 (or_7_out, comparator_2_eq, comparator_3_eq);
  or or_8 (or_8_out, comparator_4_eq, comparator_5_eq);
  or or_9 (or_9_out, R1_Ex, R2_Ex);
  Register #(.width(1), .trigger("rising"), .Select("low")) f1_2 (
    .D(not_8_out), .Q(DataIMM), .clk(CLK));  // open: en, clr
  // Probe on encoder_2_out
  Multiplexer #(.select(1), .width(32), .disabled("Z"), .enable("false")) multiplexer_9 (
    .in0(rd2), .in1(id_ex_1_imm_i_s_2), .out(multiplexer_9_out), .sel(id_ex_1_alusrcb_2));
  ALU alu_1 (
    .X(id_ex_1_imm_bj_i_2), .Y(id_ex_1_b), .AluOP(4'b0101), .Result(alu_1_result));  // open: Equal, Result_2, out_4, out_6
  and and_15 (loaduse, or_8_out, or_9_out);
  and and_16 (WB_R2, R2_Mem, or_7_out);
  and and_17 (WB_R1, R1_Mem, or_7_out);
  and and_18 (and_18_out, alu_2_equal, id_ex_1_beq_2);
  not not_9 (not_9_out, alu_2_equal);
  and and_19 (and_19_out, not_9_out, id_ex_1_bne_2);
  Comparator #(.width(32), .mode("twosComplement")) comparator_6 (
    .a(rs), .b(32'h22), .eq(comparator_6_eq));  // open: gt, lt
  ALU alu_2 (
    .X(rs), .Y(multiplexer_9_out), .AluOP(id_ex_1_aluop_2), .Equal(alu_2_equal), .Result(alu_2_result),
    .Result_2(alu_2_result_2), .out_6(alu_2_out_6));  // open: out_4
  Register #(.width(2), .trigger("rising"), .Select("low")) f2 (
    .D(encoder_2_out), .Q(f2_q), .clk(CLK), .clr(Go));  // open: en
  and and_20 (and_20_out, id_ex_1_blt_2, alu_2_out_6);
  not not_10 (not_10_out, comparator_6_eq);
  and and_21 (and_21_out, id_ex_1_ecall_2, comparator_6_eq);
  // Probe on rd2
  Multiplexer #(.select(2), .width(32), .disabled("Z"), .enable("false")) multiplexer_10 (
    .in0(R2), .in1(ALU_Result1), .in2(ALU_Result2), .in3(RDin), .out(rd2), .sel(f2_q));
  // Probe on RDin
  or or_10 (EX_Branch, id_ex_1_jal_jalr_2, B_type);
  or or_11 (B_type, and_20_out, and_18_out, and_19_out);
  and and_22 (and_22_out, id_ex_1_ecall_2, not_10_out);
  Register #(.width(32), .trigger("rising"), .Select("low")) register_1 (
    .D(rd2), .en(and_21_out), .Q(LedData), .clk(CLK));  // open: clr
  Register #(.width(1), .trigger("falling"), .Select("low")) register_2 (
    .D(and_22_out), .Q(halt), .clk(CLK), .clr(Go), .preset(halt));  // open: en, cs
  EX_MEM ex_mem_1 (
    .MemToReg(id_ex_1_memtoreg_2), .MemWrite(id_ex_1_memtoreg_3), .MemToReg_2(ex_mem_1_memtoreg_2),
    .MemWrite_2(MemWrite), .CLK(CLK), .\指令字 (EX_PC), .\指令字_2 (M_PC), .PC(EX_IR), .PC_2(MEM_IR),
    .Adress(ALU_Result1), .ALU(alu_2_result), .MDin_2(MDin), .MDin(rd2), .RegWrite(EX_RegWrite),
    .RegWrite_2(MEM_RegWrite), .\保持 (halt), .JAL_JALR(id_ex_1_jal_jalr_2), .JAL_JALR_2(ex_mem_1_jal_jalr_2),
    .Lbu(id_ex_1_lbu_2), .Lbu_2(ex_mem_1_lbu_2));  // open: halt, halt_2
  not not_11 (not_11_out, halt);
  RAM #(.addrWidth(10), .dataWidth(32), .bus("separate"), .Select("high")) ram_1 (
    .addr(ALU_Result1[11:2]), .din(MDin), .data(ram_1_data), .str(MemWrite), .sel(not_11_out), .clk(CLK));  // open: ld, clr
  Multiplexer #(.select(1), .width(32), .disabled("Z"), .enable("false")) multiplexer_11 (
    .in0(ALU_Result1), .in1(ram_1_data), .out(multiplexer_11_out), .sel(ex_mem_1_memtoreg_2));
  BitSelector #(.width(32), .group(8)) bitselector_1 (.in(ram_1_data), .out(bitselector_1_out), .sel(ALU_Result1[1:0]));
  Multiplexer #(.select(1), .width(32), .disabled("Z"), .enable("false")) multiplexer_12 (
    .in0(multiplexer_11_out), .in1(bit_extender_4_out), .out(multiplexer_12_out), .sel(ex_mem_1_lbu_2));
  assign bit_extender_4_out = {{24{1'b0}}, bitselector_1_out};  // Bit_Extender bit_extender_4
  MEM_WB mem_wb_1 (
    .\指令字 (M_PC), .PC(MEM_IR), .ALU(ALU_Result1), .\指令字_2 (WB_PC), .PC_2(WB_IR), .ALU_2(ALU_Result2),
    .CLK(CLK), .RegWrite(MEM_RegWrite), .RegWrite_2(RegWrite), .\保持 (halt), .JAL_JALR(ex_mem_1_jal_jalr_2),
    .JAL_JALR_2(mem_wb_1_jal_jalr_2), .MD(multiplexer_12_out), .MD_2(mem_wb_1_md_2), .Lbu(ex_mem_1_lbu_2));  // open: halt, halt_2, Lbu_2
  Adder #(.width(32)) adder_2 (.a(WB_PC), .b(32'h4), .out(adder_2_out));  // open: cin, cout
  Multiplexer #(.select(1), .width(32), .disabled("Z"), .enable("false")) multiplexer_13 (
    .in0(mem_wb_1_md_2), .in1(adder_2_out), .out(RDin), .sel(mem_wb_1_jal_jalr_2));

  // Other names for the same wires on the sheet: Mem_FinalData[31:0] = RDin; MEM_PC[31:0] = M_PC;
  //   WB_W_num[4:0] = WB_IR[11:7]

  // Notes on the sheet:
  //   中断源
  //   时空图监测，可删除
  //   中断等待指示
  //   OP
  //   指令存储器
  //   contents of rom_1 (hex, n*v repeats v):
  //   100493 100006f 100493 200913 300993 100006f 100493 200913 300993 100006f 100493 200913 300993
  //   100006f 100493 200913 300993 3d0000ef 100413 100493 1f49493 900533 2200893 73 24d493 48463 fedff06f
  //   900533 2200893 73 100493 249493 900533 2200893 73 48463 fedff06f 100493 1f49493 900533 2200893 73
  //   4034d493 900533 2200893 73 4044d493 900533 2200893 73 4044d493 900533 2200893 73 4044d493 900533
  //   2200893 73 4044d493 900533 2200893 73 4044d493 900533 2200893 73 4044d493 900533 2200893 73 4044d493
  //   900533 2200893 73 100413 1f41993 41f9d993 433 c00913 300b13 140413 f47413 800293 100313 499993
  //   89e9b3 1300533 2200893 73 406282b3 fe0294e3 140413 f00f93 1f47433 1c41413 800293 100313 49d993
  //   89e9b3 1300533 2200893 73 406282b3 fe0294e3 1c45413 406b0b33 b0463 f95ff06f 2b3 fff2c293 829293
  //   ff2e293 500533 2200893 73 fff00413 493 84a023 140413 448493 84a023 140413 448493 84a023 140413
  //   448493 84a023 140413 448493 84a023 140413 448493 84a023 140413 448493 84a023 140413 448493 84a023
  //   140413 448493 84a023 140413 448493 84a023 140413 448493 84a023 140413 448493 84a023 140413 448493
  //   84a023 140413 448493 84a023 140413 448493 84a023 140413 448493 84a023 140413 448493 140413 433
  //   3c00493 42983 4aa03 149a2b3 28663 134a023 1442023 ffc48493 fe9412e3 800533 2200893 73 440413 3c00493
  //   fc9416e3 3200893 73 100293 300313 800493 849493 7648493 1449493 900533 2200893 73 800e13 54d4b3
  //   64d4b3 900533 2200893 73 fffe0e13 fe0e14e3 a00893 73 fff00293 7700493 849493 7748493 900533 2200893
  //   73 1000e13 54c4b3 900533 2200893 73 fffe0e13 fe0e16e3 a00893 73 313 1000e13 8400493 849493 8348493
  //   400913 891913 490913 849493 8248493 849493 8148493 891913 490913 891913 490913 932023 12484b3 430313
  //   fffe0e13 fe0e18e3 2000e13 313 34483 900533 2200893 73 130313 fffe0e13 fe0e14e3 a00893 73 ff100493
  //   900533 2200893 73 148493 fe04c8e3 a00893 73 a00893 73 413 140413 800533 2200893 73 240413 800533
  //   2200893 73 340413 800533 2200893 73 440413 800533 2200893 73 540413 800533 2200893 73 640413 800533
  //   2200893 73 740413 800533 2200893 73 840413 800533 2200893 2200893 73 8067
  //   指令字
  //   上一条指令的W#
  //   I
  //   S
  //   控制位
  //   JAL
  //   JALR
  //   URET
  //   流水调试日志用
  //   暂停节拍，不能为0
  //   Beq
  //   Bne
  //   MemToReg
  //   MemWrite
  //   AluOP
  //   AluSrcB
  //   RegWrite
  //   ecall时,判断a17==34?
  //   ALU1的imm默认为I型，置1为S型
  //   戳工具置1进入计数暂停模式，ctrl+k时钟自动运行到对应节拍暂停
  //   ctrl+k关闭时钟连续运行，将控制位置零，进入单步调试模式调试
  //   B/J
  //   可计数暂停的时钟源
  //   BJ/I
  //   B=PC/R
  //   imm I/S
  //   imm BJ/I
  //   为方便自动评测，需要输出流水线各段保存的PC值，注意是PC不是PC+4，另外ID段寄存器写入信息，Mem段内存写入信息也要输出
  //   equal
  //   ecall模块
  //   B_type
  //   Branch模块
  //   数据存储器
  //   PC+4
  //   JAL,JALR需把PC+4存入寄存器
endmodule

module \中断按键参考电路  (
  input  CLK,
  input  \编号 ,
  input  \同步清零信号 ,
  output \与中断屏蔽位与 ,
  output \中断等待 
);

  wire and_1_out, d_ff_1_q, or_2_out;

  Clock #(.highDuration(1), .lowDuration(1)) clock_1 ();  // open: out
  Button \_1号中断  ();  // open: out
  LED #(.active("true")) \_1号中断等待指示灯  ();  // open: in
  or or_1 (\中断等待 , \与中断屏蔽位与 , d_ff_1_q);
  D_Flip_Flop #(.trigger("rising"), .Pre_Clr_Positions("LEGACY"), .NegatePresetClear("false"), .enable("true"), .NewFFLayout("false")) d_ff_1 (
    .clk(\编号 ), .D(1'b1), .Q(d_ff_1_q), .reset(\与中断屏蔽位与 ));  // open: Qn, preset, en
  or or_2 (or_2_out, d_ff_1_q, \与中断屏蔽位与 );
  and and_1 (and_1_out, or_2_out, ~\同步清零信号 );  // AND_Gate
  D_Flip_Flop #(.trigger("rising"), .Pre_Clr_Positions("LEGACY"), .NegatePresetClear("false"), .enable("true"), .NewFFLayout("false")) IR1 (
    .clk(CLK), .D(and_1_out), .Q(\与中断屏蔽位与 ));  // open: Qn, preset, en, reset

  // Notes on the sheet:
  //   中断信号采样参考电路
  //   Reset 
endmodule

module \单周期_单级中断  (
  input  IR1,
  input  IR2,
  input  IR3,
  output RegWrite,
  output MemWrite,
  output [31:0] PC,
  output [31:0] IR,
  output [31:0] RDin,
  output [31:0] MDin,
  output [31:0] LedData
);

  wire alu_2_equal, alu_2_out_6, and_1_out, and_2_out, and_3_out, and_5_out, and_6_out, and_7_out, and_8_out,
       and_9_out, CLK, clock_1_out, comparator_1_eq, comparator_2_eq, comparator_3_eq, comparator_4_eq,
       comparator_5_lt, comparator_6_eq, comparator_6_lt, d_ff_1_q, d_ff_2_q, d_ff_3_q, d_ff_4_q,
       decoder_1_out1, decoder_1_out2, decoder_1_out3, demultiplexer_1_out1, demultiplexer_1_out2,
       demultiplexer_1_out3, ecall, Go, halt, IE, Interrupt, IR1_q, IR1_t, IR2_q, IR2_t, IR3_q, IR3_t, IRA,
       IRB, IRC, JAL, JALR, LBU, multiplexer_7_out, nand_1_out, not_1_out, not_2_out, not_3_out, not_4_out,
       not_5_out, not_6_out, not_8_out, or_1_out, or_6_out, or_7_out, or_8_out, or_11_out, or_12_out,
       or_13_out, or_14_out, or_15_out, or_16_out, URET, W1, W2, W3, \单周期硬布线控制器_1_alu_src ,
       \单周期硬布线控制器_1_beq , \单周期硬布线控制器_1_blt , \单周期硬布线控制器_1_bne , \单周期硬布线控制器_1_memtoreg , \单周期硬布线控制器_1_s_type ;
  wire [1:0] IR_NUM, NUM_now;
  wire [3:0] \单周期硬布线控制器_1_alu_op ;
  wire [4:0] multiplexer_4_out, multiplexer_5_out;
  wire [11:0] multiplexer_8_out, shifter_1_out;
  wire [12:0] CNT_num;
  wire [15:0] \总周期数 ;
  wire [19:0] shifter_2_out;
  wire [31:0] adder_1_out, alu_1_result, alu_2_result, bit_extender_1_out, bit_extender_2_out,
       bit_extender_3_out, bit_extender_4_out, counter_1_q, EPC, EPC1_q, EPC2_q, EPC3_q, EPC_q, iaddr,
       multiplexer_2_out, multiplexer_3_out, multiplexer_10_out, multiplexer_11_out, multiplexer_12_out,
       multiplexer_13_out, multiplexer_14_out, multiplexer_15_out, multiplexer_17_out, PC_4, ram_1_data,
       regifile_1_r1;

  Button \u_继续运行  (.out(Go));
  Button _1 ();  // open: out
  Button _2 ();  // open: out
  Button _3 ();  // open: out
  LED #(.active("true")) led_1 (.in(W1));
  LED #(.active("true")) led_2 (.in(W2));
  LED #(.active("true")) led_3 (.in(W3));
  Hex_Digit_Display hex_digit_display_1 (.value(LedData[31:28]));  // open: dp
  Hex_Digit_Display hex_digit_display_2 (.value(LedData[27:24]));  // open: dp
  Hex_Digit_Display hex_digit_display_3 (.value(LedData[23:20]));  // open: dp
  Comparator #(.width(16), .mode("twosComplement")) comparator_1 (
    .a(16'h23b), .b(\总周期数 ), .eq(comparator_1_eq));  // open: gt, lt
  Comparator #(.width(16), .mode("twosComplement")) comparator_2 (
    .a(\总周期数 ), .b(16'h1), .eq(comparator_2_eq));  // open: gt, lt
  Comparator #(.width(16), .mode("twosComplement")) comparator_3 (
    .a(\总周期数 ), .b(16'h4), .eq(comparator_3_eq));  // open: gt, lt
  Comparator #(.width(16), .mode("twosComplement")) comparator_4 (
    .a(\总周期数 ), .b(16'h7), .eq(comparator_4_eq));  // open: gt, lt
  Hex_Digit_Display hex_digit_display_4 (.value(LedData[19:16]));  // open: dp
  Hex_Digit_Display hex_digit_display_5 (.value(LedData[15:12]));  // open: dp
  or or_1 (or_1_out, comparator_1_eq, comparator_2_eq);
  assign IRA = or_1_out ? ~CLK : 1'bz;  // Controlled_Inverter controlled_inverter_1
  assign IRB = comparator_3_eq ? ~CLK : 1'bz;  // Controlled_Inverter controlled_inverter_2
  assign IRC = comparator_4_eq ? ~CLK : 1'bz;  // Controlled_Inverter controlled_inverter_3
  Multiplexer #(.select(1), .width(32), .disabled("Z"), .enable("false")) multiplexer_1 (
    .in0(adder_1_out), .in1(alu_1_result), .out(PC_4), .sel(or_11_out));
  // Probe on URET
  Demultiplexer #(.select(2), .width(1), .tristate("false"), .disabled("Z"), .enable("false")) demultiplexer_1 (
    .out1(demultiplexer_1_out1), .out2(demultiplexer_1_out2), .out3(demultiplexer_1_out3), .in(URET),
    .sel(NUM_now));  // open: out0
  // Probe on NUM_now
  Hex_Digit_Display hex_digit_display_6 (.value(LedData[11:8]));  // open: dp
  Hex_Digit_Display hex_digit_display_7 (.value(LedData[7:4]));  // open: dp
  // Probe on \总周期数 
  Pull_Resistor #(.pull(0)) pull_resistor_1 (.node(IRA));
  Pull_Resistor #(.pull(0)) pull_resistor_2 (.node(IRB));
  Pull_Resistor #(.pull(0)) pull_resistor_3 (.node(IRC));
  Hex_Digit_Display hex_digit_display_8 (.value(LedData[3:0]));  // open: dp
  Multiplexer #(.select(1), .width(32), .disabled("Z"), .enable("false")) multiplexer_2 (
    .in0(PC_4), .in1(iaddr), .out(multiplexer_2_out), .sel(Interrupt));
  or or_2 (W1, IR1_q, d_ff_1_q);
  or or_3 (W2, IR2_q, d_ff_2_q);
  or or_4 (W3, IR3_q, d_ff_3_q);
  Multiplexer #(.select(1), .width(32), .disabled("Z"), .enable("false")) multiplexer_3 (
    .in0(multiplexer_2_out), .in1(EPC), .out(multiplexer_3_out), .sel(URET));
  D_Flip_Flop #(.trigger("rising"), .Pre_Clr_Positions("LEGACY"), .NegatePresetClear("false"), .enable("true"), .NewFFLayout("false")) d_ff_1 (
    .clk(IR1_t), .D(1'b1), .Q(d_ff_1_q), .reset(IR1_q));  // open: Qn, preset, en
  D_Flip_Flop #(.trigger("rising"), .Pre_Clr_Positions("LEGACY"), .NegatePresetClear("false"), .enable("true"), .NewFFLayout("false")) d_ff_2 (
    .clk(IR2_t), .D(1'b1), .Q(d_ff_2_q), .reset(IR2_q));  // open: Qn, preset, en
  D_Flip_Flop #(.trigger("rising"), .Pre_Clr_Positions("LEGACY"), .NegatePresetClear("false"), .enable("true"), .NewFFLayout("false")) d_ff_3 (
    .clk(IR3_t), .D(1'b1), .Q(d_ff_3_q), .reset(IR3_q));  // open: Qn, preset, en
  or or_5 (IR1_t, IR1, IRA);
  Register #(.width(32), .trigger("rising"), .Select("low")) u_PC (
    .D(multiplexer_3_out), .en(not_1_out), .Q(PC), .clk(CLK));  // open: clr
  not not_1 (not_1_out, halt);
  or or_6 (or_6_out, d_ff_1_q, IR1_q);
  or or_7 (or_7_out, d_ff_2_q, IR2_q);
  or or_8 (or_8_out, d_ff_3_q, IR3_q);
  or or_9 (IR2_t, IR2, IRB);
  and and_1 (and_1_out, or_6_out, ~demultiplexer_1_out1);  // AND_Gate
  and and_2 (and_2_out, or_7_out, ~demultiplexer_1_out2);  // AND_Gate
  and and_3 (and_3_out, or_8_out, ~demultiplexer_1_out3);  // AND_Gate
  Adder #(.width(32)) adder_1 (.a(PC), .b(32'h4), .out(adder_1_out));  // open: cin, cout
  D_Flip_Flop #(.trigger("rising"), .Pre_Clr_Positions("LEGACY"), .NegatePresetClear("false"), .enable("true"), .NewFFLayout("false")) u_IR1 (
    .clk(CLK), .D(and_1_out), .Q(IR1_q));  // open: Qn, preset, en, reset
  D_Flip_Flop #(.trigger("rising"), .Pre_Clr_Positions("LEGACY"), .NegatePresetClear("false"), .enable("true"), .NewFFLayout("false")) u_IR2 (
    .clk(CLK), .D(and_2_out), .Q(IR2_q));  // open: Qn, preset, en, reset
  D_Flip_Flop #(.trigger("rising"), .Pre_Clr_Positions("LEGACY"), .NegatePresetClear("false"), .enable("true"), .NewFFLayout("false")) u_IR3 (
    .clk(CLK), .D(and_3_out), .Q(IR3_q));  // open: Qn, preset, en, reset
  or or_10 (IR3_t, IR3, IRC);
  or or_11 (or_11_out, or_14_out, JALR, JAL);
  // RiscV_Probe riscv_probe_1: pin names not known; wires that end beside it: IR
  ROM #(.addrWidth(10), .dataWidth(32), .Select("high")) rom_1 (.addr(PC[11:2]), .data(IR));
  // Probe on IR_NUM
  Priority_Encoder #(.select(2), .disabled("Z")) priority_encoder_1 (
    .in0(1'b1), .in1(IR1_q), .in2(IR2_q), .in3(IR3_q), .out(IR_NUM));  // open: gs, en_out, en_in
  Counter #(.width(32), .max('hffffffff), .ongoal("wrap"), .trigger("rising"), .behavior("old")) counter_1 (
    .Q(counter_1_q), .clk(CLK));  // open: load, D, count, carry, clr, preset
  \单周期硬布线控制器  \u_单周期硬布线控制器_1  (
    .Funct({IR[30], IR[25], IR[14:12]}), .OP(IR[6:2]), .ALU_OP(\单周期硬布线控制器_1_alu_op ),
    .MemToReg(\单周期硬布线控制器_1_memtoreg ), .MemWrite(MemWrite), .ALU_SRC(\单周期硬布线控制器_1_alu_src ),
    .RegWrite(RegWrite), .ecall(ecall), .S_type(\单周期硬布线控制器_1_s_type ), .Jalr(JALR), .Beq(\单周期硬布线控制器_1_beq ),
    .JAL(JAL), .Bne(\单周期硬布线控制器_1_bne ), .in_3(IR[21]), .uret(URET), .LBU(LBU), .BLT(\单周期硬布线控制器_1_blt ));  // open: Csrsi, Csrci
  Multiplexer #(.select(1), .width(5), .disabled("Z"), .enable("false")) multiplexer_4 (
    .in0(IR[19:15]), .in1(5'b10001), .out(multiplexer_4_out), .sel(ecall));
  Multiplexer #(.select(1), .width(5), .disabled("Z"), .enable("false")) multiplexer_5 (
    .in0(IR[24:20]), .in1(5'b01010), .out(multiplexer_5_out), .sel(ecall));
  Multiplexer #(.select(2), .width(32), .disabled("Z"), .enable("false")) multiplexer_6 (
    .in1(32'h30ac), .in2(32'h3150), .in3(32'h31f4), .out(iaddr), .sel(IR_NUM));  // open: in0
  or or_12 (or_12_out, IR1_q, IR2_q, IR3_q);
  not not_2 (not_2_out, Interrupt);
  Multiplexer #(.select(1), .width(1), .disabled("Z"), .enable("false")) multiplexer_7 (
    .in0(not_2_out), .in1(1'b1), .out(multiplexer_7_out), .sel(URET));
  or or_13 (or_13_out, comparator_5_lt, Interrupt, URET);
  Comparator #(.width(32), .mode("unsigned")) comparator_5 (
    .a(counter_1_q), .b(32'h2), .lt(comparator_5_lt));  // open: gt, eq
  Multiplexer #(.select(1), .width(12), .disabled("Z"), .enable("false")) multiplexer_8 (
    .in0(IR[31:20]), .in1({IR[31:25], IR[11:7]}), .out(multiplexer_8_out), .sel(\单周期硬布线控制器_1_s_type ));
  Shifter #(.width(12), .shift("ll")) shifter_1 (
    .in({IR[31], IR[7], IR[30:25], IR[11:8]}), .\dist (4'b0001), .out(shifter_1_out));
  Shifter #(.width(20), .shift("ll")) shifter_2 (
    .in({IR[31], IR[19:12], IR[20], IR[30:21]}), .\dist (5'b00001), .out(shifter_2_out));
  Multiplexer #(.select(1), .width(32), .disabled("Z"), .enable("false")) multiplexer_9 (
    .in0(multiplexer_17_out), .in1(adder_1_out), .out(RDin), .sel(or_15_out));
  Register #(.width(2), .trigger("rising"), .Select("low")) u_NUM_now (
    .D(IR_NUM), .en(Interrupt), .Q(NUM_now), .clk(CLK));  // open: clr
  and and_4 (Interrupt, or_12_out, IE);
  Register #(.width(1), .trigger("rising"), .Select("low")) u_IE (
    .D(multiplexer_7_out), .en(or_13_out), .Q(IE), .clk(CLK));  // open: clr
  or or_14 (or_14_out, and_6_out, and_5_out, and_7_out);
  and and_5 (and_5_out, \单周期硬布线控制器_1_blt , alu_2_out_6);
  and and_6 (and_6_out, \单周期硬布线控制器_1_beq , alu_2_equal);
  assign bit_extender_1_out = {{20{multiplexer_8_out[11]}}, multiplexer_8_out};  // Bit_Extender bit_extender_1
  assign bit_extender_2_out = {{20{shifter_1_out[11]}}, shifter_1_out};  // Bit_Extender bit_extender_2
  Multiplexer #(.select(1), .width(32), .disabled("Z"), .enable("false")) multiplexer_10 (
    .in0(bit_extender_2_out), .in1(bit_extender_3_out), .out(multiplexer_10_out), .sel(JAL));
  assign bit_extender_3_out = {{12{shifter_2_out[19]}}, shifter_2_out};  // Bit_Extender bit_extender_3
  or or_15 (or_15_out, JAL, JALR);
  and and_7 (and_7_out, \单周期硬布线控制器_1_bne , not_3_out);
  not not_3 (not_3_out, alu_2_equal);
  Regifile regifile_1 (
    .Din(RDin), .Clk(CLK), .R1(regifile_1_r1), .R2(MDin), .WE(RegWrite), .W_num(IR[11:7]),
    .R1_num(multiplexer_4_out), .R2_num(multiplexer_5_out));
  Multiplexer #(.select(1), .width(32), .disabled("Z"), .enable("false")) multiplexer_11 (
    .in0(multiplexer_10_out), .in1(bit_extender_1_out), .out(multiplexer_11_out), .sel(JALR));
  Multiplexer #(.select(1), .width(32), .disabled("Z"), .enable("false")) multiplexer_12 (
    .in0(MDin), .in1(bit_extender_1_out), .out(multiplexer_12_out), .sel(\单周期硬布线控制器_1_alu_src ));
  Multiplexer #(.select(1), .width(32), .disabled("Z"), .enable("false")) multiplexer_13 (
    .in0(PC), .in1(regifile_1_r1), .out(multiplexer_13_out), .sel(JALR));
  D_Flip_Flop #(.trigger("high"), .Pre_Clr_Positions("LEGACY"), .NegatePresetClear("false"), .enable("true"), .NewFFLayout("false")) d_ff_4 (.Q(d_ff_4_q));  // open: clk, D, Qn, preset, en, reset
  // Probe on 13'h23b
  Decoder #(.select(2), .tristate("false"), .disabled("Z"), .enable("false")) decoder_1 (
    .out1(decoder_1_out1), .out2(decoder_1_out2), .out3(decoder_1_out3), .sel(IR_NUM));  // open: out0
  // Probe on PC_4
  Comparator #(.width(13), .mode("twosComplement")) comparator_6 (
    .a(CNT_num), .b(13'h23b), .eq(comparator_6_eq), .lt(comparator_6_lt));  // open: gt
  Clock #(.highDuration(1), .lowDuration(1)) clock_1 (.out(clock_1_out));
  Multiplexer #(.select(1), .width(32), .disabled("Z"), .enable("false")) multiplexer_14 (
    .in0(multiplexer_12_out), .in1(32'h22), .out(multiplexer_14_out), .sel(ecall));
  ALU alu_1 (
    .X(multiplexer_11_out), .Y(multiplexer_13_out), .AluOP(4'b0101), .Result(alu_1_result));  // open: Equal, Result_2, out_4, out_6
  Counter #(.width(16), .max('hffff), .ongoal("wrap"), .trigger("rising"), .behavior("old")) counter_2 (
    .count(not_4_out), .Q(\总周期数 ), .clk(CLK));  // open: load, D, carry, clr, preset
  not not_4 (not_4_out, halt);
  Register #(.width(32), .trigger("rising"), .Select("low")) u_EPC (
    .D(PC_4), .en(Interrupt), .Q(EPC_q), .clk(CLK));  // open: clr
  Counter #(.width(13), .max('h1fff), .ongoal("stay"), .trigger("rising"), .behavior("old")) counter_3 (
    .count(comparator_6_lt), .Q(CNT_num), .clk(clock_1_out));  // open: load, D, carry, clr, preset
  ALU alu_2 (
    .X(regifile_1_r1), .Y(multiplexer_14_out), .AluOP(\单周期硬布线控制器_1_alu_op ), .Equal(alu_2_equal),
    .Result(alu_2_result), .out_6(alu_2_out_6));  // open: Result_2, out_4
  nand nand_1 (nand_1_out, d_ff_4_q, comparator_6_eq);
  not not_5 (not_5_out, and_8_out);
  and and_8 (and_8_out, ecall, not_6_out);
  not not_6 (not_6_out, alu_2_equal);
  and and_9 (and_9_out, ecall, alu_2_equal);
  // Probe on EPC1_q
  Register #(.width(32), .trigger("rising"), .Select("low")) EPC1 (
    .D(EPC_q), .en(decoder_1_out1), .Q(EPC1_q), .clk(CLK));  // open: clr
  Register #(.width(32), .trigger("rising"), .Select("low")) EPC2 (
    .D(EPC_q), .en(decoder_1_out2), .Q(EPC2_q), .clk(CLK));  // open: clr
  assign CLK = nand_1_out ? clock_1_out : 1'bz;  // Controlled_Buffer controlled_buffer_1
  Pull_Resistor #(.pull(1)) pull_resistor_4 (.node(CLK));
  not not_7 (halt, or_16_out);
  or or_16 (or_16_out, Go, not_5_out);
  Register #(.width(32), .trigger("rising"), .Select("low")) register_1 (
    .D(MDin), .en(and_9_out), .Q(LedData), .clk(CLK));  // open: clr
  not not_8 (not_8_out, halt);
  Register #(.width(32), .trigger("rising"), .Select("low")) EPC3 (
    .D(EPC_q), .en(decoder_1_out3), .Q(EPC3_q), .clk(CLK));  // open: clr
  // Probe on EPC_q
  RAM #(.addrWidth(10), .dataWidth(32), .bus("separate"), .Select("high")) ram_1 (
    .addr(alu_2_result[11:2]), .din(MDin), .data(ram_1_data), .str(MemWrite), .sel(not_8_out), .clk(CLK));  // open: ld, clr
  // Probe on EPC2_q
  // Probe on EPC3_q
  Multiplexer #(.select(1), .width(32), .disabled("Z"), .enable("false")) multiplexer_15 (
    .in0(alu_2_result), .in1(ram_1_data), .out(multiplexer_15_out), .sel(\单周期硬布线控制器_1_memtoreg ));
  assign bit_extender_4_out = {{24{1'b0}}, ram_1_data[31:24]};  // Bit_Extender bit_extender_4
  // Probe on EPC
  Multiplexer #(.select(2), .width(32), .disabled("Z"), .enable("false")) multiplexer_16 (
    .in1(EPC1_q), .in2(EPC2_q), .in3(EPC3_q), .out(EPC), .sel(IR_NUM));  // open: in0
  Multiplexer #(.select(1), .width(32), .disabled("Z"), .enable("false")) multiplexer_17 (
    .in0(multiplexer_15_out), .in1(bit_extender_4_out), .out(multiplexer_17_out), .sel(LBU));

  // Notes on the sheet:
  //   中断源
  //   中断等待指示
  //   总复位信号应将除ROM以外所有存储组件全部清零
  //   单级中断测试信号模拟器
  //   数码管输出
  //   数码管输出应该用寄存器锁存，否则显示数据只能一闪而过
  //   Reset 
  //   Reset 
  //   Reset 
  //   指令存储器
  //   PC_branch
  //   指令探针
  //   contents of rom_1 (hex, n*v repeats v):
  //   7d000113 100413 1f41993 41f9d993 433 c00913 800b13 140413 f47413 800293 100313 499993 89e9b3 1300533
  //   2200893 73 406282b3 fe0294e3 140413 f00f93 1f47433 1c41413 800293 100313 49d993 89e9b3 1300533
  //   2200893 73 406282b3 fe0294e3 1c45413 406b0b33 b0463 f95ff06f 2b3 fff2c293 1029293 fff2e293 500533
  //   2200893 73 f5dff06f 1112023 410113 a12023 410113 812023 410113 1312023 410113 1412023 410113 1512023
  //   410113 1612023 410113 100b13 300a13 100a93 1600433 441413 14469b3 1300533 2200893 73 fe0416e3
  //   415a0a33 fe0a10e3 ffc10113 12b03 ffc10113 12a83 ffc10113 12a03 ffc10113 12983 ffc10113 12403
  //   ffc10113 12503 ffc10113 12883 200073 1112023 410113 a12023 410113 812023 410113 1312023 410113
  //   1412023 410113 1512023 410113 1612023 410113 200b13 300a13 100a93 1600433 441413 14469b3 1300533
  //   2200893 73 fe0416e3 415a0a33 fe0a10e3 ffc10113 12b03 ffc10113 12a83 ffc10113 12a03 ffc10113 12983
  //   ffc10113 12403 ffc10113 12503 ffc10113 12883 200073 1112023 410113 a12023 410113 812023 410113
  //   1312023 410113 1412023 410113 1512023 410113 1612023 410113 300b13 300a13 100a93 1600433 441413
  //   14469b3 1300533 2200893 73 fe0416e3 415a0a33 fe0a10e3 ffc10113 12b03 ffc10113 12a83 ffc10113 12a03
  //   ffc10113 12983 ffc10113 12403 ffc10113 12503 ffc10113 12883 200073
  //   指令字
  //   I
  //   S
  //   B
  //   J
  //   JAL,JALR需把PC+4存入寄存器
  //   Beq
  //   Bne
  //   ecall时,判断a17==34?
  //   ALU1的imm默认为I型，置1为S型
  //    PC+4
  //   为方便自动评测，需要输出PC，IR，寄存器堆写如数据RDin
  //   B_type
  //   MemToReg
  //   MemWrite
  //   AluOP
  //   AluSrcB
  //   RegWrite
  //   RAM写使能MemWrite、RAM写入数据MDin等信号
  //   equal
  //   B=PC/寄存器
  //   控制位
  //   暂停节拍，不能为0
  //   戳工具置1进入计数暂停模式，ctrl+k时钟自动运行到对应节拍暂停
  //   ctrl+k关闭时钟连续运行，将控制位置零，进入单步调试模式调试
  //   可计数暂停的时钟源
  //   数据存储器
endmodule

module \单周期_多级中断  (
  input  IR1,
  input  IR2,
  input  IR3,
  output RegWrite,
  output MemWrite,
  output [31:0] PC,
  output [31:0] IR,
  output [31:0] RDin,
  output [31:0] MDin,
  output [31:0] LedData
);

  wire alu_2_equal, alu_2_out_6, and_1_out, and_2_out, and_3_out, and_4_out, and_5_out, and_6_out, and_7_out,
       and_8_out, and_10_out, and_11_out, and_12_out, and_13_out, and_14_out, and_15_out, CLK, clock_1_out,
       comparator_1_eq, comparator_2_eq, comparator_3_eq, comparator_4_eq, comparator_5_eq, comparator_6_lt,
       comparator_7_eq, comparator_7_lt, comparator_8_lt, Csrci, Csrsi, d_ff_1_q, d_ff_2_q, d_ff_3_q,
       d_ff_4_q, decoder_1_out1, decoder_1_out2, decoder_1_out3, decoder_2_out1, decoder_2_out2,
       decoder_2_out3, demultiplexer_1_out1, demultiplexer_1_out2, demultiplexer_1_out3, ecall, Go, halt, IE,
       Interrupt, IR1_q, IR1_t, IR2_q, IR2_t, IR3_q, IR3_t, IRA, IRB, IRC, JAL, JALR, LBU, multiplexer_8_out,
       nand_1_out, not_1_out, not_2_out, not_3_out, not_4_out, not_5_out, not_6_out, not_8_out, or_1_out,
       or_2_out, or_7_out, or_8_out, or_9_out, or_12_out, or_13_out, or_14_out, or_15_out, or_16_out,
       or_17_out, or_18_out, or_19_out, URET, W1, W2, W3, \单周期硬布线控制器_1_alu_src , \单周期硬布线控制器_1_beq ,
       \单周期硬布线控制器_1_blt , \单周期硬布线控制器_1_bne , \单周期硬布线控制器_1_memtoreg , \单周期硬布线控制器_1_s_type ;
  wire [1:0] adder_2_out, IR_NUM, IR_reg1_q, IR_reg2_q, IR_reg3_q, multiplexer_15_out, NUM_now, p, queue_num;
  wire [3:0] \单周期硬布线控制器_1_alu_op ;
  wire [4:0] multiplexer_5_out, multiplexer_6_out;
  wire [11:0] multiplexer_9_out, shifter_1_out;
  wire [12:0] CNT_num;
  wire [15:0] \总周期数 ;
  wire [19:0] shifter_2_out;
  wire [31:0] adder_1_out, alu_1_result, alu_2_result, bit_extender_1_out, bit_extender_2_out,
       bit_extender_3_out, bit_extender_4_out, counter_2_q, EPC, EPC1_q, EPC2_q, EPC3_q, iaddr,
       multiplexer_2_out, multiplexer_3_out, multiplexer_11_out, multiplexer_12_out, multiplexer_13_out,
       multiplexer_14_out, multiplexer_16_out, multiplexer_18_out, multiplexer_19_out, PC_4, ram_1_data,
       regifile_1_r1;

  Button \u_继续运行  (.out(Go));
  Button _1 ();  // open: out
  Button _2 ();  // open: out
  Button _3 ();  // open: out
  LED #(.active("true")) led_1 (.in(W1));
  LED #(.active("true")) led_2 (.in(W2));
  LED #(.active("true")) led_3 (.in(W3));
  not not_1 (not_1_out, halt);
  Hex_Digit_Display hex_digit_display_1 (.value(LedData[31:28]));  // open: dp
  Counter #(.width(16), .max('hffff), .ongoal("wrap"), .trigger("rising"), .behavior("old")) counter_1 (
    .count(not_1_out), .Q(\总周期数 ), .clk(CLK));  // open: load, D, carry, clr, preset
  Hex_Digit_Display hex_digit_display_2 (.value(LedData[23:20]));  // open: dp
  Hex_Digit_Display hex_digit_display_3 (.value(LedData[27:24]));  // open: dp
  Hex_Digit_Display hex_digit_display_4 (.value(LedData[15:12]));  // open: dp
  Hex_Digit_Display hex_digit_display_5 (.value(LedData[19:16]));  // open: dp
  Comparator #(.width(16), .mode("twosComplement")) comparator_1 (
    .a(16'h258), .b(\总周期数 ), .eq(comparator_1_eq));  // open: gt, lt
  Comparator #(.width(16), .mode("twosComplement")) comparator_2 (
    .a(\总周期数 ), .b(16'h1), .eq(comparator_2_eq));  // open: gt, lt
  Comparator #(.width(16), .mode("twosComplement")) comparator_3 (
    .a(\总周期数 ), .b(16'h4), .eq(comparator_3_eq));  // open: gt, lt
  Comparator #(.width(16), .mode("twosComplement")) comparator_4 (
    .a(\总周期数 ), .b(16'h7), .eq(comparator_4_eq));  // open: gt, lt
  or or_1 (or_1_out, comparator_4_eq, comparator_5_eq);
  Comparator #(.width(16), .mode("twosComplement")) comparator_5 (
    .a(\总周期数 ), .b(16'h241), .eq(comparator_5_eq));  // open: gt, lt
  Multiplexer #(.select(1), .width(32), .disabled("Z"), .enable("false")) multiplexer_1 (
    .in0(adder_1_out), .in1(alu_1_result), .out(PC_4), .sel(or_12_out));
  // Probe on URET
  Demultiplexer #(.select(2), .width(1), .tristate("false"), .disabled("Z"), .enable("false")) demultiplexer_1 (
    .out1(demultiplexer_1_out1), .out2(demultiplexer_1_out2), .out3(demultiplexer_1_out3), .in(URET),
    .sel(IR_NUM));  // open: out0
  // Probe on IR_NUM
  Decoder #(.select(2), .tristate("false"), .disabled("Z"), .enable("false")) decoder_1 (
    .out1(decoder_1_out1), .out2(decoder_1_out2), .out3(decoder_1_out3), .sel(IR_NUM));  // open: out0
  Hex_Digit_Display hex_digit_display_6 (.value(LedData[11:8]));  // open: dp
  Hex_Digit_Display hex_digit_display_7 (.value(LedData[7:4]));  // open: dp
  // Probe on \总周期数 
  or or_2 (or_2_out, comparator_1_eq, comparator_2_eq);
  Pull_Resistor #(.pull(0)) pull_resistor_1 (.node(IRA));
  assign IRA = or_2_out ? ~CLK : 1'bz;  // Controlled_Inverter controlled_inverter_1
  Pull_Resistor #(.pull(0)) pull_resistor_2 (.node(IRB));
  assign IRB = comparator_3_eq ? ~CLK : 1'bz;  // Controlled_Inverter controlled_inverter_2
  Pull_Resistor #(.pull(0)) pull_resistor_3 (.node(IRC));
  assign IRC = or_1_out ? ~CLK : 1'bz;  // Controlled_Inverter controlled_inverter_3
  Hex_Digit_Display hex_digit_display_8 (.value(LedData[3:0]));  // open: dp
  Multiplexer #(.select(1), .width(32), .disabled("Z"), .enable("false")) multiplexer_2 (
    .in0(PC_4), .in1(iaddr), .out(multiplexer_2_out), .sel(Interrupt));
  or or_3 (W1, IR1_q, d_ff_1_q);
  or or_4 (W2, IR2_q, d_ff_2_q);
  or or_5 (W3, IR3_q, d_ff_3_q);
  and and_1 (and_1_out, decoder_1_out1, Interrupt);
  and and_2 (and_2_out, decoder_1_out2, Interrupt);
  and and_3 (and_3_out, decoder_1_out3, Interrupt);
  Multiplexer #(.select(1), .width(32), .disabled("Z"), .enable("false")) multiplexer_3 (
    .in0(multiplexer_2_out), .in1(EPC), .out(multiplexer_3_out), .sel(URET));
  D_Flip_Flop #(.trigger("rising"), .Pre_Clr_Positions("LEGACY"), .NegatePresetClear("false"), .enable("true"), .NewFFLayout("false")) d_ff_1 (
    .clk(IR1_t), .D(1'b1), .Q(d_ff_1_q), .reset(IR1_q));  // open: Qn, preset, en
  D_Flip_Flop #(.trigger("rising"), .Pre_Clr_Positions("LEGACY"), .NegatePresetClear("false"), .enable("true"), .NewFFLayout("false")) d_ff_2 (
    .clk(IR2_t), .D(1'b1), .Q(d_ff_2_q), .reset(IR2_q));  // open: Qn, preset, en
  D_Flip_Flop #(.trigger("rising"), .Pre_Clr_Positions("LEGACY"), .NegatePresetClear("false"), .enable("true"), .NewFFLayout("false")) d_ff_3 (
    .clk(IR3_t), .D(1'b1), .Q(d_ff_3_q), .reset(IR3_q));  // open: Qn, preset, en
  or or_6 (IR1_t, IR1, IRA);
  Register #(.width(32), .trigger("rising"), .Select("low")) u_PC (
    .D(multiplexer_3_out), .en(not_2_out), .Q(PC), .clk(CLK));  // open: clr
  not not_2 (not_2_out, halt);
  or or_7 (or_7_out, d_ff_1_q, IR1_q);
  or or_8 (or_8_out, d_ff_2_q, IR2_q);
  or or_9 (or_9_out, d_ff_3_q, IR3_q);
  // Probe on EPC1_q
  Register #(.width(32), .trigger("rising"), .Select("low")) EPC1 (
    .D(PC_4), .en(and_1_out), .Q(EPC1_q), .clk(CLK));  // open: clr
  Register #(.width(32), .trigger("rising"), .Select("low")) EPC2 (
    .D(PC_4), .en(and_2_out), .Q(EPC2_q), .clk(CLK));  // open: clr
  or or_10 (IR2_t, IR2, IRB);
  and and_4 (and_4_out, or_7_out, ~demultiplexer_1_out1);  // AND_Gate
  and and_5 (and_5_out, or_8_out, ~demultiplexer_1_out2);  // AND_Gate
  and and_6 (and_6_out, or_9_out, ~demultiplexer_1_out3);  // AND_Gate
  // Probe on EPC2_q
  // Probe on EPC3_q
  Register #(.width(32), .trigger("rising"), .Select("low")) EPC3 (
    .D(PC_4), .en(and_3_out), .Q(EPC3_q), .clk(CLK));  // open: clr
  // Probe on PC_4
  Adder #(.width(32)) adder_1 (.a(PC), .b(32'h4), .out(adder_1_out));  // open: cin, cout
  D_Flip_Flop #(.trigger("rising"), .Pre_Clr_Positions("LEGACY"), .NegatePresetClear("false"), .enable("true"), .NewFFLayout("false")) u_IR1 (
    .clk(CLK), .D(and_4_out), .Q(IR1_q));  // open: Qn, preset, en, reset
  D_Flip_Flop #(.trigger("rising"), .Pre_Clr_Positions("LEGACY"), .NegatePresetClear("false"), .enable("true"), .NewFFLayout("false")) u_IR2 (
    .clk(CLK), .D(and_5_out), .Q(IR2_q));  // open: Qn, preset, en, reset
  D_Flip_Flop #(.trigger("rising"), .Pre_Clr_Positions("LEGACY"), .NegatePresetClear("false"), .enable("true"), .NewFFLayout("false")) u_IR3 (
    .clk(CLK), .D(and_6_out), .Q(IR3_q));  // open: Qn, preset, en, reset
  or or_11 (IR3_t, IR3, IRC);
  or or_12 (or_12_out, or_16_out, JALR, JAL);
  // RiscV_Probe riscv_probe_1: pin names not known; wires that end beside it: IR
  ROM #(.addrWidth(10), .dataWidth(32), .Select("high")) rom_1 (.addr(PC[11:2]), .data(IR));
  Counter #(.width(32), .max('hffffffff), .ongoal("wrap"), .trigger("rising"), .behavior("old")) counter_2 (
    .Q(counter_2_q), .clk(CLK));  // open: load, D, count, carry, clr, preset
  // Probe on EPC
  Multiplexer #(.select(2), .width(32), .disabled("Z"), .enable("false")) multiplexer_4 (
    .in1(EPC1_q), .in2(EPC2_q), .in3(EPC3_q), .out(EPC), .sel(NUM_now));  // open: in0
  // Probe on IR_NUM
  Priority_Encoder #(.select(2), .disabled("Z")) priority_encoder_1 (
    .in0(1'b1), .in1(IR1_q), .in2(IR2_q), .in3(IR3_q), .out(IR_NUM));  // open: gs, en_out, en_in
  or or_13 (or_13_out, Interrupt, Csrci);
  not not_3 (not_3_out, or_13_out);
  Comparator #(.width(32), .mode("unsigned")) comparator_6 (
    .a(counter_2_q), .b(32'h2), .lt(comparator_6_lt));  // open: gt, eq
  \单周期硬布线控制器  \u_单周期硬布线控制器_1  (
    .Funct({IR[30], IR[25], IR[14:12]}), .OP(IR[6:2]), .ALU_OP(\单周期硬布线控制器_1_alu_op ),
    .MemToReg(\单周期硬布线控制器_1_memtoreg ), .MemWrite(MemWrite), .ALU_SRC(\单周期硬布线控制器_1_alu_src ),
    .RegWrite(RegWrite), .ecall(ecall), .S_type(\单周期硬布线控制器_1_s_type ), .Jalr(JALR), .Beq(\单周期硬布线控制器_1_beq ),
    .JAL(JAL), .Bne(\单周期硬布线控制器_1_bne ), .in_3(IR[21]), .uret(URET), .LBU(LBU), .BLT(\单周期硬布线控制器_1_blt ),
    .Csrsi(Csrsi), .Csrci(Csrci));
  Multiplexer #(.select(1), .width(5), .disabled("Z"), .enable("false")) multiplexer_5 (
    .in0(IR[19:15]), .in1(5'b10001), .out(multiplexer_5_out), .sel(ecall));
  Multiplexer #(.select(1), .width(5), .disabled("Z"), .enable("false")) multiplexer_6 (
    .in0(IR[24:20]), .in1(5'b01010), .out(multiplexer_6_out), .sel(ecall));
  Multiplexer #(.select(2), .width(32), .disabled("Z"), .enable("false")) multiplexer_7 (
    .in1(32'h30ac), .in2(32'h3158), .in3(32'h3204), .out(iaddr), .sel(IR_NUM));  // open: in0
  or or_14 (or_14_out, IR1_q, IR2_q, IR3_q);
  Multiplexer #(.select(1), .width(1), .disabled("Z"), .enable("false")) multiplexer_8 (
    .in0(not_3_out), .in1(1'b1), .out(multiplexer_8_out), .sel(URET));
  or or_15 (or_15_out, comparator_6_lt, Interrupt, URET, Csrsi);
  Multiplexer #(.select(1), .width(12), .disabled("Z"), .enable("false")) multiplexer_9 (
    .in0(IR[31:20]), .in1({IR[31:25], IR[11:7]}), .out(multiplexer_9_out), .sel(\单周期硬布线控制器_1_s_type ));
  Shifter #(.width(12), .shift("ll")) shifter_1 (
    .in({IR[31], IR[7], IR[30:25], IR[11:8]}), .\dist (4'b0001), .out(shifter_1_out));
  Shifter #(.width(20), .shift("ll")) shifter_2 (
    .in({IR[31], IR[19:12], IR[20], IR[30:21]}), .\dist (5'b00001), .out(shifter_2_out));
  Multiplexer #(.select(1), .width(32), .disabled("Z"), .enable("false")) multiplexer_10 (
    .in0(multiplexer_19_out), .in1(adder_1_out), .out(RDin), .sel(or_17_out));
  Register #(.width(1), .trigger("rising"), .Select("low")) u_IE (
    .D(multiplexer_8_out), .en(or_15_out), .Q(IE), .clk(CLK));  // open: clr
  or or_16 (or_16_out, and_7_out, and_8_out, and_10_out);
  and and_7 (and_7_out, \单周期硬布线控制器_1_beq , alu_2_equal);
  and and_8 (and_8_out, \单周期硬布线控制器_1_blt , alu_2_out_6);
  assign bit_extender_1_out = {{20{multiplexer_9_out[11]}}, multiplexer_9_out};  // Bit_Extender bit_extender_1
  assign bit_extender_2_out = {{20{shifter_1_out[11]}}, shifter_1_out};  // Bit_Extender bit_extender_2
  Multiplexer #(.select(1), .width(32), .disabled("Z"), .enable("false")) multiplexer_11 (
    .in0(bit_extender_2_out), .in1(bit_extender_3_out), .out(multiplexer_11_out), .sel(JAL));
  assign bit_extender_3_out = {{12{shifter_2_out[19]}}, shifter_2_out};  // Bit_Extender bit_extender_3
  or or_17 (or_17_out, JAL, JALR);
  and and_9 (Interrupt, or_14_out, IE, comparator_8_lt);
  and and_10 (and_10_out, \单周期硬布线控制器_1_bne , not_4_out);
  not not_4 (not_4_out, alu_2_equal);
  Regifile regifile_1 (
    .Din(RDin), .Clk(CLK), .R1(regifile_1_r1), .R2(MDin), .WE(RegWrite), .W_num(IR[11:7]),
    .R1_num(multiplexer_5_out), .R2_num(multiplexer_6_out));
  Multiplexer #(.select(1), .width(32), .disabled("Z"), .enable("false")) multiplexer_12 (
    .in0(multiplexer_11_out), .in1(bit_extender_1_out), .out(multiplexer_12_out), .sel(JALR));
  Multiplexer #(.select(1), .width(32), .disabled("Z"), .enable("false")) multiplexer_13 (
    .in0(MDin), .in1(bit_extender_1_out), .out(multiplexer_13_out), .sel(\单周期硬布线控制器_1_alu_src ));
  Multiplexer #(.select(1), .width(32), .disabled("Z"), .enable("false")) multiplexer_14 (
    .in0(PC), .in1(regifile_1_r1), .out(multiplexer_14_out), .sel(JALR));
  D_Flip_Flop #(.trigger("high"), .Pre_Clr_Positions("LEGACY"), .NegatePresetClear("false"), .enable("true"), .NewFFLayout("false")) d_ff_4 (.Q(d_ff_4_q));  // open: clk, D, Qn, preset, en, reset
  // Probe on 13'h180
  Adder #(.width(2)) adder_2 (.a(p), .b(multiplexer_15_out), .out(adder_2_out));  // open: cin, cout
  Multiplexer #(.select(1), .width(2), .disabled("Z"), .enable("false")) multiplexer_15 (
    .in0(2'b11), .in1(2'b01), .out(multiplexer_15_out), .sel(Interrupt));
  Decoder #(.select(2), .tristate("false"), .disabled("Z"), .enable("false")) decoder_2 (
    .out1(decoder_2_out1), .out2(decoder_2_out2), .out3(decoder_2_out3), .sel(queue_num));  // open: out0
  Comparator #(.width(13), .mode("twosComplement")) comparator_7 (
    .a(CNT_num), .b(13'h180), .eq(comparator_7_eq), .lt(comparator_7_lt));  // open: gt
  Clock #(.highDuration(1), .lowDuration(1)) clock_1 (.out(clock_1_out));
  Multiplexer #(.select(1), .width(32), .disabled("Z"), .enable("false")) multiplexer_16 (
    .in0(multiplexer_13_out), .in1(32'h22), .out(multiplexer_16_out), .sel(ecall));
  ALU alu_1 (
    .X(multiplexer_12_out), .Y(multiplexer_14_out), .AluOP(4'b0101), .Result(alu_1_result));  // open: Equal, Result_2, out_4, out_6
  Register #(.width(2), .trigger("rising"), .Select("low")) stack (
    .D(adder_2_out), .en(or_18_out), .Q(p), .clk(CLK));  // open: clr
  or or_18 (or_18_out, Interrupt, URET);
  and and_11 (and_11_out, Interrupt, decoder_2_out1);
  and and_12 (and_12_out, Interrupt, decoder_2_out2);
  and and_13 (and_13_out, Interrupt, decoder_2_out3);
  Counter #(.width(13), .max('h1fff), .ongoal("stay"), .trigger("rising"), .behavior("old")) counter_3 (
    .count(comparator_7_lt), .Q(CNT_num), .clk(clock_1_out));  // open: load, D, carry, clr, preset
  ALU alu_2 (
    .X(regifile_1_r1), .Y(multiplexer_16_out), .AluOP(\单周期硬布线控制器_1_alu_op ), .Equal(alu_2_equal),
    .Result(alu_2_result), .out_6(alu_2_out_6));  // open: Result_2, out_4
  Adder #(.width(2)) adder_3 (.a(p), .b(2'b01), .out(queue_num));  // open: cin, cout
  Register #(.width(2), .trigger("rising"), .Select("low")) IR_reg1 (
    .D(IR_NUM), .en(and_11_out), .Q(IR_reg1_q), .clk(CLK));  // open: clr
  nand nand_1 (nand_1_out, d_ff_4_q, comparator_7_eq);
  and and_14 (and_14_out, ecall, not_6_out);
  not not_5 (not_5_out, and_14_out);
  not not_6 (not_6_out, alu_2_equal);
  and and_15 (and_15_out, ecall, alu_2_equal);
  Register #(.width(2), .trigger("rising"), .Select("low")) IR_reg2 (
    .D(IR_NUM), .en(and_12_out), .Q(IR_reg2_q), .clk(CLK));  // open: clr
  assign CLK = nand_1_out ? clock_1_out : 1'bz;  // Controlled_Buffer controlled_buffer_1
  Pull_Resistor #(.pull(1)) pull_resistor_4 (.node(CLK));
  not not_7 (halt, or_19_out);
  or or_19 (or_19_out, Go, not_5_out);
  Register #(.width(32), .trigger("rising"), .Select("low")) register_1 (
    .D(MDin), .en(and_15_out), .Q(LedData), .clk(CLK));  // open: clr
  not not_8 (not_8_out, halt);
  Register #(.width(2), .trigger("rising"), .Select("low")) IR_reg3 (
    .D(IR_NUM), .en(and_13_out), .Q(IR_reg3_q), .clk(CLK));  // open: clr
  RAM #(.addrWidth(10), .dataWidth(32), .bus("separate"), .Select("high")) ram_1 (
    .addr(alu_2_result[11:2]), .din(MDin), .data(ram_1_data), .str(MemWrite), .sel(not_8_out), .clk(CLK));  // open: ld, clr
  Multiplexer #(.select(2), .width(2), .disabled("Z"), .enable("false")) multiplexer_17 (
    .in0(2'b00), .in1(IR_reg1_q), .in2(IR_reg2_q), .in3(IR_reg3_q), .out(NUM_now), .sel(p));
  // Probe on NUM_now
  Multiplexer #(.select(1), .width(32), .disabled("Z"), .enable("false")) multiplexer_18 (
    .in0(alu_2_result), .in1(ram_1_data), .out(multiplexer_18_out), .sel(\单周期硬布线控制器_1_memtoreg ));
  assign bit_extender_4_out = {{24{1'b0}}, ram_1_data[31:24]};  // Bit_Extender bit_extender_4
  Comparator #(.width(2), .mode("unsigned")) comparator_8 (
    .a(NUM_now), .b(IR_NUM), .lt(comparator_8_lt));  // open: gt, eq
  Multiplexer #(.select(1), .width(32), .disabled("Z"), .enable("false")) multiplexer_19 (
    .in0(multiplexer_18_out), .in1(bit_extender_4_out), .out(multiplexer_19_out), .sel(LBU));

  // Notes on the sheet:
  //   中断源
  //   中断等待指示
  //   总复位信号应将除ROM以外所有存储组件全部清零
  //   多级中断测试信号模拟器
  //   数码管输出
  //   数码管输出应该用寄存器锁存，否则显示数据只能一闪而过
  //   Reset 
  //   Reset 
  //   Reset 
  //   指令存储器
  //   PC_branch
  //   指令探针
  //   contents of rom_1 (hex, n*v repeats v):
  //   7d000113 100413 1f41993 41f9d993 433 c00913 800b13 140413 f47413 800293 100313 499993 89e9b3 1300533
  //   2200893 73 406282b3 fe0294e3 140413 f00f93 1f47433 1c41413 800293 100313 49d993 89e9b3 1300533
  //   2200893 73 406282b3 fe0294e3 1c45413 406b0b33 b0463 f95ff06f 2b3 fff2c293 1029293 fff2e293 500533
  //   2200893 73 f5dff06f 1112023 410113 a12023 410113 812023 410113 1312023 410113 1412023 410113 1512023
  //   410113 1612023 410113 40e073 100b13 300a13 100a93 1600433 441413 14469b3 1300533 2200893 73 fe0416e3
  //   415a0a33 fe0a10e3 40f073 ffc10113 12b03 ffc10113 12a83 ffc10113 12a03 ffc10113 12983 ffc10113 12403
  //   ffc10113 12503 ffc10113 12883 200073 1112023 410113 a12023 410113 812023 410113 1312023 410113
  //   1412023 410113 1512023 410113 1612023 410113 40e073 200b13 300a13 100a93 1600433 441413 14469b3
  //   1300533 2200893 73 fe0416e3 415a0a33 fe0a10e3 40f073 ffc10113 12b03 ffc10113 12a83 ffc10113 12a03
  //   ffc10113 12983 ffc10113 12403 ffc10113 12503 ffc10113 12883 200073 1112023 410113 a12023 410113
  //   812023 410113 1312023 410113 1412023 410113 1512023 410113 1612023 410113 40e073 300b13 300a13
  //   100a93 1600433 441413 14469b3 1300533 2200893 73 fe0416e3 415a0a33 fe0a10e3 40f073 ffc10113 12b03
  //   ffc10113 12a83 ffc10113 12a03 ffc10113 12983 ffc10113 12403 ffc10113 12503 ffc10113 12883 200073
  //   指令字
  //   I
  //   S
  //   B
  //   J
  //   JAL,JALR需把PC+4存入寄存器
  //   Beq
  //   Bne
  //   ecall时,判断a17==34?
  //   ALU1的imm默认为I型，置1为S型
  //    PC+4
  //   为方便自动评测，需要输出PC，IR，寄存器堆写如数据RDin
  //   B_type
  //   MemToReg
  //   MemWrite
  //   AluOP
  //   AluSrcB
  //   RegWrite
  //   RAM写使能MemWrite、RAM写入数据MDin等信号
  //   equal
  //   B=PC/寄存器
  //   控制位
  //   暂停节拍，不能为0
  //   戳工具置1进入计数暂停模式，ctrl+k时钟自动运行到对应节拍暂停
  //   ctrl+k关闭时钟连续运行，将控制位置零，进入单步调试模式调试
  //   多级中断新的NUM_now生成逻辑
  //   可计数暂停的时钟源
  //   数据存储器
endmodule

module \封装正确性测试  (
);

  wire IR1, IR2, IR3, MemW, RegW;
  wire [31:0] EX_PC, ID_PC, IF_PC, IR, LED, MDin, MDinr, MEM_PC, PC, RDin, RDinr, WB_PC;

  \单周期RISC_V  \u_单周期risc_v_1  (
    .IR1(IR1), .IR2(IR2), .IR3(IR3), .RegWrite(RegW), .MemWrite(MemW), .PC(PC), .IR(IR), .RDin(RDin),
    .MDin(MDin), .LedData(LED));
  \气泡流水线  \u_气泡流水线_1  (
    .RegWrite(RegW), .MemWrite(MemW), .IF_PC(IF_PC), .ID_PC(ID_PC), .EX_PC(EX_PC), .M_PC(MEM_PC),
    .WB_PC(WB_PC), .RDin(RDinr), .MDin(MDinr), .LedData(LED));
  \单周期_单级中断  \u_单周期_单级中断_1  (
    .IR1(IR1), .IR2(IR2), .IR3(IR3), .RegWrite(RegW), .MemWrite(MemW), .PC(PC), .IR(IR), .RDin(RDin),
    .MDin(MDin), .LedData(LED));
  \理想流水线  \u_理想流水线_1  (
    .RegWrite(RegW), .MemWrite(MemW), .IF_PC(IF_PC), .ID_PC(ID_PC), .EX_PC(EX_PC), .M_PC(MEM_PC),
    .WB_PC(WB_PC), .RDin(RDinr), .MDin(MDinr), .LedData(LED));
  \重定向流水线  \u_重定向流水线_1  (
    .RegWrite(RegW), .MemWrite(MemW), .IF_PC(IF_PC), .ID_PC(ID_PC), .EX_PC(EX_PC), .M_PC(MEM_PC),
    .WB_PC(WB_PC), .RDin(RDinr), .MDin(MDinr), .LedData(LED));
  \单周期_多级中断  \u_单周期_多级中断_1  (
    .IR1(IR1), .IR2(IR2), .IR3(IR3), .RegWrite(RegW), .MemWrite(MemW), .PC(PC), .IR(IR), .RDin(RDin),
    .MDin(MDin), .LedData(LED));

  // Notes on the sheet:
  //   单周期封装测试
  //   气泡流水封装测试
  //   单周期+单级中断封装测试
  //   请检查上面封装有无位宽不匹配，引脚标签是否和连接的标签相对应，否则无法在educoder平台上正确测试
  //   理想流水封装测试
  //   重定向流水封装测试
  //   单周期+多级中断封装测试
endmodule

module \Conflict_气泡  (
  input  [4:0] R1,
  input  [4:0] R2,
  input  [31:0] IR,
  input  [4:0] W_num,
  output Data_Conflict
);

  wire and_1_out, and_2_out, comparator_1_eq, comparator_2_eq, comparator_3_eq, not_1_out,
       \判断rs1_rs2是否使用_1_rs1_used , \判断rs1_rs2是否使用_1_rs2_used ;
  wire [4:0] multiplexer_1_out, multiplexer_2_out;

  \判断rs1_rs2是否使用  \u_判断rs1_rs2是否使用_1  (
    .OP2(IR[2]), .OP3(IR[3]), .OP4(IR[4]), .OP5(IR[5]), .OP6(IR[6]), .F12(IR[12]), .F13(IR[13]),
    .F14(IR[14]), .F25(IR[25]), .F30(IR[30]), .rs1_used(\判断rs1_rs2是否使用_1_rs1_used ),
    .rs2_used(\判断rs1_rs2是否使用_1_rs2_used ));
  Multiplexer #(.select(1), .width(5), .disabled("Z"), .enable("false")) multiplexer_1 (
    .in0({5{1'b0}}), .in1(R1), .out(multiplexer_1_out), .sel(\判断rs1_rs2是否使用_1_rs1_used ));
  Multiplexer #(.select(1), .width(5), .disabled("Z"), .enable("false")) multiplexer_2 (
    .in0({5{1'b0}}), .in1(R2), .out(multiplexer_2_out), .sel(\判断rs1_rs2是否使用_1_rs2_used ));
  Comparator #(.width(5), .mode("twosComplement")) comparator_1 (
    .a(multiplexer_1_out), .b(W_num), .eq(comparator_1_eq));  // open: gt, lt
  Comparator #(.width(5), .mode("twosComplement")) comparator_2 (
    .a({5{1'b0}}), .b(W_num), .eq(comparator_2_eq));  // open: gt, lt
  Comparator #(.width(5), .mode("twosComplement")) comparator_3 (
    .a(multiplexer_2_out), .b(W_num), .eq(comparator_3_eq));  // open: gt, lt
  not not_1 (not_1_out, comparator_2_eq);
  and and_1 (and_1_out, comparator_3_eq, not_1_out);
  or or_1 (Data_Conflict, and_1_out, and_2_out);
  and and_2 (and_2_out, comparator_1_eq, not_1_out);

  // Notes on the sheet:
  //   OP
  //   FUNC
  //   先判断指令是否使用R1/R2
  //   相等且不为0
endmodule

module \判断rs1_rs2是否使用  (
  input  OP2,
  input  OP3,
  input  OP4,
  input  OP5,
  input  OP6,
  input  F12,
  input  F13,
  input  F14,
  input  F25,
  input  F30,
  output rs1_used,
  output rs2_used
);

  wire and_1_out, and_2_out, and_3_out, and_4_out, and_5_out, and_6_out, and_7_out, and_8_out, and_9_out,
       and_10_out, and_11_out, and_12_out, and_13_out, and_14_out, and_15_out, and_16_out, and_17_out,
       and_18_out, and_19_out, and_20_out, and_21_out, and_22_out, and_23_out, and_24_out, and_25_out,
       and_26_out, not_1_out, not_2_out, not_3_out, not_4_out, not_5_out, not_6_out, not_7_out, not_8_out,
       not_9_out, not_10_out, not_11_out, not_12_out, not_13_out, not_14_out, not_15_out, not_16_out,
       not_17_out, not_18_out, not_19_out, not_20_out, not_21_out, not_22_out, not_23_out, not_24_out,
       not_25_out, not_26_out, not_27_out, not_28_out, not_29_out, not_30_out, not_31_out, not_32_out,
       not_33_out, not_34_out, not_35_out, not_36_out, not_37_out, not_38_out, not_39_out, not_40_out,
       not_41_out, not_42_out, not_43_out, not_44_out, not_45_out, not_46_out, not_47_out, not_48_out,
       not_49_out, not_50_out, not_51_out, not_52_out, not_53_out, not_54_out, not_55_out, not_56_out,
       not_57_out, not_58_out, not_59_out, not_60_out, not_61_out, not_62_out, not_63_out, not_64_out,
       not_65_out, not_66_out, not_67_out, not_68_out, not_69_out, not_70_out, not_71_out, not_72_out,
       not_73_out, not_74_out, not_75_out, not_76_out, not_77_out, not_78_out, not_79_out, not_80_out,
       not_81_out, not_82_out, not_83_out, not_84_out, not_85_out, not_86_out, not_87_out, not_88_out,
       not_89_out, not_90_out, not_91_out, not_92_out, not_93_out, not_94_out, not_95_out, not_96_out,
       not_97_out, not_98_out, not_99_out, not_100_out, not_101_out, not_102_out, not_103_out, not_104_out,
       not_105_out, not_106_out, not_107_out, not_108_out, not_109_out, not_110_out, not_111_out,
       not_112_out, not_113_out, not_114_out, not_115_out, not_116_out, not_117_out, not_118_out,
       not_119_out, not_120_out, not_121_out, not_122_out, not_123_out, not_124_out, not_125_out,
       not_126_out, not_127_out, not_128_out, not_129_out, not_130_out, not_131_out, not_132_out,
       not_133_out, not_134_out, not_135_out, not_136_out, not_137_out, not_138_out, not_139_out,
       not_140_out, not_141_out, not_142_out, not_143_out, not_144_out;

  not not_1 (not_1_out, OP2);
  not not_2 (not_2_out, OP3);
  not not_3 (not_3_out, OP5);
  not not_4 (not_4_out, OP6);
  not not_5 (not_5_out, F12);
  not not_6 (not_6_out, F13);
  not not_7 (not_7_out, OP2);
  not not_8 (not_8_out, OP3);
  not not_9 (not_9_out, OP4);
  not not_10 (not_10_out, OP6);
  not not_11 (not_11_out, F12);
  not not_12 (not_12_out, F14);
  not not_13 (not_13_out, OP2);
  not not_14 (not_14_out, OP3);
  not not_15 (not_15_out, OP4);
  not not_16 (not_16_out, F12);
  not not_17 (not_17_out, F13);
  not not_18 (not_18_out, OP2);
  not not_19 (not_19_out, OP3);
  not not_20 (not_20_out, OP4);
  not not_21 (not_21_out, F13);
  not not_22 (not_22_out, F14);
  not not_23 (not_23_out, OP3);
  not not_24 (not_24_out, OP4);
  not not_25 (not_25_out, F12);
  not not_26 (not_26_out, F13);
  not not_27 (not_27_out, F14);
  not not_28 (not_28_out, OP2);
  not not_29 (not_29_out, OP3);
  not not_30 (not_30_out, OP5);
  not not_31 (not_31_out, OP6);
  not not_32 (not_32_out, F12);
  not not_33 (not_33_out, OP2);
  not not_34 (not_34_out, OP3);
  not not_35 (not_35_out, OP5);
  not not_36 (not_36_out, OP6);
  not not_37 (not_37_out, F13);
  not not_38 (not_38_out, F14);
  not not_39 (not_39_out, OP2);
  not not_40 (not_40_out, OP3);
  not not_41 (not_41_out, OP5);
  not not_42 (not_42_out, OP6);
  not not_43 (not_43_out, F13);
  not not_44 (not_44_out, F25);
  not not_45 (not_45_out, OP2);
  not not_46 (not_46_out, OP3);
  not not_47 (not_47_out, OP6);
  not not_48 (not_48_out, F12);
  not not_49 (not_49_out, F13);
  not not_50 (not_50_out, F14);
  not not_51 (not_51_out, F25);
  not not_52 (not_52_out, OP2);
  not not_53 (not_53_out, OP3);
  not not_54 (not_54_out, OP6);
  not not_55 (not_55_out, F25);
  not not_56 (not_56_out, F30);
  not not_57 (not_57_out, OP2);
  not not_58 (not_58_out, OP3);
  not not_59 (not_59_out, OP5);
  not not_60 (not_60_out, OP6);
  not not_61 (not_61_out, OP2);
  not not_62 (not_62_out, OP3);
  not not_63 (not_63_out, F12);
  not not_64 (not_64_out, F13);
  not not_65 (not_65_out, F14);
  not not_66 (not_66_out, F25);
  not not_67 (not_67_out, F30);
  not not_68 (not_68_out, OP2);
  not not_69 (not_69_out, OP3);
  not not_70 (not_70_out, OP6);
  not not_71 (not_71_out, F25);
  not not_72 (not_72_out, F30);
  not not_73 (not_73_out, OP2);
  not not_74 (not_74_out, OP3);
  not not_75 (not_75_out, OP5);
  not not_76 (not_76_out, OP6);
  not not_77 (not_77_out, F12);
  not not_78 (not_78_out, F13);
  not not_79 (not_79_out, OP2);
  not not_80 (not_80_out, OP3);
  not not_81 (not_81_out, OP4);
  not not_82 (not_82_out, OP6);
  not not_83 (not_83_out, F12);
  not not_84 (not_84_out, F14);
  not not_85 (not_85_out, OP2);
  not not_86 (not_86_out, OP3);
  not not_87 (not_87_out, OP4);
  not not_88 (not_88_out, F12);
  not not_89 (not_89_out, F13);
  not not_90 (not_90_out, OP2);
  not not_91 (not_91_out, OP3);
  not not_92 (not_92_out, OP4);
  not not_93 (not_93_out, F13);
  not not_94 (not_94_out, F14);
  not not_95 (not_95_out, OP3);
  not not_96 (not_96_out, OP4);
  not not_97 (not_97_out, F12);
  not not_98 (not_98_out, F13);
  not not_99 (not_99_out, F14);
  not not_100 (not_100_out, OP2);
  not not_101 (not_101_out, OP3);
  not not_102 (not_102_out, OP5);
  not not_103 (not_103_out, OP6);
  not not_104 (not_104_out, F12);
  not not_105 (not_105_out, OP2);
  not not_106 (not_106_out, OP3);
  not not_107 (not_107_out, OP5);
  not not_108 (not_108_out, OP6);
  not not_109 (not_109_out, F13);
  not not_110 (not_110_out, F14);
  not not_111 (not_111_out, OP2);
  not not_112 (not_112_out, OP3);
  not not_113 (not_113_out, OP5);
  not not_114 (not_114_out, OP6);
  not not_115 (not_115_out, F13);
  not not_116 (not_116_out, F25);
  not not_117 (not_117_out, OP2);
  not not_118 (not_118_out, OP3);
  not not_119 (not_119_out, OP6);
  not not_120 (not_120_out, F12);
  not not_121 (not_121_out, F13);
  not not_122 (not_122_out, F14);
  not not_123 (not_123_out, F25);
  not not_124 (not_124_out, OP2);
  not not_125 (not_125_out, OP3);
  not not_126 (not_126_out, OP6);
  not not_127 (not_127_out, F25);
  not not_128 (not_128_out, F30);
  not not_129 (not_129_out, OP2);
  not not_130 (not_130_out, OP3);
  not not_131 (not_131_out, OP5);
  not not_132 (not_132_out, OP6);
  not not_133 (not_133_out, OP2);
  not not_134 (not_134_out, OP3);
  not not_135 (not_135_out, F12);
  not not_136 (not_136_out, F13);
  not not_137 (not_137_out, F14);
  not not_138 (not_138_out, F25);
  not not_139 (not_139_out, F30);
  not not_140 (not_140_out, OP2);
  not not_141 (not_141_out, OP3);
  not not_142 (not_142_out, OP6);
  not not_143 (not_143_out, F25);
  not not_144 (not_144_out, F30);
  and and_1 (and_1_out, not_1_out, not_2_out, not_3_out, not_4_out, not_5_out, not_6_out, F14);
  and and_2 (and_2_out, not_7_out, not_8_out, not_9_out, not_10_out, not_11_out, F13, not_12_out);
  and and_3 (and_3_out, not_13_out, not_14_out, not_15_out, OP5, OP6, not_16_out, not_17_out);
  and and_4 (and_4_out, not_18_out, not_19_out, not_20_out, OP5, OP6, not_21_out, not_22_out);
  and and_5 (and_5_out, not_23_out, not_24_out, OP5, OP6, not_25_out, not_26_out, not_27_out);
  and and_6 (and_6_out, not_28_out, not_29_out, OP4, not_30_out, not_31_out, not_32_out);
  and and_7 (and_7_out, not_33_out, not_34_out, OP4, not_35_out, not_36_out, not_37_out, not_38_out);
  and and_8 (and_8_out, not_39_out, not_40_out, OP4, not_41_out, not_42_out, not_43_out, not_44_out);
  and and_9 (and_9_out, not_45_out, not_46_out, OP4, not_47_out, not_48_out, not_49_out, not_50_out, not_51_out);
  and and_10 (and_10_out, not_52_out, not_53_out, OP4, not_54_out, F14, not_55_out, not_56_out);
  and and_11 (and_11_out, not_57_out, not_58_out, OP4, not_59_out, not_60_out, F13, F14);
  and and_12 (and_12_out, not_61_out, not_62_out, OP4, OP5, not_63_out, not_64_out, not_65_out, not_66_out, not_67_out);
  and and_13 (and_13_out, not_68_out, not_69_out, OP4, OP5, not_70_out, F13, not_71_out, not_72_out);
  and and_14 (and_14_out, not_73_out, not_74_out, not_75_out, not_76_out, not_77_out, not_78_out, F14);
  and and_15 (and_15_out, not_79_out, not_80_out, not_81_out, not_82_out, not_83_out, F13, not_84_out);
  and and_16 (and_16_out, not_85_out, not_86_out, not_87_out, OP5, OP6, not_88_out, not_89_out);
  and and_17 (and_17_out, not_90_out, not_91_out, not_92_out, OP5, OP6, not_93_out, not_94_out);
  and and_18 (and_18_out, not_95_out, not_96_out, OP5, OP6, not_97_out, not_98_out, not_99_out);
  and and_19 (and_19_out, not_100_out, not_101_out, OP4, not_102_out, not_103_out, not_104_out);
  and and_20 (and_20_out, not_105_out, not_106_out, OP4, not_107_out, not_108_out, not_109_out, not_110_out);
  and and_21 (and_21_out, not_111_out, not_112_out, OP4, not_113_out, not_114_out, not_115_out, not_116_out);
  and and_22 (and_22_out, not_117_out, not_118_out, OP4, not_119_out, not_120_out, not_121_out, not_122_out, not_123_out);
  and and_23 (and_23_out, not_124_out, not_125_out, OP4, not_126_out, F14, not_127_out, not_128_out);
  and and_24 (and_24_out, not_129_out, not_130_out, OP4, not_131_out, not_132_out, F13, F14);
  and and_25 (and_25_out, not_133_out, not_134_out, OP4, OP5, not_135_out, not_136_out, not_137_out, not_138_out, not_139_out);
  and and_26 (and_26_out, not_140_out, not_141_out, OP4, OP5, not_142_out, F13, not_143_out, not_144_out);
  or or_1 (rs1_used, and_1_out, and_2_out, and_3_out, and_4_out, and_5_out, and_6_out, and_7_out, and_8_out, and_9_out, and_10_out, and_11_out, and_12_out, and_13_out);
  or or_2 (rs2_used, and_14_out, and_15_out, and_16_out, and_17_out, and_18_out, and_19_out, and_20_out, and_21_out, and_22_out, and_23_out, and_24_out, and_25_out, and_26_out);
endmodule

module \Conflict_重定向  (
  input  [4:0] R1,
  input  [4:0] R2,
  input  [31:0] IR,
  input  [4:0] W_num,
  output R1_error,
  output R2_error
);

  wire comparator_1_eq, comparator_2_eq, comparator_3_eq, not_1_out, \判断rs1_rs2是否使用_1_rs1_used ,
       \判断rs1_rs2是否使用_1_rs2_used ;
  wire [4:0] multiplexer_1_out, multiplexer_2_out;

  \判断rs1_rs2是否使用  \u_判断rs1_rs2是否使用_1  (
    .OP2(IR[2]), .OP3(IR[3]), .OP4(IR[4]), .OP5(IR[5]), .OP6(IR[6]), .F12(IR[12]), .F13(IR[13]),
    .F14(IR[14]), .F25(IR[25]), .F30(IR[30]), .rs1_used(\判断rs1_rs2是否使用_1_rs1_used ),
    .rs2_used(\判断rs1_rs2是否使用_1_rs2_used ));
  Multiplexer #(.select(1), .width(5), .disabled("Z"), .enable("false")) multiplexer_1 (
    .in0({5{1'b0}}), .in1(R1), .out(multiplexer_1_out), .sel(\判断rs1_rs2是否使用_1_rs1_used ));
  Comparator #(.width(5), .mode("twosComplement")) comparator_1 (
    .a(multiplexer_1_out), .b(W_num), .eq(comparator_1_eq));  // open: gt, lt
  not not_1 (not_1_out, comparator_2_eq);
  Comparator #(.width(5), .mode("twosComplement")) comparator_2 (
    .a({5{1'b0}}), .b(W_num), .eq(comparator_2_eq));  // open: gt, lt
  Multiplexer #(.select(1), .width(5), .disabled("Z"), .enable("false")) multiplexer_2 (
    .in0({5{1'b0}}), .in1(R2), .out(multiplexer_2_out), .sel(\判断rs1_rs2是否使用_1_rs2_used ));
  Comparator #(.width(5), .mode("twosComplement")) comparator_3 (
    .a(multiplexer_2_out), .b(W_num), .eq(comparator_3_eq));  // open: gt, lt
  and and_1 (R1_error, comparator_1_eq, not_1_out);
  and and_2 (R2_error, comparator_3_eq, not_1_out);

  // Notes on the sheet:
  //   OP
  //   FUNC
  //   先判断指令是否使用R1/R2
  //   相等且不为0
endmodule

module Encoder (
  input  in1,
  input  in2,
  input  in3,
  input  in4,
  output [1:0] out
);

  wire and_1_out, and_2_out, and_3_out, and_4_out, not_1_out, not_2_out, not_3_out, not_4_out, not_5_out,
       not_6_out, not_7_out, not_8_out, not_9_out, not_10_out, not_11_out, not_12_out;

  not not_1 (not_1_out, in1);
  not not_2 (not_2_out, in2);
  not not_3 (not_3_out, in3);
  not not_4 (not_4_out, in1);
  not not_5 (not_5_out, in2);
  not not_6 (not_6_out, in4);
  not not_7 (not_7_out, in1);
  not not_8 (not_8_out, in2);
  not not_9 (not_9_out, in3);
  not not_10 (not_10_out, in1);
  not not_11 (not_11_out, in3);
  not not_12 (not_12_out, in4);
  and and_1 (and_1_out, not_1_out, not_2_out, not_3_out, in4);
  or or_1 (out[1], and_1_out, and_2_out);
  and and_2 (and_2_out, not_4_out, not_5_out, in3, not_6_out);
  and and_3 (and_3_out, not_7_out, not_8_out, not_9_out, in4);
  or or_2 (out[0], and_3_out, and_4_out);
  and and_4 (and_4_out, not_10_out, in2, not_11_out, not_12_out);
endmodule

module \分支预测  (
  output RegWrite,
  output MemWrite,
  output [31:0] IF_PC,
  output [31:0] ID_PC,
  output [31:0] EX_PC,
  output [31:0] M_PC,
  output [31:0] WB_PC,
  output [31:0] RDin,
  output [31:0] MDin,
  output [31:0] LedData
);

  wire alu_2_equal, alu_2_out_6, and_1_out, and_2_out, and_3_out, and_4_out, and_5_out, and_6_out,
       and_11_out, and_12_out, and_16_out, and_17_out, and_18_out, and_19_out, and_20_out, B_type,
       btb_1_predictjump, CLK, clock_1_out, comparator_1_eq, comparator_2_eq, comparator_2_lt,
       comparator_3_eq, comparator_4_eq, comparator_5_eq, comparator_6_eq, comparator_7_eq,
       \conflict_重定向_1_r1_error , \conflict_重定向_1_r2_error , \conflict_重定向_2_r1_error ,
       \conflict_重定向_2_r2_error , d_ff_1_q, DataIMM, EX_Branch, ex_mem_1_jal_jalr_2, ex_mem_1_lbu_2,
       ex_mem_1_memtoreg_2, EX_PredictJump, EX_RegWrite, Fail, Go, halt, id_ex_1_alusrcb_2, id_ex_1_beq_2,
       id_ex_1_blt_2, id_ex_1_bne_2, id_ex_1_ecall_2, id_ex_1_jal_jalr_2, id_ex_1_lbu_2, id_ex_1_memtoreg_2,
       id_ex_1_memtoreg_3, if_id_1_branch_pre_2, IR1, IR2, IR3, JAL, JALR, loaduse, MEM_RegWrite,
       mem_wb_1_jal_jalr_2, nand_1_out, not_1_out, not_2_out, not_3_out, not_5_out, not_6_out, not_7_out,
       not_8_out, not_9_out, not_10_out, or_1_out, or_2_out, or_3_out, or_4_out, or_5_out, or_6_out,
       or_7_out, or_8_out, or_9_out, R1_Ex, R1_Mem, R2_Ex, R2_Mem, RST, W1, W2, W3, WB_R1, WB_R2, \分支指令 ,
       \单周期硬布线控制器_1_alu_src , \单周期硬布线控制器_1_beq , \单周期硬布线控制器_1_blt , \单周期硬布线控制器_1_bne , \单周期硬布线控制器_1_ecall ,
       \单周期硬布线控制器_1_lbu , \单周期硬布线控制器_1_memtoreg , \单周期硬布线控制器_1_memwrite , \单周期硬布线控制器_1_regwrite ,
       \单周期硬布线控制器_1_s_type ;
  wire [1:0] encoder_1_out, encoder_2_out, f1_q, f2_q;
  wire [3:0] id_ex_1_aluop_2, \单周期硬布线控制器_1_alu_op ;
  wire [4:0] R1_num, R2_num;
  wire [7:0] bitselector_1_out;
  wire [11:0] multiplexer_7_out, shifter_1_out;
  wire [12:0] CNT_num;
  wire [15:0] \LoadUse次数 , \总周期数 , \插入气泡数 , \无条件分支数 , \条件分支成功数 , \预测失败次数 ;
  wire [19:0] shifter_2_out;
  wire [31:0] adder_3_out, alu_1_result, alu_2_result, alu_2_result_2, ALU_Result1, ALU_Result2,
       bit_extender_1_out, bit_extender_2_out, bit_extender_3_out, bit_extender_4_out, btb_1_jumpaddr, EX_IR,
       EX_PC_4, id_ex_1_b, id_ex_1_imm_bj_i_2, id_ex_1_imm_i_s_2, ID_IR, IF_IR, MEM_IR, mem_wb_1_md_2,
       multiplexer_1_out, multiplexer_2_out, multiplexer_3_out, multiplexer_8_out, multiplexer_9_out,
       multiplexer_10_out, multiplexer_11_out, multiplexer_13_out, multiplexer_14_out, PC_4, R1, R2,
       ram_1_data, rd2, regifile_1_r1, regifile_1_r2, rs, WB_IR;

  Button \u_总复位  (.out(RST));
  Button _1 (.out(IR1));
  Button _2 (.out(IR2));
  Button _3 (.out(IR3));
  // Probe on \总周期数 
  // Probe on \总周期数 
  Button \u_继续运行  (.out(Go));
  LED #(.active("true")) led_1 (.in(W1));
  LED #(.active("true")) led_2 (.in(W2));
  LED #(.active("true")) led_3 (.in(W3));
  Multiplexer #(.select(1), .width(32), .disabled("Z"), .enable("false")) multiplexer_1 (
    .in0(multiplexer_3_out), .in1(multiplexer_2_out), .out(multiplexer_1_out), .sel(Fail));
  Multiplexer #(.select(1), .width(32), .disabled("Z"), .enable("false")) multiplexer_2 (
    .in0(EX_PC_4), .in1(alu_1_result), .out(multiplexer_2_out), .sel(EX_Branch));
  Counter #(.width(16), .max('hffff), .ongoal("wrap"), .trigger("rising"), .behavior("old")) counter_1 (
    .count(Fail), .Q(\预测失败次数 ), .clk(and_1_out));  // open: load, D, carry, clr, preset
  and and_1 (and_1_out, CLK, not_1_out);
  not not_1 (not_1_out, halt);
  Hex_Digit_Display hex_digit_display_1 (.value(LedData[31:28]));  // open: dp
  // Probe on IF_PC[19:0]
  // RiscV_Probe riscv_probe_1: pin names not known; wires that end beside it: IF_IR
  not not_2 (not_2_out, or_1_out);
  or or_1 (or_1_out, and_2_out, halt);
  and and_2 (and_2_out, ~EX_Branch, loaduse);  // AND_Gate
  Hex_Digit_Display hex_digit_display_2 (.value(LedData[27:24]));  // open: dp
  Hex_Digit_Display hex_digit_display_3 (.value(LedData[23:20]));  // open: dp
  // Probe on ID_PC[19:0]
  // RiscV_Probe riscv_probe_2: pin names not known; wires that end beside it: ID_IR
  Register #(.width(32), .trigger("rising"), .Select("low")) PC (
    .D(multiplexer_1_out), .en(not_2_out), .Q(IF_PC), .clk(CLK), .clr(RST));
  BTB btb_1 (
    .Clk(CLK), .EX_Branch(\分支指令 ), .PC(IF_PC), .EX_PC(EX_PC), .EX_BranchAddr(alu_1_result),
    .JumpAddr(btb_1_jumpaddr), .PredictJump(btb_1_predictjump), .EX_Branched(EX_Branch));
  Comparator #(.width(1), .mode("twosComplement")) comparator_1 (
    .a(EX_PredictJump), .b(EX_Branch), .eq(comparator_1_eq));  // open: gt, lt
  Counter #(.width(16), .max('hffff), .ongoal("wrap"), .trigger("rising"), .behavior("old")) counter_2 (
    .count(not_3_out), .Q(\总周期数 ), .clk(CLK));  // open: load, D, carry, clr, preset
  not not_3 (not_3_out, halt);
  Hex_Digit_Display hex_digit_display_4 (.value(LedData[15:12]));  // open: dp
  Hex_Digit_Display hex_digit_display_5 (.value(LedData[19:16]));  // open: dp
  Adder #(.width(32)) adder_1 (.a(IF_PC), .b(32'h4), .out(PC_4));  // open: cin, cout
  not not_4 (Fail, comparator_1_eq);
  Adder #(.width(32)) adder_2 (.a(EX_PC), .b(32'h4), .out(EX_PC_4));  // open: cin, cout
  and and_3 (and_3_out, CLK, not_5_out);
  Hex_Digit_Display hex_digit_display_6 (.value(LedData[11:8]));  // open: dp
  Hex_Digit_Display hex_digit_display_7 (.value(LedData[7:4]));  // open: dp
  // Probe on EX_PC[19:0]
  // RiscV_Probe riscv_probe_3: pin names not known; wires that end beside it: EX_IR
  ROM #(.addrWidth(10), .dataWidth(32), .Select("high")) rom_1 (.addr(IF_PC[11:2]), .data(IF_IR));
  Multiplexer #(.select(1), .width(32), .disabled("Z"), .enable("false")) multiplexer_3 (
    .in0(PC_4), .in1(btb_1_jumpaddr), .out(multiplexer_3_out), .sel(btb_1_predictjump));
  Counter #(.width(16), .max('hffff), .ongoal("wrap"), .trigger("rising"), .behavior("old")) counter_3 (
    .count(loaduse), .Q(\LoadUse次数 ), .clk(and_3_out));  // open: load, D, carry, clr, preset
  not not_5 (not_5_out, halt);
  Hex_Digit_Display hex_digit_display_8 (.value(LedData[3:0]));  // open: dp
  and and_4 (and_4_out, loaduse, ~EX_Branch);  // AND_Gate
  // Probe on \总周期数 
  // Probe on M_PC[19:0]
  // RiscV_Probe riscv_probe_4: pin names not known; wires that end beside it: MEM_IR
  IF_ID if_id_1 (
    .\指令字 (IF_IR), .\指令字_2 (ID_IR), .PC_2(ID_PC), .CLK(CLK), .\保持 (or_2_out), .\同步清零 (Fail),
    .Branch_Pre(btb_1_predictjump), .Branch_PRe_2(if_id_1_branch_pre_2), .PC(IF_PC));
  or or_2 (or_2_out, halt, and_4_out);
  or or_3 (or_3_out, R1_Ex, R1_Mem, WB_R1);
  and and_5 (and_5_out, R1_Ex, ~WB_R1);  // AND_Gate
  and and_6 (and_6_out, R1_Mem, ~WB_R1);  // AND_Gate
  // Probe on \总周期数 
  // Probe on \无条件分支数 
  // Probe on \条件分支成功数 
  // Probe on \插入气泡数 
  // Probe on \LoadUse次数 
  // Probe on \预测失败次数 
  not not_6 (not_6_out, or_3_out);
  Encoder encoder_1 (.in1(not_6_out), .in2(and_5_out), .in3(and_6_out), .in4(WB_R1), .out(encoder_1_out));
  // Probe on IF_PC[11:0]
  // Probe on WB_PC[19:0]
  // RiscV_Probe riscv_probe_5: pin names not known; wires that end beside it: WB_IR
  Multiplexer #(.select(1), .width(5), .disabled("Z"), .enable("false")) multiplexer_4 (
    .in0(ID_IR[19:15]), .in1(5'b10001), .out(R1_num), .sel(\单周期硬布线控制器_1_ecall ));
  Multiplexer #(.select(1), .width(5), .disabled("Z"), .enable("false")) multiplexer_5 (
    .in0(ID_IR[24:20]), .in1(5'b01010), .out(R2_num), .sel(\单周期硬布线控制器_1_ecall ));
  \Conflict_重定向  \conflict_重定向_1  (
    .IR(ID_IR), .W_num(EX_IR[11:7]), .R1(R1_num), .R2(R2_num), .R1_error(\conflict_重定向_1_r1_error ),
    .R2_error(\conflict_重定向_1_r2_error ));
  \Conflict_重定向  \conflict_重定向_2  (
    .IR(ID_IR), .W_num(MEM_IR[11:7]), .R1(R1_num), .R2(R2_num), .R1_error(\conflict_重定向_2_r1_error ),
    .R2_error(\conflict_重定向_2_r2_error ));
  // Probe on encoder_1_out
  // Probe on EX_PC[11:0]
  // Probe on ID_PC[11:0]
  Register #(.width(2), .trigger("rising"), .Select("low")) f1 (
    .D(encoder_1_out), .Q(f1_q), .clk(CLK), .clr(Go));  // open: en
  // Probe on M_PC[11:0]
  D_Flip_Flop #(.trigger("high"), .Pre_Clr_Positions("LEGACY"), .NegatePresetClear("false"), .enable("true"), .NewFFLayout("false")) d_ff_1 (.Q(d_ff_1_q));  // open: clk, D, Qn, preset, en, reset
  // Probe on 13'h178
  or or_4 (or_4_out, JAL, JALR);
  \单周期硬布线控制器  \u_单周期硬布线控制器_1  (
    .Funct({ID_IR[30], ID_IR[25], ID_IR[14:12]}), .OP(ID_IR[6:2]), .ALU_OP(\单周期硬布线控制器_1_alu_op ),
    .MemToReg(\单周期硬布线控制器_1_memtoreg ), .MemWrite(\单周期硬布线控制器_1_memwrite ), .ALU_SRC(\单周期硬布线控制器_1_alu_src ),
    .RegWrite(\单周期硬布线控制器_1_regwrite ), .ecall(\单周期硬布线控制器_1_ecall ), .S_type(\单周期硬布线控制器_1_s_type ),
    .Jalr(JALR), .Beq(\单周期硬布线控制器_1_beq ), .JAL(JAL), .Bne(\单周期硬布线控制器_1_bne ), .in_3(ID_IR[21]),
    .LBU(\单周期硬布线控制器_1_lbu ), .BLT(\单周期硬布线控制器_1_blt ));  // open: uret, Csrsi, Csrci
  and and_7 (R1_Ex, EX_RegWrite, \conflict_重定向_1_r1_error );
  and and_8 (R2_Ex, EX_RegWrite, \conflict_重定向_1_r2_error );
  // Probe on rs
  Multiplexer #(.select(2), .width(32), .disabled("Z"), .enable("false")) multiplexer_6 (
    .in0(R1), .in1(ALU_Result1), .in2(ALU_Result2), .in3(RDin), .out(rs), .sel(f1_q));
  // Probe on RDin
  // Probe on WB_PC[11:0]
  Comparator #(.width(13), .mode("twosComplement")) comparator_2 (
    .a(CNT_num), .b(13'h178), .eq(comparator_2_eq), .lt(comparator_2_lt));  // open: gt
  Clock #(.highDuration(1), .lowDuration(1)) clock_1 (.out(clock_1_out));
  Multiplexer #(.select(1), .width(12), .disabled("Z"), .enable("false")) multiplexer_7 (
    .in0(ID_IR[31:20]), .in1({ID_IR[31:25], ID_IR[11:7]}), .out(multiplexer_7_out), .sel(\单周期硬布线控制器_1_s_type ));
  Shifter #(.width(12), .shift("ll")) shifter_1 (
    .in({ID_IR[31], ID_IR[7], ID_IR[30:25], ID_IR[11:8]}), .\dist (4'b0001), .out(shifter_1_out));
  Shifter #(.width(20), .shift("ll")) shifter_2 (
    .in({ID_IR[31], ID_IR[19:12], ID_IR[20], ID_IR[30:21]}), .\dist (5'b00001), .out(shifter_2_out));
  and and_9 (R1_Mem, \conflict_重定向_2_r1_error , ~R1_Ex, MEM_RegWrite);  // AND_Gate
  and and_10 (R2_Mem, \conflict_重定向_2_r2_error , ~R2_Ex, MEM_RegWrite);  // AND_Gate
  nand nand_1 (nand_1_out, d_ff_1_q, comparator_2_eq);
  Counter #(.width(13), .max('h1fff), .ongoal("stay"), .trigger("rising"), .behavior("old")) counter_4 (
    .count(comparator_2_lt), .Q(CNT_num), .clk(clock_1_out));  // open: load, D, carry, clr, preset
  Regifile regifile_1 (
    .Din(RDin), .Clk(CLK), .R1(regifile_1_r1), .R2(regifile_1_r2), .WE(RegWrite), .W_num(WB_IR[11:7]),
    .R1_num(R1_num), .R2_num(R2_num));
  assign bit_extender_1_out = {{20{multiplexer_7_out[11]}}, multiplexer_7_out};  // Bit_Extender bit_extender_1
  assign bit_extender_2_out = {{20{shifter_1_out[11]}}, shifter_1_out};  // Bit_Extender bit_extender_2
  Multiplexer #(.select(1), .width(32), .disabled("Z"), .enable("false")) multiplexer_8 (
    .in0(bit_extender_2_out), .in1(bit_extender_3_out), .out(multiplexer_8_out), .sel(JAL));
  assign bit_extender_3_out = {{12{shifter_2_out[19]}}, shifter_2_out};  // Bit_Extender bit_extender_3
  assign CLK = nand_1_out ? clock_1_out : 1'bz;  // Controlled_Buffer controlled_buffer_1
  Multiplexer #(.select(1), .width(32), .disabled("Z"), .enable("false")) multiplexer_9 (
    .in0(ID_PC), .in1(regifile_1_r1), .out(multiplexer_9_out), .sel(JALR));
  Multiplexer #(.select(1), .width(32), .disabled("Z"), .enable("false")) multiplexer_10 (
    .in0(multiplexer_8_out), .out(multiplexer_10_out), .sel(JALR));  // open: in1
  or or_5 (or_5_out, R2_Ex, R2_Mem, WB_R2);
  and and_11 (and_11_out, R2_Ex, ~WB_R2);  // AND_Gate
  and and_12 (and_12_out, R2_Mem, ~WB_R2);  // AND_Gate
  Pull_Resistor #(.pull(1)) pull_resistor_1 (.node(CLK));
  ID_EX id_ex_1 (
    .\指令字 (ID_PC), .PC(ID_IR), .Aluop(\单周期硬布线控制器_1_alu_op ), .AlusrcB(\单周期硬布线控制器_1_alu_src ),
    .R1(regifile_1_r1), .R2(regifile_1_r2), .imm_I_S(bit_extender_1_out), .imm_BJ_I(multiplexer_10_out),
    .PC_2(EX_PC), .IR(EX_IR), .Aluop_2(id_ex_1_aluop_2), .AlusrcB_2(id_ex_1_alusrcb_2), .R1_2(R1), .R2_2(R2),
    .imm_I_S_2(id_ex_1_imm_i_s_2), .imm_BJ_I_2(id_ex_1_imm_bj_i_2), .CLK(CLK), .B(id_ex_1_b),
    .PC_R(multiplexer_9_out), .RegWrite(\单周期硬布线控制器_1_regwrite ), .RegWrite_2(EX_RegWrite), .\保持 (halt),
    .ecall_2(id_ex_1_ecall_2), .ecall(\单周期硬布线控制器_1_ecall ), .\同步清零 (or_6_out), .Branch_Pre_2(EX_PredictJump),
    .Branch_Pre(if_id_1_branch_pre_2), .Bne(\单周期硬布线控制器_1_bne ), .Bne_2(id_ex_1_bne_2),
    .MemToReg(\单周期硬布线控制器_1_memtoreg ), .MemToReg_2(id_ex_1_memtoreg_2), .MemWrite(\单周期硬布线控制器_1_memwrite ),
    .MemToReg_3(id_ex_1_memtoreg_3), .JAL_JALR(or_4_out), .JAL_JALR_2(id_ex_1_jal_jalr_2),
    .Beq(\单周期硬布线控制器_1_beq ), .Beq_2(id_ex_1_beq_2), .Blt(\单周期硬布线控制器_1_blt ), .Blt_2(id_ex_1_blt_2),
    .Lbu(\单周期硬布线控制器_1_lbu ), .Lbu_2(id_ex_1_lbu_2));
  or or_6 (or_6_out, and_4_out, Fail);
  Comparator #(.width(5), .mode("twosComplement")) comparator_3 (
    .a(5'b00011), .b(MEM_IR[6:2]), .eq(comparator_3_eq));  // open: gt, lt
  Comparator #(.width(5), .mode("twosComplement")) comparator_4 (
    .a({5{1'b0}}), .b(MEM_IR[6:2]), .eq(comparator_4_eq));  // open: gt, lt
  Comparator #(.width(5), .mode("twosComplement")) comparator_5 (
    .a(EX_IR[6:2]), .b(5'b00011), .eq(comparator_5_eq));  // open: gt, lt
  Comparator #(.width(5), .mode("twosComplement")) comparator_6 (
    .a(EX_IR[6:2]), .b({5{1'b0}}), .eq(comparator_6_eq));  // open: gt, lt
  not not_7 (not_7_out, or_5_out);
  Encoder encoder_2 (.in1(not_7_out), .in2(and_11_out), .in3(and_12_out), .in4(WB_R2), .out(encoder_2_out));
  or or_7 (or_7_out, comparator_3_eq, comparator_4_eq);
  or or_8 (or_8_out, comparator_5_eq, comparator_6_eq);
  or or_9 (or_9_out, R1_Ex, R2_Ex);
  Register #(.width(1), .trigger("rising"), .Select("low")) f1_2 (
    .D(not_7_out), .Q(DataIMM), .clk(CLK));  // open: en, clr
  // Probe on encoder_2_out
  or or_10 (\分支指令 , id_ex_1_beq_2, id_ex_1_blt_2, id_ex_1_bne_2, id_ex_1_jal_jalr_2);
  Multiplexer #(.select(1), .width(32), .disabled("Z"), .enable("false")) multiplexer_11 (
    .in0(rd2), .in1(id_ex_1_imm_i_s_2), .out(multiplexer_11_out), .sel(id_ex_1_alusrcb_2));
  ALU alu_1 (
    .X(id_ex_1_imm_bj_i_2), .Y(id_ex_1_b), .AluOP(4'b0101), .Result(alu_1_result));  // open: Equal, Result_2, out_4, out_6
  and and_13 (loaduse, or_8_out, or_9_out);
  and and_14 (WB_R2, R2_Mem, or_7_out);
  and and_15 (WB_R1, R1_Mem, or_7_out);
  and and_16 (and_16_out, alu_2_equal, id_ex_1_beq_2);
  not not_8 (not_8_out, alu_2_equal);
  and and_17 (and_17_out, not_8_out, id_ex_1_bne_2);
  Comparator #(.width(32), .mode("twosComplement")) comparator_7 (
    .a(rs), .b(32'h22), .eq(comparator_7_eq));  // open: gt, lt
  ALU alu_2 (
    .X(rs), .Y(multiplexer_11_out), .AluOP(id_ex_1_aluop_2), .Equal(alu_2_equal), .Result(alu_2_result),
    .Result_2(alu_2_result_2), .out_6(alu_2_out_6));  // open: out_4
  Register #(.width(2), .trigger("rising"), .Select("low")) f2 (
    .D(encoder_2_out), .Q(f2_q), .clk(CLK), .clr(Go));  // open: en
  and and_18 (and_18_out, id_ex_1_blt_2, alu_2_out_6);
  not not_9 (not_9_out, comparator_7_eq);
  and and_19 (and_19_out, id_ex_1_ecall_2, comparator_7_eq);
  // Probe on rd2
  Multiplexer #(.select(2), .width(32), .disabled("Z"), .enable("false")) multiplexer_12 (
    .in0(R2), .in1(ALU_Result1), .in2(ALU_Result2), .in3(RDin), .out(rd2), .sel(f2_q));
  // Probe on RDin
  or or_11 (EX_Branch, id_ex_1_jal_jalr_2, B_type);
  or or_12 (B_type, and_18_out, and_16_out, and_17_out);
  and and_20 (and_20_out, id_ex_1_ecall_2, not_9_out);
  Register #(.width(32), .trigger("rising"), .Select("low")) register_1 (
    .D(rd2), .en(and_19_out), .Q(LedData), .clk(CLK));  // open: clr
  Register #(.width(1), .trigger("falling"), .Select("low")) register_2 (
    .D(and_20_out), .Q(halt), .clk(CLK), .clr(Go), .preset(halt));  // open: en, cs
  EX_MEM ex_mem_1 (
    .MemToReg(id_ex_1_memtoreg_2), .MemWrite(id_ex_1_memtoreg_3), .MemToReg_2(ex_mem_1_memtoreg_2),
    .MemWrite_2(MemWrite), .CLK(CLK), .\指令字 (EX_PC), .\指令字_2 (M_PC), .PC(EX_IR), .PC_2(MEM_IR),
    .Adress(ALU_Result1), .ALU(alu_2_result), .MDin_2(MDin), .MDin(rd2), .RegWrite(EX_RegWrite),
    .RegWrite_2(MEM_RegWrite), .\保持 (halt), .JAL_JALR(id_ex_1_jal_jalr_2), .JAL_JALR_2(ex_mem_1_jal_jalr_2),
    .Lbu(id_ex_1_lbu_2), .Lbu_2(ex_mem_1_lbu_2));  // open: halt, halt_2
  not not_10 (not_10_out, halt);
  RAM #(.addrWidth(10), .dataWidth(32), .bus("separate"), .Select("high")) ram_1 (
    .addr(ALU_Result1[11:2]), .din(MDin), .data(ram_1_data), .str(MemWrite), .sel(not_10_out), .clk(CLK));  // open: ld, clr
  Multiplexer #(.select(1), .width(32), .disabled("Z"), .enable("false")) multiplexer_13 (
    .in0(ALU_Result1), .in1(ram_1_data), .out(multiplexer_13_out), .sel(ex_mem_1_memtoreg_2));
  BitSelector #(.width(32), .group(8)) bitselector_1 (.in(ram_1_data), .out(bitselector_1_out), .sel(ALU_Result1[1:0]));
  Multiplexer #(.select(1), .width(32), .disabled("Z"), .enable("false")) multiplexer_14 (
    .in0(multiplexer_13_out), .in1(bit_extender_4_out), .out(multiplexer_14_out), .sel(ex_mem_1_lbu_2));
  assign bit_extender_4_out = {{24{1'b0}}, bitselector_1_out};  // Bit_Extender bit_extender_4
  MEM_WB mem_wb_1 (
    .\指令字 (M_PC), .PC(MEM_IR), .ALU(ALU_Result1), .\指令字_2 (WB_PC), .PC_2(WB_IR), .ALU_2(ALU_Result2),
    .CLK(CLK), .RegWrite(MEM_RegWrite), .RegWrite_2(RegWrite), .\保持 (halt), .JAL_JALR(ex_mem_1_jal_jalr_2),
    .JAL_JALR_2(mem_wb_1_jal_jalr_2), .MD(multiplexer_14_out), .MD_2(mem_wb_1_md_2), .Lbu(ex_mem_1_lbu_2));  // open: halt, halt_2, Lbu_2
  Adder #(.width(32)) adder_3 (.a(WB_PC), .b(32'h4), .out(adder_3_out));  // open: cin, cout
  Multiplexer #(.select(1), .width(32), .disabled("Z"), .enable("false")) multiplexer_15 (
    .in0(mem_wb_1_md_2), .in1(adder_3_out), .out(RDin), .sel(mem_wb_1_jal_jalr_2));

  // Other names for the same wires on the sheet: Mem_FinalData[31:0] = RDin; MEM_PC[31:0] = M_PC;
  //   WB_W_num[4:0] = WB_IR[11:7]

  // Notes on the sheet:
  //   中断源
  //   时空图监测，可删除
  //   中断等待指示
  //   OP
  //   指令存储器
  //   contents of rom_1 (hex, n*v repeats v):
  //   100493 100006f 100493 200913 300993 100006f 100493 200913 300993 100006f 100493 200913 300993
  //   100006f 100493 200913 300993 3d0000ef 100413 100493 1f49493 900533 2200893 73 24d493 48463 fedff06f
  //   900533 2200893 73 100493 249493 900533 2200893 73 48463 fedff06f 100493 1f49493 900533 2200893 73
  //   4034d493 900533 2200893 73 4044d493 900533 2200893 73 4044d493 900533 2200893 73 4044d493 900533
  //   2200893 73 4044d493 900533 2200893 73 4044d493 900533 2200893 73 4044d493 900533 2200893 73 4044d493
  //   900533 2200893 73 100413 1f41993 41f9d993 433 c00913 300b13 140413 f47413 800293 100313 499993
  //   89e9b3 1300533 2200893 73 406282b3 fe0294e3 140413 f00f93 1f47433 1c41413 800293 100313 49d993
  //   89e9b3 1300533 2200893 73 406282b3 fe0294e3 1c45413 406b0b33 b0463 f95ff06f 2b3 fff2c293 829293
  //   ff2e293 500533 2200893 73 fff00413 493 84a023 140413 448493 84a023 140413 448493 84a023 140413
  //   448493 84a023 140413 448493 84a023 140413 448493 84a023 140413 448493 84a023 140413 448493 84a023
  //   140413 448493 84a023 140413 448493 84a023 140413 448493 84a023 140413 448493 84a023 140413 448493
  //   84a023 140413 448493 84a023 140413 448493 84a023 140413 448493 84a023 140413 448493 140413 433
  //   3c00493 42983 4aa03 149a2b3 28663 134a023 1442023 ffc48493 fe9412e3 800533 2200893 73 440413 3c00493
  //   fc9416e3 3200893 73 100293 300313 800493 849493 7648493 1449493 900533 2200893 73 800e13 54d4b3
  //   64d4b3 900533 2200893 73 fffe0e13 fe0e14e3 a00893 73 fff00293 7700493 849493 7748493 900533 2200893
  //   73 1000e13 54c4b3 900533 2200893 73 fffe0e13 fe0e16e3 a00893 73 313 1000e13 8400493 849493 8348493
  //   400913 891913 490913 849493 8248493 849493 8148493 891913 490913 891913 490913 932023 12484b3 430313
  //   fffe0e13 fe0e18e3 2000e13 313 34483 900533 2200893 73 130313 fffe0e13 fe0e14e3 a00893 73 ff100493
  //   900533 2200893 73 148493 fe04c8e3 a00893 73 a00893 73 413 140413 800533 2200893 73 240413 800533
  //   2200893 73 340413 800533 2200893 73 440413 800533 2200893 73 540413 800533 2200893 73 640413 800533
  //   2200893 73 740413 800533 2200893 73 840413 800533 2200893 2200893 73 8067
  //   指令字
  //   上一条指令的W#
  //   I
  //   S
  //   控制位
  //   JAL
  //   JALR
  //   URET
  //   流水调试日志用
  //   暂停节拍，不能为0
  //   Beq
  //   Bne
  //   MemToReg
  //   MemWrite
  //   AluOP
  //   AluSrcB
  //   RegWrite
  //   ecall时,判断a17==34?
  //   ALU1的imm默认为I型，置1为S型
  //   戳工具置1进入计数暂停模式，ctrl+k时钟自动运行到对应节拍暂停
  //   ctrl+k关闭时钟连续运行，将控制位置零，进入单步调试模式调试
  //   B/J
  //   可计数暂停的时钟源
  //   BJ/I
  //   B=PC/R
  //   imm I/S
  //   imm BJ/I
  //   为方便自动评测，需要输出流水线各段保存的PC值，注意是PC不是PC+4，另外ID段寄存器写入信息，Mem段内存写入信息也要输出
  //   equal
  //   JAL/JALR
  //   B_type
  //   ecall模块
  //   Branch模块
  //   数据存储器
  //   PC+4
  //   JAL,JALR需把PC+4存入寄存器
endmodule
module BTB (
  input  Clk,
  input  EX_Branch,
  input  [31:0] PC,
  input  [31:0] EX_PC,
  input  [31:0] EX_BranchAddr,
  input  EX_Branched,
  output [31:0] JumpAddr,
  output PredictJump
);

  wire A0, A1, A2, A3, A4, A5, A6, A7, and_1_out, comparator_1_eq, comparator_2_eq, comparator_3_eq,
       comparator_4_eq, comparator_5_eq, comparator_6_eq, comparator_7_eq, comparator_8_eq, comparator_9_eq,
       comparator_10_eq, comparator_11_eq, comparator_12_eq, comparator_13_eq, comparator_14_eq,
       comparator_15_eq, comparator_16_eq, decoder_1_out0, decoder_1_out1, decoder_1_out2, decoder_1_out3,
       decoder_1_out4, decoder_1_out5, decoder_1_out6, decoder_1_out7, decoder_2_out0, decoder_2_out1,
       decoder_2_out2, decoder_2_out3, decoder_2_out4, decoder_2_out5, decoder_2_out6, decoder_2_out7,
       EX_Hit, EX_Miss, IF_Hit, IF_Miss, L0, L1, L2, L3, L4, L5, L6, L7, M0, M1, M2, M3, M4, M5, M6, M7,
       not_1_out, not_2_out, not_3_out, not_4_out, not_5_out, not_6_out, not_7_out, not_8_out, or_1_out,
       or_2_out, or_3_out, or_4_out, or_5_out, or_6_out, or_7_out, or_8_out, or_9_out, or_10_out, or_11_out,
       or_12_out, or_13_out, or_14_out, or_15_out, or_16_out, priority_encoder_1_gs, V0, V1, V2, V3, V4, V5,
       V6, V7, WriteL0, WriteL1, WriteL2, WriteL3, WriteL4, WriteL5, WriteL6, WriteL7;
  wire [0:0] controlled_buffer_1_out, controlled_buffer_2_out, controlled_buffer_3_out,
       controlled_buffer_4_out, controlled_buffer_5_out, controlled_buffer_6_out, controlled_buffer_7_out,
       controlled_buffer_8_out;
  wire [1:0] adder_1_out, adder_2_out, adder_3_out, adder_4_out, adder_5_out, adder_6_out, adder_7_out,
       adder_8_out, multiplexer_1_out, multiplexer_2_out, multiplexer_3_out, multiplexer_4_out,
       multiplexer_5_out, multiplexer_6_out, multiplexer_7_out, multiplexer_8_out, multiplexer_9_out,
       multiplexer_10_out, multiplexer_11_out, multiplexer_12_out, multiplexer_13_out, multiplexer_14_out,
       multiplexer_15_out, multiplexer_16_out, multiplexer_17_out, multiplexer_18_out, multiplexer_19_out,
       multiplexer_20_out, multiplexer_21_out, multiplexer_22_out, multiplexer_23_out, multiplexer_24_out,
       multiplexer_25_out, multiplexer_26_out, multiplexer_27_out, multiplexer_28_out, multiplexer_29_out,
       multiplexer_30_out, multiplexer_31_out, multiplexer_32_out, multiplexer_33_out, multiplexer_34_out,
       multiplexer_35_out, multiplexer_36_out, multiplexer_37_out, multiplexer_38_out, multiplexer_39_out,
       multiplexer_40_out, Predict0, Predict1, Predict2, Predict3, Predict4, Predict5, Predict6, Predict7;
  wire [2:0] max3_1_max_num, max3_2_max_num, max3_3_max_num, max3_4_max_num, max3_5_max_num, max3_6_max_num,
       max3_7_max_num, priority_encoder_1_out;
  wire [15:0] C0, C1, C2, C3, C4, C5, C6, C7, max3_1_max, max3_2_max, max3_3_max, max3_4_max, max3_5_max,
       max3_6_max;
  wire [31:0] Tag0, Tag1, Tag2, Tag3, Tag4, Tag5, Tag6, Tag7, \分支目标地址_2_q , \分支目标地址_3_q , \分支目标地址_4_q ,
       \分支目标地址_5_q , \分支目标地址_6_q , \分支目标地址_7_q , \分支目标地址_8_q , \分支目标地址_q ;

  Pull_Resistor #(.pull(0)) pull_resistor_1 (.node(PredictJump));
  assign {PredictJump, controlled_buffer_1_out[0]} = L0 ? Predict0 : 2'bz;  // Controlled_Buffer controlled_buffer_1
  assign {PredictJump, controlled_buffer_2_out[0]} = L1 ? Predict1 : 2'bz;  // Controlled_Buffer controlled_buffer_2
  assign {PredictJump, controlled_buffer_3_out[0]} = L2 ? Predict2 : 2'bz;  // Controlled_Buffer controlled_buffer_3
  assign {PredictJump, controlled_buffer_4_out[0]} = L3 ? Predict3 : 2'bz;  // Controlled_Buffer controlled_buffer_4
  assign {PredictJump, controlled_buffer_5_out[0]} = L4 ? Predict4 : 2'bz;  // Controlled_Buffer controlled_buffer_5
  assign {PredictJump, controlled_buffer_6_out[0]} = L5 ? Predict5 : 2'bz;  // Controlled_Buffer controlled_buffer_6
  assign {PredictJump, controlled_buffer_7_out[0]} = L6 ? Predict6 : 2'bz;  // Controlled_Buffer controlled_buffer_7
  assign {PredictJump, controlled_buffer_8_out[0]} = L7 ? Predict7 : 2'bz;  // Controlled_Buffer controlled_buffer_8
  Register #(.width(1), .trigger("rising"), .Select("low")) VALID (
    .D(1'b1), .en(WriteL0), .Q(V0), .clk(Clk));  // open: clr
  Register #(.width(1), .trigger("rising"), .Select("low")) VALID_2 (
    .D(1'b1), .en(WriteL1), .Q(V1), .clk(Clk));  // open: clr
  Register #(.width(1), .trigger("rising"), .Select("low")) VALID_3 (
    .D(1'b1), .en(WriteL2), .Q(V2), .clk(Clk));  // open: clr
  Register #(.width(1), .trigger("rising"), .Select("low")) VALID_4 (
    .D(1'b1), .en(WriteL3), .Q(V3), .clk(Clk));  // open: clr
  Register #(.width(1), .trigger("rising"), .Select("low")) VALID_5 (
    .D(1'b1), .en(WriteL4), .Q(V4), .clk(Clk));  // open: clr
  Register #(.width(1), .trigger("rising"), .Select("low")) VALID_6 (
    .D(1'b1), .en(WriteL5), .Q(V5), .clk(Clk));  // open: clr
  Register #(.width(1), .trigger("rising"), .Select("low")) VALID_7 (
    .D(1'b1), .en(WriteL6), .Q(V6), .clk(Clk));  // open: clr
  Register #(.width(1), .trigger("rising"), .Select("low")) VALID_8 (
    .D(1'b1), .en(WriteL7), .Q(V7), .clk(Clk));  // open: clr
  or or_1 (or_1_out, L1, L2, L3, L4, L5, L6, L7, WriteL1, WriteL2, WriteL3, WriteL4, WriteL5, WriteL6, WriteL7);
  or or_2 (or_2_out, L0, L1, L2, L3, L5, L6, L7, WriteL0, WriteL1, WriteL2, WriteL3, WriteL5, WriteL6, WriteL7);
  not not_1 (not_1_out, V0);
  not not_2 (not_2_out, V1);
  not not_3 (not_3_out, V2);
  not not_4 (not_4_out, V3);
  not not_5 (not_5_out, V4);
  not not_6 (not_6_out, V5);
  not not_7 (not_7_out, V6);
  not not_8 (not_8_out, V7);
  MAX3 max3_1 (.Y(C1), .X(C0), .Y_num(3'b001), .X_num(3'b000), .MAX(max3_1_max), .Max_num(max3_1_max_num));
  MAX3 max3_2 (.Y(C3), .X(C2), .Y_num(3'b011), .X_num(3'b010), .MAX(max3_2_max), .Max_num(max3_2_max_num));
  MAX3 max3_3 (.Y(C5), .X(C4), .Y_num(3'b101), .X_num(3'b100), .MAX(max3_3_max), .Max_num(max3_3_max_num));
  MAX3 max3_4 (.Y(C7), .X(C6), .Y_num(3'b111), .X_num(3'b110), .MAX(max3_4_max), .Max_num(max3_4_max_num));
  and and_1 (and_1_out, V0, V1, V2, V3, V4, V5, V6, V7);
  Priority_Encoder #(.select(3), .disabled("Z")) priority_encoder_1 (
    .in0(not_1_out), .in1(not_2_out), .in2(not_3_out), .in3(not_4_out), .in4(not_5_out), .in5(not_6_out),
    .in6(not_7_out), .in7(not_8_out), .out(priority_encoder_1_out), .gs(priority_encoder_1_gs));  // open: en_out, en_in
  MAX3 max3_5 (
    .Y(max3_2_max), .X(max3_1_max), .Y_num(max3_2_max_num), .X_num(max3_1_max_num), .MAX(max3_5_max),
    .Max_num(max3_5_max_num));
  MAX3 max3_6 (
    .Y(max3_4_max), .X(max3_3_max), .Y_num(max3_4_max_num), .X_num(max3_3_max_num), .MAX(max3_6_max),
    .Max_num(max3_6_max_num));
  Multiplexer #(.select(1), .width(2), .disabled("Z"), .enable("false")) multiplexer_1 (
    .in0(2'b00), .in1(2'b01), .out(multiplexer_1_out), .sel(EX_Branched));
  Multiplexer #(.select(1), .width(2), .disabled("Z"), .enable("false")) multiplexer_2 (
    .in0(2'b11), .in1(2'b01), .out(multiplexer_2_out), .sel(EX_Branched));
  Multiplexer #(.select(1), .width(2), .disabled("Z"), .enable("false")) multiplexer_3 (
    .in0(2'b01), .in1(2'b00), .out(multiplexer_3_out), .sel(EX_Branched));
  Multiplexer #(.select(1), .width(2), .disabled("Z"), .enable("false")) multiplexer_4 (
    .in0(2'b01), .in1(2'b11), .out(multiplexer_4_out), .sel(EX_Branched));
  Multiplexer #(.select(1), .width(2), .disabled("Z"), .enable("false")) multiplexer_5 (
    .in0(2'b00), .in1(2'b01), .out(multiplexer_5_out), .sel(EX_Branched));
  Multiplexer #(.select(1), .width(2), .disabled("Z"), .enable("false")) multiplexer_6 (
    .in0(2'b11), .in1(2'b01), .out(multiplexer_6_out), .sel(EX_Branched));
  Multiplexer #(.select(1), .width(2), .disabled("Z"), .enable("false")) multiplexer_7 (
    .in0(2'b01), .in1(2'b00), .out(multiplexer_7_out), .sel(EX_Branched));
  Multiplexer #(.select(1), .width(2), .disabled("Z"), .enable("false")) multiplexer_8 (
    .in0(2'b01), .in1(2'b11), .out(multiplexer_8_out), .sel(EX_Branched));
  Register #(.width(32), .trigger("rising"), .Select("low")) \u_分支指令地址  (
    .D(EX_PC), .en(WriteL0), .Q(Tag0), .clk(Clk));  // open: clr
  Register #(.width(32), .trigger("rising"), .Select("low")) \u_分支指令地址_2  (
    .D(EX_PC), .en(WriteL1), .Q(Tag1), .clk(Clk));  // open: clr
  Register #(.width(32), .trigger("rising"), .Select("low")) \u_分支指令地址_3  (
    .D(EX_PC), .en(WriteL2), .Q(Tag2), .clk(Clk));  // open: clr
  Register #(.width(32), .trigger("rising"), .Select("low")) \u_分支指令地址_4  (
    .D(EX_PC), .en(WriteL3), .Q(Tag3), .clk(Clk));  // open: clr
  Register #(.width(32), .trigger("rising"), .Select("low")) \u_分支指令地址_5  (
    .D(EX_PC), .en(WriteL4), .Q(Tag4), .clk(Clk));  // open: clr
  Register #(.width(32), .trigger("rising"), .Select("low")) \u_分支指令地址_6  (
    .D(EX_PC), .en(WriteL5), .Q(Tag5), .clk(Clk));  // open: clr
  Register #(.width(32), .trigger("rising"), .Select("low")) \u_分支指令地址_7  (
    .D(EX_PC), .en(WriteL6), .Q(Tag6), .clk(Clk));  // open: clr
  Register #(.width(32), .trigger("rising"), .Select("low")) \u_分支指令地址_8  (
    .D(EX_PC), .en(WriteL7), .Q(Tag7), .clk(Clk));  // open: clr
  and and_2 (A0, or_1_out, V0);
  and and_3 (A4, or_2_out, V4);
  Decoder #(.select(3), .tristate("false"), .disabled(0), .enable("true")) decoder_1 (
    .out0(decoder_1_out0), .out1(decoder_1_out1), .out2(decoder_1_out2), .out3(decoder_1_out3),
    .out4(decoder_1_out4), .out5(decoder_1_out5), .out6(decoder_1_out6), .out7(decoder_1_out7),
    .sel(priority_encoder_1_out), .en(priority_encoder_1_gs));
  Decoder #(.select(3), .tristate("false"), .disabled(0), .enable("true")) decoder_2 (
    .out0(decoder_2_out0), .out1(decoder_2_out1), .out2(decoder_2_out2), .out3(decoder_2_out3),
    .out4(decoder_2_out4), .out5(decoder_2_out5), .out6(decoder_2_out6), .out7(decoder_2_out7),
    .sel(max3_7_max_num), .en(and_1_out));
  MAX3 max3_7 (
    .Y(max3_6_max), .X(max3_5_max), .Y_num(max3_6_max_num), .X_num(max3_5_max_num), .Max_num(max3_7_max_num));  // open: MAX
  Multiplexer #(.select(2), .width(2), .disabled("Z"), .enable("false")) multiplexer_9 (
    .in0(multiplexer_1_out), .in1(multiplexer_2_out), .in2(multiplexer_3_out), .in3(multiplexer_4_out),
    .out(multiplexer_9_out), .sel(Predict0));
  Multiplexer #(.select(2), .width(2), .disabled("Z"), .enable("false")) multiplexer_10 (
    .in0(multiplexer_5_out), .in1(multiplexer_6_out), .in2(multiplexer_7_out), .in3(multiplexer_8_out),
    .out(multiplexer_10_out), .sel(Predict4));
  Counter #(.width(16), .max('hffff), .ongoal("wrap"), .trigger("rising"), .behavior("old")) \u_置换标记  (
    .count(A0), .Q(C0), .clk(Clk), .clr(L0));  // open: load, D, carry, preset
  Counter #(.width(16), .max('hffff), .ongoal("wrap"), .trigger("rising"), .behavior("old")) \u_置换标记_2  (
    .count(A1), .Q(C1), .clk(Clk), .clr(L1));  // open: load, D, carry, preset
  Counter #(.width(16), .max('hffff), .ongoal("wrap"), .trigger("rising"), .behavior("old")) \u_置换标记_3  (
    .count(A2), .Q(C2), .clk(Clk), .clr(L2));  // open: load, D, carry, preset
  Counter #(.width(16), .max('hffff), .ongoal("wrap"), .trigger("rising"), .behavior("old")) \u_置换标记_4  (
    .count(A3), .Q(C3), .clk(Clk), .clr(L3));  // open: load, D, carry, preset
  Counter #(.width(16), .max('hffff), .ongoal("wrap"), .trigger("rising"), .behavior("old")) \u_置换标记_5  (
    .count(A4), .Q(C4), .clk(Clk), .clr(L4));  // open: load, D, carry, preset
  Counter #(.width(16), .max('hffff), .ongoal("wrap"), .trigger("rising"), .behavior("old")) \u_置换标记_6  (
    .count(A5), .Q(C5), .clk(Clk), .clr(L5));  // open: load, D, carry, preset
  Counter #(.width(16), .max('hffff), .ongoal("wrap"), .trigger("rising"), .behavior("old")) \u_置换标记_7  (
    .count(A6), .Q(C6), .clk(Clk), .clr(L6));  // open: load, D, carry, preset
  Counter #(.width(16), .max('hffff), .ongoal("wrap"), .trigger("rising"), .behavior("old")) \u_置换标记_8  (
    .count(A7), .Q(C7), .clk(Clk), .clr(L7));  // open: load, D, carry, preset
  Adder #(.width(2)) adder_1 (.a(Predict0), .b(multiplexer_9_out), .out(adder_1_out));  // open: cin, cout
  Adder #(.width(2)) adder_2 (.a(Predict4), .b(multiplexer_10_out), .out(adder_2_out));  // open: cin, cout
  Register #(.width(2), .trigger("rising"), .Select("low")) \u_分支预测历史位  (
    .D(adder_1_out), .en(M0), .Q(Predict0), .clk(Clk));  // open: clr
  Register #(.width(2), .trigger("rising"), .Select("low")) \u_分支预测历史位_2  (
    .D(adder_2_out), .en(M4), .Q(Predict4), .clk(Clk));  // open: clr
  or or_3 (or_3_out, L0, L2, L3, L4, L5, L6, L7, WriteL0, WriteL2, WriteL3, WriteL4, WriteL5, WriteL6, WriteL7);
  or or_4 (or_4_out, L0, L1, L2, L3, L4, L6, L7, WriteL0, WriteL1, WriteL2, WriteL3, WriteL4, WriteL6, WriteL7);
  or or_5 (or_5_out, decoder_1_out0, decoder_2_out0);
  or or_6 (or_6_out, decoder_1_out1, decoder_2_out1);
  or or_7 (or_7_out, decoder_1_out2, decoder_2_out2);
  or or_8 (or_8_out, decoder_1_out3, decoder_2_out3);
  or or_9 (or_9_out, decoder_1_out4, decoder_2_out4);
  or or_10 (or_10_out, decoder_1_out5, decoder_2_out5);
  or or_11 (or_11_out, decoder_1_out6, decoder_2_out6);
  or or_12 (or_12_out, decoder_1_out7, decoder_2_out7);
  Register #(.width(32), .trigger("rising"), .Select("low")) \u_分支目标地址  (
    .D(EX_BranchAddr), .en(WriteL0), .Q(\分支目标地址_q ), .clk(Clk));  // open: clr
  assign JumpAddr = L0 ? \分支目标地址_q  : 32'bz;  // Controlled_Buffer controlled_buffer_9
  assign JumpAddr = L1 ? \分支目标地址_2_q  : 32'bz;  // Controlled_Buffer controlled_buffer_10
  Register #(.width(32), .trigger("rising"), .Select("low")) \u_分支目标地址_2  (
    .D(EX_BranchAddr), .en(WriteL1), .Q(\分支目标地址_2_q ), .clk(Clk));  // open: clr
  Register #(.width(32), .trigger("rising"), .Select("low")) \u_分支目标地址_3  (
    .D(EX_BranchAddr), .en(WriteL2), .Q(\分支目标地址_3_q ), .clk(Clk));  // open: clr
  assign JumpAddr = L2 ? \分支目标地址_3_q  : 32'bz;  // Controlled_Buffer controlled_buffer_11
  Register #(.width(32), .trigger("rising"), .Select("low")) \u_分支目标地址_4  (
    .D(EX_BranchAddr), .en(WriteL3), .Q(\分支目标地址_4_q ), .clk(Clk));  // open: clr
  assign JumpAddr = L3 ? \分支目标地址_4_q  : 32'bz;  // Controlled_Buffer controlled_buffer_12
  assign JumpAddr = L4 ? \分支目标地址_5_q  : 32'bz;  // Controlled_Buffer controlled_buffer_13
  Register #(.width(32), .trigger("rising"), .Select("low")) \u_分支目标地址_5  (
    .D(EX_BranchAddr), .en(WriteL4), .Q(\分支目标地址_5_q ), .clk(Clk));  // open: clr
  Register #(.width(32), .trigger("rising"), .Select("low")) \u_分支目标地址_6  (
    .D(EX_BranchAddr), .en(WriteL5), .Q(\分支目标地址_6_q ), .clk(Clk));  // open: clr
  assign JumpAddr = L5 ? \分支目标地址_6_q  : 32'bz;  // Controlled_Buffer controlled_buffer_14
  assign JumpAddr = L6 ? \分支目标地址_7_q  : 32'bz;  // Controlled_Buffer controlled_buffer_15
  Register #(.width(32), .trigger("rising"), .Select("low")) \u_分支目标地址_7  (
    .D(EX_BranchAddr), .en(WriteL6), .Q(\分支目标地址_7_q ), .clk(Clk));  // open: clr
  assign JumpAddr = L7 ? \分支目标地址_8_q  : 32'bz;  // Controlled_Buffer controlled_buffer_16
  Register #(.width(32), .trigger("rising"), .Select("low")) \u_分支目标地址_8  (
    .D(EX_BranchAddr), .en(WriteL7), .Q(\分支目标地址_8_q ), .clk(Clk));  // open: clr
  and and_4 (A1, or_3_out, V1);
  and and_5 (A5, or_4_out, V5);
  and and_6 (WriteL0, or_5_out, EX_Miss, EX_Branch);
  and and_7 (WriteL1, or_6_out, EX_Miss, EX_Branch);
  and and_8 (WriteL2, or_7_out, EX_Miss, EX_Branch);
  and and_9 (WriteL3, or_8_out, EX_Miss, EX_Branch);
  and and_10 (WriteL4, or_9_out, EX_Miss, EX_Branch);
  and and_11 (WriteL5, or_10_out, EX_Miss, EX_Branch);
  and and_12 (WriteL6, or_11_out, EX_Miss, EX_Branch);
  and and_13 (WriteL7, or_12_out, EX_Miss, EX_Branch);
  Multiplexer #(.select(1), .width(2), .disabled("Z"), .enable("false")) multiplexer_11 (
    .in0(2'b00), .in1(2'b01), .out(multiplexer_11_out), .sel(EX_Branched));
  Multiplexer #(.select(1), .width(2), .disabled("Z"), .enable("false")) multiplexer_12 (
    .in0(2'b11), .in1(2'b01), .out(multiplexer_12_out), .sel(EX_Branched));
  Multiplexer #(.select(1), .width(2), .disabled("Z"), .enable("false")) multiplexer_13 (
    .in0(2'b01), .in1(2'b00), .out(multiplexer_13_out), .sel(EX_Branched));
  Multiplexer #(.select(1), .width(2), .disabled("Z"), .enable("false")) multiplexer_14 (
    .in0(2'b01), .in1(2'b11), .out(multiplexer_14_out), .sel(EX_Branched));
  Multiplexer #(.select(1), .width(2), .disabled("Z"), .enable("false")) multiplexer_15 (
    .in0(2'b00), .in1(2'b01), .out(multiplexer_15_out), .sel(EX_Branched));
  Multiplexer #(.select(1), .width(2), .disabled("Z"), .enable("false")) multiplexer_16 (
    .in0(2'b11), .in1(2'b01), .out(multiplexer_16_out), .sel(EX_Branched));
  Multiplexer #(.select(1), .width(2), .disabled("Z"), .enable("false")) multiplexer_17 (
    .in0(2'b01), .in1(2'b00), .out(multiplexer_17_out), .sel(EX_Branched));
  Multiplexer #(.select(1), .width(2), .disabled("Z"), .enable("false")) multiplexer_18 (
    .in0(2'b01), .in1(2'b11), .out(multiplexer_18_out), .sel(EX_Branched));
  Multiplexer #(.select(2), .width(2), .disabled("Z"), .enable("false")) multiplexer_19 (
    .in0(multiplexer_11_out), .in1(multiplexer_12_out), .in2(multiplexer_13_out), .in3(multiplexer_14_out),
    .out(multiplexer_19_out), .sel(Predict1));
  Multiplexer #(.select(2), .width(2), .disabled("Z"), .enable("false")) multiplexer_20 (
    .in0(multiplexer_15_out), .in1(multiplexer_16_out), .in2(multiplexer_17_out), .in3(multiplexer_18_out),
    .out(multiplexer_20_out), .sel(Predict5));
  Register #(.width(2), .trigger("rising"), .Select("low")) \u_分支预测历史位_3  (
    .D(adder_3_out), .en(M1), .Q(Predict1), .clk(Clk));  // open: clr
  Adder #(.width(2)) adder_3 (.a(Predict1), .b(multiplexer_19_out), .out(adder_3_out));  // open: cin, cout
  Adder #(.width(2)) adder_4 (.a(Predict5), .b(multiplexer_20_out), .out(adder_4_out));  // open: cin, cout
  Register #(.width(2), .trigger("rising"), .Select("low")) \u_分支预测历史位_4  (
    .D(adder_4_out), .en(M5), .Q(Predict5), .clk(Clk));  // open: clr
  or or_13 (or_13_out, L0, L1, L3, L4, L5, L6, L7, WriteL0, WriteL1, WriteL3, WriteL4, WriteL5, WriteL6, WriteL7);
  or or_14 (or_14_out, L0, L1, L2, L3, L4, L5, L7, WriteL0, WriteL1, WriteL2, WriteL3, WriteL4, WriteL5, WriteL7);
  and and_14 (A2, or_13_out, V2);
  and and_15 (A6, or_14_out, V6);
  Comparator #(.width(32), .mode("twosComplement")) comparator_1 (
    .a(PC), .b(Tag0), .eq(comparator_1_eq));  // open: gt, lt
  Comparator #(.width(32), .mode("twosComplement")) comparator_2 (
    .a(PC), .b(Tag1), .eq(comparator_2_eq));  // open: gt, lt
  Comparator #(.width(32), .mode("twosComplement")) comparator_3 (
    .a(PC), .b(Tag2), .eq(comparator_3_eq));  // open: gt, lt
  Comparator #(.width(32), .mode("twosComplement")) comparator_4 (
    .a(PC), .b(Tag3), .eq(comparator_4_eq));  // open: gt, lt
  Comparator #(.width(32), .mode("twosComplement")) comparator_5 (
    .a(PC), .b(Tag4), .eq(comparator_5_eq));  // open: gt, lt
  Comparator #(.width(32), .mode("twosComplement")) comparator_6 (
    .a(PC), .b(Tag5), .eq(comparator_6_eq));  // open: gt, lt
  Comparator #(.width(32), .mode("twosComplement")) comparator_7 (
    .a(PC), .b(Tag6), .eq(comparator_7_eq));  // open: gt, lt
  Comparator #(.width(32), .mode("twosComplement")) comparator_8 (
    .a(PC), .b(Tag7), .eq(comparator_8_eq));  // open: gt, lt
  Comparator #(.width(32), .mode("twosComplement")) comparator_9 (
    .a(EX_PC), .b(Tag0), .eq(comparator_9_eq));  // open: gt, lt
  Comparator #(.width(32), .mode("twosComplement")) comparator_10 (
    .a(EX_PC), .b(Tag1), .eq(comparator_10_eq));  // open: gt, lt
  Comparator #(.width(32), .mode("twosComplement")) comparator_11 (
    .a(EX_PC), .b(Tag2), .eq(comparator_11_eq));  // open: gt, lt
  Comparator #(.width(32), .mode("twosComplement")) comparator_12 (
    .a(EX_PC), .b(Tag3), .eq(comparator_12_eq));  // open: gt, lt
  Comparator #(.width(32), .mode("twosComplement")) comparator_13 (
    .a(EX_PC), .b(Tag4), .eq(comparator_13_eq));  // open: gt, lt
  Comparator #(.width(32), .mode("twosComplement")) comparator_14 (
    .a(EX_PC), .b(Tag5), .eq(comparator_14_eq));  // open: gt, lt
  Comparator #(.width(32), .mode("twosComplement")) comparator_15 (
    .a(EX_PC), .b(Tag6), .eq(comparator_15_eq));  // open: gt, lt
  Comparator #(.width(32), .mode("twosComplement")) comparator_16 (
    .a(EX_PC), .b(Tag7), .eq(comparator_16_eq));  // open: gt, lt
  Multiplexer #(.select(1), .width(2), .disabled("Z"), .enable("false")) multiplexer_21 (
    .in0(2'b00), .in1(2'b01), .out(multiplexer_21_out), .sel(EX_Branched));
  Multiplexer #(.select(1), .width(2), .disabled("Z"), .enable("false")) multiplexer_22 (
    .in0(2'b11), .in1(2'b01), .out(multiplexer_22_out), .sel(EX_Branched));
  Multiplexer #(.select(1), .width(2), .disabled("Z"), .enable("false")) multiplexer_23 (
    .in0(2'b01), .in1(2'b00), .out(multiplexer_23_out), .sel(EX_Branched));
  Multiplexer #(.select(1), .width(2), .disabled("Z"), .enable("false")) multiplexer_24 (
    .in0(2'b01), .in1(2'b11), .out(multiplexer_24_out), .sel(EX_Branched));
  Multiplexer #(.select(1), .width(2), .disabled("Z"), .enable("false")) multiplexer_25 (
    .in0(2'b00), .in1(2'b01), .out(multiplexer_25_out), .sel(EX_Branched));
  Multiplexer #(.select(1), .width(2), .disabled("Z"), .enable("false")) multiplexer_26 (
    .in0(2'b11), .in1(2'b01), .out(multiplexer_26_out), .sel(EX_Branched));
  Multiplexer #(.select(1), .width(2), .disabled("Z"), .enable("false")) multiplexer_27 (
    .in0(2'b01), .in1(2'b00), .out(multiplexer_27_out), .sel(EX_Branched));
  Multiplexer #(.select(1), .width(2), .disabled("Z"), .enable("false")) multiplexer_28 (
    .in0(2'b01), .in1(2'b11), .out(multiplexer_28_out), .sel(EX_Branched));
  and and_16 (L0, comparator_1_eq, V0);
  and and_17 (L1, comparator_2_eq, V1);
  and and_18 (L2, comparator_3_eq, V2);
  and and_19 (L3, comparator_4_eq, V3);
  and and_20 (L4, comparator_5_eq, V4);
  and and_21 (L5, comparator_6_eq, V5);
  and and_22 (L6, comparator_7_eq, V6);
  and and_23 (L7, comparator_8_eq, V7);
  and and_24 (M0, comparator_9_eq, V0);
  and and_25 (M1, comparator_10_eq, V1);
  and and_26 (M2, comparator_11_eq, V2);
  and and_27 (M3, comparator_12_eq, V3);
  and and_28 (M4, comparator_13_eq, V4);
  and and_29 (M5, comparator_14_eq, V5);
  and and_30 (M6, comparator_15_eq, V6);
  and and_31 (M7, comparator_16_eq, V7);
  Adder #(.width(2)) adder_5 (.a(Predict2), .b(multiplexer_29_out), .out(adder_5_out));  // open: cin, cout
  Multiplexer #(.select(2), .width(2), .disabled("Z"), .enable("false")) multiplexer_29 (
    .in0(multiplexer_21_out), .in1(multiplexer_22_out), .in2(multiplexer_23_out), .in3(multiplexer_24_out),
    .out(multiplexer_29_out), .sel(Predict2));
  Adder #(.width(2)) adder_6 (.a(Predict6), .b(multiplexer_30_out), .out(adder_6_out));  // open: cin, cout
  Multiplexer #(.select(2), .width(2), .disabled("Z"), .enable("false")) multiplexer_30 (
    .in0(multiplexer_25_out), .in1(multiplexer_26_out), .in2(multiplexer_27_out), .in3(multiplexer_28_out),
    .out(multiplexer_30_out), .sel(Predict6));
  or or_15 (or_15_out, L0, L1, L2, L4, L5, L6, L7, WriteL0, WriteL1, WriteL2, WriteL4, WriteL5, WriteL6, WriteL7);
  or or_16 (or_16_out, L0, L1, L2, L3, L4, L5, L6, WriteL0, WriteL1, WriteL2, WriteL3, WriteL4, WriteL5, WriteL6);
  Register #(.width(2), .trigger("rising"), .Select("low")) \u_分支预测历史位_5  (
    .D(adder_5_out), .en(M2), .Q(Predict2), .clk(Clk));  // open: clr
  Register #(.width(2), .trigger("rising"), .Select("low")) \u_分支预测历史位_6  (
    .D(adder_6_out), .en(M6), .Q(Predict6), .clk(Clk));  // open: clr
  or or_17 (IF_Hit, L0, L1, L2, L3, L4, L5, L6, L7);
  or or_18 (EX_Hit, M0, M1, M2, M3, M4, M5, M6, M7);
  and and_32 (A3, or_15_out, V3);
  and and_33 (A7, or_16_out, V7);
  not not_9 (IF_Miss, IF_Hit);
  not not_10 (EX_Miss, EX_Hit);
  Multiplexer #(.select(1), .width(2), .disabled("Z"), .enable("false")) multiplexer_31 (
    .in0(2'b00), .in1(2'b01), .out(multiplexer_31_out), .sel(EX_Branched));
  Multiplexer #(.select(1), .width(2), .disabled("Z"), .enable("false")) multiplexer_32 (
    .in0(2'b11), .in1(2'b01), .out(multiplexer_32_out), .sel(EX_Branched));
  Multiplexer #(.select(1), .width(2), .disabled("Z"), .enable("false")) multiplexer_33 (
    .in0(2'b01), .in1(2'b00), .out(multiplexer_33_out), .sel(EX_Branched));
  Multiplexer #(.select(1), .width(2), .disabled("Z"), .enable("false")) multiplexer_34 (
    .in0(2'b01), .in1(2'b11), .out(multiplexer_34_out), .sel(EX_Branched));
  Multiplexer #(.select(1), .width(2), .disabled("Z"), .enable("false")) multiplexer_35 (
    .in0(2'b00), .in1(2'b01), .out(multiplexer_35_out), .sel(EX_Branched));
  Multiplexer #(.select(1), .width(2), .disabled("Z"), .enable("false")) multiplexer_36 (
    .in0(2'b11), .in1(2'b01), .out(multiplexer_36_out), .sel(EX_Branched));
  Multiplexer #(.select(1), .width(2), .disabled("Z"), .enable("false")) multiplexer_37 (
    .in0(2'b01), .in1(2'b00), .out(multiplexer_37_out), .sel(EX_Branched));
  Multiplexer #(.select(1), .width(2), .disabled("Z"), .enable("false")) multiplexer_38 (
    .in0(2'b01), .in1(2'b11), .out(multiplexer_38_out), .sel(EX_Branched));
  Multiplexer #(.select(2), .width(2), .disabled("Z"), .enable("false")) multiplexer_39 (
    .in0(multiplexer_31_out), .in1(multiplexer_32_out), .in2(multiplexer_33_out), .in3(multiplexer_34_out),
    .out(multiplexer_39_out), .sel(Predict3));
  Multiplexer #(.select(2), .width(2), .disabled("Z"), .enable("false")) multiplexer_40 (
    .in0(multiplexer_35_out), .in1(multiplexer_36_out), .in2(multiplexer_37_out), .in3(multiplexer_38_out),
    .out(multiplexer_40_out), .sel(Predict7));
  Adder #(.width(2)) adder_7 (.a(Predict3), .b(multiplexer_39_out), .out(adder_7_out));  // open: cin, cout
  Adder #(.width(2)) adder_8 (.a(Predict7), .b(multiplexer_40_out), .out(adder_8_out));  // open: cin, cout
  Register #(.width(2), .trigger("rising"), .Select("low")) \u_分支预测历史位_7  (
    .D(adder_7_out), .en(M3), .Q(Predict3), .clk(Clk));  // open: clr
  Register #(.width(2), .trigger("rising"), .Select("low")) \u_分支预测历史位_8  (
    .D(adder_8_out), .en(M7), .Q(Predict7), .clk(Clk));  // open: clr

  // Other names for the same wires on the sheet: Tag[31:0] = EX_PC

  // Notes on the sheet:
  //   Cache槽
  //   读缺失逻辑/块载入逻辑
  //   预测结果，为1跳转
  //   查找逻辑
endmodule

module MAX3 (
  input  [15:0] Y,
  input  [15:0] X,
  input  [2:0] Y_num,
  input  [2:0] X_num,
  output [15:0] MAX,
  output [2:0] Max_num
);

  wire comparator_1_eq, comparator_1_gt, or_1_out;

  Multiplexer #(.select(1), .width(16), .disabled("Z"), .enable("false")) multiplexer_1 (
    .in0(Y), .in1(X), .out(MAX), .sel(or_1_out));
  Comparator #(.width(16), .mode("unsigned")) comparator_1 (
    .a(X), .b(Y), .gt(comparator_1_gt), .eq(comparator_1_eq));  // open: lt
  or or_1 (or_1_out, comparator_1_gt, comparator_1_eq);
  Multiplexer #(.select(1), .width(3), .disabled("Z"), .enable("false")) multiplexer_2 (
    .in0(Y_num), .in1(X_num), .out(Max_num), .sel(or_1_out));

  // Notes on the sheet:
  //   输出两个输入中的较大值，并输出较大值的3位编号
endmodule
