// Logisim project 实验.circ as structural Verilog
module \_4_与门异或门电路  (
  input  X3,
  input  Y3,
  input  X2,
  input  Y2,
  input  X1,
  input  Y1,
  input  X0,
  input  Y0,
  output G3,
  output P3,
  output G2,
  output P2,
  output G1,
  output P1,
  output G0,
  output P0
);

  and and_1 (G3, X3, Y3);
  xor xor_1 (P3, X3, Y3);
  and and_2 (G2, X2, Y2);
  xor xor_2 (P2, X2, Y2);
  and and_3 (G1, X1, Y1);
  xor xor_3 (P1, X1, Y1);
  and and_4 (G0, X0, Y0);
  xor xor_4 (P0, X0, Y0);
endmodule

module CLA74182 (
  input  G3,
  input  P3,
  input  G2,
  input  P2,
  input  G1,
  input  P1,
  input  G0,
  input  P0,
  input  C0,
  output Gx,
  output Px,
  output C4,
  output C3,
  output C2,
  output C1
);

  wire and_1_out, and_2_out, and_3_out, and_5_out, and_6_out, and_7_out, and_8_out, and_9_out, and_10_out,
       and_11_out, and_12_out, and_13_out, and_14_out;

  and and_1 (and_1_out, P3, G2);
  and and_2 (and_2_out, P3, P2, G1);
  and and_3 (and_3_out, P3, P2, P1, G0);
  and and_4 (Px, P3, P2, P1, P0);
  and and_5 (and_5_out, P3, G2);
  and and_6 (and_6_out, P3, P2, G1);
  and and_7 (and_7_out, P3, P2, P1, G0);
  and and_8 (and_8_out, P3, P2, P1, P0, C0);
  and and_9 (and_9_out, P2, G1);
  and and_10 (and_10_out, P2, P1, G0);
  and and_11 (and_11_out, P2, P1, P0, C0);
  and and_12 (and_12_out, P1, G0);
  and and_13 (and_13_out, P1, P0, C0);
  and and_14 (and_14_out, P0, C0);
  or or_1 (Gx, G3, and_1_out, and_2_out, and_3_out);
  or or_2 (C4, G3, and_5_out, and_6_out, and_7_out, and_8_out);
  or or_3 (C3, G2, and_9_out, and_10_out, and_11_out);
  or or_4 (C2, G1, and_12_out, and_13_out);
  or or_5 (C1, G0, and_14_out);
endmodule

module \_4位快速加法器  (
  input  C0,
  input  X3,
  input  X2,
  input  X1,
  input  X0,
  input  Y3,
  input  Y2,
  input  Y1,
  input  Y0,
  output Gx,
  output Px,
  output S3,
  output S2,
  output S1,
  output S0,
  output C4
);

  wire cla74182_1_c1, cla74182_1_c2, cla74182_1_c3, \n4_与门异或门电路_1_g0 , \n4_与门异或门电路_1_g1 , \n4_与门异或门电路_1_g2 ,
       \n4_与门异或门电路_1_g3 , \n4_与门异或门电路_1_p0 , \n4_与门异或门电路_1_p1 , \n4_与门异或门电路_1_p2 , \n4_与门异或门电路_1_p3 ;

  CLA74182 cla74182_1 (
    .G3(\n4_与门异或门电路_1_g3 ), .P3(\n4_与门异或门电路_1_p3 ), .G2(\n4_与门异或门电路_1_g2 ), .P2(\n4_与门异或门电路_1_p2 ),
    .G1(\n4_与门异或门电路_1_g1 ), .P1(\n4_与门异或门电路_1_p1 ), .G0(\n4_与门异或门电路_1_g0 ), .P0(\n4_与门异或门电路_1_p0 ), .C0(C0),
    .Gx(Gx), .Px(Px), .C4(C4), .C3(cla74182_1_c3), .C2(cla74182_1_c2), .C1(cla74182_1_c1));
  \_4_与门异或门电路  \u_4_与门异或门电路_1  (
    .X3(X3), .Y3(Y3), .X2(X2), .Y2(Y2), .X1(X1), .Y1(Y1), .X0(X0), .Y0(Y0), .G3(\n4_与门异或门电路_1_g3 ),
    .P3(\n4_与门异或门电路_1_p3 ), .G2(\n4_与门异或门电路_1_g2 ), .P2(\n4_与门异或门电路_1_p2 ), .G1(\n4_与门异或门电路_1_g1 ),
    .P1(\n4_与门异或门电路_1_p1 ), .G0(\n4_与门异或门电路_1_g0 ), .P0(\n4_与门异或门电路_1_p0 ));
  xor xor_1 (S3, cla74182_1_c3, \n4_与门异或门电路_1_p3 );
  xor xor_2 (S2, cla74182_1_c2, \n4_与门异或门电路_1_p2 );
  xor xor_3 (S1, cla74182_1_c1, \n4_与门异或门电路_1_p1 );
  xor xor_4 (S0, \n4_与门异或门电路_1_p0 , C0);
endmodule

module \_8位快速加法器  (
  input  C0,
  input  X3,
  input  X2,
  input  X1,
  input  X0,
  input  X3_2,
  input  X2_2,
  input  X1_2,
  input  X0_2,
  input  Y3,
  input  Y2,
  input  Y1,
  input  Y0,
  input  Y3_2,
  input  Y2_2,
  input  Y1_2,
  input  Y0_2,
  output S3,
  output S2,
  output S0,
  output S0_2,
  output S3_2,
  output S2_2,
  output S1,
  output S0_3
);

  wire cla74182_1_c1, \n4位快速加法器_1_gx , \n4位快速加法器_1_px , \n4位快速加法器_2_gx , \n4位快速加法器_2_px ;

  CLA74182 cla74182_1 (
    .G1(\n4位快速加法器_1_gx ), .P1(\n4位快速加法器_1_px ), .G0(\n4位快速加法器_2_gx ), .P0(\n4位快速加法器_2_px ), .C1(cla74182_1_c1));  // open: G3, P3, G2, P2, C0, Gx, Px, C4, C3, C2
  \_4位快速加法器  \u_4位快速加法器_1  (
    .Gx(\n4位快速加法器_1_gx ), .Px(\n4位快速加法器_1_px ), .S3(S3), .S2(S2), .S1(S0), .S0(S0_2), .X3(X3), .Y3(Y3),
    .X2(X2), .Y2(Y2), .X1(X1), .Y1(Y1), .X0(X0), .Y0(Y0), .C0(cla74182_1_c1));  // open: C4
  \_4位快速加法器  \u_4位快速加法器_2  (
    .Gx(\n4位快速加法器_2_gx ), .Px(\n4位快速加法器_2_px ), .S3(S3_2), .S2(S2_2), .S1(S1), .S0(S0_3), .X3(X3_2),
    .Y3(Y3_2), .X2(X2_2), .Y2(Y2_2), .X1(X1_2), .Y1(Y1_2), .X0(X0_2), .Y0(Y0_2), .C0(C0));  // open: C4
endmodule

module \_16位快速加法器  (
  input  C0,
  input  X15,
  input  X14,
  input  X13,
  input  X12,
  input  X11,
  input  X10,
  input  X9,
  input  X8,
  input  X7,
  input  X6,
  input  X5,
  input  X4,
  input  X3,
  input  X2,
  input  X1,
  input  X0,
  input  SUB,
  input  Y15,
  input  Y14,
  input  Y13,
  input  Y12,
  input  Y11,
  input  Y10,
  input  Y9,
  input  Y8,
  input  Y7,
  input  Y6,
  input  Y5,
  input  Y4,
  input  Y3,
  input  Y2,
  input  Y1,
  input  Y0,
  output Px,
  output Gx,
  output C4,
  output out_38,
  output out_39,
  output out_40,
  output S4,
  output out_42,
  output out_43,
  output out_44,
  output S0,
  output S15,
  output out_47,
  output out_48,
  output S12,
  output out_50,
  output out_51,
  output out_52,
  output S8
);

  wire cla74182_1_c1, cla74182_1_c2, cla74182_1_c3, \n4位快速加法器_1_gx , \n4位快速加法器_1_px , \n4位快速加法器_2_gx ,
       \n4位快速加法器_2_px , \n4位快速加法器_3_gx , \n4位快速加法器_3_px , \n4位快速加法器_4_gx , \n4位快速加法器_4_px , \n4位求补_1_b0 ,
       \n4位求补_1_b2 , \n4位求补_1_b3 , \n4位求补_2_b0 , \n4位求补_2_b1 , \n4位求补_2_b2 , \n4位求补_2_b3 , \n4位求补_2_c1 ,
       \n4位求补_3_b0 , \n4位求补_3_b1 , \n4位求补_3_b2 , \n4位求补_3_b3 , \n4位求补_3_c1 , \n4位求补_4_b0 , \n4位求补_4_b1 ,
       \n4位求补_4_b2 , \n4位求补_4_b3 , \n4位求补_4_c1 ;

  \_4位快速加法器  \u_4位快速加法器_1  (
    .Gx(\n4位快速加法器_1_gx ), .Px(\n4位快速加法器_1_px ), .S3(S15), .S2(out_47), .S1(out_48), .S0(S12), .X3(X15),
    .Y3(\n4位求补_1_b3 ), .X2(X14), .Y2(\n4位求补_1_b2 ), .X1(X13), .Y1(\n4位求补_1_b2 ), .X0(X12), .Y0(\n4位求补_1_b0 ),
    .C0(cla74182_1_c3));  // open: C4
  \_4位求补  \u_4位求补_1  (
    .\S_1启用求补_S_0输出原值 (SUB), .B3(\n4位求补_1_b3 ), .B2(\n4位求补_1_b2 ), .B1(\n4位求补_1_b2 ), .B0(\n4位求补_1_b0 ),
    .A3(Y15), .A2(Y14), .A1(Y13), .A0(Y12), .\C0_1_表示已找到末位1_求反 (\n4位求补_2_c1 ));  // open: C1
  CLA74182 cla74182_1 (
    .G3(\n4位快速加法器_1_gx ), .P3(\n4位快速加法器_1_px ), .G2(\n4位快速加法器_2_gx ), .P2(\n4位快速加法器_2_px ),
    .G1(\n4位快速加法器_3_gx ), .P1(\n4位快速加法器_3_px ), .G0(\n4位快速加法器_4_gx ), .P0(\n4位快速加法器_4_px ), .C0(C0), .Gx(Gx),
    .Px(Px), .C4(C4), .C3(cla74182_1_c3), .C2(cla74182_1_c2), .C1(cla74182_1_c1));
  \_4位快速加法器  \u_4位快速加法器_2  (
    .Gx(\n4位快速加法器_2_gx ), .Px(\n4位快速加法器_2_px ), .S3(out_50), .S2(out_51), .S1(out_52), .S0(S8), .X3(X11),
    .Y3(\n4位求补_2_b3 ), .X2(X10), .Y2(\n4位求补_2_b2 ), .X1(X9), .Y1(\n4位求补_2_b1 ), .X0(X8), .Y0(\n4位求补_2_b0 ),
    .C0(cla74182_1_c2));  // open: C4
  \_4位求补  \u_4位求补_2  (
    .\S_1启用求补_S_0输出原值 (SUB), .B3(\n4位求补_2_b3 ), .B2(\n4位求补_2_b2 ), .B1(\n4位求补_2_b1 ), .B0(\n4位求补_2_b0 ),
    .A3(Y11), .A2(Y10), .A1(Y9), .A0(Y8), .\C0_1_表示已找到末位1_求反 (\n4位求补_3_c1 ), .C1(\n4位求补_2_c1 ));
  \_4位快速加法器  \u_4位快速加法器_3  (
    .Gx(\n4位快速加法器_3_gx ), .Px(\n4位快速加法器_3_px ), .S3(out_38), .S2(out_39), .S1(out_40), .S0(S4), .X3(X7),
    .Y3(\n4位求补_3_b3 ), .X2(X6), .Y2(\n4位求补_3_b2 ), .X1(X5), .Y1(\n4位求补_3_b1 ), .X0(X4), .Y0(\n4位求补_3_b0 ),
    .C0(cla74182_1_c1));  // open: C4
  \_4位求补  \u_4位求补_3  (
    .\S_1启用求补_S_0输出原值 (SUB), .B3(\n4位求补_3_b3 ), .B2(\n4位求补_3_b2 ), .B1(\n4位求补_3_b1 ), .B0(\n4位求补_3_b0 ),
    .A3(Y7), .A2(Y6), .A1(Y5), .A0(Y4), .\C0_1_表示已找到末位1_求反 (\n4位求补_4_c1 ), .C1(\n4位求补_3_c1 ));
  \_4位快速加法器  \u_4位快速加法器_4  (
    .Gx(\n4位快速加法器_4_gx ), .Px(\n4位快速加法器_4_px ), .S3(out_42), .S2(out_43), .S1(out_44), .S0(S0), .X3(X3),
    .Y3(\n4位求补_4_b3 ), .X2(X2), .Y2(\n4位求补_4_b2 ), .X1(X1), .Y1(\n4位求补_4_b1 ), .X0(X0), .Y0(\n4位求补_4_b0 ),
    .C0(C0));  // open: C4
  \_4位求补  \u_4位求补_4  (
    .\S_1启用求补_S_0输出原值 (SUB), .B3(\n4位求补_4_b3 ), .B2(\n4位求补_4_b2 ), .B1(\n4位求补_4_b1 ), .B0(\n4位求补_4_b0 ),
    .A3(Y3), .A2(Y2), .A1(Y1), .A0(Y0), .\C0_1_表示已找到末位1_求反 (1'b0), .C1(\n4位求补_4_c1 ));
endmodule

module \_32位快速加法器  (
  input  in_1,
  input  in_2,
  input  in_3,
  input  in_4,
  input  in_5,
  input  in_6,
  input  in_7,
  input  in_8,
  input  in_9,
  input  in_10,
  input  in_11,
  input  in_12,
  input  in_13,
  input  in_14,
  input  in_15,
  input  in_16,
  input  in_17,
  input  in_18,
  input  in_19,
  input  in_20,
  input  in_21,
  input  in_22,
  input  in_23,
  input  in_24,
  input  in_25,
  input  in_26,
  input  in_27,
  input  in_28,
  input  in_29,
  input  in_30,
  input  in_31,
  input  in_32,
  input  in_33,
  input  in_34,
  input  in_35,
  input  in_36,
  input  in_37,
  input  in_38,
  input  in_39,
  input  in_40,
  input  in_41,
  input  in_42,
  input  in_43,
  input  in_44,
  input  in_45,
  input  in_46,
  input  in_47,
  input  in_48,
  input  in_49,
  input  in_50,
  input  in_51,
  input  in_52,
  input  in_53,
  input  in_54,
  input  in_55,
  input  in_56,
  input  in_57,
  input  in_58,
  input  in_59,
  input  in_60,
  input  in_61,
  input  in_62,
  input  in_63,
  input  in_64,
  input  in_65,
  output out_66,
  output out_67,
  output out_68,
  output S0,
  output out_70,
  output out_71,
  output out_72,
  output S0_2,
  output out_74,
  output out_75,
  output out_76,
  output S4,
  output out_78,
  output out_79,
  output out_80,
  output S0_3,
  output out_82,
  output out_83,
  output out_84,
  output S0_4,
  output out_86,
  output out_87,
  output out_88,
  output S0_5,
  output out_90,
  output out_91,
  output out_92,
  output S4_2,
  output out_94,
  output out_95,
  output out_96,
  output S0_6,
  output Gx,
  output Px,
  output C32
);

  wire cla74182_1_c1, \n16位快速加法器_2_gx , \n16位快速加法器_2_px ;

  \_16位快速加法器  \u_16位快速加法器_1  (
    .C4(C32), .Gx(Gx), .Px(Px), .S15(out_82), .out_47(out_83), .out_48(out_84), .S12(S0_4), .out_50(out_86),
    .out_51(out_87), .out_52(out_88), .S8(S0_5), .out_38(out_90), .out_39(out_91), .out_40(out_92),
    .S4(S4_2), .out_42(out_94), .out_43(out_95), .out_44(out_96), .S0(S0_6), .X15(in_2), .Y15(in_34),
    .X14(in_3), .Y14(in_35), .X13(in_4), .Y13(in_36), .X12(in_5), .Y12(in_37), .X11(in_6), .Y11(in_38),
    .X10(in_7), .Y10(in_39), .X9(in_8), .Y9(in_40), .X8(in_9), .Y8(in_41), .X7(in_10), .Y7(in_42),
    .X6(in_11), .Y6(in_43), .X5(in_12), .Y5(in_44), .X4(in_13), .Y4(in_45), .X3(in_14), .Y3(in_46),
    .X2(in_15), .Y2(in_47), .X1(in_16), .Y1(in_48), .X0(in_17), .Y0(in_49), .C0(cla74182_1_c1));  // open: SUB
  CLA74182 cla74182_1 (
    .G0(\n16位快速加法器_2_gx ), .P0(\n16位快速加法器_2_px ), .C0(in_1), .C1(cla74182_1_c1));  // open: G3, P3, G2, P2, G1, P1, Gx, Px, C4, C3, C2
  \_16位快速加法器  \u_16位快速加法器_2  (
    .Gx(\n16位快速加法器_2_gx ), .Px(\n16位快速加法器_2_px ), .S15(out_66), .out_47(out_67), .out_48(out_68), .S12(S0),
    .out_50(out_70), .out_51(out_71), .out_52(out_72), .S8(S0_2), .out_38(out_74), .out_39(out_75),
    .out_40(out_76), .S4(S4), .out_42(out_78), .out_43(out_79), .out_44(out_80), .S0(S0_3), .X15(in_18),
    .Y15(in_50), .X14(in_19), .Y14(in_51), .X13(in_20), .Y13(in_52), .X12(in_21), .Y12(in_53), .X11(in_22),
    .Y11(in_54), .X10(in_23), .Y10(in_55), .X9(in_24), .Y9(in_56), .X8(in_25), .Y8(in_57), .X7(in_26),
    .Y7(in_58), .X6(in_27), .Y6(in_59), .X5(in_28), .Y5(in_60), .X4(in_29), .Y4(in_61), .X3(in_30),
    .Y3(in_62), .X2(in_31), .Y2(in_63), .X1(in_32), .Y1(in_64), .X0(in_33), .Y0(in_65), .C0(in_1));  // open: C4, SUB

  // Notes on the sheet:
  //   减去10~0时标志位会出问题
endmodule

// 2补
module \_2位求补  (
  input  A,
  input  B,
  input  S,
  input  C0,
  output F1,
  output F0,
  output C1
);

  wire and_1_out, and_2_out, and_3_out, and_4_out, and_5_out, and_6_out, and_7_out, and_8_out, and_9_out,
       and_10_out, not_1_out, not_2_out, not_3_out, not_4_out, not_5_out, not_6_out, not_7_out, not_8_out;

  not not_1 (not_1_out, A);
  and and_1 (and_1_out, not_1_out, S, C0);
  not not_2 (not_2_out, A);
  and and_2 (and_2_out, not_2_out, B, S);
  not not_3 (not_3_out, B);
  and and_3 (and_3_out, A, not_3_out, not_4_out);
  not not_4 (not_4_out, C0);
  and and_4 (and_4_out, A, not_5_out);
  not not_5 (not_5_out, S);
  not not_6 (not_6_out, B);
  and and_5 (and_5_out, not_6_out, S, C0);
  and and_6 (and_6_out, B, not_7_out);
  not not_7 (not_7_out, S);
  and and_7 (and_7_out, B, not_8_out);
  not not_8 (not_8_out, C0);
  and and_8 (and_8_out, S, C0);
  and and_9 (and_9_out, B, S);
  and and_10 (and_10_out, A, S);
  or or_1 (F1, and_1_out, and_2_out, and_3_out, and_4_out);
  or or_2 (F0, and_5_out, and_6_out, and_7_out);
  or or_3 (C1, and_8_out, and_9_out, and_10_out);
endmodule

module \_4位求补  (
  input  \C0_1_表示已找到末位1_求反 ,
  input  \S_1启用求补_S_0输出原值 ,
  input  A3,
  input  A2,
  input  A1,
  input  A0,
  output B3,
  output B2,
  output B1,
  output B0,
  output C1
);

  wire \n2位求补_2_c1 ;

  \_2位求补  \u_2位求补_1  (.A(A3), .B(A2), .S(\S_1启用求补_S_0输出原值 ), .C0(\n2位求补_2_c1 ), .F1(B3), .F0(B2), .C1(C1));
  \_2位求补  \u_2位求补_2  (
    .A(A1), .B(A0), .S(\S_1启用求补_S_0输出原值 ), .C0(\C0_1_表示已找到末位1_求反 ), .F1(B1), .F0(B0), .C1(\n2位求补_2_c1 ));
endmodule

module \_4位快速加_减法器  (
  input  C0,
  input  X3,
  input  X2,
  input  X1,
  input  X0,
  input  \补c0 ,
  input  SUB,
  input  Y3,
  input  Y2,
  input  Y1,
  input  Y0,
  output Gx,
  output Px,
  output S3,
  output S2,
  output S1,
  output S0,
  output C4,
  output OF,
  output \补c1 
);

  wire and_1_out, and_2_out, cla74182_1_c1, cla74182_1_c2, cla74182_1_c3, \n4_与门异或门电路_1_g0 ,
       \n4_与门异或门电路_1_g1 , \n4_与门异或门电路_1_g2 , \n4_与门异或门电路_1_g3 , \n4_与门异或门电路_1_p0 , \n4_与门异或门电路_1_p1 ,
       \n4_与门异或门电路_1_p2 , \n4_与门异或门电路_1_p3 , \n4位求补_1_b0 , \n4位求补_1_b1 , \n4位求补_1_b2 , \n4位求补_1_b3 ,
       not_1_out, not_2_out, not_3_out;

  or or_1 (OF, and_1_out, and_2_out);
  and and_1 (and_1_out, S3, not_1_out, not_2_out);
  not not_1 (not_1_out, \n4位求补_1_b3 );
  not not_2 (not_2_out, X3);
  not not_3 (not_3_out, S3);
  and and_2 (and_2_out, not_3_out, \n4位求补_1_b3 , X3);
  CLA74182 cla74182_1 (
    .G3(\n4_与门异或门电路_1_g3 ), .P3(\n4_与门异或门电路_1_p3 ), .G2(\n4_与门异或门电路_1_g2 ), .P2(\n4_与门异或门电路_1_p2 ),
    .G1(\n4_与门异或门电路_1_g1 ), .P1(\n4_与门异或门电路_1_p1 ), .G0(\n4_与门异或门电路_1_g0 ), .P0(\n4_与门异或门电路_1_p0 ), .C0(C0),
    .Gx(Gx), .Px(Px), .C4(C4), .C3(cla74182_1_c3), .C2(cla74182_1_c2), .C1(cla74182_1_c1));
  \_4_与门异或门电路  \u_4_与门异或门电路_1  (
    .X3(X3), .Y3(\n4位求补_1_b3 ), .X2(X2), .Y2(\n4位求补_1_b2 ), .X1(X1), .Y1(\n4位求补_1_b1 ), .X0(X0),
    .Y0(\n4位求补_1_b0 ), .G3(\n4_与门异或门电路_1_g3 ), .P3(\n4_与门异或门电路_1_p3 ), .G2(\n4_与门异或门电路_1_g2 ),
    .P2(\n4_与门异或门电路_1_p2 ), .G1(\n4_与门异或门电路_1_g1 ), .P1(\n4_与门异或门电路_1_p1 ), .G0(\n4_与门异或门电路_1_g0 ),
    .P0(\n4_与门异或门电路_1_p0 ));
  xor xor_1 (S3, cla74182_1_c3, \n4_与门异或门电路_1_p3 );
  \_4位求补  \u_4位求补_1  (
    .\S_1启用求补_S_0输出原值 (SUB), .B3(\n4位求补_1_b3 ), .B2(\n4位求补_1_b2 ), .B1(\n4位求补_1_b1 ), .B0(\n4位求补_1_b0 ),
    .A3(Y3), .A2(Y2), .A1(Y1), .A0(Y0), .\C0_1_表示已找到末位1_求反 (\补c0 ), .C1(\补c1 ));
  xor xor_2 (S2, cla74182_1_c2, \n4_与门异或门电路_1_p2 );
  xor xor_3 (S1, cla74182_1_c1, \n4_与门异或门电路_1_p1 );
  xor xor_4 (S0, \n4_与门异或门电路_1_p0 , C0);

  // Notes on the sheet:
  //   根据结果:”负负得正“或“正正得负”，判断overflow
  //   SUB=1,求补(做减法)
  //   C0只负责进位 
endmodule

module \_8位快速加法_减法器  (
  input  C0,
  input  \补c0 ,
  input  SUB,
  input  X7,
  input  X6,
  input  X5,
  input  X4,
  input  X3,
  input  X2,
  input  X1,
  input  X0,
  input  Y7,
  input  Y6,
  input  Y5,
  input  Y4,
  input  Y3,
  input  Y2,
  input  Y1,
  input  Y0,
  output S3,
  output S2,
  output S0,
  output S0_2,
  output S3_2,
  output S2_2,
  output S1,
  output S0_3,
  output C1,
  output \补c1 ,
  output OF
);

  wire cla74182_1_c1, \n4位快速加_减法器_1_gx , \n4位快速加_减法器_1_px , \n4位快速加_减法器_2_gx , \n4位快速加_减法器_2_px ,
       \n4位快速加_减法器_2_补c1 ;

  \_4位快速加_减法器  \u_4位快速加_减法器_1  (
    .OF(OF), .C0(cla74182_1_c1), .\补c0 (\n4位快速加_减法器_2_补c1 ), .SUB(SUB), .Gx(\n4位快速加_减法器_1_gx ),
    .Px(\n4位快速加_减法器_1_px ), .S3(S3), .S2(S2), .S1(S0), .S0(S0_2), .X3(X7), .Y3(Y7), .X2(X6), .Y2(Y6),
    .X1(X5), .Y1(X4), .X0(X4), .Y0(Y4), .\补c1 (\补c1 ));  // open: C4
  CLA74182 cla74182_1 (
    .G1(\n4位快速加_减法器_1_gx ), .P1(\n4位快速加_减法器_1_px ), .G0(\n4位快速加_减法器_2_gx ), .P0(\n4位快速加_减法器_2_px ), .C0(C0),
    .C2(C1), .C1(cla74182_1_c1));  // open: G3, P3, G2, P2, Gx, Px, C4, C3
  \_4位快速加_减法器  \u_4位快速加_减法器_2  (
    .C0(C0), .\补c0 (\补c0 ), .SUB(SUB), .Gx(\n4位快速加_减法器_2_gx ), .Px(\n4位快速加_减法器_2_px ), .S3(S3_2), .S2(S2_2),
    .S1(S1), .S0(S0_3), .X3(X3), .Y3(Y3), .X2(X2), .Y2(Y2), .X1(X1), .Y1(Y1), .X0(X0), .Y0(Y0),
    .\补c1 (\n4位快速加_减法器_2_补c1 ));  // open: C4, OF

  assign Y5 = X4;
endmodule

module \_16位快速加_减法器  (
  input  C0,
  input  \补c0 ,
  input  X15,
  input  X14,
  input  X13,
  input  X12,
  input  X11,
  input  X10,
  input  X9,
  input  X8,
  input  X7,
  input  X6,
  input  X5,
  input  X4,
  input  X3,
  input  X2,
  input  X1,
  input  X0,
  input  SUB,
  input  Y15,
  input  Y14,
  input  Y13,
  input  Y12,
  input  Y11,
  input  Y10,
  input  Y9,
  input  Y8,
  input  Y7,
  input  Y6,
  input  Y5,
  input  Y4,
  input  Y3,
  input  Y2,
  input  Y1,
  input  Y0,
  output Px,
  output Gx,
  output C4,
  output out_39,
  output out_40,
  output out_41,
  output S4,
  output out_43,
  output out_44,
  output out_45,
  output S0,
  output S15,
  output out_48,
  output out_49,
  output S12,
  output out_51,
  output out_52,
  output out_53,
  output S8,
  output OF,
  output \补c1 
);

  wire cla74182_1_c1, cla74182_1_c2, cla74182_1_c3, \n4位快速加_减法器_1_gx , \n4位快速加_减法器_1_px , \n4位快速加_减法器_2_gx ,
       \n4位快速加_减法器_2_px , \n4位快速加_减法器_2_补c1 , \n4位快速加_减法器_3_gx , \n4位快速加_减法器_3_px , \n4位快速加_减法器_3_补c1 ,
       \n4位快速加_减法器_4_gx , \n4位快速加_减法器_4_px , \n4位快速加_减法器_4_补c1 ;

  \_4位快速加_减法器  \u_4位快速加_减法器_1  (
    .OF(OF), .C0(cla74182_1_c3), .\补c0 (\n4位快速加_减法器_2_补c1 ), .SUB(SUB), .Gx(\n4位快速加_减法器_1_gx ),
    .Px(\n4位快速加_减法器_1_px ), .S3(S15), .S2(out_48), .S1(out_49), .S0(S12), .X3(X15), .Y3(Y15), .X2(X14),
    .Y2(Y14), .X1(X13), .Y1(Y13), .X0(X12), .Y0(Y12), .\补c1 (\补c1 ));  // open: C4
  CLA74182 cla74182_1 (
    .G3(\n4位快速加_减法器_1_gx ), .P3(\n4位快速加_减法器_1_px ), .G2(\n4位快速加_减法器_2_gx ), .P2(\n4位快速加_减法器_2_px ),
    .G1(\n4位快速加_减法器_3_gx ), .P1(\n4位快速加_减法器_3_px ), .G0(\n4位快速加_减法器_4_gx ), .P0(\n4位快速加_减法器_4_px ), .C0(C0),
    .Gx(Gx), .Px(Px), .C4(C4), .C3(cla74182_1_c3), .C2(cla74182_1_c2), .C1(cla74182_1_c1));
  \_4位快速加_减法器  \u_4位快速加_减法器_2  (
    .C0(cla74182_1_c2), .\补c0 (\n4位快速加_减法器_3_补c1 ), .SUB(SUB), .Gx(\n4位快速加_减法器_2_gx ),
    .Px(\n4位快速加_减法器_2_px ), .S3(out_51), .S2(out_52), .S1(out_53), .S0(S8), .X3(X11), .Y3(Y11), .X2(X10),
    .Y2(Y10), .X1(X9), .Y1(Y9), .X0(X8), .Y0(Y8), .\补c1 (\n4位快速加_减法器_2_补c1 ));  // open: C4, OF
  \_4位快速加_减法器  \u_4位快速加_减法器_3  (
    .C0(cla74182_1_c1), .\补c0 (\n4位快速加_减法器_4_补c1 ), .SUB(SUB), .Gx(\n4位快速加_减法器_3_gx ),
    .Px(\n4位快速加_减法器_3_px ), .S3(out_39), .S2(out_40), .S1(out_41), .S0(S4), .X3(X7), .Y3(Y7), .X2(X6),
    .Y2(Y6), .X1(X5), .Y1(Y5), .X0(X4), .Y0(Y4), .\补c1 (\n4位快速加_减法器_3_补c1 ));  // open: C4, OF
  \_4位快速加_减法器  \u_4位快速加_减法器_4  (
    .C0(C0), .\补c0 (\补c0 ), .SUB(SUB), .Gx(\n4位快速加_减法器_4_gx ), .Px(\n4位快速加_减法器_4_px ), .S3(out_43),
    .S2(out_44), .S1(out_45), .S0(S0), .X3(X3), .Y3(Y3), .X2(X2), .Y2(Y2), .X1(X1), .Y1(Y1), .X0(X0),
    .Y0(Y0), .\补c1 (\n4位快速加_减法器_4_补c1 ));  // open: C4, OF
endmodule

// ALU
module \_32位快速加法_减法器  (
  input  C0,
  input  SUB,
  input  [31:0] X,
  input  [31:0] Y,
  output [31:0] OUT,
  output CF,
  output OF,
  output ZF
);

  wire \n16位快速加_减法器_2_c4 , \n16位快速加_减法器_2_补c1 ;

  \_16位快速加_减法器  \u_16位快速加_减法器_1  (
    .C4(CF), .OF(OF), .C0(\n16位快速加_减法器_2_c4 ), .\补c0 (\n16位快速加_减法器_2_补c1 ), .SUB(SUB), .S15(OUT[31]),
    .out_48(OUT[30]), .out_49(OUT[29]), .S12(OUT[28]), .out_51(OUT[27]), .out_52(OUT[26]), .out_53(OUT[25]),
    .S8(OUT[24]), .out_39(OUT[23]), .out_40(OUT[22]), .out_41(OUT[21]), .S4(OUT[20]), .out_43(OUT[19]),
    .out_44(OUT[18]), .out_45(OUT[17]), .S0(OUT[16]), .X15(X[31]), .Y15(Y[31]), .X14(X[30]), .Y14(Y[30]),
    .X13(X[29]), .Y13(Y[29]), .X12(X[28]), .Y12(Y[28]), .X11(X[27]), .Y11(Y[27]), .X10(X[26]), .Y10(Y[26]),
    .X9(X[25]), .Y9(Y[25]), .X8(X[24]), .Y8(Y[24]), .X7(X[23]), .Y7(Y[23]), .X6(X[22]), .Y6(Y[22]),
    .X5(X[21]), .Y5(Y[21]), .X4(X[20]), .Y4(Y[20]), .X3(X[19]), .Y3(Y[19]), .X2(X[18]), .Y2(Y[18]),
    .X1(X[17]), .Y1(Y[17]), .X0(X[16]), .Y0(Y[16]));  // open: 补c1, Gx, Px
  \_16位快速加_减法器  \u_16位快速加_减法器_2  (
    .C4(\n16位快速加_减法器_2_c4 ), .\补c1 (\n16位快速加_减法器_2_补c1 ), .C0(C0), .\补c0 (1'b0), .SUB(SUB), .S15(OUT[15]),
    .out_48(OUT[14]), .out_49(OUT[13]), .S12(OUT[12]), .out_51(OUT[11]), .out_52(OUT[10]), .out_53(OUT[9]),
    .S8(OUT[8]), .out_39(OUT[7]), .out_40(OUT[6]), .out_41(OUT[5]), .S4(OUT[4]), .out_43(OUT[3]),
    .out_44(OUT[2]), .out_45(OUT[1]), .S0(OUT[0]), .X15(X[15]), .Y15(Y[15]), .X14(X[14]), .Y14(Y[14]),
    .X13(X[13]), .Y13(Y[13]), .X12(X[12]), .Y12(Y[12]), .X11(X[11]), .Y11(Y[11]), .X10(X[10]), .Y10(Y[10]),
    .X9(X[9]), .Y9(Y[9]), .X8(X[8]), .Y8(Y[8]), .X7(X[7]), .Y7(Y[7]), .X6(X[6]), .Y6(Y[6]), .X5(X[5]),
    .Y5(Y[5]), .X4(X[4]), .Y4(Y[4]), .X3(X[3]), .Y3(Y[3]), .X2(X[2]), .Y2(Y[2]), .X1(X[1]), .Y1(Y[1]),
    .X0(X[0]), .Y0(Y[0]));  // open: OF, Gx, Px
  Comparator #(.width(32), .mode("twosComplement")) comparator_1 (.a(Y), .b(X), .eq(ZF));  // open: gt, lt
endmodule

module FA (
  input  Cin,
  input  Xi,
  input  Yi,
  output Cout,
  output Si
);

  wire and_1_out, and_2_out, xor_2_out;

  or or_1 (Cout, and_1_out, and_2_out);
  and and_1 (and_1_out, Xi, Yi);
  and and_2 (and_2_out, Cin, xor_2_out);
  xor xor_1 (Si, Cin, xor_2_out);
  xor xor_2 (xor_2_out, Xi, Yi);
endmodule

module \与门阵列  (
  input  X0,
  input  X1,
  input  X2,
  input  X3,
  input  X4,
  input  Y0,
  input  Y1,
  input  Y2,
  input  Y3,
  input  Y4,
  output X0Y0,
  output X0Y1,
  output X0Y2,
  output X0Y3,
  output X0Y4,
  output X1Y0,
  output X1Y1,
  output X1Y2,
  output X1Y3,
  output X1Y4,
  output X2Y0,
  output X2Y1,
  output X2Y2,
  output X2Y3,
  output X2Y4,
  output X3Y0,
  output X3Y1,
  output X3Y2,
  output X3Y3,
  output X3Y4,
  output X4Y0,
  output X4Y1,
  output X4Y2,
  output X4Y3,
  output X4Y4
);

  and and_1 (X0Y0, X0, Y0);
  and and_2 (X0Y1, X0, Y1);
  and and_3 (X0Y2, X0, Y2);
  and and_4 (X0Y3, X0, Y3);
  and and_5 (X0Y4, X0, Y4);
  and and_6 (X1Y0, X1, Y0);
  and and_7 (X1Y1, X1, Y1);
  and and_8 (X1Y2, X1, Y2);
  and and_9 (X1Y3, X1, Y3);
  and and_10 (X1Y4, X1, Y4);
  and and_11 (X2Y0, X2, Y0);
  and and_12 (X2Y1, X2, Y1);
  and and_13 (X2Y2, X2, Y2);
  and and_14 (X2Y3, X2, Y3);
  and and_15 (X2Y4, X2, Y4);
  and and_16 (X3Y0, X3, Y0);
  and and_17 (X3Y1, X3, Y1);
  and and_18 (X3Y2, X3, Y2);
  and and_19 (X3Y3, X3, Y3);
  and and_20 (X3Y4, X3, Y4);
  and and_21 (X4Y0, X4, Y0);
  and and_22 (X4Y1, X4, Y1);
  and and_23 (X4Y2, X4, Y2);
  and and_24 (X4Y3, X4, Y3);
  and and_25 (X4Y4, X4, Y4);
endmodule

module \阵列乘法器  (
  input  [4:0] Y,
  input  [4:0] X,
  output Cout,
  output P7,
  output P6,
  output P5,
  output P4,
  output P3,
  output P2,
  output P1,
  output P0,
  output P0_2
);

  wire fa_2_cout, fa_2_si, fa_3_cout, fa_4_cout, fa_4_si, fa_5_cout, fa_5_si, fa_7_cout, fa_7_si, fa_8_cout,
       fa_8_si, fa_9_cout, fa_9_si, fa_11_cout, fa_11_si, fa_12_cout, fa_12_si, fa_13_cout, fa_13_si,
       fa_14_cout, fa_15_cout, fa_15_si, fa_16_cout, fa_16_si, fa_17_cout, fa_18_cout, fa_18_si, fa_19_cout,
       fa_20_cout, X0Y1, X0Y2, X0Y3, X0Y4, X1Y0, X1Y1, X1Y2, X1Y3, X1Y4, X2Y0, X2Y1, X2Y2, X2Y3, X2Y4, X3Y0,
       X3Y1, X3Y2, X3Y3, X3Y4, X4Y0, X4Y1, X4Y2, X4Y3, X4Y4;

  \与门阵列  \u_与门阵列_1  (
    .X0(X[0]), .X1(X[1]), .X2(X[2]), .X3(X[3]), .X4(X[4]), .Y0(Y[0]), .Y1(Y[1]), .Y2(Y[2]), .Y3(Y[3]),
    .Y4(Y[4]), .X0Y0(P0_2), .X0Y1(X0Y1), .X0Y2(X0Y2), .X0Y3(X0Y3), .X0Y4(X0Y4), .X1Y0(X1Y0), .X1Y1(X1Y1),
    .X1Y2(X1Y2), .X1Y3(X1Y3), .X1Y4(X1Y4), .X2Y0(X2Y0), .X2Y1(X2Y1), .X2Y2(X2Y2), .X2Y3(X2Y3), .X2Y4(X2Y4),
    .X3Y0(X3Y0), .X3Y1(X3Y1), .X3Y2(X3Y2), .X3Y3(X3Y3), .X3Y4(X3Y4), .X4Y0(X4Y0), .X4Y1(X4Y1), .X4Y2(X4Y2),
    .X4Y3(X4Y3), .X4Y4(X4Y4));
  FA fa_1 (.Cout(Cout), .Si(P7), .Cin(1'b0), .Xi(fa_2_cout), .Yi(fa_3_cout));
  FA fa_2 (.Cout(fa_2_cout), .Si(fa_2_si), .Cin(fa_4_cout), .Xi(X4Y3), .Yi(X3Y4));
  FA fa_3 (.Cout(fa_3_cout), .Si(P6), .Cin(1'b0), .Xi(fa_2_si), .Yi(fa_5_cout));
  FA fa_4 (.Cout(fa_4_cout), .Si(fa_4_si), .Cin(fa_7_cout), .Xi(X4Y2), .Yi(X3Y3));
  FA fa_5 (.Cout(fa_5_cout), .Si(fa_5_si), .Cin(fa_8_cout), .Xi(fa_4_si), .Yi(X2Y4));
  FA fa_6 (.Si(P5), .Cin(1'b0), .Xi(fa_5_si), .Yi(fa_9_cout));  // open: Cout
  FA fa_7 (.Cout(fa_7_cout), .Si(fa_7_si), .Cin(fa_11_cout), .Xi(X4Y1), .Yi(X3Y2));
  FA fa_8 (.Cout(fa_8_cout), .Si(fa_8_si), .Cin(fa_12_cout), .Xi(fa_7_si), .Yi(X2Y3));
  FA fa_9 (.Cout(fa_9_cout), .Si(fa_9_si), .Cin(fa_13_cout), .Xi(fa_8_si), .Yi(X1Y4));
  FA fa_10 (.Si(P4), .Cin(1'b0), .Xi(fa_9_si), .Yi(fa_14_cout));  // open: Cout
  FA fa_11 (.Cout(fa_11_cout), .Si(fa_11_si), .Cin(1'b0), .Xi(X4Y0), .Yi(X3Y1));
  FA fa_12 (.Cout(fa_12_cout), .Si(fa_12_si), .Cin(fa_15_cout), .Xi(fa_11_si), .Yi(X2Y3));
  FA fa_13 (.Cout(fa_13_cout), .Si(fa_13_si), .Cin(fa_16_cout), .Xi(fa_12_si), .Yi(X1Y3));
  FA fa_14 (.Cout(fa_14_cout), .Si(P3), .Cin(fa_17_cout), .Xi(fa_13_si), .Yi(X0Y4));
  FA fa_15 (.Cout(fa_15_cout), .Si(fa_15_si), .Cin(1'b0), .Xi(X3Y0), .Yi(X2Y1));
  FA fa_16 (.Cout(fa_16_cout), .Si(fa_16_si), .Cin(fa_18_cout), .Xi(fa_15_si), .Yi(X1Y2));
  FA fa_17 (.Cout(fa_17_cout), .Si(P2), .Cin(fa_19_cout), .Xi(fa_16_si), .Yi(X0Y3));
  FA fa_18 (.Cout(fa_18_cout), .Si(fa_18_si), .Cin(1'b0), .Xi(X2Y0), .Yi(X1Y1));
  FA fa_19 (.Cout(fa_19_cout), .Si(P1), .Cin(fa_20_cout), .Xi(fa_18_si), .Yi(X0Y2));
  FA fa_20 (.Cout(fa_20_cout), .Si(P0), .Cin(1'b0), .Xi(X1Y0), .Yi(X0Y1));

  // Other names for the same wires on the sheet: X0Y0 = P0_2
endmodule

// 7段_译码
module \_7段显码_译码  (
  input  DHigh,
  input  B,
  input  C,
  input  ALow,
  output a,
  output b_2,
  output c_2,
  output d,
  output e,
  output f,
  output g
);

  wire and_1_out, and_2_out, and_3_out, and_4_out, and_5_out, and_6_out, and_7_out, and_8_out, and_9_out,
       and_10_out, and_11_out, and_12_out, and_13_out, and_14_out, and_15_out, and_16_out, and_17_out,
       and_18_out, and_19_out, and_20_out, and_21_out, and_22_out, and_23_out, and_24_out, and_25_out,
       and_26_out, and_27_out, and_28_out, and_29_out, and_30_out, and_31_out, not_1_out, not_2_out,
       not_3_out, not_4_out, not_5_out, not_6_out, not_7_out, not_8_out, not_9_out, not_10_out, not_11_out,
       not_12_out, not_13_out, not_14_out, not_15_out, not_16_out, not_17_out, not_18_out, not_19_out,
       not_20_out, not_21_out, not_22_out, not_23_out, not_24_out, not_25_out, not_26_out, not_27_out,
       not_28_out, not_29_out, not_30_out, not_31_out, not_32_out, not_33_out, not_34_out, not_35_out,
       not_36_out, not_37_out, not_38_out, not_39_out, not_40_out, not_41_out, not_42_out, not_43_out;

  not not_1 (not_1_out, B);
  and and_1 (and_1_out, not_1_out, not_2_out);
  not not_2 (not_2_out, ALow);
  not not_3 (not_3_out, DHigh);
  and and_2 (and_2_out, not_3_out, C);
  and and_3 (and_3_out, B, ALow);
  and and_4 (and_4_out, DHigh, not_4_out);
  not not_4 (not_4_out, C);
  not not_5 (not_5_out, B);
  not not_6 (not_6_out, C);
  and and_5 (and_5_out, not_6_out, not_7_out);
  not not_7 (not_7_out, ALow);
  not not_8 (not_8_out, DHigh);
  and and_6 (and_6_out, not_8_out, C, ALow);
  and and_7 (and_7_out, DHigh, not_9_out);
  not not_9 (not_9_out, C);
  and and_8 (and_8_out, DHigh, not_10_out);
  not not_10 (not_10_out, ALow);
  not not_11 (not_11_out, DHigh);
  and and_9 (and_9_out, not_11_out, not_12_out);
  not not_12 (not_12_out, C);
  and and_10 (and_10_out, B, C);
  and and_11 (and_11_out, DHigh, not_13_out);
  not not_13 (not_13_out, B);
  not not_14 (not_14_out, B);
  and and_12 (and_12_out, not_14_out, not_15_out);
  not not_15 (not_15_out, ALow);
  not not_16 (not_16_out, DHigh);
  not not_17 (not_17_out, B);
  and and_13 (and_13_out, not_16_out, not_17_out, C);
  not not_18 (not_18_out, DHigh);
  and and_14 (and_14_out, not_18_out, C, not_19_out);
  not not_19 (not_19_out, ALow);
  and and_15 (and_15_out, B, not_20_out, ALow);
  not not_20 (not_20_out, C);
  and and_16 (and_16_out, DHigh, not_21_out);
  not not_21 (not_21_out, C);
  and and_17 (and_17_out, DHigh, B, ALow);
  not not_22 (not_22_out, B);
  and and_18 (and_18_out, not_22_out, not_23_out);
  not not_23 (not_23_out, ALow);
  not not_24 (not_24_out, DHigh);
  and and_19 (and_19_out, not_24_out, C, not_25_out);
  not not_25 (not_25_out, ALow);
  and and_20 (and_20_out, DHigh, not_26_out, not_27_out);
  not not_26 (not_26_out, C);
  not not_27 (not_27_out, ALow);
  not not_28 (not_28_out, DHigh);
  not not_29 (not_29_out, C);
  and and_21 (and_21_out, not_28_out, not_29_out, not_30_out);
  not not_30 (not_30_out, ALow);
  not not_31 (not_31_out, DHigh);
  and and_22 (and_22_out, not_31_out, B, not_32_out);
  not not_32 (not_32_out, C);
  not not_33 (not_33_out, DHigh);
  and and_23 (and_23_out, not_33_out, B, not_34_out);
  not not_34 (not_34_out, ALow);
  not not_35 (not_35_out, B);
  and and_24 (and_24_out, DHigh, not_35_out, not_36_out);
  not not_36 (not_36_out, C);
  not not_37 (not_37_out, B);
  and and_25 (and_25_out, DHigh, not_37_out, not_38_out);
  not not_38 (not_38_out, ALow);
  and and_26 (and_26_out, DHigh, B, C);
  not not_39 (not_39_out, DHigh);
  not not_40 (not_40_out, B);
  and and_27 (and_27_out, not_39_out, not_40_out, C);
  and and_28 (and_28_out, B, not_41_out);
  not not_41 (not_41_out, C);
  and and_29 (and_29_out, B, not_42_out);
  not not_42 (not_42_out, ALow);
  and and_30 (and_30_out, DHigh, not_43_out);
  not not_43 (not_43_out, C);
  and and_31 (and_31_out, DHigh, B);
  or or_1 (a, and_1_out, and_2_out, and_3_out, and_4_out);
  or or_2 (b_2, not_5_out, and_5_out, and_6_out, and_7_out, and_8_out);
  or or_3 (c_2, and_9_out, ALow, and_10_out, and_11_out);
  or or_4 (e, and_18_out, and_19_out, and_20_out);
  or or_5 (g, and_27_out, and_28_out, and_29_out, and_30_out, and_31_out);
  or or_6 (d, and_12_out, and_13_out, and_14_out, and_15_out, and_16_out, and_17_out);
  or or_7 (f, and_21_out, and_22_out, and_23_out, and_24_out, and_25_out, and_26_out);
endmodule

module \七段显码  (
  input  in_1,
  input  \重置 
);

  wire clock_1_out, \n7段显码_译码_1_a , \n7段显码_译码_1_b_2 , \n7段显码_译码_1_c_2 , \n7段显码_译码_1_d , \n7段显码_译码_1_e ,
       \n7段显码_译码_1_f , \n7段显码_译码_1_g ;
  wire [3:0] counter_1_q;

  Clock #(.highDuration(5), .lowDuration(5)) clock_1 (.out(clock_1_out));
  Counter #(.width(4), .max('h9), .ongoal("wrap"), .trigger("rising"), .behavior("new")) counter_1 (
    .load(in_1), .Q(counter_1_q), .clk(clock_1_out), .clr(\重置 ), .down(in_1));  // open: D, count, carry, preset
  \_7段显码_译码  \u_7段显码_译码_1  (
    .DHigh(counter_1_q[3]), .B(counter_1_q[2]), .C(counter_1_q[1]), .ALow(counter_1_q[0]),
    .a(\n7段显码_译码_1_a ), .b_2(\n7段显码_译码_1_b_2 ), .c_2(\n7段显码_译码_1_c_2 ), .d(\n7段显码_译码_1_d ),
    .e(\n7段显码_译码_1_e ), .f(\n7段显码_译码_1_f ), .g(\n7段显码_译码_1_g ));
  _7_Segment_Display #(.active("true")) u_7_segment_display_1 (
    .g(\n7段显码_译码_1_g ), .f(\n7段显码_译码_1_f ), .a(\n7段显码_译码_1_a ), .b(\n7段显码_译码_1_b_2 ), .e(\n7段显码_译码_1_e ),
    .d(\n7段显码_译码_1_d ), .c(\n7段显码_译码_1_c_2 ));  // open: dp
endmodule

module \检测101  (
  input  Z,
  output out_2,
  output Z_2,
  output out_4
);

  wire clock_1_out, d_ff_1_q, d_ff_2_qn, nor_1_out;

  Clock #(.highDuration(20), .lowDuration(20)) clock_1 (.out(clock_1_out));
  D_Flip_Flop #(.trigger("rising"), .Pre_Clr_Positions("LEGACY"), .NegatePresetClear("false"), .enable("false"), .NewFFLayout("true")) d_ff_1 (
    .clk(clock_1_out), .D(nor_1_out), .Q(d_ff_1_q));  // open: Qn, preset, reset
  nor nor_1 (nor_1_out, Z, d_ff_2_qn, d_ff_1_q);
  D_Flip_Flop #(.trigger("rising"), .Pre_Clr_Positions("LEGACY"), .NegatePresetClear("false"), .enable("false"), .NewFFLayout("true")) d_ff_2 (
    .clk(clock_1_out), .D(Z), .Qn(d_ff_2_qn));  // open: Q, preset, reset
  and and_1 (out_2, d_ff_1_q, d_ff_2_qn, Z);

  assign out_4 = out_2;
  assign Z_2 = out_2;

  // Notes on the sheet:
  //   y2
  //   y1
endmodule

// 4位计数器
module \码表_1位BCD计数器  (
  input  EN,
  input  CLK,
  input  Reset,
  output [3:0] out_4,
  output Cout
);

  Counter #(.width(4), .max('h9), .ongoal("wrap"), .trigger("falling"), .behavior("new")) counter_1 (
    .count(EN), .Q(out_4), .carry(Cout), .clk(CLK), .clr(Reset));  // open: load, D, preset, down
endmodule

// 4位BCD计数器
module \码表_4位BCD计数器  (
  input  CLK,
  input  En_Stop,
  input  ReStart,
  output [15:0] Data,
  output [6:0] D,
  output [6:0] A,
  output [6:0] C,
  output [6:0] B
);

  wire and_1_out, and_2_out, d_ff_1_q, not_1_out, not_2_out, \码表_1位bcd计数器_2_cout , \码表_1位bcd计数器_3_cout ,
       \码表_1位bcd计数器_4_cout ;

  \_7段显码_译码  \u_7段显码_译码_1  (
    .DHigh(Data[15]), .B(Data[14]), .C(Data[13]), .ALow(Data[12]), .a(D[0]), .b_2(D[1]), .c_2(D[2]),
    .d(D[3]), .e(D[4]), .f(D[5]), .g(D[6]));
  \_7段显码_译码  \u_7段显码_译码_2  (
    .DHigh(Data[11]), .B(Data[10]), .C(Data[9]), .ALow(Data[8]), .a(C[0]), .b_2(C[1]), .c_2(C[2]), .d(C[3]),
    .e(C[4]), .f(C[5]), .g(C[6]));
  \码表_1位BCD计数器  \u_码表_1位bcd计数器_1  (
    .out_4(Data[15:12]), .EN(and_1_out), .CLK(\码表_1位bcd计数器_2_cout ), .Reset(and_2_out));  // open: Cout
  and and_1 (and_1_out, not_1_out, ReStart);
  not not_1 (not_1_out, En_Stop);
  \码表_1位BCD计数器  \u_码表_1位bcd计数器_2  (
    .Cout(\码表_1位bcd计数器_2_cout ), .out_4(Data[11:8]), .EN(and_1_out), .CLK(\码表_1位bcd计数器_3_cout ),
    .Reset(and_2_out));
  and and_2 (and_2_out, ReStart, d_ff_1_q);
  \码表_1位BCD计数器  \u_码表_1位bcd计数器_3  (
    .Cout(\码表_1位bcd计数器_3_cout ), .out_4(Data[7:4]), .EN(and_1_out), .CLK(\码表_1位bcd计数器_4_cout ),
    .Reset(and_2_out));
  not not_2 (not_2_out, ReStart);
  \码表_1位BCD计数器  \u_码表_1位bcd计数器_4  (
    .Cout(\码表_1位bcd计数器_4_cout ), .out_4(Data[3:0]), .EN(and_1_out), .CLK(CLK), .Reset(and_2_out));
  D_Flip_Flop #(.trigger("rising"), .Pre_Clr_Positions("ABOVE_BELOW"), .NegatePresetClear("false"), .enable("false"), .NewFFLayout("true")) d_ff_1 (
    .clk(CLK), .D(not_2_out), .Q(d_ff_1_q));  // open: Qn, preset, reset
  \_7段显码_译码  \u_7段显码_译码_3  (
    .DHigh(Data[3]), .B(Data[2]), .C(Data[1]), .ALow(Data[0]), .a(A[0]), .b_2(A[1]), .c_2(A[2]), .d(A[3]),
    .e(A[4]), .f(A[5]), .g(A[6]));
  \_7段显码_译码  \u_7段显码_译码_4  (
    .DHigh(Data[7]), .B(Data[6]), .C(Data[5]), .ALow(Data[4]), .a(B[0]), .b_2(B[1]), .c_2(B[2]), .d(B[3]),
    .e(B[4]), .f(B[5]), .g(B[6]));
endmodule

module \码表_1位存储  (
  input  [3:0] in_1,
  input  RESET,
  input  CLK,
  output [3:0] out_4
);

  wire not_1_out;

  not not_1 (not_1_out, RESET);
  D_Flip_Flop #(.trigger("rising"), .Pre_Clr_Positions("ABOVE_BELOW"), .NegatePresetClear("false"), .enable("false"), .NewFFLayout("true")) d_ff_1 (
    .clk(CLK), .D(in_1[3]), .Q(out_4[3]), .preset(not_1_out));  // open: Qn, reset
  D_Flip_Flop #(.trigger("rising"), .Pre_Clr_Positions("ABOVE_BELOW"), .NegatePresetClear("false"), .enable("false"), .NewFFLayout("true")) d_ff_2 (
    .clk(CLK), .D(in_1[2]), .Q(out_4[2]), .reset(not_1_out));  // open: Qn, preset
  D_Flip_Flop #(.trigger("rising"), .Pre_Clr_Positions("ABOVE_BELOW"), .NegatePresetClear("false"), .enable("false"), .NewFFLayout("true")) d_ff_3 (
    .clk(CLK), .D(in_1[1]), .Q(out_4[1]), .reset(not_1_out));  // open: Qn, preset
  D_Flip_Flop #(.trigger("rising"), .Pre_Clr_Positions("ABOVE_BELOW"), .NegatePresetClear("false"), .enable("false"), .NewFFLayout("true")) d_ff_4 (
    .clk(CLK), .D(in_1[0]), .Q(out_4[0]), .preset(not_1_out));  // open: Qn, reset
endmodule

module \码表_4位Store  (
  input  [15:0] in_1,
  input  RESET,
  input  UpDate,
  output [15:0] out_4
);

  \码表_1位存储  \u_码表_1位存储_1  (.in_1(in_1[15:12]), .RESET(RESET), .CLK(UpDate), .out_4(out_4[15:12]));
  \码表_1位存储  \u_码表_1位存储_2  (.in_1(in_1[11:8]), .RESET(RESET), .CLK(UpDate), .out_4(out_4[11:8]));
  \码表_1位存储  \u_码表_1位存储_3  (.in_1(in_1[7:4]), .RESET(RESET), .CLK(UpDate), .out_4(out_4[7:4]));
  \码表_1位存储  \u_码表_1位存储_4  (.in_1(in_1[3:0]), .RESET(RESET), .CLK(UpDate), .out_4(out_4[3:0]));
endmodule

// 逻辑
module \码表_状态机逻辑  (
  input  x3,
  input  x2,
  input  x1,
  input  START,
  input  STOP,
  input  COMP,
  input  RESET,
  input  ALTB,
  output y3,
  output y2,
  output y1
);

  wire and_1_out, and_2_out, and_3_out, and_4_out, and_5_out, and_6_out, and_7_out, and_8_out, and_9_out,
       and_10_out, and_11_out, and_12_out, and_13_out, and_14_out, and_15_out, and_16_out, and_17_out,
       not_1_out, not_2_out, not_3_out, not_4_out, not_5_out, not_6_out, not_7_out, not_8_out, not_9_out,
       not_10_out, not_11_out, not_12_out, not_13_out, not_14_out, not_15_out, not_16_out, not_17_out,
       not_18_out, not_19_out, not_20_out, not_21_out, not_22_out;

  not not_1 (not_1_out, x3);
  not not_2 (not_2_out, START);
  not not_3 (not_3_out, x2);
  not not_4 (not_4_out, x2);
  not not_5 (not_5_out, x1);
  not not_6 (not_6_out, x2);
  not not_7 (not_7_out, x1);
  not not_8 (not_8_out, STOP);
  not not_9 (not_9_out, COMP);
  not not_10 (not_10_out, x3);
  not not_11 (not_11_out, x2);
  not not_12 (not_12_out, x1);
  not not_13 (not_13_out, x3);
  not not_14 (not_14_out, x2);
  not not_15 (not_15_out, START);
  not not_16 (not_16_out, x1);
  not not_17 (not_17_out, x3);
  not not_18 (not_18_out, STOP);
  not not_19 (not_19_out, x1);
  not not_20 (not_20_out, x2);
  not not_21 (not_21_out, ALTB);
  not not_22 (not_22_out, START);
  and and_1 (and_1_out, not_1_out, x2, x1, STOP);
  and and_2 (and_2_out, x3, not_2_out);
  and and_3 (and_3_out, x3, not_3_out, COMP);
  and and_4 (and_4_out, x3, not_4_out, x1);
  and and_5 (and_5_out, x3, x2, not_5_out);
  and and_6 (and_6_out, not_6_out, x1, START);
  and and_7 (and_7_out, x2, not_7_out);
  and and_8 (and_8_out, x2, not_8_out);
  and and_9 (and_9_out, x3, START, not_9_out);
  and and_10 (and_10_out, x3, x1);
  and and_11 (and_11_out, not_10_out, not_11_out, not_12_out, RESET);
  and and_12 (and_12_out, not_13_out, not_14_out, x1, not_15_out);
  and and_13 (and_13_out, x2, not_16_out, START);
  and and_14 (and_14_out, not_17_out, x2, x1, not_18_out);
  and and_15 (and_15_out, x3, not_19_out, COMP);
  and and_16 (and_16_out, x3, not_20_out, x1, not_21_out);
  and and_17 (and_17_out, x3, x2, not_22_out);
  or or_1 (y3, and_1_out, and_2_out, and_3_out, and_4_out, and_5_out);
  or or_2 (y2, and_6_out, and_7_out, and_8_out, and_9_out, and_10_out);
  or or_3 (y1, and_11_out, and_12_out, and_13_out, and_14_out, and_15_out, and_16_out, and_17_out);
endmodule

module \码表_状态机  (
  input  CLK,
  input  Start,
  input  Stop,
  input  Comp,
  input  Reset,
  input  ALTB,
  output Update
);

  wire and_1_out, d_ff_1_q, d_ff_2_q, d_ff_3_q, not_1_out, \码表_状态机逻辑_1_y1 , \码表_状态机逻辑_1_y2 , \码表_状态机逻辑_1_y3 ;

  D_Flip_Flop #(.trigger("rising"), .Pre_Clr_Positions("ABOVE_BELOW"), .NegatePresetClear("false"), .enable("false"), .NewFFLayout("true")) d_ff_1 (
    .clk(CLK), .D(\码表_状态机逻辑_1_y3 ), .Q(d_ff_1_q));  // open: Qn, preset, reset
  \码表_状态机逻辑  \u_码表_状态机逻辑_1  (
    .x3(d_ff_1_q), .x2(d_ff_2_q), .x1(d_ff_3_q), .START(Start), .STOP(Stop), .COMP(Comp), .RESET(Reset),
    .ALTB(ALTB), .y3(\码表_状态机逻辑_1_y3 ), .y2(\码表_状态机逻辑_1_y2 ), .y1(\码表_状态机逻辑_1_y1 ));
  D_Flip_Flop #(.trigger("rising"), .Pre_Clr_Positions("ABOVE_BELOW"), .NegatePresetClear("false"), .enable("false"), .NewFFLayout("true")) d_ff_2 (
    .clk(CLK), .D(\码表_状态机逻辑_1_y2 ), .Q(d_ff_2_q));  // open: Qn, preset, reset
  D_Flip_Flop #(.trigger("rising"), .Pre_Clr_Positions("ABOVE_BELOW"), .NegatePresetClear("false"), .enable("false"), .NewFFLayout("true")) d_ff_3 (
    .clk(CLK), .D(\码表_状态机逻辑_1_y1 ), .Q(d_ff_3_q));  // open: Qn, preset, reset
  and and_1 (and_1_out, d_ff_1_q, d_ff_2_q);
  not not_1 (not_1_out, d_ff_3_q);
  and and_2 (Update, and_1_out, not_1_out);

  // Notes on the sheet:
  //   <--Q_n输入给逻辑电路
endmodule

module \码表_1CMP  (
  input  [3:0] A,
  input  [3:0] B,
  output \大于 ,
  output \等于 
);

  wire and_1_out, and_2_out, and_3_out, and_4_out, and_5_out, and_6_out, and_7_out, and_8_out, and_9_out,
       and_10_out, and_11_out, and_12_out, and_13_out, and_14_out, and_15_out, and_16_out, and_17_out,
       and_18_out, and_19_out, and_20_out, and_21_out, and_22_out, and_23_out, and_24_out, not_1_out,
       not_2_out, not_3_out, not_4_out, not_5_out, not_6_out, not_7_out, not_8_out, not_9_out, not_10_out,
       not_11_out, not_12_out, not_13_out, not_14_out, not_15_out, not_16_out, not_17_out, not_18_out,
       not_19_out, not_20_out, not_21_out, not_22_out, not_23_out, not_24_out, or_1_out, or_2_out, or_3_out,
       or_4_out, or_5_out, or_6_out, or_7_out, or_8_out, or_9_out, or_10_out;

  not not_1 (not_1_out, A[3]);
  not not_2 (not_2_out, B[3]);
  not not_3 (not_3_out, A[3]);
  not not_4 (not_4_out, B[3]);
  not not_5 (not_5_out, A[2]);
  not not_6 (not_6_out, B[2]);
  not not_7 (not_7_out, A[3]);
  not not_8 (not_8_out, B[3]);
  not not_9 (not_9_out, A[2]);
  not not_10 (not_10_out, B[2]);
  not not_11 (not_11_out, A[1]);
  not not_12 (not_12_out, B[1]);
  not not_13 (not_13_out, A[3]);
  not not_14 (not_14_out, B[3]);
  not not_15 (not_15_out, A[2]);
  not not_16 (not_16_out, B[2]);
  not not_17 (not_17_out, A[1]);
  not not_18 (not_18_out, B[1]);
  not not_19 (not_19_out, A[0]);
  not not_20 (not_20_out, B[0]);
  and and_1 (and_1_out, A[3], B[3]);
  and and_2 (and_2_out, not_1_out, not_2_out);
  and and_3 (and_3_out, A[3], B[3]);
  and and_4 (and_4_out, not_3_out, not_4_out);
  and and_5 (and_5_out, A[2], B[2]);
  and and_6 (and_6_out, not_5_out, not_6_out);
  and and_7 (and_7_out, A[3], B[3]);
  and and_8 (and_8_out, not_7_out, not_8_out);
  and and_9 (and_9_out, A[2], B[2]);
  and and_10 (and_10_out, not_9_out, not_10_out);
  and and_11 (and_11_out, A[1], B[1]);
  and and_12 (and_12_out, not_11_out, not_12_out);
  and and_13 (and_13_out, A[3], B[3]);
  and and_14 (and_14_out, not_13_out, not_14_out);
  and and_15 (and_15_out, A[2], B[2]);
  and and_16 (and_16_out, not_15_out, not_16_out);
  and and_17 (and_17_out, A[1], B[1]);
  and and_18 (and_18_out, not_17_out, not_18_out);
  and and_19 (and_19_out, A[0], B[0]);
  and and_20 (and_20_out, not_19_out, not_20_out);
  not not_21 (not_21_out, B[3]);
  or or_1 (or_1_out, and_1_out, and_2_out);
  not not_22 (not_22_out, B[2]);
  or or_2 (or_2_out, and_3_out, and_4_out);
  or or_3 (or_3_out, and_5_out, and_6_out);
  not not_23 (not_23_out, B[1]);
  or or_4 (or_4_out, and_7_out, and_8_out);
  or or_5 (or_5_out, and_9_out, and_10_out);
  or or_6 (or_6_out, and_11_out, and_12_out);
  not not_24 (not_24_out, B[0]);
  or or_7 (or_7_out, and_13_out, and_14_out);
  or or_8 (or_8_out, and_15_out, and_16_out);
  or or_9 (or_9_out, and_17_out, and_18_out);
  or or_10 (or_10_out, and_19_out, and_20_out);
  and and_21 (and_21_out, A[3], not_21_out);
  and and_22 (and_22_out, or_1_out, A[2], not_22_out);
  and and_23 (and_23_out, or_2_out, or_3_out, A[1], not_23_out);
  and and_24 (and_24_out, or_4_out, or_5_out, or_6_out, A[0], not_24_out);
  and and_25 (\等于 , or_7_out, or_8_out, or_9_out, or_10_out);
  or or_11 (\大于 , and_21_out, and_22_out, and_23_out, and_24_out);
endmodule

module \码表_CMP  (
  input  [15:0] Old,
  input  [15:0] New,
  output \大于 ,
  output \等于 
);

  wire and_1_out, and_2_out, and_3_out, \码表_1cmp_1_大于 , \码表_1cmp_1_等于 , \码表_1cmp_2_大于 , \码表_1cmp_2_等于 ,
       \码表_1cmp_3_大于 , \码表_1cmp_3_等于 , \码表_1cmp_4_大于 , \码表_1cmp_4_等于 ;

  \码表_1CMP  \u_码表_1cmp_1  (.\大于 (\码表_1cmp_1_大于 ), .\等于 (\码表_1cmp_1_等于 ), .A(Old[15:12]), .B(New[15:12]));
  \码表_1CMP  \u_码表_1cmp_2  (.\大于 (\码表_1cmp_2_大于 ), .\等于 (\码表_1cmp_2_等于 ), .A(Old[11:8]), .B(New[11:8]));
  \码表_1CMP  \u_码表_1cmp_3  (.\大于 (\码表_1cmp_3_大于 ), .\等于 (\码表_1cmp_3_等于 ), .A(Old[7:4]), .B(New[7:4]));
  \码表_1CMP  \u_码表_1cmp_4  (.\大于 (\码表_1cmp_4_大于 ), .\等于 (\码表_1cmp_4_等于 ), .A(Old[3:0]), .B(New[3:0]));
  and and_1 (and_1_out, \码表_1cmp_1_等于 , \码表_1cmp_2_大于 );
  and and_2 (and_2_out, \码表_1cmp_1_等于 , \码表_1cmp_2_等于 , \码表_1cmp_3_大于 );
  and and_3 (and_3_out, \码表_1cmp_1_等于 , \码表_1cmp_2_等于 , \码表_1cmp_3_等于 , \码表_1cmp_4_大于 );
  and and_4 (\等于 , \码表_1cmp_1_等于 , \码表_1cmp_2_等于 , \码表_1cmp_3_等于 , \码表_1cmp_4_等于 );
  or or_1 (\大于 , \码表_1cmp_1_大于 , and_1_out, and_2_out, and_3_out);
endmodule

module \码表  (
  input  CMP,
  input  Stop,
  input  Start
);

  wire clock_1_out, not_1_out, Reset_out, \码表_cmp_1_大于 , \码表_状态机_1_update ;
  wire [6:0] A, Aout, B, Bout, C, Cout, D, Dout;
  wire [15:0] \码表_4位bcd计数器_1_data , \码表_4位store_1_out_4 ;

  _7_Segment_Display #(.active("true")) u_7_segment_display_1 (
    .g(D[6]), .f(D[5]), .a(D[0]), .b(D[1]), .e(D[4]), .d(D[3]), .c(D[2]));  // open: dp
  \码表_4位BCD计数器  \u_码表_4位bcd计数器_1  (
    .D(D), .C(C), .A(A), .B(B), .Data(\码表_4位bcd计数器_1_data ), .En_Stop(Stop), .ReStart(Start),
    .CLK(clock_1_out));
  Clock #(.highDuration(1), .lowDuration(1)) clock_1 (.out(clock_1_out));
  _7_Segment_Display #(.active("true")) u_7_segment_display_2 (
    .g(Dout[6]), .f(Dout[5]), .a(Dout[0]), .b(Dout[1]), .e(Dout[4]), .d(Dout[3]), .c(Dout[2]));  // open: dp
  \码表_CMP  \u_码表_cmp_1  (.\大于 (\码表_cmp_1_大于 ), .Old(\码表_4位store_1_out_4 ), .New(\码表_4位bcd计数器_1_data ));  // open: 等于
  _7_Segment_Display #(.active("true")) u_7_segment_display_3 (
    .g(C[6]), .f(C[5]), .a(C[0]), .b(C[1]), .e(C[4]), .d(C[3]), .c(C[2]), .dp(1'b1));
  not not_1 (not_1_out, Reset_out);
  Button Reset (.out(Reset_out));
  _7_Segment_Display #(.active("true")) u_7_segment_display_4 (
    .g(Cout[6]), .f(Cout[5]), .a(Cout[0]), .b(Cout[1]), .e(Cout[4]), .d(Cout[3]), .c(Cout[2]), .dp(1'b1));
  \码表_状态机  \u_码表_状态机_1  (
    .CLK(clock_1_out), .Start(Start), .Stop(Stop), .Comp(CMP), .Reset(not_1_out), .ALTB(\码表_cmp_1_大于 ),
    .Update(\码表_状态机_1_update ));
  _7_Segment_Display #(.active("true")) u_7_segment_display_5 (
    .g(B[6]), .f(B[5]), .a(B[0]), .b(B[1]), .e(B[4]), .d(B[3]), .c(B[2]));  // open: dp
  \码表_4位Store  \u_码表_4位store_1  (
    .in_1(\码表_4位bcd计数器_1_data ), .RESET(not_1_out), .out_4(\码表_4位store_1_out_4 ), .UpDate(\码表_状态机_1_update ));
  _7_Segment_Display #(.active("true")) u_7_segment_display_6 (
    .g(Bout[6]), .f(Bout[5]), .a(Bout[0]), .b(Bout[1]), .e(Bout[4]), .d(Bout[3]), .c(Bout[2]));  // open: dp
  _7_Segment_Display #(.active("true")) u_7_segment_display_7 (
    .g(A[6]), .f(A[5]), .a(A[0]), .b(A[1]), .e(A[4]), .d(A[3]), .c(A[2]));  // open: dp
  _7_Segment_Display #(.active("true")) u_7_segment_display_8 (
    .g(Aout[6]), .f(Aout[5]), .a(Aout[0]), .b(Aout[1]), .e(Aout[4]), .d(Aout[3]), .c(Aout[2]));  // open: dp
  \_7段显码_译码  \u_7段显码_译码_1  (
    .DHigh(\码表_4位store_1_out_4 [3]), .B(\码表_4位store_1_out_4 [2]), .C(\码表_4位store_1_out_4 [1]),
    .ALow(\码表_4位store_1_out_4 [0]), .a(Aout[0]), .b_2(Aout[1]), .c_2(Aout[2]), .d(Aout[3]), .e(Aout[4]),
    .f(Aout[5]), .g(Aout[6]));
  \_7段显码_译码  \u_7段显码_译码_2  (
    .DHigh(\码表_4位store_1_out_4 [7]), .B(\码表_4位store_1_out_4 [6]), .C(\码表_4位store_1_out_4 [5]),
    .ALow(\码表_4位store_1_out_4 [4]), .a(Bout[0]), .b_2(Bout[1]), .c_2(Bout[2]), .d(Bout[3]), .e(Bout[4]),
    .f(Bout[5]), .g(Bout[6]));
  \_7段显码_译码  \u_7段显码_译码_3  (
    .DHigh(\码表_4位store_1_out_4 [11]), .B(\码表_4位store_1_out_4 [10]), .C(\码表_4位store_1_out_4 [9]),
    .ALow(\码表_4位store_1_out_4 [8]), .a(Cout[0]), .b_2(Cout[1]), .c_2(Cout[2]), .d(Cout[3]), .e(Cout[4]),
    .f(Cout[5]), .g(Cout[6]));
  \_7段显码_译码  \u_7段显码_译码_4  (
    .DHigh(\码表_4位store_1_out_4 [15]), .B(\码表_4位store_1_out_4 [14]), .C(\码表_4位store_1_out_4 [13]),
    .ALow(\码表_4位store_1_out_4 [12]), .a(Dout[0]), .b_2(Dout[1]), .c_2(Dout[2]), .d(Dout[3]), .e(Dout[4]),
    .f(Dout[5]), .g(Dout[6]));

  // Notes on the sheet:
  //   为0时,置存储器为9999
endmodule

module \寄存器堆  (
  input  [31:0] Data_in,
  input  W,
  input  [2:0] W_rt___rd,
  input  clk,
  input  [2:0] rs,
  input  [2:0] rt,
  output [31:0] Data_out1,
  output [31:0] Data_out2
);

  wire and_1_out, and_2_out, and_3_out, and_4_out, and_5_out, and_6_out, and_7_out, decoder_1_out1,
       decoder_1_out2, decoder_1_out3, decoder_1_out4, decoder_1_out5, decoder_1_out6, decoder_1_out7,
       not_1_out, undriven;
  wire [31:0] multiplexer_1_out, multiplexer_2_out, register_1_q, register_2_q, register_3_q, register_4_q,
       register_5_q, register_6_q, register_7_q, register_8_q;

  not not_1 (not_1_out, undriven);
  Decoder #(.select(3), .tristate("false"), .disabled("Z"), .enable("false")) decoder_1 (
    .out1(decoder_1_out1), .out2(decoder_1_out2), .out3(decoder_1_out3), .out4(decoder_1_out4),
    .out5(decoder_1_out5), .out6(decoder_1_out6), .out7(decoder_1_out7), .sel(W_rt___rd));  // open: out0
  and and_1 (and_1_out, W, decoder_1_out1);
  and and_2 (and_2_out, W, decoder_1_out2);
  and and_3 (and_3_out, W, decoder_1_out3);
  and and_4 (and_4_out, W, decoder_1_out4);
  and and_5 (and_5_out, W, decoder_1_out5);
  and and_6 (and_6_out, W, decoder_1_out6);
  and and_7 (and_7_out, W, decoder_1_out7);
  Register #(.width(32), .trigger("rising"), .Select("low")) register_1 (
    .en(1'b0), .Q(register_1_q), .clk(clk), .clr(1'b0));  // open: D
  Register #(.width(32), .trigger("rising"), .Select("low")) register_2 (
    .D(Data_in), .en(and_1_out), .Q(register_2_q), .clk(clk));  // open: clr
  Register #(.width(32), .trigger("rising"), .Select("low")) register_3 (
    .D(Data_in), .en(and_2_out), .Q(register_3_q), .clk(clk));  // open: clr
  Register #(.width(32), .trigger("rising"), .Select("low")) register_4 (
    .D(Data_in), .en(and_3_out), .Q(register_4_q), .clk(clk));  // open: clr
  Register #(.width(32), .trigger("rising"), .Select("low")) register_5 (
    .en(and_4_out), .Q(register_5_q), .clk(clk));  // open: D, clr
  Register #(.width(32), .trigger("rising"), .Select("low")) register_6 (
    .D(Data_in), .en(and_5_out), .Q(register_6_q), .clk(clk));  // open: clr
  Register #(.width(32), .trigger("rising"), .Select("low")) register_7 (
    .D(Data_in), .en(and_6_out), .Q(register_7_q), .clk(clk));  // open: clr
  Register #(.width(32), .trigger("rising"), .Select("low")) register_8 (
    .D(Data_in), .en(and_7_out), .Q(register_8_q), .clk(clk));  // open: clr
  Multiplexer #(.select(3), .width(32), .disabled("Z"), .enable("false")) multiplexer_1 (
    .in0(register_1_q), .in1(register_2_q), .in2(register_3_q), .in3(register_4_q), .in4(register_5_q),
    .in5(register_6_q), .in6(register_7_q), .in7(register_8_q), .out(multiplexer_1_out), .sel(rs));
  Multiplexer #(.select(3), .width(32), .disabled("Z"), .enable("false")) multiplexer_2 (
    .in0(register_1_q), .in1(register_2_q), .in2(register_3_q), .in3(register_4_q), .in4(register_5_q),
    .in5(register_6_q), .in6(register_7_q), .in7(register_8_q), .out(multiplexer_2_out), .sel(rt));
  assign Data_out1 = 1'b1 ? multiplexer_1_out : 32'bz;  // Controlled_Buffer controlled_buffer_1
  assign Data_out2 = 1'b1 ? multiplexer_2_out : 32'bz;  // Controlled_Buffer controlled_buffer_2

  // Notes on the sheet:
  //   原来的逻辑是W/R不同时为真
  //   改成了一直输出
  //   000号寄存器恒为0
endmodule

// MEM
module MEM_8_32 (
  input  [31:0] Din,
  input  [7:0] Adress,
  input  W,
  input  clk,
  output [31:0] Dout
);

  wire not_1_out;

  assign Dout = W ? Din : 32'bz;  // Controlled_Buffer controlled_buffer_1
  not not_1 (not_1_out, W);
  RAM #(.addrWidth(8), .dataWidth(32), .bus("combined"), .Select("low")) ram_1 (
    .addr(Adress), .data(Dout), .clk(clk), .ld(not_1_out));  // open: sel, clr
endmodule

module \Mem_拓展  (
  input  [31:0] Data_in,
  input  [25:0] Adress,
  input  W,
  output [31:0] Data_out
);

  wire clk_out, decoder_1_out0, decoder_1_out1, decoder_1_out2, decoder_1_out3, not_1_out, not_2_out,
       not_3_out, not_4_out, not_5_out, not_6_out;
  wire [1:0] bitselector_2_out;
  wire [23:0] bitselector_1_out;
  wire [31:0] controlled_buffer_2_out;

  Clock #(.highDuration(1), .lowDuration(1)) clk (.out(clk_out));
  assign Data_out = not_1_out ? controlled_buffer_2_out : 32'bz;  // Controlled_Buffer controlled_buffer_1
  not not_1 (not_1_out, W);
  assign controlled_buffer_2_out = W ? Data_in : 32'bz;  // Controlled_Buffer controlled_buffer_2
  BitSelector #(.width(26), .group(24)) bitselector_1 (.in(Adress), .out(bitselector_1_out), .sel(1'b0));
  BitSelector #(.width(26), .group(2)) bitselector_2 (.in(Adress), .out(bitselector_2_out), .sel(4'b1100));
  not not_2 (not_2_out, W);
  Decoder #(.select(2), .tristate("false"), .disabled("Z"), .enable("false")) decoder_1 (
    .out0(decoder_1_out0), .out1(decoder_1_out1), .out2(decoder_1_out2), .out3(decoder_1_out3),
    .sel(bitselector_2_out));
  not not_3 (not_3_out, decoder_1_out0);
  RAM #(.addrWidth(24), .dataWidth(32), .bus("combined"), .Select("low")) ram_1 (
    .addr(bitselector_1_out), .data(controlled_buffer_2_out), .sel(not_3_out), .clk(clk_out), .ld(not_2_out));  // open: clr
  not not_4 (not_4_out, decoder_1_out1);
  RAM #(.addrWidth(24), .dataWidth(32), .bus("combined"), .Select("low")) ram_2 (
    .addr(bitselector_1_out), .data(controlled_buffer_2_out), .sel(not_4_out), .clk(clk_out), .ld(not_2_out));  // open: clr
  not not_5 (not_5_out, decoder_1_out2);
  RAM #(.addrWidth(24), .dataWidth(32), .bus("combined"), .Select("low")) ram_3 (
    .addr(bitselector_1_out), .data(controlled_buffer_2_out), .sel(not_5_out), .clk(clk_out), .ld(not_2_out));  // open: clr
  not not_6 (not_6_out, decoder_1_out3);
  RAM #(.addrWidth(24), .dataWidth(32), .bus("combined"), .Select("low")) ram_4 (
    .addr(bitselector_1_out), .data(controlled_buffer_2_out), .sel(not_6_out), .clk(clk_out), .ld(not_2_out));  // open: clr
endmodule

// I型译码
module \I型  (
  input  op31,
  input  op30,
  input  op29,
  input  op28,
  input  op27,
  input  op26,
  output RegDst,
  output RegW,
  output AluSrc,
  output AluOP,
  output Branch,
  output MemW,
  output MemtoReg
);

  wire and_1_out, and_2_out, not_1_out, not_2_out, not_3_out, not_4_out, not_5_out, not_6_out, not_7_out,
       not_8_out, not_9_out, not_10_out, not_11_out, not_12_out, not_13_out, not_14_out, not_15_out,
       not_16_out, not_17_out, not_18_out, not_19_out, not_20_out, not_21_out, not_22_out, not_23_out,
       not_24_out;

  not not_1 (not_1_out, op31);
  not not_2 (not_2_out, op30);
  not not_3 (not_3_out, op29);
  not not_4 (not_4_out, op27);
  not not_5 (not_5_out, op26);
  not not_6 (not_6_out, op30);
  not not_7 (not_7_out, op28);
  not not_8 (not_8_out, op30);
  not not_9 (not_9_out, op29);
  not not_10 (not_10_out, op28);
  not not_11 (not_11_out, op30);
  not not_12 (not_12_out, op28);
  not not_13 (not_13_out, op30);
  not not_14 (not_14_out, op28);
  not not_15 (not_15_out, op31);
  not not_16 (not_16_out, op30);
  not not_17 (not_17_out, op29);
  not not_18 (not_18_out, op27);
  not not_19 (not_19_out, op26);
  not not_20 (not_20_out, op30);
  not not_21 (not_21_out, op28);
  not not_22 (not_22_out, op30);
  not not_23 (not_23_out, op29);
  not not_24 (not_24_out, op28);
  and and_1 (and_1_out, not_1_out, not_2_out, not_3_out, op28, not_4_out, not_5_out);
  and and_2 (and_2_out, op31, not_6_out, op29, not_7_out, op27, op26);
  and and_3 (RegW, op31, not_8_out, not_9_out, not_10_out, op27, op26);
  and and_4 (AluSrc, op31, not_11_out, not_12_out, op27, op26);
  and and_5 (AluOP, op31, not_13_out, not_14_out, op27, op26);
  and and_6 (Branch, not_15_out, not_16_out, not_17_out, op28, not_18_out, not_19_out);
  and and_7 (MemW, op31, not_20_out, op29, not_21_out, op27, op26);
  and and_8 (MemtoReg, op31, not_22_out, not_23_out, not_24_out, op27, op26);
  or or_1 (RegDst, and_1_out, and_2_out);
endmodule

// R型译码
module \R型  (
  input  R,
  input  f0,
  input  f1,
  input  f2,
  input  f3,
  input  f4,
  input  f5,
  output MemtoReg,
  output MemW,
  output Branch,
  output AluOP,
  output AluSrc,
  output RegW,
  output Exit,
  output RegDst
);

  wire not_1_out, not_2_out, not_3_out, not_4_out, not_5_out, not_6_out, not_7_out, not_8_out, not_9_out,
       not_10_out, not_11_out, not_12_out, not_13_out, not_14_out, not_15_out, not_16_out, not_17_out,
       not_18_out, not_19_out, not_20_out, not_21_out, not_22_out, not_23_out;

  not not_1 (not_1_out, f1);
  not not_2 (not_2_out, f2);
  not not_3 (not_3_out, f3);
  not not_4 (not_4_out, f4);
  not not_5 (not_5_out, f5);
  not not_6 (not_6_out, f0);
  not not_7 (not_7_out, f1);
  not not_8 (not_8_out, f4);
  not not_9 (not_9_out, f5);
  not not_10 (not_10_out, f1);
  not not_11 (not_11_out, f2);
  not not_12 (not_12_out, f3);
  not not_13 (not_13_out, f4);
  not not_14 (not_14_out, f5);
  not not_15 (not_15_out, f0);
  not not_16 (not_16_out, f1);
  not not_17 (not_17_out, f4);
  not not_18 (not_18_out, f5);
  not not_19 (not_19_out, f1);
  not not_20 (not_20_out, f2);
  not not_21 (not_21_out, f3);
  not not_22 (not_22_out, f4);
  not not_23 (not_23_out, f5);
  and and_1 (AluOP, R, f0, not_1_out, not_2_out, not_3_out, not_4_out, not_5_out);
  and and_2 (AluSrc, R, not_6_out, not_7_out, f2, f3, not_8_out, not_9_out);
  and and_3 (RegW, R, f0, not_10_out, not_11_out, not_12_out, not_13_out, not_14_out);
  and and_4 (Exit, R, not_15_out, not_16_out, f2, f3, not_17_out, not_18_out);
  and and_5 (RegDst, R, f0, not_19_out, not_20_out, not_21_out, not_22_out, not_23_out);

  assign Branch = 1'b0;
  assign MemtoReg = 1'b0;
  assign MemW = 1'b0;
endmodule

// 控制器
module \控制器新  (
  input  [5:0] op,
  input  [5:0] func,
  output MemtoReg,
  output MemW,
  output Branch,
  output AluOP,
  output AluSrc,
  output RegW,
  output RegDst,
  output Exit
);

  wire nor_1_out;
  wire [6:0] \i型_1_memtoreg , \r型_1_memtoreg ;

  nor nor_1 (nor_1_out, op[5], op[4], op[3], op[2], op[1], op[0]);
  \I型  \i型_1  (
    .op31(op[5]), .op30(op[4]), .op29(op[3]), .RegDst(\i型_1_memtoreg [6]), .op28(op[2]), .op27(op[1]),
    .op26(op[0]), .RegW(\i型_1_memtoreg [5]), .AluSrc(\i型_1_memtoreg [4]), .AluOP(\i型_1_memtoreg [3]),
    .Branch(\i型_1_memtoreg [2]), .MemW(\i型_1_memtoreg [1]), .MemtoReg(\i型_1_memtoreg [0]));
  \R型  \r型_1  (
    .R(nor_1_out), .MemtoReg(\r型_1_memtoreg [0]), .f0(func[5]), .MemW(\r型_1_memtoreg [1]), .f1(func[4]),
    .Branch(\r型_1_memtoreg [2]), .f2(func[3]), .AluOP(\r型_1_memtoreg [3]), .f3(func[2]), .f4(func[1]),
    .f5(func[0]), .AluSrc(\r型_1_memtoreg [4]), .RegW(\r型_1_memtoreg [5]), .Exit(Exit),
    .RegDst(\r型_1_memtoreg [6]));
  assign {RegDst, RegW, AluSrc, AluOP, Branch, MemW, MemtoReg} = \i型_1_memtoreg  | \r型_1_memtoreg ;  // OR_Gate or_1, 7 bits wide

  // Notes on the sheet:
  //   注:f5是最末位
endmodule

// <<2
module \逻辑左移2位  (
  input  [31:0] in_1,
  output [31:0] out_2
);


  assign out_2 = {in_1[29:0], 2'b00};
endmodule

module \MIPS单周期CPU  (
  input  \临时_rst 
);

  wire and_1_out, clk, \n32位快速加法_减法器_1_zf , not_1_out, not_2_out, not_3_out, \控制器新_1_aluop , \控制器新_1_alusrc ,
       \控制器新_1_branch , \控制器新_1_exit , \控制器新_1_memtoreg , \控制器新_1_memw , \控制器新_1_regdst , \控制器新_1_regw ;
  wire [2:0] multiplexer_2_out;
  wire [31:0] adder_1_out, adder_2_out, bit_extender_1_out, mem_8_32_1_dout, multiplexer_1_out,
       multiplexer_3_out, multiplexer_4_out, \n32位快速加法_减法器_1_out , PC_q, \寄存器堆_1_data_out1 ,
       \寄存器堆_1_data_out2 , \指令存储器_data , \逻辑左移2位_1_out_2 ;

  Multiplexer #(.select(1), .width(32), .disabled("Z"), .enable("false")) multiplexer_1 (
    .in0(adder_1_out), .in1(adder_2_out), .out(multiplexer_1_out), .sel(and_1_out));
  Clock #(.highDuration(1), .lowDuration(1)) clock_1 (.out(clk));
  Register #(.width(32), .trigger("rising"), .Select("low")) PC (
    .D(multiplexer_1_out), .en(not_3_out), .Q(PC_q), .clk(clk), .clr(\临时_rst ));
  Adder #(.width(32)) adder_1 (.a(PC_q), .b(32'h4), .out(adder_1_out));  // open: cin, cout
  ROM #(.addrWidth(8), .dataWidth(32), .Select("low")) \u_指令存储器  (.addr(PC_q[9:2]), .data(\指令存储器_data ));
  Multiplexer #(.select(1), .width(3), .disabled("Z"), .enable("false")) multiplexer_2 (
    .in0(\指令存储器_data [18:16]), .in1(\指令存储器_data [13:11]), .out(multiplexer_2_out), .sel(\控制器新_1_regdst ));
  assign bit_extender_1_out = {{16{\指令存储器_data [15]}}, \指令存储器_data [15:0]};  // Bit_Extender bit_extender_1
  \控制器新  \u_控制器新_1  (
    .op(\指令存储器_data [31:26]), .func(\指令存储器_data [5:0]), .MemtoReg(\控制器新_1_memtoreg ), .MemW(\控制器新_1_memw ),
    .Branch(\控制器新_1_branch ), .AluOP(\控制器新_1_aluop ), .AluSrc(\控制器新_1_alusrc ), .RegW(\控制器新_1_regw ),
    .RegDst(\控制器新_1_regdst ), .Exit(\控制器新_1_exit ));
  \寄存器堆  \u_寄存器堆_1  (
    .Data_in(multiplexer_4_out), .W(\控制器新_1_regw ), .W_rt___rd(multiplexer_2_out),
    .Data_out1(\寄存器堆_1_data_out1 ), .Data_out2(\寄存器堆_1_data_out2 ), .rt(\指令存储器_data [18:16]),
    .rs(\指令存储器_data [23:21]), .clk(clk));
  Multiplexer #(.select(1), .width(32), .disabled("Z"), .enable("false")) multiplexer_3 (
    .in0(\寄存器堆_1_data_out2 ), .in1(bit_extender_1_out), .out(multiplexer_3_out), .sel(\控制器新_1_alusrc ));
  \逻辑左移2位  \u_逻辑左移2位_1  (.in_1(bit_extender_1_out), .out_2(\逻辑左移2位_1_out_2 ));
  not not_1 (not_1_out, \控制器新_1_aluop );
  \_32位快速加法_减法器  \u_32位快速加法_减法器_1  (
    .C0(1'b0), .SUB(not_1_out), .OUT(\n32位快速加法_减法器_1_out ), .X(\寄存器堆_1_data_out1 ), .Y(multiplexer_3_out),
    .ZF(\n32位快速加法_减法器_1_zf ));  // open: CF, OF
  Adder #(.width(32)) adder_2 (.a(\逻辑左移2位_1_out_2 ), .b(adder_1_out), .out(adder_2_out));  // open: cin, cout
  not not_2 (not_2_out, \n32位快速加法_减法器_1_zf );
  and and_1 (and_1_out, \控制器新_1_branch , not_2_out);
  not not_3 (not_3_out, \控制器新_1_exit );
  Multiplexer #(.select(1), .width(32), .disabled("Z"), .enable("false")) multiplexer_4 (
    .in0(\n32位快速加法_减法器_1_out ), .in1(mem_8_32_1_dout), .out(multiplexer_4_out), .sel(\控制器新_1_memtoreg ));
  MEM_8_32 mem_8_32_1 (
    .Din(\寄存器堆_1_data_out2 ), .Adress(\n32位快速加法_减法器_1_out [7:0]), .W(\控制器新_1_memw ), .clk(clk),
    .Dout(mem_8_32_1_dout));

  // Notes on the sheet:
  //   PC的单位:Byte
  //   （存储器地址只有8位，把PC先右移两位，再取低8位）
  //   contents of 指令存储器 (hex, n*v repeats v):
  //   8c010001 8c070002 221020 ac420004 1047fffd 28c
  //   只有8个寄存器,高两位不要
  //   Equal(ZF)
  //   PCsrc
endmodule

// RegFile
module \寄存器堆for多周期  (
  input  [31:0] Data_in,
  input  W,
  input  [2:0] W_rt___rd,
  input  clk,
  input  [2:0] R_num,
  output [31:0] Data_out
);

  wire and_1_out, and_2_out, and_3_out, and_4_out, and_5_out, and_6_out, and_7_out, decoder_1_out1,
       decoder_1_out2, decoder_1_out3, decoder_1_out4, decoder_1_out5, decoder_1_out6, decoder_1_out7;
  wire [31:0] register_1_q, register_2_q, register_3_q, register_4_q, register_5_q, register_6_q,
       register_7_q, register_8_q;

  // NOT_Gate not_1 has open pins: in=W, out=open
  Decoder #(.select(3), .tristate("false"), .disabled("Z"), .enable("false")) decoder_1 (
    .out1(decoder_1_out1), .out2(decoder_1_out2), .out3(decoder_1_out3), .out4(decoder_1_out4),
    .out5(decoder_1_out5), .out6(decoder_1_out6), .out7(decoder_1_out7), .sel(W_rt___rd));  // open: out0
  and and_1 (and_1_out, 1'b1, decoder_1_out1);
  and and_2 (and_2_out, 1'b1, decoder_1_out2);
  and and_3 (and_3_out, 1'b1, decoder_1_out3);
  and and_4 (and_4_out, 1'b1, decoder_1_out4);
  and and_5 (and_5_out, 1'b1, decoder_1_out5);
  and and_6 (and_6_out, 1'b1, decoder_1_out6);
  and and_7 (and_7_out, 1'b1, decoder_1_out7);
  Register #(.width(32), .trigger("rising"), .Select("low")) register_1 (
    .en(1'b0), .Q(register_1_q), .clk(clk), .clr(1'b0));  // open: D
  Register #(.width(32), .trigger("rising"), .Select("low")) register_2 (
    .D(Data_in), .en(and_1_out), .Q(register_2_q), .clk(clk));  // open: clr
  Register #(.width(32), .trigger("rising"), .Select("low")) register_3 (
    .D(Data_in), .en(and_2_out), .Q(register_3_q), .clk(clk));  // open: clr
  Register #(.width(32), .trigger("rising"), .Select("low")) register_4 (
    .D(Data_in), .en(and_3_out), .Q(register_4_q), .clk(clk));  // open: clr
  Register #(.width(32), .trigger("rising"), .Select("low")) register_5 (
    .en(and_4_out), .Q(register_5_q), .clk(clk));  // open: D, clr
  Register #(.width(32), .trigger("rising"), .Select("low")) register_6 (
    .D(Data_in), .en(and_5_out), .Q(register_6_q), .clk(clk));  // open: clr
  Register #(.width(32), .trigger("rising"), .Select("low")) register_7 (
    .D(Data_in), .en(and_6_out), .Q(register_7_q), .clk(clk));  // open: clr
  Register #(.width(32), .trigger("rising"), .Select("low")) register_8 (
    .D(Data_in), .en(and_7_out), .Q(register_8_q), .clk(clk));  // open: clr
  Multiplexer #(.select(3), .width(32), .disabled("Z"), .enable("false")) multiplexer_1 (
    .in0(register_1_q), .in1(register_2_q), .in2(register_3_q), .in3(register_4_q), .in4(register_5_q),
    .in5(register_6_q), .in6(register_7_q), .in7(register_8_q), .out(Data_out), .sel(R_num));

  // Notes on the sheet:
  //   改为0时触发
  //   000号寄存器恒为0
endmodule

module \I型译码  (
  input  op31,
  input  op30,
  input  op29,
  input  op28,
  input  op27,
  input  op26,
  output lw,
  output sw,
  output beq,
  output addi,
  output R
);

  wire not_1_out, not_2_out, not_3_out, not_4_out, not_5_out, not_6_out, not_7_out, not_8_out, not_9_out,
       not_10_out, not_11_out, not_12_out, not_13_out, not_14_out, not_15_out, not_16_out, not_17_out,
       not_18_out, not_19_out, not_20_out, not_21_out;

  not not_1 (not_1_out, op30);
  not not_2 (not_2_out, op29);
  not not_3 (not_3_out, op28);
  not not_4 (not_4_out, op30);
  not not_5 (not_5_out, op28);
  not not_6 (not_6_out, op31);
  not not_7 (not_7_out, op30);
  not not_8 (not_8_out, op29);
  not not_9 (not_9_out, op27);
  not not_10 (not_10_out, op26);
  not not_11 (not_11_out, op31);
  not not_12 (not_12_out, op30);
  not not_13 (not_13_out, op28);
  not not_14 (not_14_out, op27);
  not not_15 (not_15_out, op26);
  not not_16 (not_16_out, op31);
  not not_17 (not_17_out, op30);
  not not_18 (not_18_out, op29);
  not not_19 (not_19_out, op28);
  not not_20 (not_20_out, op27);
  not not_21 (not_21_out, op26);
  and and_1 (lw, op31, not_1_out, not_2_out, not_3_out, op27, op26);
  and and_2 (sw, op31, not_4_out, op29, not_5_out, op27, op26);
  and and_3 (beq, not_6_out, not_7_out, not_8_out, op28, not_9_out, not_10_out);
  and and_4 (addi, not_11_out, not_12_out, op29, not_13_out, not_14_out, not_15_out);
  and and_5 (R, not_16_out, not_17_out, not_18_out, not_19_out, not_20_out, not_21_out);
endmodule

module \R型译码  (
  input  R,
  input  func5,
  input  func4,
  input  func3,
  input  func2,
  input  func1,
  input  func0,
  output add,
  output syscall
);

  wire not_1_out, not_2_out, not_3_out, not_4_out, not_5_out, not_6_out, not_7_out, not_8_out, not_9_out;

  not not_1 (not_1_out, func4);
  not not_2 (not_2_out, func3);
  not not_3 (not_3_out, func2);
  not not_4 (not_4_out, func1);
  not not_5 (not_5_out, func0);
  not not_6 (not_6_out, func5);
  not not_7 (not_7_out, func4);
  not not_8 (not_8_out, func1);
  not not_9 (not_9_out, func0);
  and and_1 (add, R, func5, not_1_out, not_2_out, not_3_out, not_4_out, not_5_out);
  and and_2 (syscall, R, not_6_out, not_7_out, func3, func2, not_8_out, not_9_out);
endmodule

module \指令译码  (
  input  [5:0] op,
  input  [5:0] func,
  output lw,
  output sw,
  output beq,
  output addi,
  output add,
  output syscall
);

  wire \i型译码_1_r ;

  \I型译码  \i型译码_1  (
    .op31(op[5]), .op30(op[4]), .op29(op[3]), .op28(op[2]), .op27(op[1]), .op26(op[0]), .lw(lw), .sw(sw),
    .beq(beq), .addi(addi), .R(\i型译码_1_r ));
  \R型译码  \r型译码_1  (
    .R(\i型译码_1_r ), .func5(func[5]), .func4(func[4]), .func3(func[3]), .func2(func[2]), .func1(func[1]),
    .func0(func[0]), .add(add), .syscall(syscall));
endmodule

// 状态转移逻辑
module \状态转移  (
  input  x4,
  input  x3,
  input  x2,
  input  x1,
  input  x0,
  input  lw,
  input  sw,
  input  beq,
  input  addi,
  input  add,
  input  syscall,
  input  equal,
  output y4,
  output y3,
  output y2,
  output y1,
  output y0
);

  wire and_1_out, and_2_out, and_3_out, and_4_out, and_5_out, and_6_out, and_7_out, and_8_out, and_9_out,
       and_10_out, and_11_out, and_12_out, and_13_out, and_14_out, and_15_out, and_16_out, and_17_out,
       and_18_out, and_19_out, and_20_out, and_21_out, and_22_out, and_23_out, and_24_out, and_25_out,
       and_26_out, and_27_out, and_28_out, and_29_out, and_30_out, and_31_out, and_32_out, and_33_out,
       and_34_out, not_1_out, not_2_out, not_3_out, not_4_out, not_5_out, not_6_out, not_7_out, not_8_out,
       not_9_out, not_10_out, not_11_out, not_12_out, not_13_out, not_14_out, not_15_out, not_16_out,
       not_17_out, not_18_out, not_19_out, not_20_out, not_21_out, not_22_out, not_23_out, not_24_out,
       not_25_out, not_26_out, not_27_out, not_28_out, not_29_out, not_30_out, not_31_out, not_32_out,
       not_33_out, not_34_out, not_35_out, not_36_out, not_37_out, not_38_out, not_39_out, not_40_out,
       not_41_out, not_42_out, not_43_out, not_44_out, not_45_out, not_46_out, not_47_out, not_48_out,
       not_49_out, not_50_out, not_51_out, not_52_out, not_53_out, not_54_out, not_55_out, not_56_out,
       not_57_out, not_58_out, not_59_out, not_60_out, not_61_out, not_62_out, not_63_out, not_64_out,
       not_65_out, not_66_out, not_67_out, not_68_out, not_69_out, not_70_out, not_71_out, not_72_out,
       not_73_out, not_74_out, not_75_out, not_76_out, not_77_out, not_78_out, not_79_out, not_80_out,
       not_81_out, not_82_out, not_83_out, not_84_out, not_85_out, not_86_out, not_87_out, not_88_out,
       not_89_out, not_90_out, not_91_out, not_92_out, not_93_out, not_94_out, not_95_out, not_96_out,
       not_97_out, not_98_out, not_99_out, not_100_out, not_101_out, not_102_out, not_103_out, not_104_out,
       not_105_out, not_106_out, not_107_out, not_108_out, not_109_out, not_110_out, not_111_out,
       not_112_out, not_113_out, not_114_out, not_115_out, not_116_out, not_117_out, not_118_out,
       not_119_out, not_120_out, not_121_out, not_122_out, not_123_out, not_124_out;

  not not_1 (not_1_out, x3);
  not not_2 (not_2_out, x2);
  not not_3 (not_3_out, lw);
  not not_4 (not_4_out, sw);
  not not_5 (not_5_out, beq);
  not not_6 (not_6_out, addi);
  not not_7 (not_7_out, x3);
  not not_8 (not_8_out, x2);
  not not_9 (not_9_out, lw);
  not not_10 (not_10_out, sw);
  not not_11 (not_11_out, beq);
  not not_12 (not_12_out, add);
  not not_13 (not_13_out, x4);
  not not_14 (not_14_out, x3);
  not not_15 (not_15_out, x2);
  not not_16 (not_16_out, x1);
  not not_17 (not_17_out, x3);
  not not_18 (not_18_out, x3);
  not not_19 (not_19_out, x0);
  not not_20 (not_20_out, x4);
  not not_21 (not_21_out, x3);
  not not_22 (not_22_out, lw);
  not not_23 (not_23_out, sw);
  not not_24 (not_24_out, addi);
  not not_25 (not_25_out, add);
  not not_26 (not_26_out, x4);
  not not_27 (not_27_out, x3);
  not not_28 (not_28_out, lw);
  not not_29 (not_29_out, beq);
  not not_30 (not_30_out, addi);
  not not_31 (not_31_out, add);
  not not_32 (not_32_out, x3);
  not not_33 (not_33_out, x4);
  not not_34 (not_34_out, x2);
  not not_35 (not_35_out, x4);
  not not_36 (not_36_out, x2);
  not not_37 (not_37_out, x4);
  not not_38 (not_38_out, x0);
  not not_39 (not_39_out, x4);
  not not_40 (not_40_out, x2);
  not not_41 (not_41_out, lw);
  not not_42 (not_42_out, sw);
  not not_43 (not_43_out, beq);
  not not_44 (not_44_out, addi);
  not not_45 (not_45_out, x4);
  not not_46 (not_46_out, x2);
  not not_47 (not_47_out, lw);
  not not_48 (not_48_out, sw);
  not not_49 (not_49_out, addi);
  not not_50 (not_50_out, add);
  not not_51 (not_51_out, x4);
  not not_52 (not_52_out, x2);
  not not_53 (not_53_out, sw);
  not not_54 (not_54_out, beq);
  not not_55 (not_55_out, addi);
  not not_56 (not_56_out, add);
  not not_57 (not_57_out, x4);
  not not_58 (not_58_out, x3);
  not not_59 (not_59_out, x1);
  not not_60 (not_60_out, x4);
  not not_61 (not_61_out, x0);
  not not_62 (not_62_out, x3);
  not not_63 (not_63_out, x0);
  not not_64 (not_64_out, x4);
  not not_65 (not_65_out, x2);
  not not_66 (not_66_out, x3);
  not not_67 (not_67_out, x2);
  not not_68 (not_68_out, x4);
  not not_69 (not_69_out, x3);
  not not_70 (not_70_out, x1);
  not not_71 (not_71_out, x4);
  not not_72 (not_72_out, x2);
  not not_73 (not_73_out, x1);
  not not_74 (not_74_out, x3);
  not not_75 (not_75_out, x2);
  not not_76 (not_76_out, x1);
  not not_77 (not_77_out, x4);
  not not_78 (not_78_out, x0);
  not not_79 (not_79_out, x4);
  not not_80 (not_80_out, x3);
  not not_81 (not_81_out, x2);
  not not_82 (not_82_out, lw);
  not not_83 (not_83_out, sw);
  not not_84 (not_84_out, beq);
  not not_85 (not_85_out, addi);
  not not_86 (not_86_out, x4);
  not not_87 (not_87_out, x3);
  not not_88 (not_88_out, x2);
  not not_89 (not_89_out, lw);
  not not_90 (not_90_out, sw);
  not not_91 (not_91_out, beq);
  not not_92 (not_92_out, add);
  not not_93 (not_93_out, x4);
  not not_94 (not_94_out, x3);
  not not_95 (not_95_out, x2);
  not not_96 (not_96_out, lw);
  not not_97 (not_97_out, sw);
  not not_98 (not_98_out, addi);
  not not_99 (not_99_out, add);
  not not_100 (not_100_out, x3);
  not not_101 (not_101_out, x0);
  not not_102 (not_102_out, x3);
  not not_103 (not_103_out, x1);
  not not_104 (not_104_out, x0);
  not not_105 (not_105_out, x4);
  not not_106 (not_106_out, x0);
  not not_107 (not_107_out, x4);
  not not_108 (not_108_out, x3);
  not not_109 (not_109_out, x2);
  not not_110 (not_110_out, lw);
  not not_111 (not_111_out, sw);
  not not_112 (not_112_out, beq);
  not not_113 (not_113_out, add);
  not not_114 (not_114_out, x4);
  not not_115 (not_115_out, x3);
  not not_116 (not_116_out, x2);
  not not_117 (not_117_out, lw);
  not not_118 (not_118_out, beq);
  not not_119 (not_119_out, addi);
  not not_120 (not_120_out, add);
  not not_121 (not_121_out, x4);
  not not_122 (not_122_out, x0);
  not not_123 (not_123_out, x3);
  not not_124 (not_124_out, x0);
  and and_1 (and_1_out, not_1_out, not_2_out, x1, x0, not_3_out, not_4_out, not_5_out, not_6_out, add);
  and and_2 (and_2_out, not_7_out, not_8_out, x1, x0, not_9_out, not_10_out, not_11_out, addi, not_12_out);
  and and_3 (and_3_out, not_13_out, x3, x2, x1, x0, equal);
  and and_4 (and_4_out, x4, not_14_out, not_15_out, not_16_out);
  and and_5 (and_5_out, x4, not_17_out, x1, x0);
  and and_6 (and_6_out, x4, not_18_out, x2, not_19_out);
  and and_7 (and_7_out, not_20_out, not_21_out, x1, x0, not_22_out, not_23_out, beq, not_24_out, not_25_out);
  and and_8 (and_8_out, not_26_out, not_27_out, x1, x0, not_28_out, sw, not_29_out, not_30_out, not_31_out);
  and and_9 (and_9_out, not_32_out, x2, x1, x0);
  and and_10 (and_10_out, not_33_out, x3, not_34_out, x0);
  and and_11 (and_11_out, not_35_out, x3, not_36_out, x1);
  and and_12 (and_12_out, not_37_out, x3, x2, not_38_out);
  and and_13 (and_13_out, not_39_out, not_40_out, x1, x0, not_41_out, not_42_out, not_43_out, not_44_out, add);
  and and_14 (and_14_out, not_45_out, not_46_out, x1, x0, not_47_out, not_48_out, beq, not_49_out, not_50_out);
  and and_15 (and_15_out, not_51_out, not_52_out, x1, x0, lw, not_53_out, not_54_out, not_55_out, not_56_out);
  and and_16 (and_16_out, not_57_out, not_58_out, x2, not_59_out);
  and and_17 (and_17_out, not_60_out, x2, not_61_out);
  and and_18 (and_18_out, not_62_out, x2, not_63_out);
  and and_19 (and_19_out, not_64_out, x3, not_65_out, x1, x0);
  and and_20 (and_20_out, x4, not_66_out, not_67_out, x1, x0);
  and and_21 (and_21_out, not_68_out, not_69_out, not_70_out, x0);
  and and_22 (and_22_out, not_71_out, not_72_out, not_73_out, x0);
  and and_23 (and_23_out, not_74_out, not_75_out, not_76_out, x0);
  and and_24 (and_24_out, not_77_out, x1, not_78_out);
  and and_25 (and_25_out, not_79_out, not_80_out, not_81_out, x1, not_82_out, not_83_out, not_84_out, not_85_out, add);
  and and_26 (and_26_out, not_86_out, not_87_out, not_88_out, x1, not_89_out, not_90_out, not_91_out, addi, not_92_out);
  and and_27 (and_27_out, not_93_out, not_94_out, not_95_out, x1, not_96_out, not_97_out, beq, not_98_out, not_99_out);
  and and_28 (and_28_out, not_100_out, x2, x1, not_101_out);
  and and_29 (and_29_out, not_102_out, not_103_out, not_104_out);
  and and_30 (and_30_out, not_105_out, x1, not_106_out);
  and and_31 (and_31_out, not_107_out, not_108_out, not_109_out, x1, not_110_out, not_111_out, not_112_out, addi, not_113_out);
  and and_32 (and_32_out, not_114_out, not_115_out, not_116_out, x1, not_117_out, sw, not_118_out, not_119_out, not_120_out);
  and and_33 (and_33_out, not_121_out, x2, not_122_out);
  and and_34 (and_34_out, not_123_out, x2, not_124_out);
  or or_1 (y4, and_1_out, and_2_out, and_3_out, and_4_out, and_5_out, and_6_out, syscall);
  or or_2 (y3, and_7_out, and_8_out, and_9_out, and_10_out, and_11_out, and_12_out, syscall);
  or or_3 (y2, and_13_out, and_14_out, and_15_out, and_16_out, and_17_out, and_18_out, and_19_out, and_20_out, syscall);
  or or_4 (y1, and_21_out, and_22_out, and_23_out, and_24_out, and_25_out, and_26_out, and_27_out, and_28_out, syscall);
  or or_5 (y0, and_29_out, and_30_out, and_31_out, and_32_out, and_33_out, and_34_out, syscall);
endmodule

// 输出逻辑
module \硬布线输出逻辑  (
  input  s4,
  input  s3,
  input  s2,
  input  s1,
  input  s0,
  output PCout,
  output ARin,
  output Xin,
  output Read,
  output DRMin,
  output Ads,
  output ADD,
  output Zout,
  output PCin,
  output DRout,
  output IRin,
  output RegR,
  output Rout,
  output IR_immout,
  output Zin,
  output RegW,
  output Rin,
  output DRin,
  output Write,
  output SUB,
  output PSWin,
  output I_imms,
  output RegDst
);

  wire and_2_out, and_3_out, and_4_out, and_5_out, and_6_out, and_7_out, and_8_out, and_9_out, and_10_out,
       and_11_out, and_12_out, and_13_out, and_14_out, and_15_out, and_16_out, and_17_out, and_18_out,
       and_19_out, and_20_out, and_21_out, and_22_out, and_23_out, and_24_out, and_25_out, and_26_out,
       and_27_out, and_28_out, and_29_out, and_30_out, and_32_out, and_33_out, and_35_out, and_36_out,
       and_37_out, and_38_out, and_39_out, and_40_out, and_41_out, and_42_out, and_43_out, and_44_out,
       and_45_out, and_46_out, and_47_out, and_48_out, and_49_out, and_50_out, and_51_out, and_52_out,
       and_53_out, and_58_out, and_59_out, and_60_out, not_1_out, not_2_out, not_3_out, not_4_out, not_5_out,
       not_6_out, not_7_out, not_8_out, not_9_out, not_10_out, not_11_out, not_12_out, not_13_out,
       not_14_out, not_15_out, not_16_out, not_17_out, not_18_out, not_19_out, not_20_out, not_21_out,
       not_22_out, not_23_out, not_24_out, not_25_out, not_26_out, not_27_out, not_28_out, not_29_out,
       not_30_out, not_31_out, not_32_out, not_33_out, not_34_out, not_35_out, not_36_out, not_37_out,
       not_38_out, not_39_out, not_40_out, not_41_out, not_42_out, not_43_out, not_44_out, not_45_out,
       not_46_out, not_47_out, not_48_out, not_49_out, not_50_out, not_51_out, not_52_out, not_53_out,
       not_54_out, not_55_out, not_56_out, not_57_out, not_58_out, not_59_out, not_60_out, not_61_out,
       not_62_out, not_63_out, not_64_out, not_65_out, not_66_out, not_67_out, not_68_out, not_69_out,
       not_70_out, not_71_out, not_72_out, not_73_out, not_74_out, not_75_out, not_76_out, not_77_out,
       not_78_out, not_79_out, not_80_out, not_81_out, not_82_out, not_83_out, not_84_out, not_85_out,
       not_86_out, not_87_out, not_88_out, not_89_out, not_90_out, not_91_out, not_92_out, not_93_out,
       not_94_out, not_95_out, not_96_out, not_97_out, not_98_out, not_99_out, not_100_out, not_101_out,
       not_102_out, not_103_out, not_104_out, not_105_out, not_106_out, not_107_out, not_108_out,
       not_109_out, not_110_out, not_111_out, not_112_out, not_113_out, not_114_out, not_115_out,
       not_116_out, not_117_out, not_118_out, not_119_out, not_120_out, not_121_out, not_122_out,
       not_123_out, not_124_out, not_125_out, not_126_out, not_127_out, not_128_out, not_129_out,
       not_130_out, not_131_out, not_132_out, not_133_out, not_134_out, not_135_out, not_136_out,
       not_137_out, not_138_out, not_139_out, not_140_out, not_141_out, not_142_out, not_143_out,
       not_144_out, not_145_out, not_146_out, not_147_out, not_148_out, not_149_out, not_150_out,
       not_151_out, not_152_out, not_153_out, not_154_out, not_155_out, not_156_out;

  not not_1 (not_1_out, s3);
  not not_2 (not_2_out, s2);
  not not_3 (not_3_out, s1);
  not not_4 (not_4_out, s0);
  not not_5 (not_5_out, s4);
  not not_6 (not_6_out, s3);
  not not_7 (not_7_out, s2);
  not not_8 (not_8_out, s1);
  not not_9 (not_9_out, s0);
  not not_10 (not_10_out, s4);
  not not_11 (not_11_out, s3);
  not not_12 (not_12_out, s0);
  not not_13 (not_13_out, s4);
  not not_14 (not_14_out, s2);
  not not_15 (not_15_out, s4);
  not not_16 (not_16_out, s3);
  not not_17 (not_17_out, s1);
  not not_18 (not_18_out, s0);
  not not_19 (not_19_out, s3);
  not not_20 (not_20_out, s2);
  not not_21 (not_21_out, s1);
  not not_22 (not_22_out, s0);
  not not_23 (not_23_out, s4);
  not not_24 (not_24_out, s1);
  not not_25 (not_25_out, s4);
  not not_26 (not_26_out, s0);
  not not_27 (not_27_out, s3);
  not not_28 (not_28_out, s2);
  not not_29 (not_29_out, s3);
  not not_30 (not_30_out, s0);
  not not_31 (not_31_out, s4);
  not not_32 (not_32_out, s3);
  not not_33 (not_33_out, s2);
  not not_34 (not_34_out, s1);
  not not_35 (not_35_out, s4);
  not not_36 (not_36_out, s3);
  not not_37 (not_37_out, s4);
  not not_38 (not_38_out, s3);
  not not_39 (not_39_out, s2);
  not not_40 (not_40_out, s1);
  not not_41 (not_41_out, s4);
  not not_42 (not_42_out, s3);
  not not_43 (not_43_out, s4);
  not not_44 (not_44_out, s3);
  not not_45 (not_45_out, s1);
  not not_46 (not_46_out, s4);
  not not_47 (not_47_out, s2);
  not not_48 (not_48_out, s0);
  not not_49 (not_49_out, s4);
  not not_50 (not_50_out, s3);
  not not_51 (not_51_out, s2);
  not not_52 (not_52_out, s1);
  not not_53 (not_53_out, s3);
  not not_54 (not_54_out, s1);
  not not_55 (not_55_out, s0);
  not not_56 (not_56_out, s3);
  not not_57 (not_57_out, s4);
  not not_58 (not_58_out, s3);
  not not_59 (not_59_out, s1);
  not not_60 (not_60_out, s3);
  not not_61 (not_61_out, s2);
  not not_62 (not_62_out, s1);
  not not_63 (not_63_out, s4);
  not not_64 (not_64_out, s2);
  not not_65 (not_65_out, s0);
  not not_66 (not_66_out, s3);
  not not_67 (not_67_out, s1);
  not not_68 (not_68_out, s0);
  not not_69 (not_69_out, s3);
  not not_70 (not_70_out, s4);
  not not_71 (not_71_out, s3);
  not not_72 (not_72_out, s0);
  not not_73 (not_73_out, s3);
  not not_74 (not_74_out, s2);
  not not_75 (not_75_out, s0);
  not not_76 (not_76_out, s4);
  not not_77 (not_77_out, s2);
  not not_78 (not_78_out, s3);
  not not_79 (not_79_out, s1);
  not not_80 (not_80_out, s2);
  not not_81 (not_81_out, s1);
  not not_82 (not_82_out, s0);
  not not_83 (not_83_out, s3);
  not not_84 (not_84_out, s2);
  not not_85 (not_85_out, s0);
  not not_86 (not_86_out, s4);
  not not_87 (not_87_out, s3);
  not not_88 (not_88_out, s2);
  not not_89 (not_89_out, s4);
  not not_90 (not_90_out, s2);
  not not_91 (not_91_out, s1);
  not not_92 (not_92_out, s0);
  not not_93 (not_93_out, s4);
  not not_94 (not_94_out, s3);
  not not_95 (not_95_out, s2);
  not not_96 (not_96_out, s4);
  not not_97 (not_97_out, s1);
  not not_98 (not_98_out, s0);
  not not_99 (not_99_out, s4);
  not not_100 (not_100_out, s3);
  not not_101 (not_101_out, s4);
  not not_102 (not_102_out, s1);
  not not_103 (not_103_out, s0);
  not not_104 (not_104_out, s4);
  not not_105 (not_105_out, s1);
  not not_106 (not_106_out, s4);
  not not_107 (not_107_out, s3);
  not not_108 (not_108_out, s3);
  not not_109 (not_109_out, s4);
  not not_110 (not_110_out, s3);
  not not_111 (not_111_out, s1);
  not not_112 (not_112_out, s4);
  not not_113 (not_113_out, s2);
  not not_114 (not_114_out, s0);
  not not_115 (not_115_out, s3);
  not not_116 (not_116_out, s2);
  not not_117 (not_117_out, s1);
  not not_118 (not_118_out, s3);
  not not_119 (not_119_out, s1);
  not not_120 (not_120_out, s0);
  not not_121 (not_121_out, s4);
  not not_122 (not_122_out, s3);
  not not_123 (not_123_out, s1);
  not not_124 (not_124_out, s3);
  not not_125 (not_125_out, s2);
  not not_126 (not_126_out, s1);
  not not_127 (not_127_out, s4);
  not not_128 (not_128_out, s2);
  not not_129 (not_129_out, s0);
  not not_130 (not_130_out, s3);
  not not_131 (not_131_out, s1);
  not not_132 (not_132_out, s0);
  not not_133 (not_133_out, s3);
  not not_134 (not_134_out, s2);
  not not_135 (not_135_out, s1);
  not not_136 (not_136_out, s0);
  not not_137 (not_137_out, s3);
  not not_138 (not_138_out, s1);
  not not_139 (not_139_out, s4);
  not not_140 (not_140_out, s1);
  not not_141 (not_141_out, s0);
  not not_142 (not_142_out, s4);
  not not_143 (not_143_out, s1);
  not not_144 (not_144_out, s4);
  not not_145 (not_145_out, s4);
  not not_146 (not_146_out, s4);
  not not_147 (not_147_out, s3);
  not not_148 (not_148_out, s1);
  not not_149 (not_149_out, s4);
  not not_150 (not_150_out, s2);
  not not_151 (not_151_out, s0);
  not not_152 (not_152_out, s3);
  not not_153 (not_153_out, s1);
  not not_154 (not_154_out, s0);
  not not_155 (not_155_out, s3);
  not not_156 (not_156_out, s1);
  and and_1 (PCout, not_1_out, not_2_out, not_3_out, not_4_out);
  and and_2 (and_2_out, not_5_out, not_6_out, not_7_out, not_8_out, not_9_out);
  and and_3 (and_3_out, not_10_out, not_11_out, s2, s1, not_12_out);
  and and_4 (and_4_out, not_13_out, s3, not_14_out, s1, s0);
  and and_5 (and_5_out, not_15_out, not_16_out, not_17_out, not_18_out);
  and and_6 (and_6_out, not_19_out, not_20_out, not_21_out, not_22_out);
  and and_7 (and_7_out, not_23_out, s3, not_24_out, s0);
  and and_8 (and_8_out, not_25_out, s3, s2, s1, not_26_out);
  and and_9 (and_9_out, s4, not_27_out, not_28_out, s1, s0);
  and and_10 (and_10_out, s4, not_29_out, s2, s1, not_30_out);
  and and_11 (and_11_out, not_31_out, not_32_out, not_33_out, not_34_out, s0);
  and and_12 (and_12_out, not_35_out, not_36_out, s2, s1, s0);
  and and_13 (and_13_out, not_37_out, not_38_out, not_39_out, not_40_out, s0);
  and and_14 (and_14_out, not_41_out, not_42_out, s2, s1, s0);
  and and_15 (and_15_out, not_43_out, not_44_out, s2, not_45_out, s0);
  and and_16 (and_16_out, not_46_out, s3, not_47_out, s1, not_48_out);
  and and_17 (and_17_out, not_49_out, s3, s2, s1, s0);
  and and_18 (and_18_out, s4, not_50_out, not_51_out, not_52_out, s0);
  and and_19 (and_19_out, s4, not_53_out, s2, not_54_out, not_55_out);
  and and_20 (and_20_out, s4, not_56_out, s2, s1, s0);
  and and_21 (and_21_out, not_57_out, not_58_out, not_59_out, s0);
  and and_22 (and_22_out, not_60_out, not_61_out, not_62_out, s0);
  and and_23 (and_23_out, not_63_out, s3, not_64_out, s1, not_65_out);
  and and_24 (and_24_out, s4, not_66_out, s2, not_67_out, not_68_out);
  and and_25 (and_25_out, s4, not_69_out, s2, s1, s0);
  and and_26 (and_26_out, not_70_out, not_71_out, s1, not_72_out);
  and and_27 (and_27_out, not_73_out, not_74_out, s1, not_75_out);
  and and_28 (and_28_out, not_76_out, s3, not_77_out, s1, s0);
  and and_29 (and_29_out, s4, not_78_out, s2, not_79_out, s0);
  and and_30 (and_30_out, s4, s3, not_80_out, not_81_out, not_82_out);
  and and_31 (PCin, not_83_out, not_84_out, s1, not_85_out);
  and and_32 (and_32_out, not_86_out, not_87_out, not_88_out, s1, s0);
  and and_33 (and_33_out, not_89_out, s3, not_90_out, not_91_out, not_92_out);
  and and_34 (IRin, not_93_out, not_94_out, not_95_out, s1, s0);
  and and_35 (and_35_out, not_96_out, s3, s2, not_97_out, not_98_out);
  and and_36 (and_36_out, not_99_out, s3, s2, s1, s0);
  and and_37 (and_37_out, s4, not_100_out, s2, s1, s0);
  and and_38 (and_38_out, not_101_out, s2, not_102_out, not_103_out);
  and and_39 (and_39_out, not_104_out, s3, not_105_out, s0);
  and and_40 (and_40_out, not_106_out, s3, s2);
  and and_41 (and_41_out, s4, not_107_out, s1, s0);
  and and_42 (and_42_out, s4, not_108_out, s2, s1);
  and and_43 (and_43_out, not_109_out, not_110_out, s2, not_111_out, s0);
  and and_44 (and_44_out, not_112_out, s3, not_113_out, s1, not_114_out);
  and and_45 (and_45_out, s4, not_115_out, not_116_out, not_117_out, s0);
  and and_46 (and_46_out, s4, not_118_out, s2, not_119_out, not_120_out);
  and and_47 (and_47_out, not_121_out, not_122_out, not_123_out, s0);
  and and_48 (and_48_out, not_124_out, not_125_out, not_126_out, s0);
  and and_49 (and_49_out, not_127_out, s3, not_128_out, s1, not_129_out);
  and and_50 (and_50_out, s4, not_130_out, s2, not_131_out, not_132_out);
  and and_51 (and_51_out, s4, not_133_out, s2, s1, s0);
  and and_52 (and_52_out, s3, not_134_out, not_135_out, not_136_out);
  and and_53 (and_53_out, s4, not_137_out, s2, not_138_out, s0);
  and and_54 (DRin, not_139_out, s3, s2, not_140_out, not_141_out);
  and and_55 (Write, not_142_out, s3, s2, not_143_out, s0);
  and and_56 (SUB, not_144_out, s3, s2, s1, s0);
  and and_57 (PSWin, not_145_out, s3, s2, s1, s0);
  and and_58 (and_58_out, not_146_out, not_147_out, s2, not_148_out, s0);
  and and_59 (and_59_out, not_149_out, s3, not_150_out, s1, not_151_out);
  and and_60 (and_60_out, s4, not_152_out, s2, not_153_out, not_154_out);
  and and_61 (RegDst, s4, not_155_out, s2, not_156_out, s0);
  or or_1 (ARin, and_2_out, and_3_out, and_4_out);
  or or_2 (Xin, and_5_out, and_6_out, and_7_out, and_8_out, and_9_out, and_10_out);
  or or_3 (Read, and_11_out, and_12_out);
  or or_4 (DRMin, and_13_out, and_14_out);
  or or_5 (Ads, and_15_out, and_16_out, and_17_out, and_18_out, and_19_out, and_20_out);
  or or_6 (ADD, and_21_out, and_22_out, and_23_out, and_24_out, and_25_out);
  or or_7 (Zout, and_26_out, and_27_out, and_28_out, and_29_out, and_30_out);
  or or_8 (DRout, and_32_out, and_33_out);
  or or_9 (RegR, and_35_out, and_36_out, and_37_out);
  or or_10 (Rout, and_38_out, and_39_out, and_40_out, and_41_out, and_42_out);
  or or_11 (IR_immout, and_43_out, and_44_out, and_45_out, and_46_out);
  or or_12 (Zin, and_47_out, and_48_out, and_49_out, and_50_out, and_51_out);
  or or_13 (Rin, and_52_out, and_53_out);
  or or_14 (I_imms, and_58_out, and_59_out, and_60_out);

  assign RegW = 1'b0;
endmodule

module \控制器  (
  input  [5:0] op,
  input  [5:0] func,
  input  not_equal,
  input  clk,
  output PCout,
  output ARin,
  output Xin,
  output Read,
  output DRMin,
  output Ads,
  output ADD,
  output Zout,
  output PCin,
  output DRout,
  output IRin,
  output RegR,
  output Rout,
  output IR_immout,
  output Zin,
  output RegW,
  output Rin,
  output DRin,
  output Write,
  output SUB,
  output PSWin,
  output I_imms,
  output RegDst
);

  wire \指令译码_1_add , \指令译码_1_addi , \指令译码_1_beq , \指令译码_1_lw , \指令译码_1_sw , \指令译码_1_syscall ;
  wire [4:0] FSMreg_q, \状态转移_1_y0 ;

  \指令译码  \u_指令译码_1  (
    .op(op), .func(func), .lw(\指令译码_1_lw ), .sw(\指令译码_1_sw ), .beq(\指令译码_1_beq ), .addi(\指令译码_1_addi ),
    .add(\指令译码_1_add ), .syscall(\指令译码_1_syscall ));
  Register #(.width(5), .trigger("falling"), .Select("low")) FSMreg (
    .D(\状态转移_1_y0 ), .Q(FSMreg_q), .clk(clk));  // open: en, clr
  \状态转移  \u_状态转移_1  (
    .x4(FSMreg_q[4]), .x3(FSMreg_q[3]), .x2(FSMreg_q[2]), .x1(FSMreg_q[1]), .x0(FSMreg_q[0]),
    .lw(\指令译码_1_lw ), .sw(\指令译码_1_sw ), .beq(\指令译码_1_beq ), .addi(\指令译码_1_addi ), .add(\指令译码_1_add ),
    .syscall(\指令译码_1_syscall ), .equal(not_equal), .y4(\状态转移_1_y0 [4]), .y3(\状态转移_1_y0 [3]),
    .y2(\状态转移_1_y0 [2]), .y1(\状态转移_1_y0 [1]), .y0(\状态转移_1_y0 [0]));
  \硬布线输出逻辑  \u_硬布线输出逻辑_1  (
    .s4(FSMreg_q[4]), .s3(FSMreg_q[3]), .s2(FSMreg_q[2]), .s1(FSMreg_q[1]), .s0(FSMreg_q[0]), .PCout(PCout),
    .ARin(ARin), .Xin(Xin), .Read(Read), .DRMin(DRMin), .Ads(Ads), .ADD(ADD), .Zout(Zout), .PCin(PCin),
    .DRout(DRout), .IRin(IRin), .RegR(RegR), .Rout(Rout), .IR_immout(IR_immout), .Zin(Zin), .RegW(RegW),
    .Rin(Rin), .DRin(DRin), .Write(Write), .SUB(SUB), .PSWin(PSWin), .I_imms(I_imms), .RegDst(RegDst));

  // Notes on the sheet:
  //   调整为下降沿触发
endmodule

module \MIPS多周期  (
);

  wire ADD, Ads, ARin, clk, DRin, DRMin, DRout, I_imms, IR_immout, IRin, \n32位快速加法_减法器_1_zf , notequal, PCin,
       PCout, PSW_q, PSWin, Read, RegDst, RegR, RegW, Rin, Rout, SUB, Write, Xin, Zin, Zout;
  wire [2:0] multiplexer_2_out, multiplexer_3_out;
  wire [5:0] IR_q, IR_q_3;
  wire [25:6] IR_q_2;
  wire [31:0] AR_q, bit_extender_1_out, controlled_buffer_1_out, controlled_buffer_2_out,
       controlled_buffer_3_out, controlled_buffer_4_out, controlled_buffer_8_out, DR_q, mem_8_32_1_dout,
       multiplexer_1_out, multiplexer_4_out, \n32位快速加法_减法器_1_out , PC_q, X_q, Z_q, \寄存器堆for多周期_1_data_out ,
       \逻辑左移2位_1_out_2 ;

  Clock #(.highDuration(1), .lowDuration(1)) clock_1 (.out(clk));
  assign controlled_buffer_1_out = PCout ? PC_q : 32'bz;  // Controlled_Buffer controlled_buffer_1
  assign controlled_buffer_2_out = PCin ? controlled_buffer_1_out : 32'bz;  // Controlled_Buffer controlled_buffer_2
  Register #(.width(32), .trigger("rising"), .Select("low")) PC (
    .D(controlled_buffer_2_out), .Q(PC_q), .clk(clk));  // open: en, clr
  Register #(.width(32), .trigger("rising"), .Select("low")) AR (
    .D(controlled_buffer_1_out), .en(ARin), .Q(AR_q), .clk(clk));  // open: clr
  \控制器  \u_控制器_1  (
    .op(IR_q_3), .func(IR_q), .clk(clk), .not_equal(notequal), .PCout(PCout), .ARin(ARin), .Xin(Xin),
    .Read(Read), .DRMin(DRMin), .Ads(Ads), .ADD(ADD), .Zout(Zout), .PCin(PCin), .DRout(DRout), .IRin(IRin),
    .RegR(RegR), .Rout(Rout), .IR_immout(IR_immout), .Zin(Zin), .RegW(RegW), .Rin(Rin), .DRin(DRin),
    .Write(Write), .SUB(SUB), .PSWin(PSWin), .I_imms(I_imms), .RegDst(RegDst));
  MEM_8_32 mem_8_32_1 (.Din(controlled_buffer_3_out), .Adress(AR_q[9:2]), .W(Write), .clk(clk), .Dout(mem_8_32_1_dout));
  assign controlled_buffer_3_out = Write ? DR_q : 32'bz;  // Controlled_Buffer controlled_buffer_3
  assign controlled_buffer_4_out = DRin ? controlled_buffer_1_out : 32'bz;  // Controlled_Buffer controlled_buffer_4
  assign controlled_buffer_4_out = DRMin ? mem_8_32_1_dout : 32'bz;  // Controlled_Buffer controlled_buffer_5
  Register #(.width(32), .trigger("rising"), .Select("low")) IR (
    .D(controlled_buffer_1_out), .en(IRin), .Q({IR_q_3, IR_q_2, IR_q}), .clk(clk));  // open: clr
  assign controlled_buffer_1_out = DRout ? DR_q : 32'bz;  // Controlled_Buffer controlled_buffer_6
  Register #(.width(32), .trigger("rising"), .Select("low")) DR (
    .D(controlled_buffer_4_out), .Q(DR_q), .clk(clk));  // open: en, clr
  Multiplexer #(.select(1), .width(32), .disabled("Z"), .enable("false")) multiplexer_1 (
    .in0(32'h4), .in1(controlled_buffer_1_out), .out(multiplexer_1_out), .sel(Ads));
  Register #(.width(32), .trigger("rising"), .Select("low")) X (
    .D(controlled_buffer_1_out), .en(Xin), .Q(X_q), .clk(clk));  // open: clr
  assign bit_extender_1_out = {{16{IR_q_2[15]}}, {IR_q_2[15:6], IR_q}};  // Bit_Extender bit_extender_1
  \逻辑左移2位  \u_逻辑左移2位_1  (.in_1(bit_extender_1_out), .out_2(\逻辑左移2位_1_out_2 ));
  \_32位快速加法_减法器  \u_32位快速加法_减法器_1  (
    .C0(1'b0), .SUB(1'b0), .OUT(\n32位快速加法_减法器_1_out ), .X(multiplexer_1_out), .Y(X_q),
    .ZF(\n32位快速加法_减法器_1_zf ));  // open: CF, OF
  Multiplexer #(.select(1), .width(3), .disabled("Z"), .enable("false")) multiplexer_2 (
    .in0(IR_q_2[23:21]), .in1(IR_q_2[18:16]), .out(multiplexer_2_out), .sel(RegR));
  Multiplexer #(.select(1), .width(3), .disabled("Z"), .enable("false")) multiplexer_3 (
    .in0(IR_q_2[18:16]), .in1(IR_q_2[13:11]), .out(multiplexer_3_out), .sel(RegW));
  Multiplexer #(.select(1), .width(32), .disabled("Z"), .enable("false")) multiplexer_4 (
    .in0(\逻辑左移2位_1_out_2 ), .in1(bit_extender_1_out), .out(multiplexer_4_out), .sel(I_imms));
  assign controlled_buffer_1_out = IR_immout ? multiplexer_4_out : 32'bz;  // Controlled_Buffer controlled_buffer_7
  assign controlled_buffer_8_out = Rin ? controlled_buffer_1_out : 32'bz;  // Controlled_Buffer controlled_buffer_8
  not not_1 (notequal, PSW_q);
  Register #(.width(1), .trigger("rising"), .Select("low")) PSW (
    .D(\n32位快速加法_减法器_1_zf ), .en(PSWin), .Q(PSW_q), .clk(clk));  // open: clr
  \寄存器堆for多周期  \u_寄存器堆for多周期_1  (
    .Data_in(controlled_buffer_8_out), .W_rt___rd(multiplexer_3_out), .clk(clk),
    .Data_out(\寄存器堆for多周期_1_data_out ), .R_num(multiplexer_2_out));  // open: W
  assign controlled_buffer_1_out = Rout ? \寄存器堆for多周期_1_data_out  : 32'bz;  // Controlled_Buffer controlled_buffer_9
  Register #(.width(32), .trigger("rising"), .Select("low")) Z (
    .D(\n32位快速加法_减法器_1_out ), .en(Zin), .Q(Z_q), .clk(clk));  // open: clr
  assign controlled_buffer_1_out = Zout ? Z_q : 32'bz;  // Controlled_Buffer controlled_buffer_10
endmodule
